// Logisim project 中断按键信号产生.circ as structural Verilog: 2 circuits, main circuit main
module main (
  input  \同步清零信号 ,
  output \与中断屏蔽位与 
);

  wire \_1号中断 , \_1号中断_out , \_1号中断等待指示 , \_2号中断 , \_2号中断等待指示 , \_3号中断 , \_3号中断等待指示 , and_1_out, clock_1_out,
       d_ff_1_q, or_1_out, or_2_out;

  Button _1 (.out(\_1号中断 ));
  Button _2 (.out(\_2号中断 ));
  Button _3 (.out(\_3号中断 ));
  Clock #(.highDuration(1), .lowDuration(1)) clock_1 (.out(clock_1_out));
  Button \u__1号中断  (.out(\_1号中断_out ));
  LED #(.active("true")) \_1号中断等待指示灯  (.in(or_1_out));
  Hex_Digit_Display hex_digit_display_1 (.value(4'b1000));  // open: dp
  Hex_Digit_Display hex_digit_display_2 (.value(4'b1000));  // open: dp
  D_Flip_Flop #(.trigger("rising"), .Pre_Clr_Positions("LEGACY"), .NegatePresetClear("false"), .enable("true"), .NewFFLayout("false")) d_ff_1 (
    .clk(\_1号中断_out ), .D(1'b1), .Q(d_ff_1_q), .reset(\与中断屏蔽位与 ));  // open: Qn, preset, en
  or or_1 (or_1_out, \与中断屏蔽位与 , d_ff_1_q);
  Hex_Digit_Display hex_digit_display_3 (.value(4'b1000));  // open: dp
  Hex_Digit_Display hex_digit_display_4 (.value(4'b1000));  // open: dp
  LED #(.active("true")) _1_2 (.in(\_1号中断等待指示 ));
  LED #(.active("true")) _2_2 (.in(\_2号中断等待指示 ));
  LED #(.active("true")) _3_2 (.in(\_3号中断等待指示 ));
  Hex_Digit_Display hex_digit_display_5 (.value(4'b1000));  // open: dp
  Hex_Digit_Display hex_digit_display_6 (.value(4'b1000));  // open: dp
  or or_2 (or_2_out, d_ff_1_q, \与中断屏蔽位与 );
  and and_1 (and_1_out, or_2_out, ~\同步清零信号 );  // AND_Gate
  Hex_Digit_Display hex_digit_display_7 (.value(4'b1000));  // open: dp
  Hex_Digit_Display hex_digit_display_8 (.value(4'b1000));  // open: dp
  // Probe on \_1号中断 
  D_Flip_Flop #(.trigger("rising"), .Pre_Clr_Positions("LEGACY"), .NegatePresetClear("false"), .enable("true"), .NewFFLayout("false")) IR1 (
    .clk(clock_1_out), .D(and_1_out), .Q(\与中断屏蔽位与 ));  // open: Qn, preset, en, reset

  // Notes on the sheet:
  //   中断按键和显示区域放一起，方便检查
  //   中断信号源及指示电路规范（优先级3>2>1>CPU(0）)
  //   中断信号采样参考电路
  //   Reset 
endmodule

module \中断电路规范  (
  input  \同步清零信号 ,
  output \与中断屏蔽位与 
);

  wire \_1号中断_out , and_1_out, clock_1_out, d_ff_1_q, or_1_out, or_2_out;

  Clock #(.highDuration(1), .lowDuration(1)) clock_1 (.out(clock_1_out));
  Button \_1号中断  (.out(\_1号中断_out ));
  LED #(.active("true")) \_1号中断等待指示灯  (.in(or_1_out));
  or or_1 (or_1_out, \与中断屏蔽位与 , d_ff_1_q);
  D_Flip_Flop #(.trigger("rising"), .Pre_Clr_Positions("LEGACY"), .NegatePresetClear("false"), .enable("true"), .NewFFLayout("false")) d_ff_1 (
    .clk(\_1号中断_out ), .D(1'b1), .Q(d_ff_1_q), .reset(\与中断屏蔽位与 ));  // open: Qn, preset, en
  or or_2 (or_2_out, d_ff_1_q, \与中断屏蔽位与 );
  and and_1 (and_1_out, or_2_out, ~\同步清零信号 );  // AND_Gate
  D_Flip_Flop #(.trigger("rising"), .Pre_Clr_Positions("LEGACY"), .NegatePresetClear("false"), .enable("true"), .NewFFLayout("false")) IR1 (
    .clk(clock_1_out), .D(and_1_out), .Q(\与中断屏蔽位与 ));  // open: Qn, preset, en, reset

  // Notes on the sheet:
  //   中断信号采样参考电路
  //   Reset 
endmodule
