// Logisim project 4-ymx10086.circ as structural Verilog: 27 circuits, main circuit ◇单周期RISC-V
module \单周期RISC_V  (
  input  IR1,
  input  IR2,
  input  IR3,
  output RegWrite,
  output MemWrite,
  output [31:0] PC,
  output [31:0] IR,
  output [31:0] RDin,
  output [31:0] MDin,
  output [31:0] LedData
);

  wire ALU_SRC, and_1_out, and_2_out, and_3_out, and_5_out, and_6_out, and_7_out, CLK, clock_1_out,
       comparator_1_eq, comparator_2_eq, comparator_2_lt, d_ff_2_q, ecall, equal, Go, great, halt, IR1_t,
       IR2_t, IR3_t, IRA, IRB, IRC, JAL, JALR, LB, lb_t, MemToReg, nand_1_out, not_1_out, not_2_out,
       not_3_out, not_5_out, or_1_out, or_5_out, riscv_probe_1_p2, RST, tALU_SRC, tMemToReg, tRegWrite, W1,
       W2, W3, \单周期硬布线控制器_1_beq , \单周期硬布线控制器_1_bge , \单周期硬布线控制器_1_bne , \单周期硬布线控制器_1_s_type ;
  wire [1:0] priority_encoder_1_out;
  wire [3:0] \单周期硬布线控制器_1_alu_op ;
  wire [4:0] multiplexer_3_out, multiplexer_4_out;
  wire [7:0] multiplexer_11_out;
  wire [11:0] bit_extender_1_out, multiplexer_5_out, multiplexer_6_out;
  wire [12:0] CNT_num;
  wire [15:0] \总周期数 ;
  wire [31:0] adder_1_out, adder_2_out, adder_3_out, aluresult, bit_extender_2_out, bit_extender_3_out,
       bit_extender_4_out, Dre, LBR, multiplexer_1_out, multiplexer_7_out, multiplexer_9_out,
       multiplexer_10_out, regifile_1_r1, shifter_1_out, shifter_2_out;

  Button \u_继续运行  (.out(Go));
  Button _1 (.out(IRA));
  Button _2 (.out(IRB));
  Button _3 (.out(IRC));
  LED #(.active("true")) led_1 (.in(W1));
  LED #(.active("true")) led_2 (.in(W2));
  LED #(.active("true")) led_3 (.in(W3));
  Button \u_继续运行_2  (.out(RST));
  and and_1 (and_1_out, great, \单周期硬布线控制器_1_bge );
  Hex_Digit_Display hex_digit_display_1 (.value(LedData[31:28]));  // open: dp
  not not_1 (not_1_out, equal);
  and and_2 (and_2_out, \单周期硬布线控制器_1_bne , not_1_out);
  and and_3 (and_3_out, equal, \单周期硬布线控制器_1_beq );
  or or_1 (or_1_out, and_2_out, and_1_out, and_3_out);
  Priority_Encoder #(.select(2), .disabled("Z")) priority_encoder_1 (
    .in0(1'b1), .in1(JALR), .in2(JAL), .in3(or_1_out), .out(priority_encoder_1_out));  // open: gs, en_out, en_in
  Multiplexer #(.select(2), .width(32), .disabled("Z"), .enable("false")) multiplexer_1 (
    .in0(adder_1_out), .in1(aluresult), .in2(adder_3_out), .in3(adder_2_out), .out(multiplexer_1_out),
    .sel(priority_encoder_1_out));
  Hex_Digit_Display hex_digit_display_2 (.value(LedData[27:24]));  // open: dp
  Hex_Digit_Display hex_digit_display_3 (.value(LedData[23:20]));  // open: dp
  not not_2 (not_2_out, halt);
  Hex_Digit_Display hex_digit_display_4 (.value(LedData[15:12]));  // open: dp
  Hex_Digit_Display hex_digit_display_5 (.value(LedData[19:16]));  // open: dp
  // Probe on PC
  Register #(.width(32), .trigger("rising"), .Select("low")) u_PC (
    .D(multiplexer_1_out), .en(not_2_out), .Q(PC), .clk(CLK), .clr(RST));
  Hex_Digit_Display hex_digit_display_6 (.value(LedData[7:4]));  // open: dp
  Hex_Digit_Display hex_digit_display_7 (.value(LedData[11:8]));  // open: dp
  // Probe on \总周期数 
  Adder #(.width(32)) adder_1 (.a(PC), .b(32'h4), .out(adder_1_out));  // open: cin, cout
  Hex_Digit_Display hex_digit_display_8 (.value(LedData[3:0]));  // open: dp
  // RiscV_Probe riscv_probe_1: pin names not known; wires that end beside it: IR, riscv_probe_1_p2
  and and_4 (lb_t, LB, IR[0]);
  ROM #(.addrWidth(10), .dataWidth(32), .Select("high")) rom_1 (.addr(PC[11:2]), .data(IR));
  Adder #(.width(32)) adder_2 (.a(PC), .b(shifter_1_out), .out(adder_2_out));  // open: cin, cout
  Adder #(.width(32)) adder_3 (.a(PC), .b(shifter_2_out), .out(adder_3_out));  // open: cin, cout
  not not_3 (not_3_out, IR[0]);
  and and_5 (and_5_out, LB, not_3_out);
  Multiplexer #(.select(1), .width(3), .disabled("Z"), .enable("false")) multiplexer_2 (
    .in0({tRegWrite, tALU_SRC, tMemToReg}), .in1(3'b000), .out({RegWrite, ALU_SRC, MemToReg}), .sel(and_5_out));
  or or_2 (IR1_t, IR1, IRA);
  or or_3 (IR2_t, IR2, IRB);
  \单周期硬布线控制器  \u_单周期硬布线控制器_1  (
    .Funct({IR[30], IR[25], IR[14:12]}), .OP(IR[6:2]), .ALU_OP(\单周期硬布线控制器_1_alu_op ), .MemToReg(tMemToReg),
    .MemWrite(MemWrite), .ALU_SRC(tALU_SRC), .RegWrite(tRegWrite), .ecall(ecall),
    .S_type(\单周期硬布线控制器_1_s_type ), .Jalr(JALR), .Beq(\单周期硬布线控制器_1_beq ), .JAL(JAL), .Bne(\单周期硬布线控制器_1_bne ),
    .in_3(IR[21]), .uret(riscv_probe_1_p2), .BGE(\单周期硬布线控制器_1_bge ), .LB(LB));
  Multiplexer #(.select(1), .width(5), .disabled("Z"), .enable("false")) multiplexer_3 (
    .in0(IR[19:15]), .in1(5'b10001), .out(multiplexer_3_out), .sel(ecall));
  Multiplexer #(.select(1), .width(5), .disabled("Z"), .enable("false")) multiplexer_4 (
    .in0(IR[24:20]), .in1(5'b01010), .out(multiplexer_4_out), .sel(ecall));
  Multiplexer #(.select(1), .width(12), .disabled("Z"), .enable("false")) multiplexer_5 (
    .in0(IR[31:20]), .in1(bit_extender_1_out), .out(multiplexer_5_out), .sel(lb_t));
  assign bit_extender_1_out = {{4{IR[31]}}, IR[31:24]};  // Bit_Extender bit_extender_1
  Multiplexer #(.select(1), .width(12), .disabled("Z"), .enable("false")) multiplexer_6 (
    .in0(multiplexer_5_out), .in1({IR[31:25], IR[11:7]}), .out(multiplexer_6_out), .sel(\单周期硬布线控制器_1_s_type ));
  or or_4 (IR3_t, IR3, IRC);
  assign bit_extender_2_out = {{20{IR[31]}}, {IR[31], IR[7], IR[30:25], IR[11:8]}};  // Bit_Extender bit_extender_2
  assign bit_extender_3_out = {{12{IR[31]}}, {IR[31], IR[19:12], IR[20], IR[30:21]}};  // Bit_Extender bit_extender_3
  Regifile regifile_1 (
    .Din(RDin), .Clk(CLK), .R1(regifile_1_r1), .R2(MDin), .WE(RegWrite), .W_num(IR[11:7]),
    .R1_num(multiplexer_3_out), .R2_num(multiplexer_4_out));
  assign bit_extender_4_out = {{20{multiplexer_6_out[11]}}, multiplexer_6_out};  // Bit_Extender bit_extender_4
  // Probe on \单周期硬布线控制器_1_alu_op 
  Multiplexer #(.select(1), .width(32), .disabled("Z"), .enable("false")) multiplexer_7 (
    .in0(MDin), .in1(bit_extender_4_out), .out(multiplexer_7_out), .sel(ALU_SRC));
  Shifter #(.width(32), .shift("ll")) shifter_1 (.in(bit_extender_2_out), .\dist (5'b00001), .out(shifter_1_out));
  Shifter #(.width(32), .shift("ll")) shifter_2 (.in(bit_extender_3_out), .\dist (5'b00001), .out(shifter_2_out));
  not not_4 (great, aluresult[0]);
  // Probe on regifile_1_r1
  // Probe on aluresult
  ALU alu_1 (
    .X(regifile_1_r1), .Y(multiplexer_7_out), .AluOP(\单周期硬布线控制器_1_alu_op ), .Equal(equal), .Result(aluresult));  // open: Result_2, out_4, out_6
  Comparator #(.width(32), .mode("twosComplement")) comparator_1 (
    .a(regifile_1_r1), .b(32'h22), .eq(comparator_1_eq));  // open: gt, lt
  Multiplexer #(.select(1), .width(32), .disabled("Z"), .enable("false")) multiplexer_8 (
    .in0(multiplexer_10_out), .in1(adder_1_out), .out(RDin), .sel(or_5_out));
  or or_5 (or_5_out, JAL, JALR);
  and and_6 (and_6_out, comparator_1_eq, ecall);
  not not_5 (not_5_out, comparator_1_eq);
  RAM #(.addrWidth(10), .dataWidth(32), .bus("separate"), .Select("high")) ram_1 (
    .addr(aluresult[11:2]), .din(MDin), .data(Dre), .str(MemWrite), .clk(CLK), .ld(1'b1), .clr(RST));  // open: sel
  Register #(.width(32), .trigger("rising"), .Select("low")) register_1 (
    .D(MDin), .en(and_6_out), .Q(LedData), .clk(CLK));  // open: clr
  D_Flip_Flop #(.trigger("falling"), .Pre_Clr_Positions("ABOVE_BELOW"), .NegatePresetClear("false"), .enable("true"), .NewFFLayout("true")) d_ff_1 (
    .clk(CLK), .D(not_5_out), .Q(halt), .en(ecall), .reset(Go));  // open: Qn, preset
  D_Flip_Flop #(.trigger("high"), .Pre_Clr_Positions("LEGACY"), .NegatePresetClear("false"), .enable("true"), .NewFFLayout("false")) d_ff_2 (.Q(d_ff_2_q));  // open: clk, D, Qn, preset, en, reset
  // Probe on 13'hc
  Multiplexer #(.select(1), .width(32), .disabled("Z"), .enable("false")) multiplexer_9 (
    .in0(aluresult), .in1(Dre), .out(multiplexer_9_out), .sel(MemToReg));
  Comparator #(.width(13), .mode("twosComplement")) comparator_2 (
    .a(CNT_num), .b(13'hc), .eq(comparator_2_eq), .lt(comparator_2_lt));  // open: gt
  Clock #(.highDuration(1), .lowDuration(1)) clock_1 (.out(clock_1_out));
  Counter #(.width(13), .max('h1fff), .ongoal("stay"), .trigger("rising"), .behavior("old")) counter_1 (
    .count(comparator_2_lt), .Q(CNT_num), .clk(clock_1_out));  // open: load, D, carry, clr, preset
  Multiplexer #(.select(1), .width(32), .disabled("Z"), .enable("false")) multiplexer_10 (
    .in0(multiplexer_9_out), .in1(LBR), .out(multiplexer_10_out), .sel(lb_t));
  nand nand_1 (nand_1_out, d_ff_2_q, comparator_2_eq);
  assign LBR = {{24{multiplexer_11_out[7]}}, multiplexer_11_out};  // Bit_Extender bit_extender_5
  Multiplexer #(.select(2), .width(8), .disabled("Z"), .enable("false")) multiplexer_11 (
    .in0(Dre[7:0]), .in1(Dre[15:8]), .in2(Dre[23:16]), .in3(Dre[31:24]), .out(multiplexer_11_out),
    .sel(aluresult[1:0]));
  assign CLK = nand_1_out ? clock_1_out : 1'bz;  // Controlled_Buffer controlled_buffer_1
  Pull_Resistor #(.pull(1)) pull_resistor_1 (.node(CLK));
  and and_7 (and_7_out, ~halt, CLK);  // AND_Gate
  Counter #(.width(16), .max('hffff), .ongoal("wrap"), .trigger("rising"), .behavior("new")) counter_2 (
    .Q(\总周期数 ), .clk(and_7_out));  // open: load, D, count, carry, clr, preset, down

  // Other names for the same wires on the sheet: func[4:0] = {IR[30], IR[25], IR[14:12]}; op[4:0] = IR[6:2]

  // Notes on the sheet:
  //   中断源
  //   中断等待指示
  //   数码管输出应该用寄存器锁存，否则显示数据只能一闪而过
  //   BranchAddress
  //   数码管输出
  //   指令探针
  //   指令存储器
  //   指令字
  //   contents of rom_1 (hex, n*v repeats v):
  //   100493 100006f 100493 200913 300993 100006f 100493 200913 300993 100006f 100493 200913 300993
  //   100006f 100493 200913 300993 2c4000ef 100413 100493 1f49493 900533 2200893 73 24d493 48463 fedff06f
  //   900533 2200893 73 100493 249493 900533 2200893 73 48463 fedff06f 100493 1f49493 900533 2200893 73
  //   4034d493 900533 2200893 73 4044d493 900533 2200893 73 4044d493 900533 2200893 73 4044d493 900533
  //   2200893 73 4044d493 900533 2200893 73 4044d493 900533 2200893 73 4044d493 900533 2200893 73 4044d493
  //   900533 2200893 73 100413 1f41993 41f9d993 433 c00913 300b13 140413 f47413 800293 100313 499993
  //   89e9b3 1300533 2200893 73 406282b3 fe0294e3 140413 f00f93 1f47433 1c41413 800293 100313 49d993
  //   89e9b3 1300533 2200893 73 406282b3 fe0294e3 1c45413 406b0b33 b0463 f95ff06f 2b3 fff2c293 829293
  //   ff2e293 500533 2200893 73 fff00413 493 84a023 140413 448493 84a023 140413 448493 84a023 140413
  //   448493 84a023 140413 448493 84a023 140413 448493 84a023 140413 448493 84a023 140413 448493 84a023
  //   140413 448493 84a023 140413 448493 84a023 140413 448493 84a023 140413 448493 84a023 140413 448493
  //   84a023 140413 448493 84a023 140413 448493 84a023 140413 448493 84a023 140413 448493 140413 433
  //   3c00493 42983 4aa03 149a2b3 28663 134a023 1442023 ffc48493 fe9412e3 800533 2200893 73 440413 3c00493
  //   fc9416e3 3200893 73 f00493 900533 2200893 73 fff48493 fe04d8e3 a00893 73 a00893 73 413 140413 800533
  //   2200893 73 240413 800533 2200893 73 340413 800533 2200893 73 440413 800533 2200893 73 540413 800533
  //   2200893 73 640413 800533 2200893 73 740413 800533 2200893 73 840413 800533 2200893 2200893 73 8067
  //   JAL
  //   JALR
  //   URET
  //   S型指令
  //   B型指令
  //   J型指令
  //   I型指令
  //   Beq
  //   Bne
  //   MemToReg
  //   MemWrite
  //   AluOP
  //   AluSrcB
  //   RegWrite
  //   为方便自动评测，需要输出PC，IR，寄存器堆写如数据RDin
  //   RAM写使能MemWrite、RAM写入数据MDin等信号
  //   数据存储器
  //   控制位
  //   暂停节拍，不能为0
  //   戳工具置1进入计数暂停模式，ctrl+k时钟自动运行到对应节拍暂停
  //   ctrl+k关闭时钟连续运行，将控制位置零，进入单步调试模式调试
  //   用这个时钟源需要去掉电路中的其他时钟源
  //   可计数暂停的时钟源
endmodule

// 运算器控制器
module \运算控制器自动生成  (
  input  OP2,
  input  OP3,
  input  OP4,
  input  OP5,
  input  OP6,
  input  F12,
  input  F13,
  input  F14,
  input  F25,
  input  F30,
  output S0,
  output S1,
  output S2,
  output S3
);

  wire and_1_out, and_2_out, and_3_out, and_4_out, and_5_out, and_6_out, and_7_out, and_8_out, and_9_out,
       and_10_out, and_11_out, and_12_out, and_13_out, and_14_out, and_15_out, and_16_out, and_17_out,
       and_18_out, and_19_out, and_20_out, and_21_out, and_22_out, and_23_out, and_24_out, and_25_out,
       and_26_out, and_27_out, and_28_out, and_29_out, and_30_out, and_31_out, and_32_out, and_33_out,
       and_34_out, and_35_out, and_36_out, and_37_out, and_38_out, and_39_out, not_1_out, not_2_out,
       not_3_out, not_4_out, not_5_out, not_6_out, not_7_out, not_8_out, not_9_out, not_10_out, not_11_out,
       not_12_out, not_13_out, not_14_out, not_15_out, not_16_out, not_17_out, not_18_out, not_19_out,
       not_20_out, not_21_out, not_22_out, not_23_out, not_24_out, not_25_out, not_26_out, not_27_out,
       not_28_out, not_29_out, not_30_out, not_31_out, not_32_out, not_33_out, not_34_out, not_35_out,
       not_36_out, not_37_out, not_38_out, not_39_out, not_40_out, not_41_out, not_42_out, not_43_out,
       not_44_out, not_45_out, not_46_out, not_47_out, not_48_out, not_49_out, not_50_out, not_51_out,
       not_52_out, not_53_out, not_54_out, not_55_out, not_56_out, not_57_out, not_58_out, not_59_out,
       not_60_out, not_61_out, not_62_out, not_63_out, not_64_out, not_65_out, not_66_out, not_67_out,
       not_68_out, not_69_out, not_70_out, not_71_out, not_72_out, not_73_out, not_74_out, not_75_out,
       not_76_out, not_77_out, not_78_out, not_79_out, not_80_out, not_81_out, not_82_out, not_83_out,
       not_84_out, not_85_out, not_86_out, not_87_out, not_88_out, not_89_out, not_90_out, not_91_out,
       not_92_out, not_93_out, not_94_out, not_95_out, not_96_out, not_97_out, not_98_out, not_99_out,
       not_100_out, not_101_out, not_102_out, not_103_out, not_104_out, not_105_out, not_106_out,
       not_107_out, not_108_out, not_109_out, not_110_out, not_111_out, not_112_out, not_113_out,
       not_114_out, not_115_out, not_116_out, not_117_out, not_118_out, not_119_out, not_120_out,
       not_121_out, not_122_out, not_123_out, not_124_out, not_125_out, not_126_out, not_127_out,
       not_128_out, not_129_out, not_130_out, not_131_out, not_132_out, not_133_out, not_134_out,
       not_135_out, not_136_out, not_137_out, not_138_out, not_139_out, not_140_out, not_141_out,
       not_142_out, not_143_out, not_144_out, not_145_out, not_146_out, not_147_out, not_148_out,
       not_149_out, not_150_out, not_151_out, not_152_out, not_153_out, not_154_out, not_155_out,
       not_156_out, not_157_out, not_158_out, not_159_out, not_160_out, not_161_out, not_162_out,
       not_163_out, not_164_out, not_165_out, not_166_out, not_167_out, not_168_out, not_169_out,
       not_170_out, not_171_out, not_172_out, not_173_out, not_174_out, not_175_out, not_176_out,
       not_177_out, not_178_out, not_179_out, not_180_out, not_181_out, not_182_out, not_183_out,
       not_184_out, not_185_out, not_186_out, not_187_out, not_188_out, not_189_out, not_190_out,
       not_191_out, not_192_out, not_193_out, not_194_out, not_195_out, not_196_out, not_197_out,
       not_198_out, not_199_out, not_200_out, not_201_out, not_202_out, not_203_out, not_204_out,
       not_205_out, not_206_out, not_207_out, not_208_out, not_209_out, not_210_out, not_211_out,
       not_212_out, not_213_out, not_214_out, not_215_out, not_216_out, not_217_out, not_218_out,
       not_219_out, not_220_out, not_221_out, not_222_out, not_223_out, not_224_out, not_225_out, not_226_out;

  not not_1 (not_1_out, F30);
  not not_2 (not_2_out, F25);
  not not_3 (not_3_out, F14);
  not not_4 (not_4_out, F13);
  not not_5 (not_5_out, F12);
  not not_6 (not_6_out, OP6);
  not not_7 (not_7_out, OP3);
  not not_8 (not_8_out, OP2);
  not not_9 (not_9_out, F30);
  not not_10 (not_10_out, F25);
  not not_11 (not_11_out, OP6);
  not not_12 (not_12_out, OP3);
  not not_13 (not_13_out, OP2);
  not not_14 (not_14_out, F30);
  not not_15 (not_15_out, F25);
  not not_16 (not_16_out, F14);
  not not_17 (not_17_out, F12);
  not not_18 (not_18_out, OP6);
  not not_19 (not_19_out, OP3);
  not not_20 (not_20_out, OP2);
  not not_21 (not_21_out, F14);
  not not_22 (not_22_out, F13);
  not not_23 (not_23_out, F12);
  not not_24 (not_24_out, OP6);
  not not_25 (not_25_out, OP5);
  not not_26 (not_26_out, OP3);
  not not_27 (not_27_out, OP2);
  not not_28 (not_28_out, OP6);
  not not_29 (not_29_out, OP5);
  not not_30 (not_30_out, OP3);
  not not_31 (not_31_out, OP2);
  not not_32 (not_32_out, F13);
  not not_33 (not_33_out, F12);
  not not_34 (not_34_out, OP6);
  not not_35 (not_35_out, OP5);
  not not_36 (not_36_out, OP3);
  not not_37 (not_37_out, OP2);
  not not_38 (not_38_out, F14);
  not not_39 (not_39_out, F12);
  not not_40 (not_40_out, OP6);
  not not_41 (not_41_out, OP5);
  not not_42 (not_42_out, OP3);
  not not_43 (not_43_out, OP2);
  not not_44 (not_44_out, F25);
  not not_45 (not_45_out, F13);
  not not_46 (not_46_out, OP6);
  not not_47 (not_47_out, OP5);
  not not_48 (not_48_out, OP3);
  not not_49 (not_49_out, OP2);
  not not_50 (not_50_out, F30);
  not not_51 (not_51_out, F25);
  not not_52 (not_52_out, F13);
  not not_53 (not_53_out, F12);
  not not_54 (not_54_out, OP6);
  not not_55 (not_55_out, OP3);
  not not_56 (not_56_out, OP2);
  not not_57 (not_57_out, F13);
  not not_58 (not_58_out, OP4);
  not not_59 (not_59_out, OP3);
  not not_60 (not_60_out, OP2);
  not not_61 (not_61_out, F25);
  not not_62 (not_62_out, F14);
  not not_63 (not_63_out, F13);
  not not_64 (not_64_out, F12);
  not not_65 (not_65_out, OP6);
  not not_66 (not_66_out, OP3);
  not not_67 (not_67_out, OP2);
  not not_68 (not_68_out, F30);
  not not_69 (not_69_out, F25);
  not not_70 (not_70_out, OP6);
  not not_71 (not_71_out, OP3);
  not not_72 (not_72_out, OP2);
  not not_73 (not_73_out, F30);
  not not_74 (not_74_out, F25);
  not not_75 (not_75_out, F14);
  not not_76 (not_76_out, F12);
  not not_77 (not_77_out, OP6);
  not not_78 (not_78_out, OP3);
  not not_79 (not_79_out, OP2);
  not not_80 (not_80_out, OP6);
  not not_81 (not_81_out, OP5);
  not not_82 (not_82_out, OP3);
  not not_83 (not_83_out, OP2);
  not not_84 (not_84_out, F14);
  not not_85 (not_85_out, F12);
  not not_86 (not_86_out, OP6);
  not not_87 (not_87_out, OP5);
  not not_88 (not_88_out, OP3);
  not not_89 (not_89_out, OP2);
  not not_90 (not_90_out, F30);
  not not_91 (not_91_out, F25);
  not not_92 (not_92_out, F13);
  not not_93 (not_93_out, OP6);
  not not_94 (not_94_out, OP5);
  not not_95 (not_95_out, OP3);
  not not_96 (not_96_out, OP2);
  not not_97 (not_97_out, F14);
  not not_98 (not_98_out, F13);
  not not_99 (not_99_out, F12);
  not not_100 (not_100_out, OP4);
  not not_101 (not_101_out, OP3);
  not not_102 (not_102_out, OP2);
  not not_103 (not_103_out, F14);
  not not_104 (not_104_out, F13);
  not not_105 (not_105_out, OP4);
  not not_106 (not_106_out, OP3);
  not not_107 (not_107_out, OP2);
  not not_108 (not_108_out, F14);
  not not_109 (not_109_out, F13);
  not not_110 (not_110_out, F12);
  not not_111 (not_111_out, OP4);
  not not_112 (not_112_out, OP3);
  not not_113 (not_113_out, F13);
  not not_114 (not_114_out, OP4);
  not not_115 (not_115_out, OP3);
  not not_116 (not_116_out, OP2);
  not not_117 (not_117_out, F30);
  not not_118 (not_118_out, F25);
  not not_119 (not_119_out, F14);
  not not_120 (not_120_out, F13);
  not not_121 (not_121_out, F12);
  not not_122 (not_122_out, OP6);
  not not_123 (not_123_out, OP3);
  not not_124 (not_124_out, OP2);
  not not_125 (not_125_out, F25);
  not not_126 (not_126_out, F14);
  not not_127 (not_127_out, F13);
  not not_128 (not_128_out, F12);
  not not_129 (not_129_out, OP6);
  not not_130 (not_130_out, OP3);
  not not_131 (not_131_out, OP2);
  not not_132 (not_132_out, F30);
  not not_133 (not_133_out, F25);
  not not_134 (not_134_out, OP6);
  not not_135 (not_135_out, OP3);
  not not_136 (not_136_out, OP2);
  not not_137 (not_137_out, F30);
  not not_138 (not_138_out, F25);
  not not_139 (not_139_out, F14);
  not not_140 (not_140_out, OP6);
  not not_141 (not_141_out, OP3);
  not not_142 (not_142_out, OP2);
  not not_143 (not_143_out, F14);
  not not_144 (not_144_out, F13);
  not not_145 (not_145_out, F12);
  not not_146 (not_146_out, OP6);
  not not_147 (not_147_out, OP5);
  not not_148 (not_148_out, OP3);
  not not_149 (not_149_out, OP2);
  not not_150 (not_150_out, OP6);
  not not_151 (not_151_out, OP5);
  not not_152 (not_152_out, OP3);
  not not_153 (not_153_out, OP2);
  not not_154 (not_154_out, F14);
  not not_155 (not_155_out, F13);
  not not_156 (not_156_out, F12);
  not not_157 (not_157_out, OP4);
  not not_158 (not_158_out, OP3);
  not not_159 (not_159_out, OP2);
  not not_160 (not_160_out, F14);
  not not_161 (not_161_out, F13);
  not not_162 (not_162_out, OP4);
  not not_163 (not_163_out, OP3);
  not not_164 (not_164_out, OP2);
  not not_165 (not_165_out, F14);
  not not_166 (not_166_out, F13);
  not not_167 (not_167_out, F12);
  not not_168 (not_168_out, OP4);
  not not_169 (not_169_out, OP3);
  not not_170 (not_170_out, F14);
  not not_171 (not_171_out, OP6);
  not not_172 (not_172_out, OP5);
  not not_173 (not_173_out, OP3);
  not not_174 (not_174_out, OP2);
  not not_175 (not_175_out, F30);
  not not_176 (not_176_out, F25);
  not not_177 (not_177_out, F12);
  not not_178 (not_178_out, OP6);
  not not_179 (not_179_out, OP3);
  not not_180 (not_180_out, OP2);
  not not_181 (not_181_out, F30);
  not not_182 (not_182_out, F25);
  not not_183 (not_183_out, F14);
  not not_184 (not_184_out, F12);
  not not_185 (not_185_out, OP6);
  not not_186 (not_186_out, OP3);
  not not_187 (not_187_out, OP2);
  not not_188 (not_188_out, F30);
  not not_189 (not_189_out, F25);
  not not_190 (not_190_out, F14);
  not not_191 (not_191_out, OP6);
  not not_192 (not_192_out, OP3);
  not not_193 (not_193_out, OP2);
  not not_194 (not_194_out, F12);
  not not_195 (not_195_out, OP6);
  not not_196 (not_196_out, OP5);
  not not_197 (not_197_out, OP3);
  not not_198 (not_198_out, OP2);
  not not_199 (not_199_out, F13);
  not not_200 (not_200_out, F12);
  not not_201 (not_201_out, OP6);
  not not_202 (not_202_out, OP5);
  not not_203 (not_203_out, OP3);
  not not_204 (not_204_out, OP2);
  not not_205 (not_205_out, F14);
  not not_206 (not_206_out, F12);
  not not_207 (not_207_out, OP6);
  not not_208 (not_208_out, OP5);
  not not_209 (not_209_out, OP3);
  not not_210 (not_210_out, OP2);
  not not_211 (not_211_out, F30);
  not not_212 (not_212_out, F25);
  not not_213 (not_213_out, F13);
  not not_214 (not_214_out, F12);
  not not_215 (not_215_out, OP6);
  not not_216 (not_216_out, OP3);
  not not_217 (not_217_out, OP2);
  not not_218 (not_218_out, F14);
  not not_219 (not_219_out, OP6);
  not not_220 (not_220_out, OP5);
  not not_221 (not_221_out, OP3);
  not not_222 (not_222_out, OP2);
  not not_223 (not_223_out, F13);
  not not_224 (not_224_out, OP4);
  not not_225 (not_225_out, OP3);
  not not_226 (not_226_out, OP2);
  and and_1 (and_1_out, not_1_out, not_2_out, not_3_out, not_4_out, not_5_out, not_6_out, OP5, OP4, not_7_out, not_8_out);
  and and_2 (and_2_out, not_9_out, not_10_out, F14, F13, F12, not_11_out, OP5, OP4, not_12_out, not_13_out);
  and and_3 (and_3_out, not_14_out, not_15_out, not_16_out, F13, not_17_out, not_18_out, OP5, OP4, not_19_out, not_20_out);
  and and_4 (and_4_out, not_21_out, not_22_out, not_23_out, not_24_out, not_25_out, OP4, not_26_out, not_27_out);
  and and_5 (and_5_out, F14, F13, F12, not_28_out, not_29_out, OP4, not_30_out, not_31_out);
  and and_6 (and_6_out, F14, not_32_out, not_33_out, not_34_out, not_35_out, OP4, not_36_out, not_37_out);
  and and_7 (and_7_out, not_38_out, F13, not_39_out, not_40_out, not_41_out, OP4, not_42_out, not_43_out);
  and and_8 (and_8_out, F30, not_44_out, F14, not_45_out, F12, not_46_out, not_47_out, OP4, not_48_out, not_49_out);
  and and_9 (and_9_out, not_50_out, not_51_out, F14, not_52_out, not_53_out, not_54_out, OP5, OP4, not_55_out, not_56_out);
  and and_10 (and_10_out, F14, not_57_out, F12, OP6, OP5, not_58_out, not_59_out, not_60_out);
  and and_11 (and_11_out, F30, not_61_out, not_62_out, not_63_out, not_64_out, not_65_out, OP5, OP4, not_66_out, not_67_out);
  and and_12 (and_12_out, not_68_out, not_69_out, F14, F13, F12, not_70_out, OP5, OP4, not_71_out, not_72_out);
  and and_13 (and_13_out, not_73_out, not_74_out, not_75_out, F13, not_76_out, not_77_out, OP5, OP4, not_78_out, not_79_out);
  and and_14 (and_14_out, F14, F13, F12, not_80_out, not_81_out, OP4, not_82_out, not_83_out);
  and and_15 (and_15_out, not_84_out, F13, not_85_out, not_86_out, not_87_out, OP4, not_88_out, not_89_out);
  and and_16 (and_16_out, not_90_out, not_91_out, F14, not_92_out, F12, not_93_out, not_94_out, OP4, not_95_out, not_96_out);
  and and_17 (and_17_out, not_97_out, not_98_out, not_99_out, OP6, OP5, not_100_out, not_101_out, not_102_out);
  and and_18 (and_18_out, not_103_out, not_104_out, F12, OP6, OP5, not_105_out, not_106_out, not_107_out);
  and and_19 (and_19_out, not_108_out, not_109_out, not_110_out, OP6, OP5, not_111_out, not_112_out, OP2);
  and and_20 (and_20_out, F14, not_113_out, F12, OP6, OP5, not_114_out, not_115_out, not_116_out);
  and and_21 (and_21_out, not_117_out, not_118_out, not_119_out, not_120_out, not_121_out, not_122_out, OP5, OP4, not_123_out, not_124_out);
  and and_22 (and_22_out, F30, not_125_out, not_126_out, not_127_out, not_128_out, not_129_out, OP5, OP4, not_130_out, not_131_out);
  and and_23 (and_23_out, not_132_out, not_133_out, F14, F13, F12, not_134_out, OP5, OP4, not_135_out, not_136_out);
  and and_24 (and_24_out, not_137_out, not_138_out, not_139_out, F13, F12, not_140_out, OP5, OP4, not_141_out, not_142_out);
  and and_25 (and_25_out, not_143_out, not_144_out, not_145_out, not_146_out, not_147_out, OP4, not_148_out, not_149_out);
  and and_26 (and_26_out, F14, F13, F12, not_150_out, not_151_out, OP4, not_152_out, not_153_out);
  and and_27 (and_27_out, not_154_out, not_155_out, not_156_out, OP6, OP5, not_157_out, not_158_out, not_159_out);
  and and_28 (and_28_out, not_160_out, not_161_out, F12, OP6, OP5, not_162_out, not_163_out, not_164_out);
  and and_29 (and_29_out, not_165_out, not_166_out, not_167_out, OP6, OP5, not_168_out, not_169_out, OP2);
  and and_30 (and_30_out, not_170_out, F13, F12, not_171_out, not_172_out, OP4, not_173_out, not_174_out);
  and and_31 (and_31_out, not_175_out, not_176_out, F14, F13, not_177_out, not_178_out, OP5, OP4, not_179_out, not_180_out);
  and and_32 (and_32_out, not_181_out, not_182_out, not_183_out, F13, not_184_out, not_185_out, OP5, OP4, not_186_out, not_187_out);
  and and_33 (and_33_out, not_188_out, not_189_out, not_190_out, F13, F12, not_191_out, OP5, OP4, not_192_out, not_193_out);
  and and_34 (and_34_out, F14, F13, not_194_out, not_195_out, not_196_out, OP4, not_197_out, not_198_out);
  and and_35 (and_35_out, F14, not_199_out, not_200_out, not_201_out, not_202_out, OP4, not_203_out, not_204_out);
  and and_36 (and_36_out, not_205_out, F13, not_206_out, not_207_out, not_208_out, OP4, not_209_out, not_210_out);
  and and_37 (and_37_out, not_211_out, not_212_out, F14, not_213_out, not_214_out, not_215_out, OP5, OP4, not_216_out, not_217_out);
  and and_38 (and_38_out, not_218_out, F13, F12, not_219_out, not_220_out, OP4, not_221_out, not_222_out);
  and and_39 (and_39_out, F14, not_223_out, F12, OP6, OP5, not_224_out, not_225_out, not_226_out);
  or or_1 (S0, and_1_out, and_2_out, and_3_out, and_4_out, and_5_out, and_6_out, and_7_out, and_8_out, and_9_out, and_10_out);
  or or_2 (S1, and_11_out, and_12_out, and_13_out, and_14_out, and_15_out, and_16_out, and_17_out, and_18_out, and_19_out, and_20_out);
  or or_3 (S2, and_21_out, and_22_out, and_23_out, and_24_out, and_25_out, and_26_out, and_27_out, and_28_out, and_29_out, and_30_out);
  or or_4 (S3, and_31_out, and_32_out, and_33_out, and_34_out, and_35_out, and_36_out, and_37_out, and_38_out, and_39_out);
endmodule

// 控制信号生成
module \控制信号自动生成  (
  input  OP2,
  input  OP3,
  input  OP4,
  input  OP5,
  input  OP6,
  input  F12,
  input  F13,
  input  F14,
  input  F25,
  input  F30,
  output MemToReg,
  output MemWrite,
  output ALU_SRC,
  output RegWrite,
  output ecall,
  output S_Type,
  output BEQ,
  output BNE,
  output JALR,
  output JAL,
  output bge,
  output lb
);

  wire and_1_out, and_2_out, and_4_out, and_5_out, and_6_out, and_7_out, and_8_out, and_9_out, and_10_out,
       and_11_out, and_12_out, and_13_out, and_14_out, and_15_out, and_16_out, and_17_out, and_18_out,
       and_19_out, and_20_out, and_21_out, and_22_out, and_23_out, and_24_out, and_25_out, and_26_out,
       and_27_out, and_28_out, and_29_out, and_30_out, and_31_out, and_32_out, and_33_out, and_34_out,
       and_35_out, and_36_out, and_37_out, and_38_out, not_1_out, not_2_out, not_3_out, not_4_out, not_5_out,
       not_6_out, not_7_out, not_8_out, not_9_out, not_10_out, not_11_out, not_12_out, not_13_out,
       not_14_out, not_15_out, not_16_out, not_17_out, not_18_out, not_19_out, not_20_out, not_21_out,
       not_22_out, not_23_out, not_24_out, not_25_out, not_26_out, not_27_out, not_28_out, not_29_out,
       not_30_out, not_31_out, not_32_out, not_33_out, not_34_out, not_35_out, not_36_out, not_37_out,
       not_38_out, not_39_out, not_40_out, not_41_out, not_42_out, not_43_out, not_44_out, not_45_out,
       not_46_out, not_47_out, not_48_out, not_49_out, not_50_out, not_51_out, not_52_out, not_53_out,
       not_54_out, not_55_out, not_56_out, not_57_out, not_58_out, not_59_out, not_60_out, not_61_out,
       not_62_out, not_63_out, not_64_out, not_65_out, not_66_out, not_67_out, not_68_out, not_69_out,
       not_70_out, not_71_out, not_72_out, not_73_out, not_74_out, not_75_out, not_76_out, not_77_out,
       not_78_out, not_79_out, not_80_out, not_81_out, not_82_out, not_83_out, not_84_out, not_85_out,
       not_86_out, not_87_out, not_88_out, not_89_out, not_90_out, not_91_out, not_92_out, not_93_out,
       not_94_out, not_95_out, not_96_out, not_97_out, not_98_out, not_99_out, not_100_out, not_101_out,
       not_102_out, not_103_out, not_104_out, not_105_out, not_106_out, not_107_out, not_108_out,
       not_109_out, not_110_out, not_111_out, not_112_out, not_113_out, not_114_out, not_115_out,
       not_116_out, not_117_out, not_118_out, not_119_out, not_120_out, not_121_out, not_122_out,
       not_123_out, not_124_out, not_125_out, not_126_out, not_127_out, not_128_out, not_129_out,
       not_130_out, not_131_out, not_132_out, not_133_out, not_134_out, not_135_out, not_136_out,
       not_137_out, not_138_out, not_139_out, not_140_out, not_141_out, not_142_out, not_143_out,
       not_144_out, not_145_out, not_146_out, not_147_out, not_148_out, not_149_out, not_150_out,
       not_151_out, not_152_out, not_153_out, not_154_out, not_155_out, not_156_out, not_157_out,
       not_158_out, not_159_out, not_160_out, not_161_out, not_162_out, not_163_out, not_164_out,
       not_165_out, not_166_out, not_167_out, not_168_out, not_169_out, not_170_out, not_171_out,
       not_172_out, not_173_out, not_174_out, not_175_out, not_176_out, not_177_out, not_178_out,
       not_179_out, not_180_out, not_181_out, not_182_out, not_183_out, not_184_out, not_185_out,
       not_186_out, not_187_out, not_188_out, not_189_out, not_190_out, not_191_out, not_192_out,
       not_193_out, not_194_out, not_195_out, not_196_out, not_197_out, not_198_out, not_199_out,
       not_200_out, not_201_out, not_202_out, not_203_out, not_204_out, not_205_out, not_206_out,
       not_207_out, not_208_out, not_209_out, not_210_out, not_211_out, not_212_out, not_213_out,
       not_214_out, not_215_out, not_216_out, not_217_out, not_218_out, not_219_out, not_220_out,
       not_221_out, not_222_out, not_223_out, not_224_out, not_225_out, not_226_out, not_227_out,
       not_228_out, not_229_out, not_230_out, not_231_out, not_232_out, not_233_out, not_234_out,
       not_235_out, not_236_out, not_237_out, not_238_out, not_239_out, not_240_out, not_241_out,
       not_242_out, not_243_out, not_244_out, not_245_out, not_246_out, not_247_out, not_248_out,
       not_249_out, not_250_out, not_251_out, not_252_out, not_253_out, not_254_out, not_255_out,
       not_256_out, not_257_out, not_258_out, not_259_out, not_260_out, not_261_out, not_262_out,
       not_263_out, not_264_out, not_265_out, not_266_out, not_267_out, not_268_out, not_269_out,
       not_270_out, not_271_out;

  not not_1 (not_1_out, F14);
  not not_2 (not_2_out, F12);
  not not_3 (not_3_out, OP6);
  not not_4 (not_4_out, OP5);
  not not_5 (not_5_out, OP4);
  not not_6 (not_6_out, OP3);
  not not_7 (not_7_out, OP2);
  not not_8 (not_8_out, F14);
  not not_9 (not_9_out, F13);
  not not_10 (not_10_out, F12);
  not not_11 (not_11_out, OP6);
  not not_12 (not_12_out, OP5);
  not not_13 (not_13_out, OP4);
  not not_14 (not_14_out, OP3);
  not not_15 (not_15_out, OP2);
  not not_16 (not_16_out, F14);
  not not_17 (not_17_out, F12);
  not not_18 (not_18_out, OP6);
  not not_19 (not_19_out, OP4);
  not not_20 (not_20_out, OP3);
  not not_21 (not_21_out, OP2);
  not not_22 (not_22_out, F14);
  not not_23 (not_23_out, F13);
  not not_24 (not_24_out, F12);
  not not_25 (not_25_out, OP6);
  not not_26 (not_26_out, OP5);
  not not_27 (not_27_out, OP3);
  not not_28 (not_28_out, OP2);
  not not_29 (not_29_out, OP6);
  not not_30 (not_30_out, OP5);
  not not_31 (not_31_out, OP3);
  not not_32 (not_32_out, OP2);
  not not_33 (not_33_out, F12);
  not not_34 (not_34_out, OP6);
  not not_35 (not_35_out, OP5);
  not not_36 (not_36_out, OP3);
  not not_37 (not_37_out, OP2);
  not not_38 (not_38_out, F13);
  not not_39 (not_39_out, F12);
  not not_40 (not_40_out, OP6);
  not not_41 (not_41_out, OP5);
  not not_42 (not_42_out, OP3);
  not not_43 (not_43_out, OP2);
  not not_44 (not_44_out, F14);
  not not_45 (not_45_out, F12);
  not not_46 (not_46_out, OP6);
  not not_47 (not_47_out, OP5);
  not not_48 (not_48_out, OP3);
  not not_49 (not_49_out, OP2);
  not not_50 (not_50_out, F30);
  not not_51 (not_51_out, F25);
  not not_52 (not_52_out, F14);
  not not_53 (not_53_out, F13);
  not not_54 (not_54_out, OP6);
  not not_55 (not_55_out, OP5);
  not not_56 (not_56_out, OP3);
  not not_57 (not_57_out, OP2);
  not not_58 (not_58_out, F30);
  not not_59 (not_59_out, F25);
  not not_60 (not_60_out, F13);
  not not_61 (not_61_out, OP6);
  not not_62 (not_62_out, OP5);
  not not_63 (not_63_out, OP3);
  not not_64 (not_64_out, OP2);
  not not_65 (not_65_out, F25);
  not not_66 (not_66_out, F13);
  not not_67 (not_67_out, OP6);
  not not_68 (not_68_out, OP5);
  not not_69 (not_69_out, OP3);
  not not_70 (not_70_out, OP2);
  not not_71 (not_71_out, F14);
  not not_72 (not_72_out, F12);
  not not_73 (not_73_out, OP6);
  not not_74 (not_74_out, OP5);
  not not_75 (not_75_out, OP4);
  not not_76 (not_76_out, OP3);
  not not_77 (not_77_out, OP2);
  not not_78 (not_78_out, F14);
  not not_79 (not_79_out, F12);
  not not_80 (not_80_out, OP6);
  not not_81 (not_81_out, OP4);
  not not_82 (not_82_out, OP3);
  not not_83 (not_83_out, OP2);
  not not_84 (not_84_out, F14);
  not not_85 (not_85_out, F13);
  not not_86 (not_86_out, F12);
  not not_87 (not_87_out, OP4);
  not not_88 (not_88_out, OP3);
  not not_89 (not_89_out, F14);
  not not_90 (not_90_out, OP6);
  not not_91 (not_91_out, OP5);
  not not_92 (not_92_out, OP3);
  not not_93 (not_93_out, OP2);
  not not_94 (not_94_out, F14);
  not not_95 (not_95_out, F13);
  not not_96 (not_96_out, F12);
  not not_97 (not_97_out, OP6);
  not not_98 (not_98_out, OP5);
  not not_99 (not_99_out, OP4);
  not not_100 (not_100_out, OP3);
  not not_101 (not_101_out, OP2);
  not not_102 (not_102_out, F30);
  not not_103 (not_103_out, F25);
  not not_104 (not_104_out, F14);
  not not_105 (not_105_out, F13);
  not not_106 (not_106_out, F12);
  not not_107 (not_107_out, OP6);
  not not_108 (not_108_out, OP3);
  not not_109 (not_109_out, OP2);
  not not_110 (not_110_out, F25);
  not not_111 (not_111_out, F14);
  not not_112 (not_112_out, F13);
  not not_113 (not_113_out, F12);
  not not_114 (not_114_out, OP6);
  not not_115 (not_115_out, OP3);
  not not_116 (not_116_out, OP2);
  not not_117 (not_117_out, F30);
  not not_118 (not_118_out, F25);
  not not_119 (not_119_out, OP6);
  not not_120 (not_120_out, OP3);
  not not_121 (not_121_out, OP2);
  not not_122 (not_122_out, F30);
  not not_123 (not_123_out, F25);
  not not_124 (not_124_out, F12);
  not not_125 (not_125_out, OP6);
  not not_126 (not_126_out, OP3);
  not not_127 (not_127_out, OP2);
  not not_128 (not_128_out, F30);
  not not_129 (not_129_out, F25);
  not not_130 (not_130_out, F14);
  not not_131 (not_131_out, F12);
  not not_132 (not_132_out, OP6);
  not not_133 (not_133_out, OP3);
  not not_134 (not_134_out, OP2);
  not not_135 (not_135_out, F30);
  not not_136 (not_136_out, F25);
  not not_137 (not_137_out, F14);
  not not_138 (not_138_out, OP6);
  not not_139 (not_139_out, OP3);
  not not_140 (not_140_out, OP2);
  not not_141 (not_141_out, F14);
  not not_142 (not_142_out, F13);
  not not_143 (not_143_out, F12);
  not not_144 (not_144_out, OP6);
  not not_145 (not_145_out, OP5);
  not not_146 (not_146_out, OP3);
  not not_147 (not_147_out, OP2);
  not not_148 (not_148_out, OP6);
  not not_149 (not_149_out, OP5);
  not not_150 (not_150_out, OP3);
  not not_151 (not_151_out, OP2);
  not not_152 (not_152_out, F12);
  not not_153 (not_153_out, OP6);
  not not_154 (not_154_out, OP5);
  not not_155 (not_155_out, OP3);
  not not_156 (not_156_out, OP2);
  not not_157 (not_157_out, F13);
  not not_158 (not_158_out, F12);
  not not_159 (not_159_out, OP6);
  not not_160 (not_160_out, OP5);
  not not_161 (not_161_out, OP3);
  not not_162 (not_162_out, OP2);
  not not_163 (not_163_out, F14);
  not not_164 (not_164_out, F12);
  not not_165 (not_165_out, OP6);
  not not_166 (not_166_out, OP5);
  not not_167 (not_167_out, OP3);
  not not_168 (not_168_out, OP2);
  not not_169 (not_169_out, F30);
  not not_170 (not_170_out, F25);
  not not_171 (not_171_out, F14);
  not not_172 (not_172_out, F13);
  not not_173 (not_173_out, OP6);
  not not_174 (not_174_out, OP5);
  not not_175 (not_175_out, OP3);
  not not_176 (not_176_out, OP2);
  not not_177 (not_177_out, F30);
  not not_178 (not_178_out, F25);
  not not_179 (not_179_out, F13);
  not not_180 (not_180_out, OP6);
  not not_181 (not_181_out, OP5);
  not not_182 (not_182_out, OP3);
  not not_183 (not_183_out, OP2);
  not not_184 (not_184_out, F25);
  not not_185 (not_185_out, F13);
  not not_186 (not_186_out, OP6);
  not not_187 (not_187_out, OP5);
  not not_188 (not_188_out, OP3);
  not not_189 (not_189_out, OP2);
  not not_190 (not_190_out, F14);
  not not_191 (not_191_out, F12);
  not not_192 (not_192_out, OP6);
  not not_193 (not_193_out, OP5);
  not not_194 (not_194_out, OP4);
  not not_195 (not_195_out, OP3);
  not not_196 (not_196_out, OP2);
  not not_197 (not_197_out, OP4);
  not not_198 (not_198_out, F14);
  not not_199 (not_199_out, F13);
  not not_200 (not_200_out, F12);
  not not_201 (not_201_out, OP4);
  not not_202 (not_202_out, OP3);
  not not_203 (not_203_out, F30);
  not not_204 (not_204_out, F25);
  not not_205 (not_205_out, F13);
  not not_206 (not_206_out, F12);
  not not_207 (not_207_out, OP6);
  not not_208 (not_208_out, OP3);
  not not_209 (not_209_out, OP2);
  not not_210 (not_210_out, F14);
  not not_211 (not_211_out, OP6);
  not not_212 (not_212_out, OP5);
  not not_213 (not_213_out, OP3);
  not not_214 (not_214_out, OP2);
  not not_215 (not_215_out, F14);
  not not_216 (not_216_out, F13);
  not not_217 (not_217_out, F12);
  not not_218 (not_218_out, OP6);
  not not_219 (not_219_out, OP5);
  not not_220 (not_220_out, OP4);
  not not_221 (not_221_out, OP3);
  not not_222 (not_222_out, OP2);
  not not_223 (not_223_out, F30);
  not not_224 (not_224_out, F25);
  not not_225 (not_225_out, F14);
  not not_226 (not_226_out, F13);
  not not_227 (not_227_out, F12);
  not not_228 (not_228_out, OP3);
  not not_229 (not_229_out, OP2);
  not not_230 (not_230_out, F30);
  not not_231 (not_231_out, F25);
  not not_232 (not_232_out, F14);
  not not_233 (not_233_out, F13);
  not not_234 (not_234_out, F12);
  not not_235 (not_235_out, OP3);
  not not_236 (not_236_out, OP2);
  not not_237 (not_237_out, F14);
  not not_238 (not_238_out, F12);
  not not_239 (not_239_out, OP6);
  not not_240 (not_240_out, OP4);
  not not_241 (not_241_out, OP3);
  not not_242 (not_242_out, OP2);
  not not_243 (not_243_out, F14);
  not not_244 (not_244_out, F13);
  not not_245 (not_245_out, F12);
  not not_246 (not_246_out, OP4);
  not not_247 (not_247_out, OP3);
  not not_248 (not_248_out, OP2);
  not not_249 (not_249_out, F14);
  not not_250 (not_250_out, F13);
  not not_251 (not_251_out, OP4);
  not not_252 (not_252_out, OP3);
  not not_253 (not_253_out, OP2);
  not not_254 (not_254_out, F14);
  not not_255 (not_255_out, F13);
  not not_256 (not_256_out, F12);
  not not_257 (not_257_out, OP4);
  not not_258 (not_258_out, OP3);
  not not_259 (not_259_out, OP4);
  not not_260 (not_260_out, F13);
  not not_261 (not_261_out, OP4);
  not not_262 (not_262_out, OP3);
  not not_263 (not_263_out, OP2);
  not not_264 (not_264_out, F14);
  not not_265 (not_265_out, F13);
  not not_266 (not_266_out, F12);
  not not_267 (not_267_out, OP6);
  not not_268 (not_268_out, OP5);
  not not_269 (not_269_out, OP4);
  not not_270 (not_270_out, OP3);
  not not_271 (not_271_out, OP2);
  and and_1 (and_1_out, not_1_out, F13, not_2_out, not_3_out, not_4_out, not_5_out, not_6_out, not_7_out);
  and and_2 (and_2_out, not_8_out, not_9_out, not_10_out, not_11_out, not_12_out, not_13_out, not_14_out, not_15_out);
  and and_3 (MemWrite, not_16_out, F13, not_17_out, not_18_out, OP5, not_19_out, not_20_out, not_21_out);
  and and_4 (and_4_out, not_22_out, not_23_out, not_24_out, not_25_out, not_26_out, OP4, not_27_out, not_28_out);
  and and_5 (and_5_out, F14, F13, F12, not_29_out, not_30_out, OP4, not_31_out, not_32_out);
  and and_6 (and_6_out, F14, F13, not_33_out, not_34_out, not_35_out, OP4, not_36_out, not_37_out);
  and and_7 (and_7_out, F14, not_38_out, not_39_out, not_40_out, not_41_out, OP4, not_42_out, not_43_out);
  and and_8 (and_8_out, not_44_out, F13, not_45_out, not_46_out, not_47_out, OP4, not_48_out, not_49_out);
  and and_9 (and_9_out, not_50_out, not_51_out, not_52_out, not_53_out, F12, not_54_out, not_55_out, OP4, not_56_out, not_57_out);
  and and_10 (and_10_out, not_58_out, not_59_out, F14, not_60_out, F12, not_61_out, not_62_out, OP4, not_63_out, not_64_out);
  and and_11 (and_11_out, F30, not_65_out, F14, not_66_out, F12, not_67_out, not_68_out, OP4, not_69_out, not_70_out);
  and and_12 (and_12_out, not_71_out, F13, not_72_out, not_73_out, not_74_out, not_75_out, not_76_out, not_77_out);
  and and_13 (and_13_out, not_78_out, F13, not_79_out, not_80_out, OP5, not_81_out, not_82_out, not_83_out);
  and and_14 (and_14_out, not_84_out, not_85_out, not_86_out, OP6, OP5, not_87_out, not_88_out, OP2);
  and and_15 (and_15_out, not_89_out, F13, F12, not_90_out, not_91_out, OP4, not_92_out, not_93_out);
  and and_16 (and_16_out, not_94_out, not_95_out, not_96_out, not_97_out, not_98_out, not_99_out, not_100_out, not_101_out);
  and and_17 (and_17_out, not_102_out, not_103_out, not_104_out, not_105_out, not_106_out, not_107_out, OP5, OP4, not_108_out, not_109_out);
  and and_18 (and_18_out, F30, not_110_out, not_111_out, not_112_out, not_113_out, not_114_out, OP5, OP4, not_115_out, not_116_out);
  and and_19 (and_19_out, not_117_out, not_118_out, F14, F13, F12, not_119_out, OP5, OP4, not_120_out, not_121_out);
  and and_20 (and_20_out, not_122_out, not_123_out, F14, F13, not_124_out, not_125_out, OP5, OP4, not_126_out, not_127_out);
  and and_21 (and_21_out, not_128_out, not_129_out, not_130_out, F13, not_131_out, not_132_out, OP5, OP4, not_133_out, not_134_out);
  and and_22 (and_22_out, not_135_out, not_136_out, not_137_out, F13, F12, not_138_out, OP5, OP4, not_139_out, not_140_out);
  and and_23 (and_23_out, not_141_out, not_142_out, not_143_out, not_144_out, not_145_out, OP4, not_146_out, not_147_out);
  and and_24 (and_24_out, F14, F13, F12, not_148_out, not_149_out, OP4, not_150_out, not_151_out);
  and and_25 (and_25_out, F14, F13, not_152_out, not_153_out, not_154_out, OP4, not_155_out, not_156_out);
  and and_26 (and_26_out, F14, not_157_out, not_158_out, not_159_out, not_160_out, OP4, not_161_out, not_162_out);
  and and_27 (and_27_out, not_163_out, F13, not_164_out, not_165_out, not_166_out, OP4, not_167_out, not_168_out);
  and and_28 (and_28_out, not_169_out, not_170_out, not_171_out, not_172_out, F12, not_173_out, not_174_out, OP4, not_175_out, not_176_out);
  and and_29 (and_29_out, not_177_out, not_178_out, F14, not_179_out, F12, not_180_out, not_181_out, OP4, not_182_out, not_183_out);
  and and_30 (and_30_out, F30, not_184_out, F14, not_185_out, F12, not_186_out, not_187_out, OP4, not_188_out, not_189_out);
  and and_31 (and_31_out, not_190_out, F13, not_191_out, not_192_out, not_193_out, not_194_out, not_195_out, not_196_out);
  and and_32 (and_32_out, OP6, OP5, not_197_out, OP3, OP2);
  and and_33 (and_33_out, not_198_out, not_199_out, not_200_out, OP6, OP5, not_201_out, not_202_out, OP2);
  and and_34 (and_34_out, not_203_out, not_204_out, F14, not_205_out, not_206_out, not_207_out, OP5, OP4, not_208_out, not_209_out);
  and and_35 (and_35_out, not_210_out, F13, F12, not_211_out, not_212_out, OP4, not_213_out, not_214_out);
  and and_36 (and_36_out, not_215_out, not_216_out, not_217_out, not_218_out, not_219_out, not_220_out, not_221_out, not_222_out);
  and and_37 (and_37_out, not_223_out, not_224_out, not_225_out, not_226_out, not_227_out, OP6, OP5, OP4, not_228_out, not_229_out);
  and and_38 (and_38_out, not_230_out, not_231_out, not_232_out, not_233_out, not_234_out, OP6, OP5, OP4, not_235_out, not_236_out);
  and and_39 (S_Type, not_237_out, F13, not_238_out, not_239_out, OP5, not_240_out, not_241_out, not_242_out);
  and and_40 (BEQ, not_243_out, not_244_out, not_245_out, OP6, OP5, not_246_out, not_247_out, not_248_out);
  and and_41 (BNE, not_249_out, not_250_out, F12, OP6, OP5, not_251_out, not_252_out, not_253_out);
  and and_42 (JALR, not_254_out, not_255_out, not_256_out, OP6, OP5, not_257_out, not_258_out, OP2);
  and and_43 (JAL, OP6, OP5, not_259_out, OP3, OP2);
  and and_44 (bge, F14, not_260_out, F12, OP6, OP5, not_261_out, not_262_out, not_263_out);
  and and_45 (lb, not_264_out, not_265_out, not_266_out, not_267_out, not_268_out, not_269_out, not_270_out, not_271_out);
  or or_1 (MemToReg, and_1_out, and_2_out);
  or or_2 (ecall, and_37_out, and_38_out);
  or or_3 (ALU_SRC, and_4_out, and_5_out, and_6_out, and_7_out, and_8_out, and_9_out, and_10_out, and_11_out, and_12_out, and_13_out, and_14_out, and_15_out, and_16_out);
  or or_4 (RegWrite, and_17_out, and_18_out, and_19_out, and_20_out, and_21_out, and_22_out, and_23_out, and_24_out, and_25_out, and_26_out, and_27_out, and_28_out, and_29_out, and_30_out, and_31_out, and_32_out, and_33_out, and_34_out, and_35_out, and_36_out);
endmodule

module \理想流水线  (
  output RegWrite,
  output MemWrite,
  output [31:0] IF_PC,
  output [31:0] ID_PC,
  output [31:0] EX_PC,
  output [31:0] M_PC,
  output [31:0] WB_PC,
  output [31:0] RDin,
  output [31:0] MDin,
  output [31:0] LedData
);

  wire ALU_SRC, and_1_out, and_2_out, and_3_out, and_4_out, and_5_out, and_6_out, and_7_out, and_8_out, Beq,
       BGE, Bne, BranchTaken, CLK, clock_1_out, comparator_1_eq, comparator_1_lt, comparator_2_eq, d_ff_1_q,
       ecall, equal, ex_mem_1_ex_ecall, ex_mem_1_ex_jal, ex_mem_1_ex_jalr, ex_mem_1_ex_memtoreg,
       ex_mem_1_ex_regwrite, ex_mem_1_ex_uret, Go, great, halt, id_ex_1_ex_alusrcb, id_ex_1_ex_beq,
       id_ex_1_ex_bge, id_ex_1_ex_bne, id_ex_1_ex_ecall, id_ex_1_ex_jal, id_ex_1_ex_jalr,
       id_ex_1_ex_memtoreg, id_ex_1_ex_memtoreg_2, id_ex_1_ex_regwrite, id_ex_1_ex_uret, ID_MemWrite,
       ID_MenToReg, ID_RegWrite, IR1, IR2, IR3, JAL, JALR, LB, mem_wb_1_ex_ecall, mem_wb_1_ex_jal,
       mem_wb_1_ex_jalr, mem_wb_1_ex_memtoreg, nand_1_out, not_1_out, not_2_out, or_1_out, or_6_out,
       or_8_out, RST, URET, W1, W2, W3, \单周期硬布线控制器_1_s_type , \无条件分支 , \有条件分支 ;
  wire [1:0] or_4_out, priority_encoder_1_out;
  wire [3:0] ALU_OP, id_ex_1_ex_aluop;
  wire [4:0] multiplexer_2_out, multiplexer_3_out;
  wire [11:0] bit_extender_3_out, multiplexer_4_out, multiplexer_5_out;
  wire [12:0] CNT_num;
  wire [15:0] \LoadUse次数 , \总周期数 , \插入气泡数 , \无条件分支数 , \有条件分支数 , \条件分支成功数 ;
  wire [31:0] adder_1_out, adder_2_out, adder_3_out, aluresult, bit_extender_1_out, bit_extender_2_out,
       bit_extender_4_out, EX_IMM, EX_IR, ex_mem_1_mem_alu, ex_mem_1_mem_r1, ex_mem_1_mem_r2, id_ex_1_ex_r1,
       id_ex_1_ex_r2, ID_IR, IF_IR, MEM_IR, mem_wb_1_wb_alu, mem_wb_1_wb_din, mem_wb_1_wb_r1, mem_wb_1_wb_r2,
       multiplexer_1_out, multiplexer_6_out, multiplexer_7_out, multiplexer_8_out, ram_1_data, regifile_1_r1,
       regifile_1_r2, shifter_1_out, shifter_2_out, WB_IR;

  Button \u_总复位  (.out(RST));
  Button _1 (.out(IR1));
  Button _2 (.out(IR2));
  Button _3 (.out(IR3));
  // Probe on \总周期数 
  // Probe on \总周期数 
  Button \u_继续运行  (.out(Go));
  LED #(.active("true")) led_1 (.in(W1));
  LED #(.active("true")) led_2 (.in(W2));
  LED #(.active("true")) led_3 (.in(W3));
  Hex_Digit_Display hex_digit_display_1 (.value(LedData[31:28]));  // open: dp
  // Probe on IF_PC[19:0]
  // RiscV_Probe riscv_probe_1: pin names not known; wires that end beside it: IF_IR
  Hex_Digit_Display hex_digit_display_2 (.value(LedData[27:24]));  // open: dp
  Hex_Digit_Display hex_digit_display_3 (.value(LedData[23:20]));  // open: dp
  // Probe on ID_PC[19:0]
  // RiscV_Probe riscv_probe_2: pin names not known; wires that end beside it: ID_IR
  Hex_Digit_Display hex_digit_display_4 (.value(LedData[15:12]));  // open: dp
  Hex_Digit_Display hex_digit_display_5 (.value(LedData[19:16]));  // open: dp
  Hex_Digit_Display hex_digit_display_6 (.value(LedData[11:8]));  // open: dp
  Hex_Digit_Display hex_digit_display_7 (.value(LedData[7:4]));  // open: dp
  // Probe on EX_PC[19:0]
  // RiscV_Probe riscv_probe_3: pin names not known; wires that end beside it: EX_IR
  Hex_Digit_Display hex_digit_display_8 (.value(LedData[3:0]));  // open: dp
  // Probe on \总周期数 
  // Probe on M_PC[19:0]
  // RiscV_Probe riscv_probe_4: pin names not known; wires that end beside it: MEM_IR
  // Probe on \总周期数 
  // Probe on \无条件分支数 
  // Probe on \条件分支成功数 
  // Probe on \插入气泡数 
  // Probe on \LoadUse次数 
  // Probe on IF_PC[11:0]
  // Probe on WB_PC[19:0]
  // RiscV_Probe riscv_probe_5: pin names not known; wires that end beside it: WB_IR
  // Probe on ID_PC[11:0]
  // Probe on EX_PC[11:0]
  Priority_Encoder #(.select(2), .disabled("Z")) priority_encoder_1 (
    .in0(1'b1), .in1(id_ex_1_ex_jalr), .in2(id_ex_1_ex_jal), .in3(\无条件分支 ), .out(priority_encoder_1_out));  // open: gs, en_out, en_in
  Counter #(.width(16), .max('hffff), .ongoal("wrap"), .trigger("rising"), .behavior("new")) counter_1 (
    .Q(\总周期数 ), .clk(and_1_out));  // open: load, D, count, carry, clr, preset, down
  and and_1 (and_1_out, ~halt, CLK);  // AND_Gate
  // Probe on M_PC[11:0]
  D_Flip_Flop #(.trigger("high"), .Pre_Clr_Positions("LEGACY"), .NegatePresetClear("false"), .enable("true"), .NewFFLayout("false")) d_ff_1 (.Q(d_ff_1_q));  // open: clk, D, Qn, preset, en, reset
  // Probe on 13'hc
  Multiplexer #(.select(2), .width(32), .disabled("Z"), .enable("false")) multiplexer_1 (
    .in0(adder_1_out), .in1(aluresult), .in2(adder_2_out), .in3(adder_2_out), .out(multiplexer_1_out),
    .sel(priority_encoder_1_out));
  not not_1 (not_1_out, halt);
  and and_2 (and_2_out, \有条件分支 , CLK);
  // Probe on WB_PC[11:0]
  Comparator #(.width(13), .mode("twosComplement")) comparator_1 (
    .a(CNT_num), .b(13'hc), .eq(comparator_1_eq), .lt(comparator_1_lt));  // open: gt
  Clock #(.highDuration(1), .lowDuration(1)) clock_1 (.out(clock_1_out));
  Register #(.width(32), .trigger("rising"), .Select("low")) PC (
    .D(multiplexer_1_out), .en(not_1_out), .Q(IF_PC), .clk(CLK), .clr(RST));
  Counter #(.width(16), .max('hffff), .ongoal("wrap"), .trigger("rising"), .behavior("new")) counter_2 (
    .Q(\有条件分支数 ), .clk(and_2_out));  // open: load, D, count, carry, clr, preset, down
  nand nand_1 (nand_1_out, d_ff_1_q, comparator_1_eq);
  Counter #(.width(13), .max('h1fff), .ongoal("stay"), .trigger("rising"), .behavior("old")) counter_3 (
    .count(comparator_1_lt), .Q(CNT_num), .clk(clock_1_out));  // open: load, D, carry, clr, preset
  assign CLK = nand_1_out ? clock_1_out : 1'bz;  // Controlled_Buffer controlled_buffer_1
  Adder #(.width(32)) adder_1 (.a(IF_PC), .b(32'h4), .out(adder_1_out));  // open: cin, cout
  Adder #(.width(32)) adder_2 (.a(EX_IMM), .b(EX_PC), .out(adder_2_out));  // open: cin, cout
  Counter #(.width(16), .max('hffff), .ongoal("wrap"), .trigger("rising"), .behavior("new")) counter_4 (
    .Q(\无条件分支数 ), .clk(and_3_out));  // open: load, D, count, carry, clr, preset, down
  and and_3 (and_3_out, \无条件分支 , CLK);
  Pull_Resistor #(.pull(1)) pull_resistor_1 (.node(CLK));
  ROM #(.addrWidth(10), .dataWidth(32), .Select("high")) rom_1 (.addr(IF_PC[11:2]), .data(IF_IR));
  or or_1 (or_1_out, BranchTaken, RST);
  IF_ID if_id_1 (
    .CLK(CLK), .\使能端 (1'b1), .\清零端 (or_1_out), .IF_IR(IF_IR), .IF_PC(IF_PC), .ID_IR(ID_IR), .ID_PC(ID_PC));  // open: PD, PD_2
  Counter #(.width(16), .max('hffff), .ongoal("wrap"), .trigger("rising"), .behavior("new")) counter_5 (
    .Q(\条件分支成功数 ), .clk(and_4_out));  // open: load, D, count, carry, clr, preset, down
  and and_4 (and_4_out, BranchTaken, CLK);
  // Probe on ID_IR[31:20]
  or or_2 (\有条件分支 , id_ex_1_ex_jal, id_ex_1_ex_jalr);
  assign bit_extender_1_out = {{20{ID_IR[31]}}, {ID_IR[31], ID_IR[7], ID_IR[30:25], ID_IR[11:8]}};  // Bit_Extender bit_extender_1
  assign bit_extender_2_out = {{12{ID_IR[31]}}, {ID_IR[31], ID_IR[19:12], ID_IR[20], ID_IR[30:21]}};  // Bit_Extender bit_extender_2
  \单周期硬布线控制器  \u_单周期硬布线控制器_1  (
    .Funct({ID_IR[30], ID_IR[25], ID_IR[14:12]}), .OP(ID_IR[6:2]), .ALU_OP(ALU_OP), .MemToReg(ID_MenToReg),
    .MemWrite(ID_MemWrite), .ALU_SRC(ALU_SRC), .RegWrite(ID_RegWrite), .ecall(ecall),
    .S_type(\单周期硬布线控制器_1_s_type ), .Jalr(JALR), .Beq(Beq), .JAL(JAL), .Bne(Bne), .in_3(ID_IR[21]),
    .uret(URET), .BGE(BGE), .LB(LB));
  Multiplexer #(.select(1), .width(5), .disabled("Z"), .enable("false")) multiplexer_2 (
    .in0(ID_IR[19:15]), .in1(5'b10001), .out(multiplexer_2_out), .sel(ecall));
  Multiplexer #(.select(1), .width(5), .disabled("Z"), .enable("false")) multiplexer_3 (
    .in0(ID_IR[24:20]), .in1(5'b01010), .out(multiplexer_3_out), .sel(ecall));
  assign bit_extender_3_out = {{4{ID_IR[27]}}, ID_IR[27:20]};  // Bit_Extender bit_extender_3
  Shifter #(.width(32), .shift("ll")) shifter_1 (.in(bit_extender_1_out), .\dist (5'b00001), .out(shifter_1_out));
  Shifter #(.width(32), .shift("ll")) shifter_2 (.in(bit_extender_2_out), .\dist (5'b00001), .out(shifter_2_out));
  or or_3 (BranchTaken, id_ex_1_ex_jalr, id_ex_1_ex_jal, \无条件分支 );
  Multiplexer #(.select(1), .width(12), .disabled("Z"), .enable("false")) multiplexer_4 (
    .in0(ID_IR[31:20]), .in1(bit_extender_3_out), .out(multiplexer_4_out), .sel(LB));
  Multiplexer #(.select(1), .width(12), .disabled("Z"), .enable("false")) multiplexer_5 (
    .in0(multiplexer_4_out), .in1({ID_IR[31:25], ID_IR[11:7]}), .out(multiplexer_5_out),
    .sel(\单周期硬布线控制器_1_s_type ));
  or or_4 (or_4_out[0], Beq, Bne, BGE);
  assign bit_extender_4_out = {{20{multiplexer_5_out[11]}}, multiplexer_5_out};  // Bit_Extender bit_extender_4
  // Probe on bit_extender_4_out
  or or_5 (or_4_out[1], JAL, JALR);
  Multiplexer #(.select(2), .width(32), .disabled("Z"), .enable("false")) multiplexer_6 (
    .in0(bit_extender_4_out), .in1(shifter_1_out), .in2(shifter_2_out), .out(multiplexer_6_out),
    .sel(or_4_out));  // open: in3
  Regifile regifile_1 (
    .Din(RDin), .Clk(CLK), .R1(regifile_1_r1), .R2(regifile_1_r2), .WE(RegWrite), .W_num(WB_IR[11:7]),
    .R1_num(multiplexer_2_out), .R2_num(multiplexer_3_out));
  or or_6 (or_6_out, BranchTaken, RST);
  ID_EX id_ex_1 (
    .CLK(CLK), .\使能端 (1'b1), .\清零端 (or_6_out), .ID_IR(ID_IR), .EX_IR(EX_IR), .ID_PC(ID_PC), .EX_PC(EX_PC),
    .ID_R1(regifile_1_r1), .EX_R1(id_ex_1_ex_r1), .ID_R2(regifile_1_r2), .EX_R2(id_ex_1_ex_r2),
    .ID_MemToReg(ID_MenToReg), .EX_MemToReg(id_ex_1_ex_memtoreg), .ID_MemWrite(ID_MemWrite),
    .EX_MemToReg_2(id_ex_1_ex_memtoreg_2), .ID_AluOP(ALU_OP), .EX_AluOP(id_ex_1_ex_aluop),
    .ID_AluSrcB(ALU_SRC), .EX_AluSrcB(id_ex_1_ex_alusrcb), .ID_RegWrite(ID_RegWrite),
    .EX_RegWrite(id_ex_1_ex_regwrite), .ID_ecall(ecall), .EX_ecall(id_ex_1_ex_ecall), .ID_JAL(JAL),
    .EX_JAL(id_ex_1_ex_jal), .ID_JALR(JALR), .EX_JALR(id_ex_1_ex_jalr), .ID_Beq(Beq),
    .EX_Beq(id_ex_1_ex_beq), .ID_Bne(Bne), .EX_Bne(id_ex_1_ex_bne), .ID_URET(URET),
    .EX_URET(id_ex_1_ex_uret), .ID_BGE(BGE), .EX_BGE(id_ex_1_ex_bge), .ID_IMM(multiplexer_6_out),
    .EX_IMM(EX_IMM));  // open: ID_R1_F, EX_R1_F, ID_R2_F, EX_R2_F, ID_LB, EX_LB, PD, PD_2
  // Probe on EX_IMM
  Multiplexer #(.select(1), .width(32), .disabled("Z"), .enable("false")) multiplexer_7 (
    .in0(id_ex_1_ex_r2), .in1(EX_IMM), .out(multiplexer_7_out), .sel(id_ex_1_ex_alusrcb));
  // Probe on multiplexer_7_out
  and and_5 (and_5_out, id_ex_1_ex_beq, equal);
  or or_7 (\无条件分支 , and_5_out, and_6_out, and_7_out);
  and and_6 (and_6_out, ~equal, id_ex_1_ex_bne);  // AND_Gate
  ALU alu_1 (
    .X(id_ex_1_ex_r1), .Y(multiplexer_7_out), .AluOP(id_ex_1_ex_aluop), .Equal(equal), .Result(aluresult),
    .out_4(great));  // open: Result_2, out_6
  and and_7 (and_7_out, great, id_ex_1_ex_bge);
  // Probe on aluresult
  // Probe on RDin
  EX_MEM ex_mem_1 (
    .CLK(CLK), .\使能端 (1'b1), .\清零端 (RST), .EX_IR(EX_IR), .EX_PC(EX_PC), .EX_R1(id_ex_1_ex_r1),
    .ID_RegWrite(id_ex_1_ex_regwrite), .EX_R2(id_ex_1_ex_r2), .EX_ALU(aluresult),
    .ID_ecall(id_ex_1_ex_ecall), .EX_DATA(id_ex_1_ex_r2), .ID_URET(id_ex_1_ex_uret), .MEM_IR(MEM_IR),
    .MEM_PC(M_PC), .MEM_R1(ex_mem_1_mem_r1), .EX_RegWrite(ex_mem_1_ex_regwrite), .MEM_R2(ex_mem_1_mem_r2),
    .MEM_ALU(ex_mem_1_mem_alu), .EX_ecall(ex_mem_1_ex_ecall), .MEM_DATA(MDin), .EX_URET(ex_mem_1_ex_uret),
    .ID_MemToReg(id_ex_1_ex_memtoreg), .EX_MemToReg(ex_mem_1_ex_memtoreg),
    .ID_MemWrite(id_ex_1_ex_memtoreg_2), .EX_MemWrite(MemWrite), .ID_JAL(id_ex_1_ex_jal),
    .EX_JAL(ex_mem_1_ex_jal), .ID_JALR(id_ex_1_ex_jalr), .EX_JALR(ex_mem_1_ex_jalr));  // open: ID_LB, EX_LB
  // Probe on ex_mem_1_mem_alu
  RAM #(.addrWidth(10), .dataWidth(32), .bus("separate"), .Select("high")) ram_1 (
    .addr(ex_mem_1_mem_alu[9:0]), .din(MDin), .data(ram_1_data), .str(MemWrite), .clk(CLK), .ld(1'b1));  // open: sel, clr
  // Probe on ram_1_data
  // Probe on ex_mem_1_mem_alu
  MEM_WB mem_wb_1 (
    .CLK(CLK), .\使能端 (1'b1), .\清零端 (RST), .MEM_IR(MEM_IR), .ID_MemToReg(ex_mem_1_ex_memtoreg),
    .ID_RegWrite(ex_mem_1_ex_regwrite), .MEM_PC(M_PC), .ID_ecall(ex_mem_1_ex_ecall),
    .MEM_R1(ex_mem_1_mem_r1), .ID_URET(ex_mem_1_ex_uret), .MEM_R2(ex_mem_1_mem_r2), .WB_IR(WB_IR),
    .EX_MemToReg(mem_wb_1_ex_memtoreg), .EX_RegWrite(RegWrite), .WB_PC(WB_PC), .EX_ecall(mem_wb_1_ex_ecall),
    .WB_R1(mem_wb_1_wb_r1), .WB_R2(mem_wb_1_wb_r2), .MEM_DIN(ram_1_data), .WB_DIN(mem_wb_1_wb_din),
    .MEM_ALU(ex_mem_1_mem_alu), .WB_ALU(mem_wb_1_wb_alu), .ID_JAL(ex_mem_1_ex_jal), .EX_JAL(mem_wb_1_ex_jal),
    .ID_JALR(ex_mem_1_ex_jalr), .EX_JALR(mem_wb_1_ex_jalr));  // open: EX_URET, ID_LB, EX_LB
  // Probe on mem_wb_1_wb_alu
  // Probe on mem_wb_1_wb_alu
  Multiplexer #(.select(1), .width(32), .disabled("Z"), .enable("false")) multiplexer_8 (
    .in0(mem_wb_1_wb_alu), .in1(mem_wb_1_wb_din), .out(multiplexer_8_out), .sel(mem_wb_1_ex_memtoreg));
  Adder #(.width(32)) adder_3 (.a(WB_PC), .b(32'h4), .out(adder_3_out));  // open: cin, cout
  Comparator #(.width(32), .mode("twosComplement")) comparator_2 (
    .a(mem_wb_1_wb_r1), .b(32'h22), .eq(comparator_2_eq));  // open: gt, lt
  Multiplexer #(.select(1), .width(32), .disabled("Z"), .enable("false")) multiplexer_9 (
    .in0(multiplexer_8_out), .in1(adder_3_out), .out(RDin), .sel(or_8_out));
  or or_8 (or_8_out, mem_wb_1_ex_jal, mem_wb_1_ex_jalr);
  and and_8 (and_8_out, comparator_2_eq, mem_wb_1_ex_ecall);
  not not_2 (not_2_out, comparator_2_eq);
  // Probe on RDin
  Register #(.width(32), .trigger("rising"), .Select("low")) register_1 (
    .D(mem_wb_1_wb_r2), .en(and_8_out), .Q(LedData), .clk(CLK));  // open: clr
  D_Flip_Flop #(.trigger("falling"), .Pre_Clr_Positions("ABOVE_BELOW"), .NegatePresetClear("false"), .enable("true"), .NewFFLayout("true")) d_ff_2 (
    .clk(CLK), .D(not_2_out), .Q(halt), .en(mem_wb_1_ex_ecall), .reset(Go));  // open: Qn, preset

  // Other names for the same wires on the sheet: MEM_PC[31:0] = M_PC

  // Notes on the sheet:
  //   中断源
  //   时空图监测，可删除
  //   中断等待指示
  //   数码管输出
  //   控制位
  //   流水调试日志用
  //   暂停节拍，不能为0
  //   戳工具置1进入计数暂停模式，ctrl+k时钟自动运行到对应节拍暂停
  //   ctrl+k关闭时钟连续运行，将控制位置零，进入单步调试模式调试
  //   用这个时钟源需要去掉电路中的其他时钟源
  //   可计数暂停的时钟源
  //   contents of rom_1 (hex, n*v repeats v):
  //   413 493 913 993 46413 14e493 296913 39e993 842023 942223 1242423 1342623 a00893 493 913 993 73
  //   指令字
  //   为方便自动评测，需要输出流水线各段保存的PC值，注意是PC不是PC+4，另外ID段寄存器写入信息，Mem段内存写入信息也要输出
  //   I型指令
  //   S型指令
  //   B型指令
  //   J型指令
endmodule

module \气泡流水线  (
  output RegWrite,
  output MemWrite,
  output [31:0] IF_PC,
  output [31:0] ID_PC,
  output [31:0] EX_PC,
  output [31:0] M_PC,
  output [31:0] WB_PC,
  output [31:0] RDin,
  output [31:0] MDin,
  output [31:0] LedData
);

  wire ALU_SRC, and_1_out, and_2_out, and_3_out, and_4_out, and_5_out, and_6_out, and_7_out, and_9_out,
       and_10_out, and_11_out, and_12_out, and_13_out, and_14_out, and_15_out, and_16_out, Beq, BGE, Bne,
       BranchTaken, CLK, clock_1_out, comparator_1_eq, comparator_1_lt, comparator_2_eq, comparator_3_eq,
       comparator_4_eq, comparator_5_eq, comparator_6_eq, comparator_7_eq, comparator_8_eq, d_ff_1_q,
       DataHazzard, ecall, equal, ex_mem_1_ex_ecall, ex_mem_1_ex_jal, ex_mem_1_ex_jalr, ex_mem_1_ex_lb,
       ex_mem_1_ex_memtoreg, ex_mem_1_ex_uret, EX_RegWrite, Go, great, halt, id_ex_1_ex_alusrcb,
       id_ex_1_ex_beq, id_ex_1_ex_bge, id_ex_1_ex_bne, id_ex_1_ex_ecall, id_ex_1_ex_jal, id_ex_1_ex_jalr,
       id_ex_1_ex_lb, id_ex_1_ex_memtoreg, id_ex_1_ex_memtoreg_2, id_ex_1_ex_uret, ID_MemWrite, ID_MenToReg,
       ID_RegWrite, IDt_MenToReg, IDt_RegWrite, IR1, IR2, IR3, JAL, JALR, LB, lb_t, MEM_RegWrite,
       mem_wb_1_ex_ecall, mem_wb_1_ex_jal, mem_wb_1_ex_jalr, mem_wb_1_ex_memtoreg, nand_1_out, not_1_out,
       not_2_out, not_3_out, not_4_out, not_5_out, not_6_out, not_7_out, not_8_out, not_9_out, or_1_out,
       or_5_out, or_8_out, RST, RsUsed, RtUsed, tALU_SRC, URET, W1, W2, W3, WB_lb, \单周期硬布线控制器_1_s_type ,
       \无条件分支 , \有条件分支 ;
  wire [0:0] or_4_out;
  wire [1:0] priority_encoder_1_out;
  wire [3:0] ALU_OP, id_ex_1_ex_aluop;
  wire [4:0] func, rs, rt;
  wire [7:0] multiplexer_11_out;
  wire [11:0] bit_extender_3_out, multiplexer_5_out, multiplexer_6_out;
  wire [12:0] CNT_num;
  wire [15:0] \LoadUse次数 , \总周期数 , \插入气泡数 , \无条件分支数 , \有条件分支数 , \条件分支成功数 ;
  wire [31:0] adder_1_out, adder_2_out, adder_3_out, aluresult, bit_extender_1_out, bit_extender_2_out,
       bit_extender_4_out, EX_IMM, EX_IR, ex_mem_1_mem_alu, ex_mem_1_mem_r1, ex_mem_1_mem_r2, id_ex_1_ex_r1,
       id_ex_1_ex_r2, ID_IR, IF_IR, LBR, MEM_IR, mem_wb_1_wb_r1, mem_wb_1_wb_r2, multiplexer_1_out,
       multiplexer_7_out, multiplexer_8_out, multiplexer_9_out, multiplexer_10_out, ram_1_data,
       regifile_down_1_r1, regifile_down_1_r2, shifter_1_out, shifter_2_out, WB_alu, WB_Dre, WB_IR;

  Button \u_总复位  (.out(RST));
  Button _1 (.out(IR1));
  Button _2 (.out(IR2));
  Button _3 (.out(IR3));
  // Probe on \总周期数 
  // Probe on \总周期数 
  Button \u_继续运行  (.out(Go));
  LED #(.active("true")) led_1 (.in(W1));
  LED #(.active("true")) led_2 (.in(W2));
  LED #(.active("true")) led_3 (.in(W3));
  Hex_Digit_Display hex_digit_display_1 (.value(LedData[31:28]));  // open: dp
  // Probe on IF_PC[19:0]
  // RiscV_Probe riscv_probe_1: pin names not known; wires that end beside it: IF_IR
  Hex_Digit_Display hex_digit_display_2 (.value(LedData[27:24]));  // open: dp
  Hex_Digit_Display hex_digit_display_3 (.value(LedData[23:20]));  // open: dp
  // Probe on ID_PC[19:0]
  // RiscV_Probe riscv_probe_2: pin names not known; wires that end beside it: {ID_IR[31], func[4], ID_IR[29:26], func[3], ID_IR[24:15], func[2:0], ID_IR[11:0]}
  Hex_Digit_Display hex_digit_display_4 (.value(LedData[19:16]));  // open: dp
  Hex_Digit_Display hex_digit_display_5 (.value(LedData[15:12]));  // open: dp
  Hex_Digit_Display hex_digit_display_6 (.value(LedData[7:4]));  // open: dp
  Hex_Digit_Display hex_digit_display_7 (.value(LedData[11:8]));  // open: dp
  // Probe on EX_PC[19:0]
  // RiscV_Probe riscv_probe_3: pin names not known; wires that end beside it: EX_IR
  Hex_Digit_Display hex_digit_display_8 (.value(LedData[3:0]));  // open: dp
  // Probe on priority_encoder_1_out
  // Probe on adder_2_out
  and and_1 (and_1_out, not_2_out, not_1_out);
  not not_1 (not_1_out, halt);
  not not_2 (not_2_out, DataHazzard);
  // Probe on \总周期数 
  // Probe on M_PC[19:0]
  // RiscV_Probe riscv_probe_4: pin names not known; wires that end beside it: MEM_IR
  Priority_Encoder #(.select(2), .disabled("Z")) priority_encoder_1 (
    .in0(1'b1), .in1(id_ex_1_ex_jalr), .in2(id_ex_1_ex_jal), .in3(\无条件分支 ), .out(priority_encoder_1_out));  // open: gs, en_out, en_in
  // Probe on \总周期数 
  // Probe on \无条件分支数 
  // Probe on \条件分支成功数 
  // Probe on \插入气泡数 
  // Probe on \LoadUse次数 
  Multiplexer #(.select(2), .width(32), .disabled("Z"), .enable("false")) multiplexer_1 (
    .in0(adder_1_out), .in1(aluresult), .in2(adder_2_out), .in3(adder_2_out), .out(multiplexer_1_out),
    .sel(priority_encoder_1_out));
  Counter #(.width(16), .max('hffff), .ongoal("wrap"), .trigger("rising"), .behavior("new")) counter_1 (
    .Q(\总周期数 ), .clk(and_2_out));  // open: load, D, count, carry, clr, preset, down
  and and_2 (and_2_out, ~halt, CLK);  // AND_Gate
  // Probe on IF_PC[11:0]
  // Probe on WB_PC[19:0]
  // RiscV_Probe riscv_probe_5: pin names not known; wires that end beside it: WB_IR
  // Probe on IF_PC
  Register #(.width(32), .trigger("rising"), .Select("low")) PC (
    .D(multiplexer_1_out), .en(and_1_out), .Q(IF_PC), .clk(CLK), .clr(RST));
  and and_3 (and_3_out, \有条件分支 , CLK);
  // Probe on ID_PC[11:0]
  // Probe on EX_PC[11:0]
  not not_3 (not_3_out, DataHazzard);
  and and_4 (and_4_out, not_3_out, not_4_out);
  not not_4 (not_4_out, halt);
  // Probe on EX_IMM
  Counter #(.width(16), .max('hffff), .ongoal("wrap"), .trigger("rising"), .behavior("new")) counter_2 (
    .Q(\有条件分支数 ), .clk(and_3_out));  // open: load, D, count, carry, clr, preset, down
  // Probe on M_PC[11:0]
  D_Flip_Flop #(.trigger("high"), .Pre_Clr_Positions("LEGACY"), .NegatePresetClear("false"), .enable("true"), .NewFFLayout("false")) d_ff_1 (.Q(d_ff_1_q));  // open: clk, D, Qn, preset, en, reset
  // Probe on 13'hc
  Adder #(.width(32)) adder_1 (.a(IF_PC), .b(32'h4), .out(adder_1_out));  // open: cin, cout
  Adder #(.width(32)) adder_2 (.a(EX_IMM), .b(EX_PC), .out(adder_2_out));  // open: cin, cout
  // Probe on WB_PC[11:0]
  Comparator #(.width(13), .mode("twosComplement")) comparator_1 (
    .a(CNT_num), .b(13'hc), .eq(comparator_1_eq), .lt(comparator_1_lt));  // open: gt
  Clock #(.highDuration(1), .lowDuration(1)) clock_1 (.out(clock_1_out));
  ROM #(.addrWidth(10), .dataWidth(32), .Select("high")) rom_1 (.addr(IF_PC[11:2]), .data(IF_IR));
  Counter #(.width(16), .max('hffff), .ongoal("wrap"), .trigger("rising"), .behavior("new")) counter_3 (
    .Q(\无条件分支数 ), .clk(and_5_out));  // open: load, D, count, carry, clr, preset, down
  and and_5 (and_5_out, \无条件分支 , CLK);
  nand nand_1 (nand_1_out, d_ff_1_q, comparator_1_eq);
  Counter #(.width(13), .max('h1fff), .ongoal("stay"), .trigger("rising"), .behavior("old")) counter_4 (
    .count(comparator_1_lt), .Q(CNT_num), .clk(clock_1_out));  // open: load, D, carry, clr, preset
  or or_1 (or_1_out, BranchTaken, RST);
  IF_ID if_id_1 (
    .CLK(CLK), .\使能端 (and_4_out), .\清零端 (or_1_out), .IF_IR(IF_IR), .IF_PC(IF_PC),
    .ID_IR({ID_IR[31], func[4], ID_IR[29:26], func[3], ID_IR[24:15], func[2:0], ID_IR[11:0]}), .ID_PC(ID_PC));  // open: PD, PD_2
  assign CLK = nand_1_out ? clock_1_out : 1'bz;  // Controlled_Buffer controlled_buffer_1
  Counter #(.width(16), .max('hffff), .ongoal("wrap"), .trigger("rising"), .behavior("new")) counter_5 (
    .Q(\条件分支成功数 ), .clk(and_6_out));  // open: load, D, count, carry, clr, preset, down
  and and_6 (and_6_out, BranchTaken, CLK);
  Pull_Resistor #(.pull(1)) pull_resistor_1 (.node(CLK));
  not not_5 (not_5_out, halt);
  // Probe on {ID_IR[31], func[4], ID_IR[29:26], func[3], ID_IR[24:20]}
  or or_2 (\有条件分支 , id_ex_1_ex_jal, id_ex_1_ex_jalr);
  assign bit_extender_1_out = {{20{ID_IR[31]}}, {ID_IR[31], ID_IR[7], func[4], ID_IR[29:26], func[3], ID_IR[11:8]}};  // Bit_Extender bit_extender_1
  assign bit_extender_2_out = {{12{ID_IR[31]}}, {ID_IR[31], ID_IR[19:15], func[2:0], ID_IR[20], func[4], ID_IR[29:26], func[3], ID_IR[24:21]}};  // Bit_Extender bit_extender_2
  \单周期硬布线控制器  \u_单周期硬布线控制器_1  (
    .Funct(func), .OP(ID_IR[6:2]), .ALU_OP(ALU_OP), .MemToReg(IDt_MenToReg), .MemWrite(ID_MemWrite),
    .ALU_SRC(tALU_SRC), .RegWrite(IDt_RegWrite), .ecall(ecall), .S_type(\单周期硬布线控制器_1_s_type ), .Jalr(JALR),
    .Beq(Beq), .JAL(JAL), .Bne(Bne), .in_3(ID_IR[21]), .uret(URET), .BGE(BGE), .LB(LB));
  Multiplexer #(.select(1), .width(5), .disabled("Z"), .enable("false")) multiplexer_2 (
    .in0(ID_IR[19:15]), .in1(5'b10001), .out(rs), .sel(ecall));
  Multiplexer #(.select(1), .width(5), .disabled("Z"), .enable("false")) multiplexer_3 (
    .in0(ID_IR[24:20]), .in1(5'b01010), .out(rt), .sel(ecall));
  assign bit_extender_3_out = {{4{ID_IR[27]}}, {ID_IR[27:26], func[3], ID_IR[24:20]}};  // Bit_Extender bit_extender_3
  Shifter #(.width(32), .shift("ll")) shifter_1 (.in(bit_extender_1_out), .\dist (5'b00001), .out(shifter_1_out));
  Shifter #(.width(32), .shift("ll")) shifter_2 (.in(bit_extender_2_out), .\dist (5'b00001), .out(shifter_2_out));
  not not_6 (not_6_out, ID_IR[0]);
  and and_7 (and_7_out, LB, not_6_out);
  Multiplexer #(.select(1), .width(3), .disabled("Z"), .enable("false")) multiplexer_4 (
    .in0({IDt_RegWrite, tALU_SRC, IDt_MenToReg}), .in1(3'b000), .out({ID_RegWrite, ALU_SRC, ID_MenToReg}),
    .sel(and_7_out));
  and and_8 (lb_t, LB, ID_IR[0]);
  or or_3 (BranchTaken, id_ex_1_ex_jalr, id_ex_1_ex_jal, \无条件分支 );
  Multiplexer #(.select(1), .width(12), .disabled("Z"), .enable("false")) multiplexer_5 (
    .in0({ID_IR[31], func[4], ID_IR[29:26], func[3], ID_IR[24:20]}), .in1(bit_extender_3_out),
    .out(multiplexer_5_out), .sel(lb_t));
  Multiplexer #(.select(1), .width(12), .disabled("Z"), .enable("false")) multiplexer_6 (
    .in0(multiplexer_5_out), .in1({ID_IR[31], func[4], ID_IR[29:26], func[3], ID_IR[11:7]}),
    .out(multiplexer_6_out), .sel(\单周期硬布线控制器_1_s_type ));
  // Probe on {ID_IR[31], ID_IR[19:15], func[2:0], ID_IR[20], func[4], ID_IR[29:26], func[3], ID_IR[24:21]}
  or or_4 (or_4_out[0], Beq, Bne, BGE);
  assign bit_extender_4_out = {{20{multiplexer_6_out[11]}}, multiplexer_6_out};  // Bit_Extender bit_extender_4
  // Probe on bit_extender_4_out
  \used控制电路  \used控制电路_1  (
    .OP2(ID_IR[2]), .OP3(ID_IR[3]), .OP4(ID_IR[4]), .OP5(ID_IR[5]), .OP6(ID_IR[6]), .F12(func[0]),
    .F13(func[1]), .F14(func[2]), .F25(func[3]), .F30(func[4]), .RsUsed(RsUsed), .RtUesd(RtUsed));
  Multiplexer #(.select(2), .width(32), .disabled("Z"), .enable("false")) multiplexer_7 (
    .in0(bit_extender_4_out), .in1(shifter_1_out), .in2(shifter_2_out), .out(multiplexer_7_out),
    .sel({JAL, or_4_out[0]}));  // open: in3
  Regifile_down regifile_down_1 (
    .Din(RDin), .Clk(CLK), .R1(regifile_down_1_r1), .R2(regifile_down_1_r2), .WE(RegWrite),
    .W_num(WB_IR[11:7]), .R1_num(rs), .R2_num(rt));
  // Probe on multiplexer_7_out
  Comparator #(.width(5), .mode("twosComplement")) comparator_2 (
    .a(rs), .b(EX_IR[11:7]), .eq(comparator_2_eq));  // open: gt, lt
  Comparator #(.width(5), .mode("twosComplement")) comparator_3 (
    .a(rs), .b(MEM_IR[11:7]), .eq(comparator_3_eq));  // open: gt, lt
  Comparator #(.width(5), .mode("twosComplement")) comparator_4 (
    .a(rt), .b(EX_IR[11:7]), .eq(comparator_4_eq));  // open: gt, lt
  Comparator #(.width(5), .mode("twosComplement")) comparator_5 (
    .a(rt), .b(MEM_IR[11:7]), .eq(comparator_5_eq));  // open: gt, lt
  Comparator #(.width(5), .mode("twosComplement")) comparator_6 (
    .a(rs), .b({5{1'b0}}), .eq(comparator_6_eq));  // open: gt, lt
  Comparator #(.width(5), .mode("twosComplement")) comparator_7 (
    .a(rt), .b({5{1'b0}}), .eq(comparator_7_eq));  // open: gt, lt
  or or_5 (or_5_out, BranchTaken, RST, DataHazzard);
  ID_EX id_ex_1 (
    .CLK(CLK), .\使能端 (not_5_out), .\清零端 (or_5_out),
    .ID_IR({ID_IR[31], func[4], ID_IR[29:26], func[3], ID_IR[24:15], func[2:0], ID_IR[11:0]}), .EX_IR(EX_IR),
    .ID_PC(ID_PC), .EX_PC(EX_PC), .ID_R1(regifile_down_1_r1), .EX_R1(id_ex_1_ex_r1),
    .ID_R2(regifile_down_1_r2), .EX_R2(id_ex_1_ex_r2), .ID_MemToReg(ID_MenToReg),
    .EX_MemToReg(id_ex_1_ex_memtoreg), .ID_MemWrite(ID_MemWrite), .EX_MemToReg_2(id_ex_1_ex_memtoreg_2),
    .ID_AluOP(ALU_OP), .EX_AluOP(id_ex_1_ex_aluop), .ID_AluSrcB(ALU_SRC), .EX_AluSrcB(id_ex_1_ex_alusrcb),
    .ID_RegWrite(ID_RegWrite), .EX_RegWrite(EX_RegWrite), .ID_ecall(ecall), .EX_ecall(id_ex_1_ex_ecall),
    .ID_JAL(JAL), .EX_JAL(id_ex_1_ex_jal), .ID_JALR(JALR), .EX_JALR(id_ex_1_ex_jalr), .ID_Beq(Beq),
    .EX_Beq(id_ex_1_ex_beq), .ID_Bne(Bne), .EX_Bne(id_ex_1_ex_bne), .ID_URET(URET),
    .EX_URET(id_ex_1_ex_uret), .ID_BGE(BGE), .EX_BGE(id_ex_1_ex_bge), .ID_IMM(multiplexer_7_out),
    .EX_IMM(EX_IMM), .ID_LB(lb_t), .EX_LB(id_ex_1_ex_lb));  // open: ID_R1_F, EX_R1_F, ID_R2_F, EX_R2_F, PD, PD_2
  // Probe on EX_IMM
  not not_7 (not_7_out, comparator_6_eq);
  not not_8 (not_8_out, comparator_7_eq);
  and and_9 (and_9_out, RsUsed, EX_RegWrite, not_7_out, comparator_2_eq);
  and and_10 (and_10_out, RsUsed, MEM_RegWrite, not_7_out, comparator_3_eq);
  and and_11 (and_11_out, RtUsed, EX_RegWrite, not_8_out, comparator_4_eq);
  and and_12 (and_12_out, RtUsed, MEM_RegWrite, not_8_out, comparator_5_eq);
  Multiplexer #(.select(1), .width(32), .disabled("Z"), .enable("false")) multiplexer_8 (
    .in0(id_ex_1_ex_r2), .in1(EX_IMM), .out(multiplexer_8_out), .sel(id_ex_1_ex_alusrcb));
  // Probe on multiplexer_8_out
  and and_13 (and_13_out, id_ex_1_ex_beq, equal);
  or or_6 (DataHazzard, and_9_out, and_10_out, and_11_out, and_12_out);
  or or_7 (\无条件分支 , and_13_out, and_14_out, and_15_out);
  and and_14 (and_14_out, ~equal, id_ex_1_ex_bne);  // AND_Gate
  ALU alu_1 (
    .X(id_ex_1_ex_r1), .Y(multiplexer_8_out), .AluOP(id_ex_1_ex_aluop), .Equal(equal), .Result(aluresult),
    .out_4(great));  // open: Result_2, out_6
  and and_15 (and_15_out, great, id_ex_1_ex_bge);
  // Probe on aluresult
  // Probe on RDin
  EX_MEM ex_mem_1 (
    .CLK(CLK), .\使能端 (not_5_out), .\清零端 (RST), .EX_IR(EX_IR), .EX_PC(EX_PC), .EX_R1(id_ex_1_ex_r1),
    .ID_RegWrite(EX_RegWrite), .EX_R2(id_ex_1_ex_r2), .EX_ALU(aluresult), .ID_ecall(id_ex_1_ex_ecall),
    .EX_DATA(id_ex_1_ex_r2), .ID_URET(id_ex_1_ex_uret), .MEM_IR(MEM_IR), .MEM_PC(M_PC),
    .MEM_R1(ex_mem_1_mem_r1), .EX_RegWrite(MEM_RegWrite), .MEM_R2(ex_mem_1_mem_r2),
    .MEM_ALU(ex_mem_1_mem_alu), .EX_ecall(ex_mem_1_ex_ecall), .MEM_DATA(MDin), .EX_URET(ex_mem_1_ex_uret),
    .ID_MemToReg(id_ex_1_ex_memtoreg), .EX_MemToReg(ex_mem_1_ex_memtoreg),
    .ID_MemWrite(id_ex_1_ex_memtoreg_2), .EX_MemWrite(MemWrite), .ID_JAL(id_ex_1_ex_jal),
    .EX_JAL(ex_mem_1_ex_jal), .ID_JALR(id_ex_1_ex_jalr), .EX_JALR(ex_mem_1_ex_jalr), .ID_LB(id_ex_1_ex_lb),
    .EX_LB(ex_mem_1_ex_lb));
  // Probe on ex_mem_1_mem_alu
  RAM #(.addrWidth(10), .dataWidth(32), .bus("separate"), .Select("high")) ram_1 (
    .addr(ex_mem_1_mem_alu[11:2]), .din(MDin), .data(ram_1_data), .str(MemWrite), .clk(CLK), .ld(1'b1));  // open: sel, clr
  // Probe on ram_1_data
  // Probe on ex_mem_1_mem_alu
  MEM_WB mem_wb_1 (
    .CLK(CLK), .\使能端 (not_5_out), .\清零端 (RST), .MEM_IR(MEM_IR), .ID_MemToReg(ex_mem_1_ex_memtoreg),
    .ID_RegWrite(MEM_RegWrite), .MEM_PC(M_PC), .ID_ecall(ex_mem_1_ex_ecall), .MEM_R1(ex_mem_1_mem_r1),
    .ID_URET(ex_mem_1_ex_uret), .MEM_R2(ex_mem_1_mem_r2), .WB_IR(WB_IR), .EX_MemToReg(mem_wb_1_ex_memtoreg),
    .EX_RegWrite(RegWrite), .WB_PC(WB_PC), .EX_ecall(mem_wb_1_ex_ecall), .WB_R1(mem_wb_1_wb_r1),
    .WB_R2(mem_wb_1_wb_r2), .MEM_DIN(ram_1_data), .WB_DIN(WB_Dre), .MEM_ALU(ex_mem_1_mem_alu),
    .WB_ALU(WB_alu), .ID_JAL(ex_mem_1_ex_jal), .EX_JAL(mem_wb_1_ex_jal), .ID_JALR(ex_mem_1_ex_jalr),
    .EX_JALR(mem_wb_1_ex_jalr), .ID_LB(ex_mem_1_ex_lb), .EX_LB(WB_lb));  // open: EX_URET
  // Probe on WB_alu
  Multiplexer #(.select(1), .width(32), .disabled("Z"), .enable("false")) multiplexer_9 (
    .in0(WB_alu), .in1(WB_Dre), .out(multiplexer_9_out), .sel(mem_wb_1_ex_memtoreg));
  Adder #(.width(32)) adder_3 (.a(WB_PC), .b(32'h4), .out(adder_3_out));  // open: cin, cout
  Comparator #(.width(32), .mode("twosComplement")) comparator_8 (
    .a(mem_wb_1_wb_r1), .b(32'h22), .eq(comparator_8_eq));  // open: gt, lt
  and and_16 (and_16_out, comparator_8_eq, mem_wb_1_ex_ecall);
  not not_9 (not_9_out, comparator_8_eq);
  Multiplexer #(.select(1), .width(32), .disabled("Z"), .enable("false")) multiplexer_10 (
    .in0(multiplexer_9_out), .in1(LBR), .out(multiplexer_10_out), .sel(WB_lb));
  Register #(.width(32), .trigger("rising"), .Select("low")) register_1 (
    .D(mem_wb_1_wb_r2), .en(and_16_out), .Q(LedData), .clk(CLK));  // open: clr
  D_Flip_Flop #(.trigger("falling"), .Pre_Clr_Positions("ABOVE_BELOW"), .NegatePresetClear("false"), .enable("true"), .NewFFLayout("true")) d_ff_2 (
    .clk(CLK), .D(not_9_out), .Q(halt), .en(mem_wb_1_ex_ecall), .reset(Go));  // open: Qn, preset
  assign LBR = {{24{multiplexer_11_out[7]}}, multiplexer_11_out};  // Bit_Extender bit_extender_5
  Multiplexer #(.select(2), .width(8), .disabled("Z"), .enable("false")) multiplexer_11 (
    .in0(WB_Dre[7:0]), .in1(WB_Dre[15:8]), .in2(WB_Dre[23:16]), .in3(WB_Dre[31:24]),
    .out(multiplexer_11_out), .sel(WB_alu[1:0]));
  Multiplexer #(.select(1), .width(32), .disabled("Z"), .enable("false")) multiplexer_12 (
    .in0(multiplexer_10_out), .in1(adder_3_out), .out(RDin), .sel(or_8_out));
  or or_8 (or_8_out, mem_wb_1_ex_jal, mem_wb_1_ex_jalr);

  // Other names for the same wires on the sheet: ID_IR (some bits) = func; EX_WriteReg_num[4:0] = EX_IR[11:7];
  //   op[4:0] = ID_IR[6:2]; MEM_WriteReg_num[4:0] = MEM_IR[11:7]; MEM_PC[31:0] = M_PC

  // Notes on the sheet:
  //   中断源
  //   时空图监测，可删除
  //   中断等待指示
  //   数码管输出
  //   控制位
  //   流水调试日志用
  //   暂停节拍，不能为0
  //   用这个时钟源需要去掉电路中的其他时钟源
  //   戳工具置1进入计数暂停模式，ctrl+k时钟自动运行到对应节拍暂停
  //   ctrl+k关闭时钟连续运行，将控制位置零，进入单步调试模式调试
  //   ctrl+k关闭时钟连续运行，将控制位置零，进入单步调试模式调试
  //   contents of rom_1 (hex, n*v repeats v):
  //   100493 100006f 100493 200913 300993 100006f 100493 200913 300993 100006f 100493 200913 300993
  //   100006f 100493 200913 300993 3bc000ef 100413 100493 1f49493 900533 2200893 73 24d493 48463 fedff06f
  //   900533 2200893 73 100493 249493 900533 2200893 73 48463 fedff06f 100493 1f49493 900533 2200893 73
  //   4034d493 900533 2200893 73 4044d493 900533 2200893 73 4044d493 900533 2200893 73 4044d493 900533
  //   2200893 73 4044d493 900533 2200893 73 4044d493 900533 2200893 73 4044d493 900533 2200893 73 4044d493
  //   900533 2200893 73 100413 1f41993 41f9d993 433 c00913 300b13 140413 f47413 800293 100313 499993
  //   89e9b3 1300533 2200893 73 406282b3 fe0294e3 140413 f00f93 1f47433 1c41413 800293 100313 49d993
  //   89e9b3 1300533 2200893 73 406282b3 fe0294e3 1c45413 406b0b33 b0463 f95ff06f 2b3 fff2c293 829293
  //   ff2e293 500533 2200893 73 fff00413 493 84a023 140413 448493 84a023 140413 448493 84a023 140413
  //   448493 84a023 140413 448493 84a023 140413 448493 84a023 140413 448493 84a023 140413 448493 84a023
  //   140413 448493 84a023 140413 448493 84a023 140413 448493 84a023 140413 448493 84a023 140413 448493
  //   84a023 140413 448493 84a023 140413 448493 84a023 140413 448493 84a023 140413 448493 140413 433
  //   3c00493 42983 4aa03 149a2b3 28663 134a023 1442023 ffc48493 fe9412e3 800533 2200893 73 440413 3c00493
  //   fc9416e3 3200893 73 f00493 900533 2200893 73 fff48493 fe04d8e3 a00893 73 fff00293 7700493 849493
  //   7748493 900533 2200893 73 1000e13 54c4b3 900533 2200893 73 fffe0e13 fe0e16e3 a00893 73 fff00293 313
  //   1900413 841413 9700493 940533 2200893 73 5484b3 494b313 fe0306e3 a00893 73 313 1000e13 13 8400493
  //   849493 8348493 400913 891913 490913 849493 8248493 849493 8148493 891913 490913 891913 490913 932023
  //   12484b3 430313 fffe0e13 fe0e18e3 2000e13 313 30483 900533 2200893 73 130313 fffe0e13 fe0e14e3 a00893
  //   73 a00893 73 413 140413 800533 2200893 73 240413 800533 2200893 73 340413 800533 2200893 73 440413
  //   800533 2200893 73 540413 800533 2200893 73 640413 800533 2200893 73 740413 800533 2200893 73 840413
  //   800533 2200893 2200893 73 8067
  //   可计数暂停的时钟源
  //   指令字
  //   I型指令
  //   S型指令
  //   B型指令
  //   J型指令
  //   为方便自动评测，需要输出流水线各段保存的PC值，注意是PC不是PC+4，另外ID段寄存器写入信息，Mem段内存写入信息也要输出
endmodule
module \重定向流水线  (
  output RegWrite,
  output MemWrite,
  output [31:0] IF_PC,
  output [31:0] ID_PC,
  output [31:0] EX_PC,
  output [31:0] M_PC,
  output [31:0] WB_PC,
  output [31:0] RDin,
  output [31:0] MDin,
  output [31:0] LedData
);

  wire ALU_SRC, and_1_out, and_2_out, and_3_out, and_4_out, and_5_out, and_6_out, and_7_out, and_9_out,
       and_10_out, and_11_out, and_12_out, Beq, BGE, Bne, BranchTaken, CLK, clock_1_out, comparator_1_eq,
       comparator_1_lt, comparator_2_eq, d_ff_1_q, ecall, equal, ex_mem_1_ex_ecall, ex_mem_1_ex_jal,
       ex_mem_1_ex_jalr, ex_mem_1_ex_lb, ex_mem_1_ex_memtoreg, ex_mem_1_ex_uret, EX_MemToReg, EX_RegWrite,
       Go, great, halt, id_ex_1_ex_alusrcb, id_ex_1_ex_beq, id_ex_1_ex_bge, id_ex_1_ex_bne, id_ex_1_ex_ecall,
       id_ex_1_ex_jal, id_ex_1_ex_jalr, id_ex_1_ex_lb, id_ex_1_ex_memtoreg_2, id_ex_1_ex_uret, ID_MemToReg,
       ID_MemWrite, ID_RegWrite, IDt_MemToReg, IDt_RegWrite, IR1, IR2, IR3, JAL, JALR, LB, lb_t, LoadUse,
       MEM_RegWrite, mem_wb_1_ex_ecall, mem_wb_1_ex_jal, mem_wb_1_ex_jalr, mem_wb_1_ex_memtoreg, nand_1_out,
       not_1_out, not_2_out, not_3_out, not_4_out, not_5_out, not_6_out, not_7_out, or_1_out, or_5_out,
       or_7_out, RST, RsUsed, RtUsed, tALU_SRC, URET, W1, W2, W3, WB_lb, \单周期硬布线控制器_1_s_type , \无条件分支 ,
       \有条件分支 ;
  wire [0:0] or_4_out;
  wire [1:0] EX_R1_F, EX_R2_F, ID_R1_F, ID_R2_F, priority_encoder_1_out;
  wire [3:0] ALU_OP, id_ex_1_ex_aluop;
  wire [4:0] func, rs, rt;
  wire [7:0] multiplexer_13_out;
  wire [11:0] bit_extender_3_out, multiplexer_5_out, multiplexer_6_out;
  wire [12:0] CNT_num;
  wire [15:0] \LoadUse次数 , \总周期数 , \插入气泡数 , \无条件分支数 , \有条件分支数 , \条件分支成功数 ;
  wire [31:0] adder_1_out, adder_2_out, adder_3_out, aluresult, bit_extender_1_out, bit_extender_2_out,
       bit_extender_4_out, EX_IMM, EX_IR, ex_mem_1_mem_r1, ex_mem_1_mem_r2, EX_NRS, EX_NRT, EX_RS, EX_RT,
       ID_IR, IF_IR, LBR, MEM_AluData, MEM_IR, mem_wb_1_wb_r1, mem_wb_1_wb_r2, multiplexer_1_out,
       multiplexer_7_out, multiplexer_8_out, multiplexer_11_out, multiplexer_12_out, ram_1_data,
       regifile_down_1_r1, regifile_down_1_r2, shifter_1_out, shifter_2_out, WB_alu, WB_Dre, WB_IR;

  Button \u_总复位  (.out(RST));
  Button _1 (.out(IR1));
  Button _2 (.out(IR2));
  Button _3 (.out(IR3));
  // Probe on \总周期数 
  // Probe on \总周期数 
  Button \u_继续运行  (.out(Go));
  LED #(.active("true")) led_1 (.in(W1));
  LED #(.active("true")) led_2 (.in(W2));
  LED #(.active("true")) led_3 (.in(W3));
  // Probe on adder_2_out
  and and_1 (and_1_out, not_2_out, not_1_out);
  not not_1 (not_1_out, halt);
  not not_2 (not_2_out, LoadUse);
  Hex_Digit_Display hex_digit_display_1 (.value(LedData[31:28]));  // open: dp
  // Probe on IF_PC[19:0]
  // RiscV_Probe riscv_probe_1: pin names not known; wires that end beside it: IF_IR
  Priority_Encoder #(.select(2), .disabled("Z")) priority_encoder_1 (
    .in0(1'b1), .in1(id_ex_1_ex_jalr), .in2(id_ex_1_ex_jal), .in3(\无条件分支 ), .out(priority_encoder_1_out));  // open: gs, en_out, en_in
  Multiplexer #(.select(2), .width(32), .disabled("Z"), .enable("false")) multiplexer_1 (
    .in0(adder_1_out), .in1(aluresult), .in2(adder_2_out), .in3(adder_2_out), .out(multiplexer_1_out),
    .sel(priority_encoder_1_out));
  and and_2 (and_2_out, ~halt, CLK);  // AND_Gate
  Hex_Digit_Display hex_digit_display_2 (.value(LedData[23:20]));  // open: dp
  Hex_Digit_Display hex_digit_display_3 (.value(LedData[27:24]));  // open: dp
  // Probe on ID_PC[19:0]
  // RiscV_Probe riscv_probe_2: pin names not known; wires that end beside it: {ID_IR[31], func[4], ID_IR[29:26], func[3], ID_IR[24:15], func[2:0], ID_IR[11:0]}
  Counter #(.width(16), .max('hffff), .ongoal("wrap"), .trigger("rising"), .behavior("new")) counter_1 (
    .Q(\总周期数 ), .clk(and_2_out));  // open: load, D, count, carry, clr, preset, down
  Hex_Digit_Display hex_digit_display_4 (.value(LedData[19:16]));  // open: dp
  Hex_Digit_Display hex_digit_display_5 (.value(LedData[15:12]));  // open: dp
  // Probe on IF_PC
  Register #(.width(32), .trigger("rising"), .Select("low")) PC (
    .D(multiplexer_1_out), .en(and_1_out), .Q(IF_PC), .clk(CLK), .clr(RST));
  Counter #(.width(16), .max('hffff), .ongoal("wrap"), .trigger("rising"), .behavior("new")) counter_2 (
    .Q(\有条件分支数 ), .clk(and_3_out));  // open: load, D, count, carry, clr, preset, down
  and and_3 (and_3_out, \有条件分支 , CLK);
  Hex_Digit_Display hex_digit_display_6 (.value(LedData[7:4]));  // open: dp
  Hex_Digit_Display hex_digit_display_7 (.value(LedData[11:8]));  // open: dp
  // Probe on EX_PC[19:0]
  // RiscV_Probe riscv_probe_3: pin names not known; wires that end beside it: EX_IR
  not not_3 (not_3_out, LoadUse);
  and and_4 (and_4_out, not_3_out, not_4_out);
  not not_4 (not_4_out, halt);
  // Probe on EX_IMM
  Hex_Digit_Display hex_digit_display_8 (.value(LedData[3:0]));  // open: dp
  Adder #(.width(32)) adder_1 (.a(IF_PC), .b(32'h4), .out(adder_1_out));  // open: cin, cout
  Adder #(.width(32)) adder_2 (.a(EX_IMM), .b(EX_PC), .out(adder_2_out));  // open: cin, cout
  and and_5 (and_5_out, \无条件分支 , CLK);
  // Probe on \总周期数 
  // Probe on M_PC[19:0]
  // RiscV_Probe riscv_probe_4: pin names not known; wires that end beside it: MEM_IR
  ROM #(.addrWidth(10), .dataWidth(32), .Select("high")) rom_1 (.addr(IF_PC[11:2]), .data(IF_IR));
  Counter #(.width(16), .max('hffff), .ongoal("wrap"), .trigger("rising"), .behavior("new")) counter_3 (
    .Q(\无条件分支数 ), .clk(and_5_out));  // open: load, D, count, carry, clr, preset, down
  // Probe on \总周期数 
  // Probe on \无条件分支数 
  // Probe on \条件分支成功数 
  // Probe on \插入气泡数 
  // Probe on \LoadUse次数 
  or or_1 (or_1_out, BranchTaken, RST);
  IF_ID if_id_1 (
    .CLK(CLK), .\使能端 (and_4_out), .\清零端 (or_1_out), .IF_IR(IF_IR), .IF_PC(IF_PC),
    .ID_IR({ID_IR[31], func[4], ID_IR[29:26], func[3], ID_IR[24:15], func[2:0], ID_IR[11:0]}), .ID_PC(ID_PC));  // open: PD, PD_2
  and and_6 (and_6_out, BranchTaken, CLK);
  // Probe on IF_PC[11:0]
  // Probe on WB_PC[19:0]
  // RiscV_Probe riscv_probe_5: pin names not known; wires that end beside it: WB_IR
  not not_5 (not_5_out, halt);
  Counter #(.width(16), .max('hffff), .ongoal("wrap"), .trigger("rising"), .behavior("new")) counter_4 (
    .Q(\条件分支成功数 ), .clk(and_6_out));  // open: load, D, count, carry, clr, preset, down
  // Probe on ID_PC[11:0]
  // Probe on EX_PC[11:0]
  // Probe on M_PC[11:0]
  D_Flip_Flop #(.trigger("high"), .Pre_Clr_Positions("LEGACY"), .NegatePresetClear("false"), .enable("true"), .NewFFLayout("false")) d_ff_1 (.Q(d_ff_1_q));  // open: clk, D, Qn, preset, en, reset
  // Probe on 13'h340
  assign bit_extender_1_out = {{20{ID_IR[31]}}, {ID_IR[31], ID_IR[7], func[4], ID_IR[29:26], func[3], ID_IR[11:8]}};  // Bit_Extender bit_extender_1
  assign bit_extender_2_out = {{12{ID_IR[31]}}, {ID_IR[31], ID_IR[19:15], func[2:0], ID_IR[20], func[4], ID_IR[29:26], func[3], ID_IR[24:21]}};  // Bit_Extender bit_extender_2
  // Probe on {ID_IR[31], func[4], ID_IR[29:26], func[3], ID_IR[24:20]}
  // Probe on WB_PC[11:0]
  Comparator #(.width(13), .mode("twosComplement")) comparator_1 (
    .a(CNT_num), .b(13'h340), .eq(comparator_1_eq), .lt(comparator_1_lt));  // open: gt
  Clock #(.highDuration(1), .lowDuration(1)) clock_1 (.out(clock_1_out));
  or or_2 (\有条件分支 , id_ex_1_ex_jal, id_ex_1_ex_jalr);
  assign bit_extender_3_out = {{4{ID_IR[27]}}, {ID_IR[27:26], func[3], ID_IR[24:20]}};  // Bit_Extender bit_extender_3
  nand nand_1 (nand_1_out, d_ff_1_q, comparator_1_eq);
  Counter #(.width(13), .max('h1fff), .ongoal("stay"), .trigger("rising"), .behavior("old")) counter_5 (
    .count(comparator_1_lt), .Q(CNT_num), .clk(clock_1_out));  // open: load, D, carry, clr, preset
  \单周期硬布线控制器  \u_单周期硬布线控制器_1  (
    .Funct(func), .OP(ID_IR[6:2]), .ALU_OP(ALU_OP), .MemToReg(IDt_MemToReg), .MemWrite(ID_MemWrite),
    .ALU_SRC(tALU_SRC), .RegWrite(IDt_RegWrite), .ecall(ecall), .S_type(\单周期硬布线控制器_1_s_type ), .Jalr(JALR),
    .Beq(Beq), .JAL(JAL), .Bne(Bne), .in_3(ID_IR[21]), .uret(URET), .BGE(BGE), .LB(LB));
  Multiplexer #(.select(1), .width(5), .disabled("Z"), .enable("false")) multiplexer_2 (
    .in0(ID_IR[19:15]), .in1(5'b10001), .out(rs), .sel(ecall));
  Multiplexer #(.select(1), .width(5), .disabled("Z"), .enable("false")) multiplexer_3 (
    .in0(ID_IR[24:20]), .in1(5'b01010), .out(rt), .sel(ecall));
  Shifter #(.width(32), .shift("ll")) shifter_1 (.in(bit_extender_1_out), .\dist (5'b00001), .out(shifter_1_out));
  Shifter #(.width(32), .shift("ll")) shifter_2 (.in(bit_extender_2_out), .\dist (5'b00001), .out(shifter_2_out));
  not not_6 (not_6_out, ID_IR[0]);
  and and_7 (and_7_out, LB, not_6_out);
  Multiplexer #(.select(1), .width(3), .disabled("Z"), .enable("false")) multiplexer_4 (
    .in0({IDt_RegWrite, tALU_SRC, IDt_MemToReg}), .in1(3'b000), .out({ID_RegWrite, ALU_SRC, ID_MemToReg}),
    .sel(and_7_out));
  and and_8 (lb_t, LB, ID_IR[0]);
  assign CLK = nand_1_out ? clock_1_out : 1'bz;  // Controlled_Buffer controlled_buffer_1
  or or_3 (BranchTaken, id_ex_1_ex_jalr, id_ex_1_ex_jal, \无条件分支 );
  Multiplexer #(.select(1), .width(12), .disabled("Z"), .enable("false")) multiplexer_5 (
    .in0({ID_IR[31], func[4], ID_IR[29:26], func[3], ID_IR[24:20]}), .in1(bit_extender_3_out),
    .out(multiplexer_5_out), .sel(lb_t));
  Multiplexer #(.select(1), .width(12), .disabled("Z"), .enable("false")) multiplexer_6 (
    .in0(multiplexer_5_out), .in1({ID_IR[31], func[4], ID_IR[29:26], func[3], ID_IR[11:7]}),
    .out(multiplexer_6_out), .sel(\单周期硬布线控制器_1_s_type ));
  Pull_Resistor #(.pull(1)) pull_resistor_1 (.node(CLK));
  // Probe on {ID_IR[31], ID_IR[19:15], func[2:0], ID_IR[20], func[4], ID_IR[29:26], func[3], ID_IR[24:21]}
  or or_4 (or_4_out[0], Beq, Bne, BGE);
  assign bit_extender_4_out = {{20{multiplexer_6_out[11]}}, multiplexer_6_out};  // Bit_Extender bit_extender_4
  // Probe on bit_extender_4_out
  Multiplexer #(.select(2), .width(32), .disabled("Z"), .enable("false")) multiplexer_7 (
    .in0(bit_extender_4_out), .in1(shifter_1_out), .in2(shifter_2_out), .out(multiplexer_7_out),
    .sel({JAL, or_4_out[0]}));  // open: in3
  Regifile_down regifile_down_1 (
    .Din(RDin), .Clk(CLK), .R1(regifile_down_1_r1), .R2(regifile_down_1_r2), .WE(RegWrite),
    .W_num(WB_IR[11:7]), .R1_num(rs), .R2_num(rt));
  or or_5 (or_5_out, BranchTaken, RST, LoadUse);
  ID_EX id_ex_1 (
    .CLK(CLK), .\使能端 (not_5_out), .\清零端 (or_5_out),
    .ID_IR({ID_IR[31], func[4], ID_IR[29:26], func[3], ID_IR[24:15], func[2:0], ID_IR[11:0]}), .EX_IR(EX_IR),
    .ID_PC(ID_PC), .EX_PC(EX_PC), .ID_R1(regifile_down_1_r1), .EX_R1(EX_RS), .ID_R2(regifile_down_1_r2),
    .EX_R2(EX_RT), .ID_MemToReg(ID_MemToReg), .EX_MemToReg(EX_MemToReg), .ID_MemWrite(ID_MemWrite),
    .EX_MemToReg_2(id_ex_1_ex_memtoreg_2), .ID_AluOP(ALU_OP), .EX_AluOP(id_ex_1_ex_aluop),
    .ID_AluSrcB(ALU_SRC), .EX_AluSrcB(id_ex_1_ex_alusrcb), .ID_RegWrite(ID_RegWrite),
    .EX_RegWrite(EX_RegWrite), .ID_ecall(ecall), .EX_ecall(id_ex_1_ex_ecall), .ID_JAL(JAL),
    .EX_JAL(id_ex_1_ex_jal), .ID_JALR(JALR), .EX_JALR(id_ex_1_ex_jalr), .ID_Beq(Beq),
    .EX_Beq(id_ex_1_ex_beq), .ID_Bne(Bne), .EX_Bne(id_ex_1_ex_bne), .ID_URET(URET),
    .EX_URET(id_ex_1_ex_uret), .ID_BGE(BGE), .EX_BGE(id_ex_1_ex_bge), .ID_IMM(multiplexer_7_out),
    .EX_IMM(EX_IMM), .ID_R1_F(ID_R1_F), .EX_R1_F(EX_R1_F), .ID_R2_F(ID_R2_F), .EX_R2_F(EX_R2_F),
    .ID_LB(lb_t), .EX_LB(id_ex_1_ex_lb));  // open: PD, PD_2
  Multiplexer #(.select(1), .width(32), .disabled("Z"), .enable("false")) multiplexer_8 (
    .in0(EX_NRT), .in1(EX_IMM), .out(multiplexer_8_out), .sel(id_ex_1_ex_alusrcb));
  and and_9 (and_9_out, id_ex_1_ex_beq, equal);
  or or_6 (\无条件分支 , and_9_out, and_10_out, and_11_out);
  and and_10 (and_10_out, ~equal, id_ex_1_ex_bne);  // AND_Gate
  ALU alu_1 (
    .X(EX_NRS), .Y(multiplexer_8_out), .AluOP(id_ex_1_ex_aluop), .Equal(equal), .Result(aluresult),
    .out_4(great));  // open: Result_2, out_6
  and and_11 (and_11_out, great, id_ex_1_ex_bge);
  // Probe on EX_NRS
  // Probe on RDin
  EX_MEM ex_mem_1 (
    .CLK(CLK), .\使能端 (not_5_out), .\清零端 (RST), .EX_IR(EX_IR), .EX_PC(EX_PC), .EX_R1(EX_NRS),
    .ID_RegWrite(EX_RegWrite), .EX_R2(EX_NRT), .EX_ALU(aluresult), .ID_ecall(id_ex_1_ex_ecall),
    .EX_DATA(EX_NRT), .ID_URET(id_ex_1_ex_uret), .MEM_IR(MEM_IR), .MEM_PC(M_PC), .MEM_R1(ex_mem_1_mem_r1),
    .EX_RegWrite(MEM_RegWrite), .MEM_R2(ex_mem_1_mem_r2), .MEM_ALU(MEM_AluData),
    .EX_ecall(ex_mem_1_ex_ecall), .MEM_DATA(MDin), .EX_URET(ex_mem_1_ex_uret), .ID_MemToReg(EX_MemToReg),
    .EX_MemToReg(ex_mem_1_ex_memtoreg), .ID_MemWrite(id_ex_1_ex_memtoreg_2), .EX_MemWrite(MemWrite),
    .ID_JAL(id_ex_1_ex_jal), .EX_JAL(ex_mem_1_ex_jal), .ID_JALR(id_ex_1_ex_jalr), .EX_JALR(ex_mem_1_ex_jalr),
    .ID_LB(id_ex_1_ex_lb), .EX_LB(ex_mem_1_ex_lb));
  \used控制电路  \used控制电路_1  (
    .OP2(ID_IR[2]), .OP3(ID_IR[3]), .OP4(ID_IR[4]), .OP5(ID_IR[5]), .OP6(ID_IR[6]), .F12(func[0]),
    .F13(func[1]), .F14(func[2]), .F25(func[3]), .F30(func[4]), .RsUsed(RsUsed), .RtUesd(RtUsed));
  \LoadUse信号生成  \loaduse信号生成_1  (
    .R1Used(RsUsed), .EX_MemToReg(EX_MemToReg), .ID_R1(rs), .EX_RD(EX_IR[11:7]), .ID_R2(rt), .R2Used(RtUsed),
    .LoadUse(LoadUse));
  Multiplexer #(.select(2), .width(32), .disabled("Z"), .enable("false")) multiplexer_9 (
    .in0(EX_RS), .in1(RDin), .in2(MEM_AluData), .out(EX_NRS), .sel(EX_R1_F));  // open: in3
  Multiplexer #(.select(2), .width(32), .disabled("Z"), .enable("false")) multiplexer_10 (
    .in0(EX_RT), .in1(RDin), .in2(MEM_AluData), .out(EX_NRT), .sel(EX_R2_F));  // open: in3
  // Probe on ram_1_data
  RAM #(.addrWidth(10), .dataWidth(32), .bus("separate"), .Select("high")) ram_1 (
    .addr(MEM_AluData[11:2]), .din(MDin), .data(ram_1_data), .str(MemWrite), .clk(CLK), .ld(1'b1));  // open: sel, clr
  // Probe on MEM_AluData
  \R1_F_R2_F信号生成  \r1_f_r2_f信号生成_1  (
    .R1Used(RsUsed), .ID_R1(rs), .EX_RegWrite(EX_RegWrite), .EX_RD(EX_IR[11:7]), .MEM_RegWrite(MEM_RegWrite),
    .MEM_RD(MEM_IR[11:7]), .R2Used(RtUsed), .ID_R2(rt), .R1_F(ID_R1_F), .R2_F(ID_R2_F));
  MEM_WB mem_wb_1 (
    .CLK(CLK), .\使能端 (not_5_out), .\清零端 (RST), .MEM_IR(MEM_IR), .ID_MemToReg(ex_mem_1_ex_memtoreg),
    .ID_RegWrite(MEM_RegWrite), .MEM_PC(M_PC), .ID_ecall(ex_mem_1_ex_ecall), .MEM_R1(ex_mem_1_mem_r1),
    .ID_URET(ex_mem_1_ex_uret), .MEM_R2(ex_mem_1_mem_r2), .WB_IR(WB_IR), .EX_MemToReg(mem_wb_1_ex_memtoreg),
    .EX_RegWrite(RegWrite), .WB_PC(WB_PC), .EX_ecall(mem_wb_1_ex_ecall), .WB_R1(mem_wb_1_wb_r1),
    .WB_R2(mem_wb_1_wb_r2), .MEM_DIN(ram_1_data), .WB_DIN(WB_Dre), .MEM_ALU(MEM_AluData), .WB_ALU(WB_alu),
    .ID_JAL(ex_mem_1_ex_jal), .EX_JAL(mem_wb_1_ex_jal), .ID_JALR(ex_mem_1_ex_jalr),
    .EX_JALR(mem_wb_1_ex_jalr), .ID_LB(ex_mem_1_ex_lb), .EX_LB(WB_lb));  // open: EX_URET
  // Probe on WB_alu
  Multiplexer #(.select(1), .width(32), .disabled("Z"), .enable("false")) multiplexer_11 (
    .in0(WB_alu), .in1(WB_Dre), .out(multiplexer_11_out), .sel(mem_wb_1_ex_memtoreg));
  Adder #(.width(32)) adder_3 (.a(WB_PC), .b(32'h4), .out(adder_3_out));  // open: cin, cout
  Comparator #(.width(32), .mode("twosComplement")) comparator_2 (
    .a(mem_wb_1_wb_r1), .b(32'h22), .eq(comparator_2_eq));  // open: gt, lt
  Multiplexer #(.select(1), .width(32), .disabled("Z"), .enable("false")) multiplexer_12 (
    .in0(multiplexer_11_out), .in1(LBR), .out(multiplexer_12_out), .sel(WB_lb));
  Register #(.width(32), .trigger("rising"), .Select("low")) register_1 (
    .D(mem_wb_1_wb_r2), .en(and_12_out), .Q(LedData), .clk(CLK));  // open: clr
  and and_12 (and_12_out, comparator_2_eq, mem_wb_1_ex_ecall);
  not not_7 (not_7_out, comparator_2_eq);
  Multiplexer #(.select(2), .width(8), .disabled("Z"), .enable("false")) multiplexer_13 (
    .in0(WB_Dre[7:0]), .in1(WB_Dre[15:8]), .in2(WB_Dre[23:16]), .in3(WB_Dre[31:24]),
    .out(multiplexer_13_out), .sel(WB_alu[1:0]));
  Multiplexer #(.select(1), .width(32), .disabled("Z"), .enable("false")) multiplexer_14 (
    .in0(multiplexer_12_out), .in1(adder_3_out), .out(RDin), .sel(or_7_out));
  or or_7 (or_7_out, mem_wb_1_ex_jal, mem_wb_1_ex_jalr);
  D_Flip_Flop #(.trigger("falling"), .Pre_Clr_Positions("ABOVE_BELOW"), .NegatePresetClear("false"), .enable("true"), .NewFFLayout("true")) d_ff_2 (
    .clk(CLK), .D(not_7_out), .Q(halt), .en(mem_wb_1_ex_ecall), .reset(Go));  // open: Qn, preset
  assign LBR = {{24{multiplexer_13_out[7]}}, multiplexer_13_out};  // Bit_Extender bit_extender_5

  // Other names for the same wires on the sheet: ID_IR (some bits) = func; EX_WriteReg_num[4:0] = EX_IR[11:7];
  //   op[4:0] = ID_IR[6:2]; MEM_WriteReg_num[4:0] = MEM_IR[11:7]; MEM_PC[31:0] = M_PC

  // Notes on the sheet:
  //   中断源
  //   时空图监测，可删除
  //   中断等待指示
  //   数码管输出
  //   contents of rom_1 (hex, n*v repeats v):
  //   100493 100006f 100493 200913 300993 100006f 100493 200913 300993 100006f 100493 200913 300993
  //   100006f 100493 200913 300993 3bc000ef 100413 100493 1f49493 900533 2200893 73 24d493 48463 fedff06f
  //   900533 2200893 73 100493 249493 900533 2200893 73 48463 fedff06f 100493 1f49493 900533 2200893 73
  //   4034d493 900533 2200893 73 4044d493 900533 2200893 73 4044d493 900533 2200893 73 4044d493 900533
  //   2200893 73 4044d493 900533 2200893 73 4044d493 900533 2200893 73 4044d493 900533 2200893 73 4044d493
  //   900533 2200893 73 100413 1f41993 41f9d993 433 c00913 300b13 140413 f47413 800293 100313 499993
  //   89e9b3 1300533 2200893 73 406282b3 fe0294e3 140413 f00f93 1f47433 1c41413 800293 100313 49d993
  //   89e9b3 1300533 2200893 73 406282b3 fe0294e3 1c45413 406b0b33 b0463 f95ff06f 2b3 fff2c293 829293
  //   ff2e293 500533 2200893 73 fff00413 493 84a023 140413 448493 84a023 140413 448493 84a023 140413
  //   448493 84a023 140413 448493 84a023 140413 448493 84a023 140413 448493 84a023 140413 448493 84a023
  //   140413 448493 84a023 140413 448493 84a023 140413 448493 84a023 140413 448493 84a023 140413 448493
  //   84a023 140413 448493 84a023 140413 448493 84a023 140413 448493 84a023 140413 448493 140413 433
  //   3c00493 42983 4aa03 149a2b3 28663 134a023 1442023 ffc48493 fe9412e3 800533 2200893 73 440413 3c00493
  //   fc9416e3 3200893 73 f00493 900533 2200893 73 fff48493 fe04d8e3 a00893 73 fff00293 7700493 849493
  //   7748493 900533 2200893 73 1000e13 54c4b3 900533 2200893 73 fffe0e13 fe0e16e3 a00893 73 fff00293 313
  //   1900413 841413 9700493 940533 2200893 73 5484b3 494b313 fe0306e3 a00893 73 313 1000e13 13 8400493
  //   849493 8348493 400913 891913 490913 849493 8248493 849493 8148493 891913 490913 891913 490913 932023
  //   12484b3 430313 fffe0e13 fe0e18e3 2000e13 313 30483 900533 2200893 73 130313 fffe0e13 fe0e14e3 a00893
  //   73 a00893 73 413 140413 800533 2200893 73 240413 800533 2200893 73 340413 800533 2200893 73 440413
  //   800533 2200893 73 540413 800533 2200893 73 640413 800533 2200893 73 740413 800533 2200893 73 840413
  //   800533 2200893 2200893 73 8067
  //   指令字
  //   I型指令
  //   控制位
  //   S型指令
  //   B型指令
  //   J型指令
  //   流水调试日志用
  //   暂停节拍，不能为0
  //   戳工具置1进入计数暂停模式，ctrl+k时钟自动运行到对应节拍暂停
  //   ctrl+k关闭时钟连续运行，将控制位置零，进入单步调试模式调试
  //   用这个时钟源需要去掉电路中的其他时钟源
  //   可计数暂停的时钟源
  //   为方便自动评测，需要输出流水线各段保存的PC值，注意是PC不是PC+4，另外ID段寄存器写入信息，Mem段内存写入信息也要输出
  //   rd
  //   重定向设置
endmodule

module \单周期_单级中断  (
  input  IR1,
  input  IR2,
  input  IR3,
  output RegWrite,
  output MemWrite,
  output [31:0] PC,
  output [31:0] IR,
  output [31:0] RDin,
  output [31:0] MDin,
  output [31:0] LedData
);

  wire and_1_out, and_2_out, and_4_out, and_5_out, and_6_out, and_10_out, CLK, clock_1_out, Clr1, Clr2, Clr3,
       comparator_1_eq, comparator_2_eq, comparator_3_eq, comparator_4_eq, comparator_5_eq, comparator_5_lt,
       comparator_6_eq, d_ff_2_q, decoder_1_out1, decoder_1_out2, decoder_1_out3, ecall, equal, Go, great,
       halt, IE, INT, IR1_t, IR2_t, IR3_t, IRA, IRB, IRC, JAL, JALR, LB, nand_1_out, not_1_out, not_2_out,
       not_3_out, or_1_out, or_3_out, or_6_out, RST, URET, W1, W2, W3, \中断信号 , \单周期硬布线控制器_1_alu_src ,
       \单周期硬布线控制器_1_beq , \单周期硬布线控制器_1_bge , \单周期硬布线控制器_1_bne , \单周期硬布线控制器_1_memtoreg , \单周期硬布线控制器_1_s_type ;
  wire [1:0] priority_encoder_1_out, register_1_q, \中断号 ;
  wire [3:0] \单周期硬布线控制器_1_alu_op ;
  wire [4:0] multiplexer_4_out, multiplexer_5_out;
  wire [11:0] bit_extender_1_out, multiplexer_6_out, multiplexer_7_out;
  wire [12:0] CNT_num;
  wire [15:0] \总周期数 ;
  wire [31:0] adder_1_out, adder_2_out, adder_3_out, aluresult, bit_extender_2_out, bit_extender_3_out,
       bit_extender_4_out, INT_Addar, multiplexer_1_out, multiplexer_9_out, multiplexer_11_out, N_PC, NPC,
       ram_1_data, regifile_1_r1, RET_PC, shifter_1_out, shifter_2_out;

  Button \u_继续运行  (.out(Go));
  Button _1 ();  // open: out
  Button _2 ();  // open: out
  Button _3 ();  // open: out
  LED #(.active("true")) led_1 (.in(W1));
  LED #(.active("true")) led_2 (.in(W2));
  LED #(.active("true")) led_3 (.in(W3));
  Hex_Digit_Display hex_digit_display_1 (.value(LedData[31:28]));  // open: dp
  Comparator #(.width(16), .mode("twosComplement")) comparator_1 (
    .a(16'h23b), .b(\总周期数 ), .eq(comparator_1_eq));  // open: gt, lt
  Comparator #(.width(16), .mode("twosComplement")) comparator_2 (
    .a(\总周期数 ), .b(16'h1), .eq(comparator_2_eq));  // open: gt, lt
  Comparator #(.width(16), .mode("twosComplement")) comparator_3 (
    .a(\总周期数 ), .b(16'h4), .eq(comparator_3_eq));  // open: gt, lt
  Comparator #(.width(16), .mode("twosComplement")) comparator_4 (
    .a(\总周期数 ), .b(16'h7), .eq(comparator_4_eq));  // open: gt, lt
  Counter #(.width(16), .max('hffff), .ongoal("wrap"), .trigger("rising"), .behavior("new")) counter_1 (
    .Q(\总周期数 ), .clk(and_1_out));  // open: load, D, count, carry, clr, preset, down
  and and_1 (and_1_out, ~halt, CLK);  // AND_Gate
  Hex_Digit_Display hex_digit_display_2 (.value(LedData[23:20]));  // open: dp
  Hex_Digit_Display hex_digit_display_3 (.value(LedData[27:24]));  // open: dp
  or or_1 (or_1_out, comparator_1_eq, comparator_2_eq);
  assign IRA = or_1_out ? ~CLK : 1'bz;  // Controlled_Inverter controlled_inverter_1
  assign IRB = comparator_3_eq ? ~CLK : 1'bz;  // Controlled_Inverter controlled_inverter_2
  assign IRC = comparator_4_eq ? ~CLK : 1'bz;  // Controlled_Inverter controlled_inverter_3
  Hex_Digit_Display hex_digit_display_4 (.value(LedData[19:16]));  // open: dp
  Hex_Digit_Display hex_digit_display_5 (.value(LedData[15:12]));  // open: dp
  Pull_Resistor #(.pull(0)) pull_resistor_1 (.node(IRA));
  Pull_Resistor #(.pull(0)) pull_resistor_2 (.node(IRB));
  Pull_Resistor #(.pull(0)) pull_resistor_3 (.node(IRC));
  Multiplexer #(.select(1), .width(32), .disabled("Z"), .enable("false")) multiplexer_1 (
    .in0(NPC), .in1(RET_PC), .out(multiplexer_1_out), .sel(URET));
  Hex_Digit_Display hex_digit_display_6 (.value(LedData[7:4]));  // open: dp
  Hex_Digit_Display hex_digit_display_7 (.value(LedData[11:8]));  // open: dp
  // Probe on \总周期数 
  Multiplexer #(.select(1), .width(32), .disabled("Z"), .enable("false")) multiplexer_2 (
    .in0(multiplexer_1_out), .in1(INT_Addar), .out(N_PC), .sel(INT));
  and and_2 (and_2_out, ~URET, \中断信号 );  // AND_Gate
  and and_3 (INT, IE, \中断信号 );
  Hex_Digit_Display hex_digit_display_8 (.value(LedData[3:0]));  // open: dp
  Button \u_继续运行_2  (.out(RST));
  and and_4 (and_4_out, great, \单周期硬布线控制器_1_bge );
  \中断控制器  \u_中断控制器_1  (
    .IRA(IRA), .W1(W1), .Clr1(Clr1), .IRB(IRB), .W2(W2), .Clr2(Clr2), .IRC(IRC), .W3(W3), .Clr3(Clr3),
    .\中断号 (\中断号 ), .\中断请求 (\中断信号 ), .CLK(CLK), .RST(RST));
  D_Flip_Flop #(.trigger("rising"), .Pre_Clr_Positions("LEGACY"), .NegatePresetClear("false"), .enable("true"), .NewFFLayout("false")) d_ff_1 (
    .clk(CLK), .D(and_2_out), .Qn(IE));  // open: Q, preset, en, reset
  not not_1 (not_1_out, equal);
  and and_5 (and_5_out, \单周期硬布线控制器_1_bne , not_1_out);
  Priority_Encoder #(.select(2), .disabled("Z")) priority_encoder_1 (
    .in0(1'b1), .in1(JALR), .in2(JAL), .in3(or_3_out), .out(priority_encoder_1_out));  // open: gs, en_out, en_in
  buf or_2 (IR1_t, IRA);  // OR_Gate
  and and_6 (and_6_out, equal, \单周期硬布线控制器_1_beq );
  or or_3 (or_3_out, and_5_out, and_4_out, and_6_out);
  Multiplexer #(.select(2), .width(32), .disabled("Z"), .enable("false")) multiplexer_3 (
    .in0(adder_1_out), .in1(aluresult), .in2(adder_3_out), .in3(adder_2_out), .out(NPC),
    .sel(priority_encoder_1_out));
  buf or_4 (IR2_t, IRB);  // OR_Gate
  // Probe on PC
  not not_2 (not_2_out, halt);
  Register #(.width(32), .trigger("rising"), .Select("low")) u_PC (
    .D(N_PC), .en(not_2_out), .Q(PC), .clk(CLK), .clr(RST));
  buf or_5 (IR3_t, IRC);  // OR_Gate
  Adder #(.width(32)) adder_1 (.a(PC), .b(32'h4), .out(adder_1_out));  // open: cin, cout
  Register #(.width(2), .trigger("rising"), .Select("low")) register_1 (
    .D(\中断号 ), .en(INT), .Q(register_1_q), .clk(CLK), .clr(RST));
  Decoder #(.select(2), .tristate("false"), .disabled("Z"), .enable("false")) decoder_1 (
    .out1(decoder_1_out1), .out2(decoder_1_out2), .out3(decoder_1_out3), .sel(register_1_q));  // open: out0
  // RiscV_Probe riscv_probe_1: pin names not known; wires that end beside it: IR
  ROM #(.addrWidth(10), .dataWidth(32), .Select("high")) rom_1 (.addr(PC[11:2]), .data(IR));
  Adder #(.width(32)) adder_2 (.a(PC), .b(shifter_1_out), .out(adder_2_out));  // open: cin, cout
  Adder #(.width(32)) adder_3 (.a(PC), .b(shifter_2_out), .out(adder_3_out));  // open: cin, cout
  and and_7 (Clr1, decoder_1_out1, URET);
  and and_8 (Clr2, decoder_1_out2, URET);
  and and_9 (Clr3, decoder_1_out3, URET);
  \单周期硬布线控制器  \u_单周期硬布线控制器_1  (
    .Funct({IR[30], IR[25], IR[14:12]}), .OP(IR[6:2]), .ALU_OP(\单周期硬布线控制器_1_alu_op ),
    .MemToReg(\单周期硬布线控制器_1_memtoreg ), .MemWrite(MemWrite), .ALU_SRC(\单周期硬布线控制器_1_alu_src ),
    .RegWrite(RegWrite), .ecall(ecall), .S_type(\单周期硬布线控制器_1_s_type ), .Jalr(JALR), .Beq(\单周期硬布线控制器_1_beq ),
    .JAL(JAL), .Bne(\单周期硬布线控制器_1_bne ), .in_3(IR[21]), .uret(URET), .BGE(\单周期硬布线控制器_1_bge ), .LB(LB));
  Multiplexer #(.select(1), .width(5), .disabled("Z"), .enable("false")) multiplexer_4 (
    .in0(IR[19:15]), .in1(5'b10001), .out(multiplexer_4_out), .sel(ecall));
  Multiplexer #(.select(1), .width(5), .disabled("Z"), .enable("false")) multiplexer_5 (
    .in0(IR[24:20]), .in1(5'b01010), .out(multiplexer_5_out), .sel(ecall));
  assign bit_extender_1_out = {{4{IR[27]}}, IR[27:20]};  // Bit_Extender bit_extender_1
  Multiplexer #(.select(1), .width(12), .disabled("Z"), .enable("false")) multiplexer_6 (
    .in0(IR[31:20]), .in1(bit_extender_1_out), .out(multiplexer_6_out), .sel(LB));
  Multiplexer #(.select(1), .width(12), .disabled("Z"), .enable("false")) multiplexer_7 (
    .in0(multiplexer_6_out), .in1({IR[31:25], IR[11:7]}), .out(multiplexer_7_out), .sel(\单周期硬布线控制器_1_s_type ));
  Multiplexer #(.select(2), .width(32), .disabled("Z"), .enable("false")) multiplexer_8 (
    .in1(32'h30ac), .in2(32'h3150), .in3(32'h31f4), .out(INT_Addar), .sel(\中断号 ));  // open: in0
  assign bit_extender_2_out = {{20{multiplexer_7_out[11]}}, multiplexer_7_out};  // Bit_Extender bit_extender_2
  assign bit_extender_3_out = {{20{IR[31]}}, {IR[31], IR[7], IR[30:25], IR[11:8]}};  // Bit_Extender bit_extender_3
  assign bit_extender_4_out = {{12{IR[31]}}, {IR[31], IR[19:12], IR[20], IR[30:21]}};  // Bit_Extender bit_extender_4
  D_Flip_Flop #(.trigger("high"), .Pre_Clr_Positions("LEGACY"), .NegatePresetClear("false"), .enable("true"), .NewFFLayout("false")) d_ff_2 (.Q(d_ff_2_q));  // open: clk, D, Qn, preset, en, reset
  // Probe on 13'hc
  Regifile regifile_1 (
    .Din(RDin), .Clk(CLK), .R1(regifile_1_r1), .R2(MDin), .WE(RegWrite), .W_num(IR[11:7]),
    .R1_num(multiplexer_4_out), .R2_num(multiplexer_5_out));
  Shifter #(.width(32), .shift("ll")) shifter_1 (.in(bit_extender_3_out), .\dist (5'b00001), .out(shifter_1_out));
  Shifter #(.width(32), .shift("ll")) shifter_2 (.in(bit_extender_4_out), .\dist (5'b00001), .out(shifter_2_out));
  Comparator #(.width(13), .mode("twosComplement")) comparator_5 (
    .a(CNT_num), .b(13'hc), .eq(comparator_5_eq), .lt(comparator_5_lt));  // open: gt
  Clock #(.highDuration(1), .lowDuration(1)) clock_1 (.out(clock_1_out));
  // Probe on \单周期硬布线控制器_1_alu_op 
  Multiplexer #(.select(1), .width(32), .disabled("Z"), .enable("false")) multiplexer_9 (
    .in0(MDin), .in1(bit_extender_2_out), .out(multiplexer_9_out), .sel(\单周期硬布线控制器_1_alu_src ));
  Counter #(.width(13), .max('h1fff), .ongoal("stay"), .trigger("rising"), .behavior("old")) counter_2 (
    .count(comparator_5_lt), .Q(CNT_num), .clk(clock_1_out));  // open: load, D, carry, clr, preset
  // Probe on aluresult
  ALU alu_1 (
    .X(regifile_1_r1), .Y(multiplexer_9_out), .AluOP(\单周期硬布线控制器_1_alu_op ), .Equal(equal),
    .Result(aluresult), .out_4(great));  // open: Result_2, out_6
  Multiplexer #(.select(1), .width(32), .disabled("Z"), .enable("false")) multiplexer_10 (
    .in0(multiplexer_11_out), .in1(adder_1_out), .out(RDin), .sel(or_6_out));
  // Probe on regifile_1_r1
  nand nand_1 (nand_1_out, d_ff_2_q, comparator_5_eq);
  Comparator #(.width(32), .mode("twosComplement")) comparator_6 (
    .a(regifile_1_r1), .b(32'h22), .eq(comparator_6_eq));  // open: gt, lt
  or or_6 (or_6_out, JAL, JALR);
  Register #(.width(32), .trigger("falling"), .Select("low")) EPC (.D(NPC), .en(INT), .Q(RET_PC), .clk(CLK), .clr(RST));
  assign CLK = nand_1_out ? clock_1_out : 1'bz;  // Controlled_Buffer controlled_buffer_1
  Pull_Resistor #(.pull(1)) pull_resistor_4 (.node(CLK));
  and and_10 (and_10_out, comparator_6_eq, ecall);
  not not_3 (not_3_out, comparator_6_eq);
  RAM #(.addrWidth(10), .dataWidth(32), .bus("separate"), .Select("high")) ram_1 (
    .addr(aluresult[11:2]), .din(MDin), .data(ram_1_data), .str(MemWrite), .clk(CLK), .ld(1'b1), .clr(RST));  // open: sel
  Register #(.width(32), .trigger("rising"), .Select("low")) register_2 (
    .D(MDin), .en(and_10_out), .Q(LedData), .clk(CLK));  // open: clr
  D_Flip_Flop #(.trigger("falling"), .Pre_Clr_Positions("ABOVE_BELOW"), .NegatePresetClear("false"), .enable("true"), .NewFFLayout("true")) d_ff_3 (
    .clk(CLK), .D(not_3_out), .Q(halt), .en(ecall), .reset(Go));  // open: Qn, preset
  Multiplexer #(.select(1), .width(32), .disabled("Z"), .enable("false")) multiplexer_11 (
    .in0(aluresult), .in1(ram_1_data), .out(multiplexer_11_out), .sel(\单周期硬布线控制器_1_memtoreg ));

  // Other names for the same wires on the sheet: func[4:0] = {IR[30], IR[25], IR[14:12]}; op[4:0] = IR[6:2]

  // Notes on the sheet:
  //   中断源
  //   中断等待指示
  //   总复位信号应将除ROM以外所有存储组件全部清零
  //   单级中断测试信号模拟器
  //   数码管输出
  //   数码管输出应该用寄存器锁存，否则显示数据只能一闪而过
  //   中断控制逻辑
  //   中断请求信号产生
  //   BranchAddress
  //   中断清零信号产生
  //   指令探针
  //   指令存储器
  //   contents of rom_1 (hex, n*v repeats v):
  //   7d000113 100413 1f41993 41f9d993 433 c00913 800b13 140413 f47413 800293 100313 499993 89e9b3 1300533
  //   2200893 73 406282b3 fe0294e3 140413 f00f93 1f47433 1c41413 800293 100313 49d993 89e9b3 1300533
  //   2200893 73 406282b3 fe0294e3 1c45413 406b0b33 b0463 f95ff06f 2b3 fff2c293 1029293 fff2e293 500533
  //   2200893 73 f5dff06f 1112023 410113 a12023 410113 812023 410113 1312023 410113 1412023 410113 1512023
  //   410113 1612023 410113 100b13 300a13 100a93 1600433 441413 14469b3 1300533 2200893 73 fe0416e3
  //   415a0a33 fe0a10e3 ffc10113 12b03 ffc10113 12a83 ffc10113 12a03 ffc10113 12983 ffc10113 12403
  //   ffc10113 12503 ffc10113 12883 200073 1112023 410113 a12023 410113 812023 410113 1312023 410113
  //   1412023 410113 1512023 410113 1612023 410113 200b13 300a13 100a93 1600433 441413 14469b3 1300533
  //   2200893 73 fe0416e3 415a0a33 fe0a10e3 ffc10113 12b03 ffc10113 12a83 ffc10113 12a03 ffc10113 12983
  //   ffc10113 12403 ffc10113 12503 ffc10113 12883 200073 1112023 410113 a12023 410113 812023 410113
  //   1312023 410113 1412023 410113 1512023 410113 1612023 410113 300b13 300a13 100a93 1600433 441413
  //   14469b3 1300533 2200893 73 fe0416e3 415a0a33 fe0a10e3 ffc10113 12b03 ffc10113 12a83 ffc10113 12a03
  //   ffc10113 12983 ffc10113 12403 ffc10113 12503 ffc10113 12883 200073
  //   指令字
  //   I型指令
  //   S型指令
  //   J型指令
  //   为方便自动评测，需要输出PC，IR，寄存器堆写如数据RDin
  //   JAL
  //   JALR
  //   URET
  //   B型指令
  //   RAM写使能MemWrite、RAM写入数据MDin等信号
  //   Beq
  //   Bne
  //   MemToReg
  //   MemWrite
  //   AluOP
  //   AluSrcB
  //   RegWrite
  //   中断入口逻辑
  //   控制位
  //   暂停节拍，不能为0
  //   戳工具置1进入计数暂停模式，ctrl+k时钟自动运行到对应节拍暂停
  //   ctrl+k关闭时钟连续运行，将控制位置零，进入单步调试模式调试
  //   保护现场
  //   可计数暂停的时钟源
  //   数据存储器
endmodule

module \单周期_多级中断  (
  input  IR1,
  input  IR2,
  input  IR3,
  output RegWrite,
  output MemWrite,
  output [31:0] PC,
  output [31:0] IR,
  output [31:0] RDin,
  output [31:0] MDin,
  output [31:0] LedData
);

  wire _1_out, _2_out, _3_out, and_1_out, and_5_out, and_6_out, and_7_out, and_8_out, and_12_out, CLK,
       clock_1_out, Clr1, Clr2, Clr3, comparator_1_eq, comparator_2_eq, comparator_3_eq, comparator_5_eq,
       comparator_6_eq, comparator_7_eq, comparator_8_eq, comparator_9_eq, comparator_11_eq,
       comparator_11_lt, comparator_12_eq, csrrci, csrrsi, d_ff_1_q, decoder_1_out1, decoder_1_out2,
       decoder_1_out3, demultiplexer_1_out1, demultiplexer_1_out2, demultiplexer_1_out3,
       demultiplexer_2_out0, demultiplexer_2_out1, demultiplexer_2_out2, ecall, equal, Go, great, halt, IE,
       init, INT, IR1_t, IR2_t, IR3_t, IRA, IRB, IRC, JAL, JALR, LB, nand_1_out, not_1_out, not_2_out,
       not_3_out, or_1_out, or_2_out, or_4_out, or_6_out, or_8_out, or_9_out, RST, URET, W1, W2, W3, \中断信号 ,
       \优先级高 , \单周期硬布线控制器_1_alu_src , \单周期硬布线控制器_1_beq , \单周期硬布线控制器_1_bge , \单周期硬布线控制器_1_bne ,
       \单周期硬布线控制器_1_memtoreg , \单周期硬布线控制器_1_s_type ;
  wire [1:0] counter_2_q, IR1_q, IR2_q, IR3_q, priority_encoder_1_out, \中断号 , \当前中断号 ;
  wire [3:0] \单周期硬布线控制器_1_alu_op ;
  wire [4:0] multiplexer_5_out, multiplexer_6_out;
  wire [11:0] bit_extender_1_out, multiplexer_7_out, multiplexer_8_out;
  wire [12:0] CNT_num;
  wire [15:0] \总周期数 ;
  wire [31:0] adder_1_out, adder_2_out, adder_3_out, aluresult, bit_extender_2_out, bit_extender_3_out,
       bit_extender_4_out, EPC1_q, EPC2_q, EPC3_q, INT_Addar, multiplexer_1_out, multiplexer_10_out,
       multiplexer_13_out, N_PC, NPC, ram_1_data, regifile_1_r1, RET_PC, shifter_1_out, shifter_2_out;

  Button \u_继续运行  (.out(Go));
  Button _1 (.out(_1_out));
  Button _2 (.out(_2_out));
  Button _3 (.out(_3_out));
  LED #(.active("true")) led_1 (.in(W1));
  LED #(.active("true")) led_2 (.in(W2));
  LED #(.active("true")) led_3 (.in(W3));
  Hex_Digit_Display hex_digit_display_1 (.value(LedData[31:28]));  // open: dp
  Counter #(.width(16), .max('hffff), .ongoal("wrap"), .trigger("rising"), .behavior("new")) counter_1 (
    .Q(\总周期数 ), .clk(and_1_out));  // open: load, D, count, carry, clr, preset, down
  and and_1 (and_1_out, ~halt, CLK);  // AND_Gate
  Comparator #(.width(5), .mode("unsigned")) comparator_1 (
    .a(IR[6:2]), .b(5'b11100), .eq(comparator_1_eq));  // open: gt, lt
  Comparator #(.width(3), .mode("unsigned")) comparator_2 (
    .a(3'b110), .b(IR[14:12]), .eq(comparator_2_eq));  // open: gt, lt
  Comparator #(.width(3), .mode("unsigned")) comparator_3 (
    .a(IR[14:12]), .b(3'b111), .eq(comparator_3_eq));  // open: gt, lt
  Hex_Digit_Display hex_digit_display_2 (.value(LedData[23:20]));  // open: dp
  Hex_Digit_Display hex_digit_display_3 (.value(LedData[27:24]));  // open: dp
  Comparator #(.width(16), .mode("twosComplement")) comparator_4 (
    .a({16{1'b0}}), .b(\总周期数 ), .eq(init));  // open: gt, lt
  Comparator #(.width(16), .mode("twosComplement")) comparator_5 (
    .a(16'h241), .b(\总周期数 ), .eq(comparator_5_eq));  // open: gt, lt
  Comparator #(.width(16), .mode("twosComplement")) comparator_6 (
    .a(\总周期数 ), .b(16'h1), .eq(comparator_6_eq));  // open: gt, lt
  Comparator #(.width(16), .mode("twosComplement")) comparator_7 (
    .a(\总周期数 ), .b(16'h2), .eq(comparator_7_eq));  // open: gt, lt
  Comparator #(.width(16), .mode("twosComplement")) comparator_8 (
    .a(\总周期数 ), .b(16'h3), .eq(comparator_8_eq));  // open: gt, lt
  or or_1 (or_1_out, comparator_8_eq, comparator_5_eq);
  Multiplexer #(.select(1), .width(32), .disabled("Z"), .enable("false")) multiplexer_1 (
    .in0(NPC), .in1(RET_PC), .out(multiplexer_1_out), .sel(URET));
  and and_2 (csrrsi, comparator_1_eq, comparator_2_eq);
  and and_3 (csrrci, comparator_1_eq, comparator_3_eq);
  \中断控制器  \u_中断控制器_1  (
    .IRA(IR1_t), .W1(W1), .Clr1(Clr1), .IRB(IR2_t), .W2(W2), .Clr2(Clr2), .IRC(IR3_t), .W3(W3), .Clr3(Clr3),
    .\中断号 (\中断号 ), .\中断请求 (\中断信号 ), .CLK(CLK), .RST(RST));
  Hex_Digit_Display hex_digit_display_4 (.value(LedData[19:16]));  // open: dp
  Hex_Digit_Display hex_digit_display_5 (.value(LedData[15:12]));  // open: dp
  Comparator #(.width(16), .mode("twosComplement")) comparator_9 (
    .a(\总周期数 ), .b(16'h2fd), .eq(comparator_9_eq));  // open: gt, lt
  or or_2 (or_2_out, comparator_9_eq, comparator_6_eq);
  Pull_Resistor #(.pull(0)) pull_resistor_1 (.node(IRA));
  assign IRA = or_2_out ? ~CLK : 1'bz;  // Controlled_Inverter controlled_inverter_1
  Pull_Resistor #(.pull(0)) pull_resistor_2 (.node(IRB));
  assign IRB = comparator_7_eq ? ~CLK : 1'bz;  // Controlled_Inverter controlled_inverter_2
  Pull_Resistor #(.pull(0)) pull_resistor_3 (.node(IRC));
  assign IRC = or_1_out ? ~CLK : 1'bz;  // Controlled_Inverter controlled_inverter_3
  Multiplexer #(.select(1), .width(32), .disabled("Z"), .enable("false")) multiplexer_2 (
    .in0(multiplexer_1_out), .in1(INT_Addar), .out(N_PC), .sel(INT));
  and and_4 (INT, \中断信号 , \优先级高 , IE);
  Hex_Digit_Display hex_digit_display_6 (.value(LedData[11:8]));  // open: dp
  Hex_Digit_Display hex_digit_display_7 (.value(LedData[7:4]));  // open: dp
  // Probe on \总周期数 
  // Probe on \总周期数 
  Comparator #(.width(2), .mode("unsigned")) comparator_10 (.a(\中断号 ), .b(\当前中断号 ), .gt(\优先级高 ));  // open: eq, lt
  Hex_Digit_Display hex_digit_display_8 (.value(LedData[3:0]));  // open: dp
  Button \u_继续运行_2  (.out(RST));
  and and_5 (and_5_out, great, \单周期硬布线控制器_1_bge );
  // Probe on PC
  not not_1 (not_1_out, equal);
  and and_6 (and_6_out, \单周期硬布线控制器_1_bne , not_1_out);
  Priority_Encoder #(.select(2), .disabled("Z")) priority_encoder_1 (
    .in0(1'b1), .in1(JALR), .in2(JAL), .in3(or_4_out), .out(priority_encoder_1_out));  // open: gs, en_out, en_in
  // Probe on \中断号 
  or or_3 (IR1_t, IR1, IRA);
  and and_7 (and_7_out, equal, \单周期硬布线控制器_1_beq );
  or or_4 (or_4_out, and_6_out, and_5_out, and_7_out);
  Multiplexer #(.select(2), .width(32), .disabled("Z"), .enable("false")) multiplexer_3 (
    .in0(adder_1_out), .in1(aluresult), .in2(adder_3_out), .in3(adder_2_out), .out(NPC),
    .sel(priority_encoder_1_out));
  Demultiplexer #(.select(2), .width(1), .tristate("false"), .disabled("Z"), .enable("false")) demultiplexer_1 (
    .out1(demultiplexer_1_out1), .out2(demultiplexer_1_out2), .out3(demultiplexer_1_out3), .in(INT),
    .sel(\中断号 ));  // open: out0
  Pull_Resistor #(.pull(0)) pull_resistor_4 (.node(demultiplexer_1_out1));
  Pull_Resistor #(.pull(0)) pull_resistor_5 (.node(demultiplexer_1_out2));
  Pull_Resistor #(.pull(0)) pull_resistor_6 (.node(demultiplexer_1_out3));
  or or_5 (IR2_t, IR2, IRB);
  // Probe on PC
  not not_2 (not_2_out, halt);
  Register #(.width(32), .trigger("rising"), .Select("low")) u_PC (
    .D(N_PC), .en(not_2_out), .Q(PC), .clk(CLK), .clr(RST));
  and and_8 (and_8_out, ~INT, ~csrrci);  // AND_Gate
  or or_6 (or_6_out, INT, csrrci, csrrsi, URET, init);
  Register #(.width(32), .trigger("rising"), .Select("low")) EPC1 (
    .D(NPC), .en(demultiplexer_1_out1), .Q(EPC1_q), .clk(CLK));  // open: clr
  Register #(.width(32), .trigger("rising"), .Select("low")) EPC2 (
    .D(NPC), .en(demultiplexer_1_out2), .Q(EPC2_q), .clk(CLK));  // open: clr
  Register #(.width(32), .trigger("rising"), .Select("low")) EPC3 (
    .D(NPC), .en(demultiplexer_1_out3), .Q(EPC3_q), .clk(CLK));  // open: clr
  or or_7 (IR3_t, IR3, IRC);
  Adder #(.width(32)) adder_1 (.a(PC), .b(32'h4), .out(adder_1_out));  // open: cin, cout
  Register #(.width(1), .trigger("rising"), .Select("low")) u_IE (
    .D(and_8_out), .en(or_6_out), .Q(IE), .clk(CLK));  // open: clr
  Multiplexer #(.select(2), .width(32), .disabled("Z"), .enable("false")) multiplexer_4 (
    .in1(EPC1_q), .in2(EPC2_q), .in3(EPC3_q), .out(RET_PC), .sel(\当前中断号 ));  // open: in0
  // RiscV_Probe riscv_probe_1: pin names not known; wires that end beside it: IR
  ROM #(.addrWidth(10), .dataWidth(32), .Select("high")) rom_1 (.addr(PC[11:2]), .data(IR));
  Adder #(.width(32)) adder_2 (.a(PC), .b(shifter_1_out), .out(adder_2_out));  // open: cin, cout
  Adder #(.width(32)) adder_3 (.a(PC), .b(shifter_2_out), .out(adder_3_out));  // open: cin, cout
  \单周期硬布线控制器  \u_单周期硬布线控制器_1  (
    .Funct({IR[30], IR[25], IR[14:12]}), .OP(IR[6:2]), .ALU_OP(\单周期硬布线控制器_1_alu_op ),
    .MemToReg(\单周期硬布线控制器_1_memtoreg ), .MemWrite(MemWrite), .ALU_SRC(\单周期硬布线控制器_1_alu_src ),
    .RegWrite(RegWrite), .ecall(ecall), .S_type(\单周期硬布线控制器_1_s_type ), .Jalr(JALR), .Beq(\单周期硬布线控制器_1_beq ),
    .JAL(JAL), .Bne(\单周期硬布线控制器_1_bne ), .in_3(IR[21]), .uret(URET), .BGE(\单周期硬布线控制器_1_bge ), .LB(LB));
  Multiplexer #(.select(1), .width(5), .disabled("Z"), .enable("false")) multiplexer_5 (
    .in0(IR[19:15]), .in1(5'b10001), .out(multiplexer_5_out), .sel(ecall));
  Multiplexer #(.select(1), .width(5), .disabled("Z"), .enable("false")) multiplexer_6 (
    .in0(IR[24:20]), .in1(5'b01010), .out(multiplexer_6_out), .sel(ecall));
  assign bit_extender_1_out = {{4{IR[27]}}, IR[27:20]};  // Bit_Extender bit_extender_1
  Multiplexer #(.select(1), .width(12), .disabled("Z"), .enable("false")) multiplexer_7 (
    .in0(IR[31:20]), .in1(bit_extender_1_out), .out(multiplexer_7_out), .sel(LB));
  or or_8 (or_8_out, URET, INT);
  Counter #(.width(2), .max('h3), .ongoal("wrap"), .trigger("rising"), .behavior("new")) counter_2 (
    .count(or_8_out), .Q(counter_2_q), .clk(CLK), .down(URET));  // open: load, D, carry, clr, preset
  Demultiplexer #(.select(2), .width(1), .tristate("false"), .disabled("Z"), .enable("false")) demultiplexer_2 (
    .out0(demultiplexer_2_out0), .out1(demultiplexer_2_out1), .out2(demultiplexer_2_out2), .in(INT),
    .sel(counter_2_q));  // open: out3
  Pull_Resistor #(.pull(0)) pull_resistor_7 (.node(demultiplexer_2_out0));
  Pull_Resistor #(.pull(0)) pull_resistor_8 (.node(demultiplexer_2_out1));
  Pull_Resistor #(.pull(0)) pull_resistor_9 (.node(demultiplexer_2_out2));
  Multiplexer #(.select(1), .width(12), .disabled("Z"), .enable("false")) multiplexer_8 (
    .in0(multiplexer_7_out), .in1({IR[31:25], IR[11:7]}), .out(multiplexer_8_out), .sel(\单周期硬布线控制器_1_s_type ));
  Multiplexer #(.select(2), .width(32), .disabled("Z"), .enable("false")) multiplexer_9 (
    .in1(32'h30ac), .in2(32'h3158), .in3(32'h3204), .out(INT_Addar), .sel(\中断号 ));  // open: in0
  assign bit_extender_2_out = {{20{multiplexer_8_out[11]}}, multiplexer_8_out};  // Bit_Extender bit_extender_2
  assign bit_extender_3_out = {{20{IR[31]}}, {IR[31], IR[7], IR[30:25], IR[11:8]}};  // Bit_Extender bit_extender_3
  assign bit_extender_4_out = {{12{IR[31]}}, {IR[31], IR[19:12], IR[20], IR[30:21]}};  // Bit_Extender bit_extender_4
  Register #(.width(2), .trigger("rising"), .Select("low")) u_IR1 (
    .D(\中断号 ), .en(demultiplexer_2_out0), .Q(IR1_q), .clk(CLK));  // open: clr
  Register #(.width(2), .trigger("rising"), .Select("low")) u_IR2 (
    .D(\中断号 ), .en(demultiplexer_2_out1), .Q(IR2_q), .clk(CLK));  // open: clr
  Register #(.width(2), .trigger("rising"), .Select("low")) u_IR3 (
    .D(\中断号 ), .en(demultiplexer_2_out2), .Q(IR3_q), .clk(CLK));  // open: clr
  D_Flip_Flop #(.trigger("high"), .Pre_Clr_Positions("LEGACY"), .NegatePresetClear("false"), .enable("true"), .NewFFLayout("false")) d_ff_1 (.Q(d_ff_1_q));  // open: clk, D, Qn, preset, en, reset
  // Probe on 13'h3
  Regifile regifile_1 (
    .Din(RDin), .Clk(CLK), .R1(regifile_1_r1), .R2(MDin), .WE(RegWrite), .W_num(IR[11:7]),
    .R1_num(multiplexer_5_out), .R2_num(multiplexer_6_out));
  Shifter #(.width(32), .shift("ll")) shifter_1 (.in(bit_extender_3_out), .\dist (5'b00001), .out(shifter_1_out));
  Shifter #(.width(32), .shift("ll")) shifter_2 (.in(bit_extender_4_out), .\dist (5'b00001), .out(shifter_2_out));
  Comparator #(.width(13), .mode("twosComplement")) comparator_11 (
    .a(CNT_num), .b(13'h3), .eq(comparator_11_eq), .lt(comparator_11_lt));  // open: gt
  Clock #(.highDuration(1), .lowDuration(1)) clock_1 (.out(clock_1_out));
  // Probe on \单周期硬布线控制器_1_alu_op 
  Multiplexer #(.select(1), .width(32), .disabled("Z"), .enable("false")) multiplexer_10 (
    .in0(MDin), .in1(bit_extender_2_out), .out(multiplexer_10_out), .sel(\单周期硬布线控制器_1_alu_src ));
  Multiplexer #(.select(2), .width(2), .disabled("Z"), .enable("false")) multiplexer_11 (
    .in1(IR1_q), .in2(IR2_q), .in3(IR3_q), .out(\当前中断号 ), .sel(counter_2_q));  // open: in0
  Pull_Resistor #(.pull(0)) pull_resistor_10 (.node(\当前中断号 ));
  Counter #(.width(13), .max('h1fff), .ongoal("stay"), .trigger("rising"), .behavior("old")) counter_3 (
    .count(comparator_11_lt), .Q(CNT_num), .clk(clock_1_out));  // open: load, D, carry, clr, preset
  // Probe on aluresult
  ALU alu_1 (
    .X(regifile_1_r1), .Y(multiplexer_10_out), .AluOP(\单周期硬布线控制器_1_alu_op ), .Equal(equal),
    .Result(aluresult), .out_4(great));  // open: Result_2, out_6
  Multiplexer #(.select(1), .width(32), .disabled("Z"), .enable("false")) multiplexer_12 (
    .in0(multiplexer_13_out), .in1(adder_1_out), .out(RDin), .sel(or_9_out));
  Decoder #(.select(2), .tristate("false"), .disabled("Z"), .enable("false")) decoder_1 (
    .out1(decoder_1_out1), .out2(decoder_1_out2), .out3(decoder_1_out3), .sel(\当前中断号 ));  // open: out0
  Pull_Resistor #(.pull(0)) pull_resistor_11 (.node(decoder_1_out1));
  Pull_Resistor #(.pull(0)) pull_resistor_12 (.node(decoder_1_out2));
  Pull_Resistor #(.pull(0)) pull_resistor_13 (.node(decoder_1_out3));
  nand nand_1 (nand_1_out, d_ff_1_q, comparator_11_eq);
  Comparator #(.width(32), .mode("twosComplement")) comparator_12 (
    .a(regifile_1_r1), .b(32'h22), .eq(comparator_12_eq));  // open: gt, lt
  or or_9 (or_9_out, JAL, JALR);
  and and_9 (Clr1, URET, decoder_1_out1);
  and and_10 (Clr2, decoder_1_out2, URET);
  and and_11 (Clr3, decoder_1_out3, URET);
  assign CLK = nand_1_out ? clock_1_out : 1'bz;  // Controlled_Buffer controlled_buffer_1
  Pull_Resistor #(.pull(1)) pull_resistor_14 (.node(CLK));
  and and_12 (and_12_out, comparator_12_eq, ecall);
  not not_3 (not_3_out, comparator_12_eq);
  RAM #(.addrWidth(10), .dataWidth(32), .bus("separate"), .Select("high")) ram_1 (
    .addr(aluresult[11:2]), .din(MDin), .data(ram_1_data), .str(MemWrite), .clk(CLK), .ld(1'b1), .clr(RST));  // open: sel
  Register #(.width(32), .trigger("rising"), .Select("low")) register_1 (
    .D(MDin), .en(and_12_out), .Q(LedData), .clk(CLK));  // open: clr
  D_Flip_Flop #(.trigger("falling"), .Pre_Clr_Positions("ABOVE_BELOW"), .NegatePresetClear("false"), .enable("true"), .NewFFLayout("true")) d_ff_2 (
    .clk(CLK), .D(not_3_out), .Q(halt), .en(ecall), .reset(Go));  // open: Qn, preset
  Multiplexer #(.select(1), .width(32), .disabled("Z"), .enable("false")) multiplexer_13 (
    .in0(aluresult), .in1(ram_1_data), .out(multiplexer_13_out), .sel(\单周期硬布线控制器_1_memtoreg ));

  // Other names for the same wires on the sheet: func[4:0] = {IR[30], IR[25], IR[14:12]}; Funct3[2:0] = IR[14:12];
  //   op[4:0] = IR[6:2]; Opcode[4:0] = IR[6:2]

  // Notes on the sheet:
  //   中断源
  //   中断等待指示
  //   总复位信号应将除ROM以外所有存储组件全部清零
  //   单级中断测试信号模拟器
  //   生成开关中断信号
  //   中断控制逻辑
  //   数码管输出
  //   开中断
  //   关中断
  //   中断控制信号逻辑生成
  //   中断优先级比较
  //   数码管输出应该用寄存器锁存，否则显示数据只能一闪而过
  //   关中断
  //   开中断
  //   BranchAddress
  //   中断寄存器保护
  //   中断使能信号
  //   指令探针
  //   指令存储器
  //   contents of rom_1 (hex, n*v repeats v):
  //   7d000113 100413 1f41993 41f9d993 433 c00913 800b13 140413 f47413 800293 100313 499993 89e9b3 1300533
  //   2200893 73 406282b3 fe0294e3 140413 f00f93 1f47433 1c41413 800293 100313 49d993 89e9b3 1300533
  //   2200893 73 406282b3 fe0294e3 1c45413 406b0b33 b0463 f95ff06f 2b3 fff2c293 1029293 fff2e293 500533
  //   2200893 73 f5dff06f 1112023 410113 a12023 410113 812023 410113 1312023 410113 1412023 410113 1512023
  //   410113 1612023 410113 40e073 100b13 300a13 100a93 1600433 441413 14469b3 1300533 2200893 73 fe0416e3
  //   415a0a33 fe0a10e3 40f073 ffc10113 12b03 ffc10113 12a83 ffc10113 12a03 ffc10113 12983 ffc10113 12403
  //   ffc10113 12503 ffc10113 12883 200073 1112023 410113 a12023 410113 812023 410113 1312023 410113
  //   1412023 410113 1512023 410113 1612023 410113 40e073 200b13 300a13 100a93 1600433 441413 14469b3
  //   1300533 2200893 73 fe0416e3 415a0a33 fe0a10e3 40f073 ffc10113 12b03 ffc10113 12a83 ffc10113 12a03
  //   ffc10113 12983 ffc10113 12403 ffc10113 12503 ffc10113 12883 200073 1112023 410113 a12023 410113
  //   812023 410113 1312023 410113 1412023 410113 1512023 410113 1612023 410113 40e073 300b13 300a13
  //   100a93 1600433 441413 14469b3 1300533 2200893 73 fe0416e3 415a0a33 fe0a10e3 40f073 ffc10113 12b03
  //   ffc10113 12a83 ffc10113 12a03 ffc10113 12983 ffc10113 12403 ffc10113 12503 ffc10113 12883 200073
  //   指令字
  //   I型指令
  //   S型指令
  //   J型指令
  //   为方便自动评测，需要输出PC，IR，寄存器堆写如数据RDin
  //   JAL
  //   JALR
  //   URET
  //   B型指令
  //   RAM写使能MemWrite、RAM写入数据MDin等信号
  //   Beq
  //   Bne
  //   MemToReg
  //   MemWrite
  //   AluOP
  //   AluSrcB
  //   RegWrite
  //   中断地址输出逻辑
  //   中断比较逻辑
  //   控制位
  //   暂停节拍，不能为0
  //   戳工具置1进入计数暂停模式，ctrl+k时钟自动运行到对应节拍暂停
  //   ctrl+k关闭时钟连续运行，将控制位置零，进入单步调试模式调试
  //   中断清零信号产生
  //   可计数暂停的时钟源
  //   数据存储器
endmodule

module \流水线_多级中断  (
  output RegWrite,
  output MemWrite,
  output [31:0] IF_PC,
  output [31:0] ID_PC,
  output [31:0] EX_PC,
  output [31:0] M_PC,
  output [31:0] WB_PC,
  output [31:0] RDin,
  output [31:0] MDin,
  output [31:0] LedData
);

  wire _1_out, _2_out, _3_out, ALU_SRC, and_1_out, and_2_out, and_3_out, and_5_out, and_8_out, and_9_out,
       and_10_out, and_12_out, and_13_out, and_14_out, and_15_out, and_16_out, and_17_out, and_18_out,
       and_22_out, and_23_out, Beq, BGE, Bne, BranchTaken, CLK, clock_1_out, Clr1, Clr2, Clr3,
       comparator_1_eq, comparator_2_eq, comparator_3_eq, comparator_5_eq, comparator_5_lt, comparator_6_eq,
       comparator_7_eq, comparator_8_eq, comparator_9_eq, comparator_10_eq, comparator_11_eq,
       comparator_13_eq, comparator_14_eq, comparator_15_eq, comparator_16_eq, comparator_17_eq,
       comparator_18_eq, csrrci, csrrsi, d_ff_1_q, DataHazzard, decoder_1_out1, decoder_1_out2,
       decoder_1_out3, demultiplexer_1_out1, demultiplexer_1_out2, demultiplexer_1_out3,
       demultiplexer_2_out0, demultiplexer_2_out1, demultiplexer_2_out2, ecall, equal, ex_mem_1_ex_ecall,
       ex_mem_1_ex_jal, ex_mem_1_ex_jalr, ex_mem_1_ex_lb, ex_mem_1_ex_memtoreg, ex_mem_1_ex_uret,
       EX_MemToReg, EX_RegWrite, Go, great, halt, id_ex_1_ex_alusrcb, id_ex_1_ex_beq, id_ex_1_ex_bge,
       id_ex_1_ex_bne, id_ex_1_ex_ecall, id_ex_1_ex_jal, id_ex_1_ex_jalr, id_ex_1_ex_lb,
       id_ex_1_ex_memtoreg_2, id_ex_1_ex_uret, ID_MemToReg, ID_MemWrite, ID_RegWrite, IDt_MemToReg,
       IDt_RegWrite, IE, init, INT, IR1, IR2, IR3, JAL, JALR, LB, lb_t, LoadUse, MEM_RegWrite,
       mem_wb_1_ex_ecall, mem_wb_1_ex_jal, mem_wb_1_ex_jalr, mem_wb_1_ex_memtoreg, nand_1_out, not_1_out,
       not_2_out, not_3_out, not_4_out, not_5_out, not_6_out, not_7_out, not_8_out, not_9_out, or_1_out,
       or_4_out, or_6_out, or_7_out, or_10_out, or_11_out, or_12_out, RST, RsUsed, RtUsed, tALU_SRC, URET,
       W1, W2, W3, WB_lb, \中断信号 , \优先级高 , \单周期硬布线控制器_1_s_type , \无条件分支 , \有条件分支 ;
  wire [0:0] or_5_out;
  wire [1:0] counter_6_q, EX_R1_F, EX_R2_F, ID_R1_F, ID_R2_F, IR1_q, IR2_q, IR3_q, priority_encoder_1_out,
       \中断号 , \当前中断号 ;
  wire [2:0] Funct3;
  wire [3:0] ALU_OP, id_ex_1_ex_aluop;
  wire [4:0] func, rs, rt;
  wire [7:0] multiplexer_18_out;
  wire [11:0] bit_extender_3_out, multiplexer_7_out, multiplexer_8_out;
  wire [12:0] CNT_num;
  wire [15:0] \LoadUse次数 , \总周期数 , \插入气泡数 , \无条件分支数 , \有条件分支数 , \条件分支成功数 ;
  wire [31:0] adder_1_out, adder_2_out, adder_3_out, aluresult, bit_extender_1_out, bit_extender_2_out,
       bit_extender_4_out, EPC1_q, EPC2_q, EPC3_q, EX_IMM, EX_IR, ex_mem_1_mem_r1, ex_mem_1_mem_r2, EX_NRS,
       EX_NRT, EX_RS, EX_RT, ID_IR, IF_IR, INT_Addar, LBR, MEM_AluData, MEM_IR, mem_wb_1_wb_r1,
       mem_wb_1_wb_r2, multiplexer_2_out, multiplexer_9_out, multiplexer_12_out, multiplexer_16_out,
       multiplexer_17_out, N_PC, NPC, ram_1_data, regifile_down_1_r1, regifile_down_1_r2, RET_PC,
       shifter_1_out, shifter_2_out, WB_alu, WB_Dre, WB_IR;

  Button \u_总复位  (.out(RST));
  Button _1 (.out(_1_out));
  Button _2 (.out(_2_out));
  Button _3 (.out(_3_out));
  // Probe on \总周期数 
  // Probe on \总周期数 
  Button \u_继续运行  (.out(Go));
  LED #(.active("true")) led_1 (.in(W1));
  LED #(.active("true")) led_2 (.in(W2));
  LED #(.active("true")) led_3 (.in(W3));
  // Probe on adder_2_out
  and and_1 (and_1_out, not_2_out, not_1_out);
  not not_1 (not_1_out, halt);
  not not_2 (not_2_out, LoadUse);
  Hex_Digit_Display hex_digit_display_1 (.value(LedData[31:28]));  // open: dp
  // Probe on IF_PC[19:0]
  // RiscV_Probe riscv_probe_1: pin names not known; wires that end beside it: _1_out, _2_out, _3_out, IR1, IR2, IR3, {IF_IR[31:15], Funct3, IF_IR[11:0]}
  Priority_Encoder #(.select(2), .disabled("Z")) priority_encoder_1 (
    .in0(1'b1), .in1(id_ex_1_ex_jalr), .in2(id_ex_1_ex_jal), .in3(\无条件分支 ), .out(priority_encoder_1_out));  // open: gs, en_out, en_in
  Multiplexer #(.select(2), .width(32), .disabled("Z"), .enable("false")) multiplexer_1 (
    .in0(adder_1_out), .in1(aluresult), .in2(adder_2_out), .in3(adder_2_out), .out(NPC),
    .sel(priority_encoder_1_out));
  and and_2 (and_2_out, ~halt, CLK);  // AND_Gate
  Hex_Digit_Display hex_digit_display_2 (.value(LedData[23:20]));  // open: dp
  Hex_Digit_Display hex_digit_display_3 (.value(LedData[27:24]));  // open: dp
  // Probe on ID_PC[19:0]
  // RiscV_Probe riscv_probe_2: pin names not known; wires that end beside it: {ID_IR[31], func[4], ID_IR[29:26], func[3], ID_IR[24:15], func[2:0], ID_IR[11:0]}
  Counter #(.width(16), .max('hffff), .ongoal("wrap"), .trigger("rising"), .behavior("new")) counter_1 (
    .Q(\总周期数 ), .clk(and_2_out));  // open: load, D, count, carry, clr, preset, down
  Hex_Digit_Display hex_digit_display_4 (.value(LedData[19:16]));  // open: dp
  Hex_Digit_Display hex_digit_display_5 (.value(LedData[15:12]));  // open: dp
  // Probe on IF_PC
  Register #(.width(32), .trigger("rising"), .Select("low")) PC (
    .D(N_PC), .en(and_1_out), .Q(IF_PC), .clk(CLK), .clr(RST));
  Counter #(.width(16), .max('hffff), .ongoal("wrap"), .trigger("rising"), .behavior("new")) counter_2 (
    .Q(\有条件分支数 ), .clk(and_3_out));  // open: load, D, count, carry, clr, preset, down
  and and_3 (and_3_out, \有条件分支 , CLK);
  Multiplexer #(.select(1), .width(32), .disabled("Z"), .enable("false")) multiplexer_2 (
    .in0(NPC), .in1(RET_PC), .out(multiplexer_2_out), .sel(URET));
  Comparator #(.width(5), .mode("unsigned")) comparator_1 (
    .a(IF_IR[6:2]), .b(5'b11100), .eq(comparator_1_eq));  // open: gt, lt
  Comparator #(.width(3), .mode("unsigned")) comparator_2 (
    .a(3'b110), .b(Funct3), .eq(comparator_2_eq));  // open: gt, lt
  Comparator #(.width(3), .mode("unsigned")) comparator_3 (
    .a(Funct3), .b(3'b111), .eq(comparator_3_eq));  // open: gt, lt
  and and_4 (INT, \中断信号 , \优先级高 , IE);
  Hex_Digit_Display hex_digit_display_6 (.value(LedData[7:4]));  // open: dp
  Hex_Digit_Display hex_digit_display_7 (.value(LedData[11:8]));  // open: dp
  // Probe on EX_PC[19:0]
  // RiscV_Probe riscv_probe_3: pin names not known; wires that end beside it: EX_IR
  not not_3 (not_3_out, LoadUse);
  and and_5 (and_5_out, not_3_out, not_4_out);
  not not_4 (not_4_out, halt);
  // Probe on EX_IMM
  Multiplexer #(.select(1), .width(32), .disabled("Z"), .enable("false")) multiplexer_3 (
    .in0(multiplexer_2_out), .in1(INT_Addar), .out(N_PC), .sel(INT));
  and and_6 (csrrsi, comparator_1_eq, comparator_2_eq);
  and and_7 (csrrci, comparator_1_eq, comparator_3_eq);
  \中断控制器  \u_中断控制器_1  (
    .IRA(IR1), .W1(W1), .Clr1(Clr1), .IRB(IR2), .W2(W2), .Clr2(Clr2), .IRC(IR3), .W3(W3), .Clr3(Clr3),
    .\中断号 (\中断号 ), .\中断请求 (\中断信号 ), .CLK(CLK), .RST(RST));
  Comparator #(.width(2), .mode("unsigned")) comparator_4 (.a(\中断号 ), .b(\当前中断号 ), .gt(\优先级高 ));  // open: eq, lt
  Hex_Digit_Display hex_digit_display_8 (.value(LedData[3:0]));  // open: dp
  Adder #(.width(32)) adder_1 (.a(IF_PC), .b(32'h4), .out(adder_1_out));  // open: cin, cout
  Adder #(.width(32)) adder_2 (.a(EX_IMM), .b(EX_PC), .out(adder_2_out));  // open: cin, cout
  and and_8 (and_8_out, \无条件分支 , CLK);
  // Probe on \总周期数 
  // Probe on M_PC[19:0]
  // RiscV_Probe riscv_probe_4: pin names not known; wires that end beside it: MEM_IR
  ROM #(.addrWidth(10), .dataWidth(32), .Select("high")) rom_1 (
    .addr(IF_PC[11:2]), .data({IF_IR[31:15], Funct3, IF_IR[11:0]}));
  Counter #(.width(16), .max('hffff), .ongoal("wrap"), .trigger("rising"), .behavior("new")) counter_3 (
    .Q(\无条件分支数 ), .clk(and_8_out));  // open: load, D, count, carry, clr, preset, down
  // Probe on \总周期数 
  // Probe on \无条件分支数 
  // Probe on \条件分支成功数 
  // Probe on \插入气泡数 
  // Probe on \LoadUse次数 
  or or_1 (or_1_out, BranchTaken, RST);
  IF_ID if_id_1 (
    .CLK(CLK), .\使能端 (and_5_out), .\清零端 (or_1_out), .IF_IR({IF_IR[31:15], Funct3, IF_IR[11:0]}),
    .IF_PC(IF_PC), .ID_IR({ID_IR[31], func[4], ID_IR[29:26], func[3], ID_IR[24:15], func[2:0], ID_IR[11:0]}),
    .ID_PC(ID_PC));  // open: PD, PD_2
  and and_9 (and_9_out, BranchTaken, CLK);
  // Probe on \中断号 
  // Probe on IF_PC[11:0]
  // Probe on WB_PC[19:0]
  // RiscV_Probe riscv_probe_5: pin names not known; wires that end beside it: WB_IR
  not not_5 (not_5_out, halt);
  Counter #(.width(16), .max('hffff), .ongoal("wrap"), .trigger("rising"), .behavior("new")) counter_4 (
    .Q(\条件分支成功数 ), .clk(and_9_out));  // open: load, D, count, carry, clr, preset, down
  // Probe on EX_PC[11:0]
  // Probe on ID_PC[11:0]
  // Probe on M_PC[11:0]
  D_Flip_Flop #(.trigger("high"), .Pre_Clr_Positions("LEGACY"), .NegatePresetClear("false"), .enable("true"), .NewFFLayout("false")) d_ff_1 (.Q(d_ff_1_q));  // open: clk, D, Qn, preset, en, reset
  // Probe on 13'h340
  assign bit_extender_1_out = {{20{ID_IR[31]}}, {ID_IR[31], ID_IR[7], func[4], ID_IR[29:26], func[3], ID_IR[11:8]}};  // Bit_Extender bit_extender_1
  assign bit_extender_2_out = {{12{ID_IR[31]}}, {ID_IR[31], ID_IR[19:15], func[2:0], ID_IR[20], func[4], ID_IR[29:26], func[3], ID_IR[24:21]}};  // Bit_Extender bit_extender_2
  // Probe on {ID_IR[31], func[4], ID_IR[29:26], func[3], ID_IR[24:20]}
  // Probe on WB_PC[11:0]
  Comparator #(.width(13), .mode("twosComplement")) comparator_5 (
    .a(CNT_num), .b(13'h340), .eq(comparator_5_eq), .lt(comparator_5_lt));  // open: gt
  Clock #(.highDuration(1), .lowDuration(1)) clock_1 (.out(clock_1_out));
  or or_2 (\有条件分支 , id_ex_1_ex_jal, id_ex_1_ex_jalr);
  assign bit_extender_3_out = {{4{ID_IR[27]}}, {ID_IR[27:26], func[3], ID_IR[24:20]}};  // Bit_Extender bit_extender_3
  nand nand_1 (nand_1_out, d_ff_1_q, comparator_5_eq);
  Counter #(.width(13), .max('h1fff), .ongoal("stay"), .trigger("rising"), .behavior("old")) counter_5 (
    .count(comparator_5_lt), .Q(CNT_num), .clk(clock_1_out));  // open: load, D, carry, clr, preset
  \单周期硬布线控制器  \u_单周期硬布线控制器_1  (
    .Funct(func), .OP(ID_IR[6:2]), .ALU_OP(ALU_OP), .MemToReg(IDt_MemToReg), .MemWrite(ID_MemWrite),
    .ALU_SRC(tALU_SRC), .RegWrite(IDt_RegWrite), .ecall(ecall), .S_type(\单周期硬布线控制器_1_s_type ), .Jalr(JALR),
    .Beq(Beq), .JAL(JAL), .Bne(Bne), .in_3(ID_IR[21]), .uret(URET), .BGE(BGE), .LB(LB));
  Multiplexer #(.select(1), .width(5), .disabled("Z"), .enable("false")) multiplexer_4 (
    .in0(ID_IR[19:15]), .in1(5'b10001), .out(rs), .sel(ecall));
  Multiplexer #(.select(1), .width(5), .disabled("Z"), .enable("false")) multiplexer_5 (
    .in0(ID_IR[24:20]), .in1(5'b01010), .out(rt), .sel(ecall));
  Shifter #(.width(32), .shift("ll")) shifter_1 (.in(bit_extender_1_out), .\dist (5'b00001), .out(shifter_1_out));
  Shifter #(.width(32), .shift("ll")) shifter_2 (.in(bit_extender_2_out), .\dist (5'b00001), .out(shifter_2_out));
  not not_6 (not_6_out, ID_IR[0]);
  and and_10 (and_10_out, LB, not_6_out);
  Multiplexer #(.select(1), .width(3), .disabled("Z"), .enable("false")) multiplexer_6 (
    .in0({IDt_RegWrite, tALU_SRC, IDt_MemToReg}), .in1(3'b000), .out({ID_RegWrite, ALU_SRC, ID_MemToReg}),
    .sel(and_10_out));
  and and_11 (lb_t, LB, ID_IR[0]);
  assign CLK = nand_1_out ? clock_1_out : 1'bz;  // Controlled_Buffer controlled_buffer_1
  or or_3 (BranchTaken, id_ex_1_ex_jalr, id_ex_1_ex_jal, \无条件分支 );
  Multiplexer #(.select(1), .width(12), .disabled("Z"), .enable("false")) multiplexer_7 (
    .in0({ID_IR[31], func[4], ID_IR[29:26], func[3], ID_IR[24:20]}), .in1(bit_extender_3_out),
    .out(multiplexer_7_out), .sel(lb_t));
  Multiplexer #(.select(1), .width(12), .disabled("Z"), .enable("false")) multiplexer_8 (
    .in0(multiplexer_7_out), .in1({ID_IR[31], func[4], ID_IR[29:26], func[3], ID_IR[11:7]}),
    .out(multiplexer_8_out), .sel(\单周期硬布线控制器_1_s_type ));
  Demultiplexer #(.select(2), .width(1), .tristate("false"), .disabled("Z"), .enable("false")) demultiplexer_1 (
    .out1(demultiplexer_1_out1), .out2(demultiplexer_1_out2), .out3(demultiplexer_1_out3), .in(INT),
    .sel(\中断号 ));  // open: out0
  Pull_Resistor #(.pull(0)) pull_resistor_1 (.node(demultiplexer_1_out1));
  Pull_Resistor #(.pull(0)) pull_resistor_2 (.node(demultiplexer_1_out2));
  Pull_Resistor #(.pull(0)) pull_resistor_3 (.node(demultiplexer_1_out3));
  Pull_Resistor #(.pull(1)) pull_resistor_4 (.node(CLK));
  // Probe on {ID_IR[31], ID_IR[19:15], func[2:0], ID_IR[20], func[4], ID_IR[29:26], func[3], ID_IR[24:21]}
  and and_12 (and_12_out, ~INT, ~csrrci);  // AND_Gate
  or or_4 (or_4_out, INT, csrrci, csrrsi, URET, init);
  or or_5 (or_5_out[0], Beq, Bne, BGE);
  assign bit_extender_4_out = {{20{multiplexer_8_out[11]}}, multiplexer_8_out};  // Bit_Extender bit_extender_4
  // Probe on bit_extender_4_out
  \used控制电路  \used控制电路_1  (
    .OP2(ID_IR[2]), .OP3(ID_IR[3]), .OP4(ID_IR[4]), .OP5(ID_IR[5]), .OP6(ID_IR[6]), .F12(func[0]),
    .F13(func[1]), .F14(func[2]), .F25(func[3]), .F30(func[4]), .RsUsed(RsUsed), .RtUesd(RtUsed));
  Register #(.width(1), .trigger("rising"), .Select("low")) u_IE (
    .D(and_12_out), .en(or_4_out), .Q(IE), .clk(CLK));  // open: clr
  Register #(.width(32), .trigger("rising"), .Select("low")) EPC1 (
    .D(NPC), .en(demultiplexer_1_out1), .Q(EPC1_q), .clk(CLK));  // open: clr
  Register #(.width(32), .trigger("rising"), .Select("low")) EPC2 (
    .D(NPC), .en(demultiplexer_1_out2), .Q(EPC2_q), .clk(CLK));  // open: clr
  Register #(.width(32), .trigger("rising"), .Select("low")) EPC3 (
    .D(NPC), .en(demultiplexer_1_out3), .Q(EPC3_q), .clk(CLK));  // open: clr
  Multiplexer #(.select(2), .width(32), .disabled("Z"), .enable("false")) multiplexer_9 (
    .in0(bit_extender_4_out), .in1(shifter_1_out), .in2(shifter_2_out), .out(multiplexer_9_out),
    .sel({JAL, or_5_out[0]}));  // open: in3
  Multiplexer #(.select(2), .width(32), .disabled("Z"), .enable("false")) multiplexer_10 (
    .in1(EPC1_q), .in2(EPC2_q), .in3(EPC3_q), .out(RET_PC), .sel(\当前中断号 ));  // open: in0
  Regifile_down regifile_down_1 (
    .Din(RDin), .Clk(CLK), .R1(regifile_down_1_r1), .R2(regifile_down_1_r2), .WE(RegWrite),
    .W_num(WB_IR[11:7]), .R1_num(rs), .R2_num(rt));
  Comparator #(.width(5), .mode("twosComplement")) comparator_6 (
    .a(rs), .b(EX_IR[11:7]), .eq(comparator_6_eq));  // open: gt, lt
  Comparator #(.width(5), .mode("twosComplement")) comparator_7 (
    .a(rs), .b(MEM_IR[11:7]), .eq(comparator_7_eq));  // open: gt, lt
  Comparator #(.width(5), .mode("twosComplement")) comparator_8 (
    .a(rt), .b(EX_IR[11:7]), .eq(comparator_8_eq));  // open: gt, lt
  Comparator #(.width(5), .mode("twosComplement")) comparator_9 (
    .a(rt), .b(MEM_IR[11:7]), .eq(comparator_9_eq));  // open: gt, lt
  or or_6 (or_6_out, BranchTaken, RST, LoadUse);
  ID_EX id_ex_1 (
    .CLK(CLK), .\使能端 (not_5_out), .\清零端 (or_6_out),
    .ID_IR({ID_IR[31], func[4], ID_IR[29:26], func[3], ID_IR[24:15], func[2:0], ID_IR[11:0]}), .EX_IR(EX_IR),
    .ID_PC(ID_PC), .EX_PC(EX_PC), .ID_R1(regifile_down_1_r1), .EX_R1(EX_RS), .ID_R2(regifile_down_1_r2),
    .EX_R2(EX_RT), .ID_MemToReg(ID_MemToReg), .EX_MemToReg(EX_MemToReg), .ID_MemWrite(ID_MemWrite),
    .EX_MemToReg_2(id_ex_1_ex_memtoreg_2), .ID_AluOP(ALU_OP), .EX_AluOP(id_ex_1_ex_aluop),
    .ID_AluSrcB(ALU_SRC), .EX_AluSrcB(id_ex_1_ex_alusrcb), .ID_RegWrite(ID_RegWrite),
    .EX_RegWrite(EX_RegWrite), .ID_ecall(ecall), .EX_ecall(id_ex_1_ex_ecall), .ID_JAL(JAL),
    .EX_JAL(id_ex_1_ex_jal), .ID_JALR(JALR), .EX_JALR(id_ex_1_ex_jalr), .ID_Beq(Beq),
    .EX_Beq(id_ex_1_ex_beq), .ID_Bne(Bne), .EX_Bne(id_ex_1_ex_bne), .ID_URET(URET),
    .EX_URET(id_ex_1_ex_uret), .ID_BGE(BGE), .EX_BGE(id_ex_1_ex_bge), .ID_IMM(multiplexer_9_out),
    .EX_IMM(EX_IMM), .ID_R1_F(ID_R1_F), .EX_R1_F(EX_R1_F), .ID_R2_F(ID_R2_F), .EX_R2_F(EX_R2_F),
    .ID_LB(lb_t), .EX_LB(id_ex_1_ex_lb));  // open: PD, PD_2
  Comparator #(.width(5), .mode("twosComplement")) comparator_10 (
    .a(rs), .b({5{1'b0}}), .eq(comparator_10_eq));  // open: gt, lt
  not not_7 (not_7_out, comparator_10_eq);
  not not_8 (not_8_out, comparator_11_eq);
  Comparator #(.width(5), .mode("twosComplement")) comparator_11 (
    .a(rt), .b({5{1'b0}}), .eq(comparator_11_eq));  // open: gt, lt
  Multiplexer #(.select(2), .width(32), .disabled("Z"), .enable("false")) multiplexer_11 (
    .in1(32'h30ac), .in2(32'h3158), .in3(32'h3204), .out(INT_Addar), .sel(\中断号 ));  // open: in0
  or or_7 (or_7_out, URET, INT);
  Counter #(.width(2), .max('h3), .ongoal("wrap"), .trigger("rising"), .behavior("new")) counter_6 (
    .count(or_7_out), .Q(counter_6_q), .clk(CLK), .down(URET));  // open: load, D, carry, clr, preset
  Demultiplexer #(.select(2), .width(1), .tristate("false"), .disabled("Z"), .enable("false")) demultiplexer_2 (
    .out0(demultiplexer_2_out0), .out1(demultiplexer_2_out1), .out2(demultiplexer_2_out2), .in(INT),
    .sel(counter_6_q));  // open: out3
  Pull_Resistor #(.pull(0)) pull_resistor_5 (.node(demultiplexer_2_out0));
  Pull_Resistor #(.pull(0)) pull_resistor_6 (.node(demultiplexer_2_out1));
  Pull_Resistor #(.pull(0)) pull_resistor_7 (.node(demultiplexer_2_out2));
  and and_13 (and_13_out, RsUsed, EX_RegWrite, not_7_out, comparator_6_eq);
  and and_14 (and_14_out, RsUsed, MEM_RegWrite, not_7_out, comparator_7_eq);
  and and_15 (and_15_out, RtUsed, EX_RegWrite, not_8_out, comparator_8_eq);
  and and_16 (and_16_out, RtUsed, MEM_RegWrite, not_8_out, comparator_9_eq);
  Register #(.width(2), .trigger("rising"), .Select("low")) u_IR1 (
    .D(\中断号 ), .en(demultiplexer_2_out0), .Q(IR1_q), .clk(CLK));  // open: clr
  Register #(.width(2), .trigger("rising"), .Select("low")) u_IR2 (
    .D(\中断号 ), .en(demultiplexer_2_out1), .Q(IR2_q), .clk(CLK));  // open: clr
  Register #(.width(2), .trigger("rising"), .Select("low")) u_IR3 (
    .D(\中断号 ), .en(demultiplexer_2_out2), .Q(IR3_q), .clk(CLK));  // open: clr
  Multiplexer #(.select(1), .width(32), .disabled("Z"), .enable("false")) multiplexer_12 (
    .in0(EX_NRT), .in1(EX_IMM), .out(multiplexer_12_out), .sel(id_ex_1_ex_alusrcb));
  Multiplexer #(.select(2), .width(2), .disabled("Z"), .enable("false")) multiplexer_13 (
    .in1(IR1_q), .in2(IR2_q), .in3(IR3_q), .out(\当前中断号 ), .sel(counter_6_q));  // open: in0
  and and_17 (and_17_out, id_ex_1_ex_beq, equal);
  or or_8 (DataHazzard, and_13_out, and_14_out, and_15_out, and_16_out);
  Decoder #(.select(2), .tristate("false"), .disabled("Z"), .enable("false")) decoder_1 (
    .out1(decoder_1_out1), .out2(decoder_1_out2), .out3(decoder_1_out3), .sel(\当前中断号 ));  // open: out0
  Pull_Resistor #(.pull(0)) pull_resistor_8 (.node(decoder_1_out1));
  Pull_Resistor #(.pull(0)) pull_resistor_9 (.node(decoder_1_out2));
  Pull_Resistor #(.pull(0)) pull_resistor_10 (.node(decoder_1_out3));
  Pull_Resistor #(.pull(0)) pull_resistor_11 (.node(\当前中断号 ));
  or or_9 (\无条件分支 , and_17_out, and_18_out, and_22_out);
  and and_18 (and_18_out, ~equal, id_ex_1_ex_bne);  // AND_Gate
  ALU alu_1 (
    .X(EX_NRS), .Y(multiplexer_12_out), .AluOP(id_ex_1_ex_aluop), .Equal(equal), .Result(aluresult),
    .out_4(great));  // open: Result_2, out_6
  \封装正确性测试  \u_封装正确性测试_1  ();
  and and_19 (Clr1, URET, decoder_1_out1);
  and and_20 (Clr2, decoder_1_out2, URET);
  and and_21 (Clr3, decoder_1_out3, URET);
  and and_22 (and_22_out, great, id_ex_1_ex_bge);
  // Probe on EX_NRS
  // Probe on RDin
  EX_MEM ex_mem_1 (
    .CLK(CLK), .\使能端 (not_5_out), .\清零端 (RST), .EX_IR(EX_IR), .EX_PC(EX_PC), .EX_R1(EX_NRS),
    .ID_RegWrite(EX_RegWrite), .EX_R2(EX_NRT), .EX_ALU(aluresult), .ID_ecall(id_ex_1_ex_ecall),
    .EX_DATA(EX_NRT), .ID_URET(id_ex_1_ex_uret), .MEM_IR(MEM_IR), .MEM_PC(M_PC), .MEM_R1(ex_mem_1_mem_r1),
    .EX_RegWrite(MEM_RegWrite), .MEM_R2(ex_mem_1_mem_r2), .MEM_ALU(MEM_AluData),
    .EX_ecall(ex_mem_1_ex_ecall), .MEM_DATA(MDin), .EX_URET(ex_mem_1_ex_uret), .ID_MemToReg(EX_MemToReg),
    .EX_MemToReg(ex_mem_1_ex_memtoreg), .ID_MemWrite(id_ex_1_ex_memtoreg_2), .EX_MemWrite(MemWrite),
    .ID_JAL(id_ex_1_ex_jal), .EX_JAL(ex_mem_1_ex_jal), .ID_JALR(id_ex_1_ex_jalr), .EX_JALR(ex_mem_1_ex_jalr),
    .ID_LB(id_ex_1_ex_lb), .EX_LB(ex_mem_1_ex_lb));
  \used控制电路  \used控制电路_2  (
    .OP2(ID_IR[2]), .OP3(ID_IR[3]), .OP4(ID_IR[4]), .OP5(ID_IR[5]), .OP6(ID_IR[6]), .F12(func[0]),
    .F13(func[1]), .F14(func[2]), .F25(func[3]), .F30(func[4]), .RsUsed(RsUsed), .RtUesd(RtUsed));
  Comparator #(.width(16), .mode("twosComplement")) comparator_12 (
    .a({16{1'b0}}), .b(\总周期数 ), .eq(init));  // open: gt, lt
  Comparator #(.width(16), .mode("twosComplement")) comparator_13 (
    .a(16'h241), .b(\总周期数 ), .eq(comparator_13_eq));  // open: gt, lt
  or or_10 (or_10_out, comparator_17_eq, comparator_14_eq);
  Comparator #(.width(16), .mode("twosComplement")) comparator_14 (
    .a(\总周期数 ), .b(16'h1), .eq(comparator_14_eq));  // open: gt, lt
  Comparator #(.width(16), .mode("twosComplement")) comparator_15 (
    .a(\总周期数 ), .b(16'h2), .eq(comparator_15_eq));  // open: gt, lt
  Comparator #(.width(16), .mode("twosComplement")) comparator_16 (
    .a(\总周期数 ), .b(16'h3), .eq(comparator_16_eq));  // open: gt, lt
  or or_11 (or_11_out, comparator_16_eq, comparator_13_eq);
  \LoadUse信号生成  \loaduse信号生成_1  (
    .R1Used(RsUsed), .EX_MemToReg(EX_MemToReg), .ID_R1(rs), .EX_RD(EX_IR[11:7]), .ID_R2(rt), .R2Used(RtUsed),
    .LoadUse(LoadUse));
  Multiplexer #(.select(2), .width(32), .disabled("Z"), .enable("false")) multiplexer_14 (
    .in0(EX_RS), .in1(RDin), .in2(MEM_AluData), .out(EX_NRS), .sel(EX_R1_F));  // open: in3
  Multiplexer #(.select(2), .width(32), .disabled("Z"), .enable("false")) multiplexer_15 (
    .in0(EX_RT), .in1(RDin), .in2(MEM_AluData), .out(EX_NRT), .sel(EX_R2_F));  // open: in3
  Comparator #(.width(16), .mode("twosComplement")) comparator_17 (
    .a(\总周期数 ), .b(16'h2fd), .eq(comparator_17_eq));  // open: gt, lt
  Pull_Resistor #(.pull(0)) pull_resistor_12 (.node(IR1));
  assign IR1 = or_10_out ? ~CLK : 1'bz;  // Controlled_Inverter controlled_inverter_1
  Pull_Resistor #(.pull(0)) pull_resistor_13 (.node(IR2));
  assign IR2 = comparator_15_eq ? ~CLK : 1'bz;  // Controlled_Inverter controlled_inverter_2
  Pull_Resistor #(.pull(0)) pull_resistor_14 (.node(IR3));
  assign IR3 = or_11_out ? ~CLK : 1'bz;  // Controlled_Inverter controlled_inverter_3
  // Probe on ram_1_data
  RAM #(.addrWidth(10), .dataWidth(32), .bus("separate"), .Select("high")) ram_1 (
    .addr(MEM_AluData[11:2]), .din(MDin), .data(ram_1_data), .str(MemWrite), .clk(CLK), .ld(1'b1));  // open: sel, clr
  // Probe on MEM_AluData
  \R1_F_R2_F信号生成  \r1_f_r2_f信号生成_1  (
    .R1Used(RsUsed), .ID_R1(rs), .EX_RegWrite(EX_RegWrite), .EX_RD(EX_IR[11:7]), .MEM_RegWrite(MEM_RegWrite),
    .MEM_RD(MEM_IR[11:7]), .R2Used(RtUsed), .ID_R2(rt), .R1_F(ID_R1_F), .R2_F(ID_R2_F));
  MEM_WB mem_wb_1 (
    .CLK(CLK), .\使能端 (not_5_out), .\清零端 (RST), .MEM_IR(MEM_IR), .ID_MemToReg(ex_mem_1_ex_memtoreg),
    .ID_RegWrite(MEM_RegWrite), .MEM_PC(M_PC), .ID_ecall(ex_mem_1_ex_ecall), .MEM_R1(ex_mem_1_mem_r1),
    .ID_URET(ex_mem_1_ex_uret), .MEM_R2(ex_mem_1_mem_r2), .WB_IR(WB_IR), .EX_MemToReg(mem_wb_1_ex_memtoreg),
    .EX_RegWrite(RegWrite), .WB_PC(WB_PC), .EX_ecall(mem_wb_1_ex_ecall), .WB_R1(mem_wb_1_wb_r1),
    .WB_R2(mem_wb_1_wb_r2), .MEM_DIN(ram_1_data), .WB_DIN(WB_Dre), .MEM_ALU(MEM_AluData), .WB_ALU(WB_alu),
    .ID_JAL(ex_mem_1_ex_jal), .EX_JAL(mem_wb_1_ex_jal), .ID_JALR(ex_mem_1_ex_jalr),
    .EX_JALR(mem_wb_1_ex_jalr), .ID_LB(ex_mem_1_ex_lb), .EX_LB(WB_lb));  // open: EX_URET
  // Probe on WB_alu
  Multiplexer #(.select(1), .width(32), .disabled("Z"), .enable("false")) multiplexer_16 (
    .in0(WB_alu), .in1(WB_Dre), .out(multiplexer_16_out), .sel(mem_wb_1_ex_memtoreg));
  Adder #(.width(32)) adder_3 (.a(WB_PC), .b(32'h4), .out(adder_3_out));  // open: cin, cout
  Comparator #(.width(32), .mode("twosComplement")) comparator_18 (
    .a(mem_wb_1_wb_r1), .b(32'h22), .eq(comparator_18_eq));  // open: gt, lt
  Multiplexer #(.select(1), .width(32), .disabled("Z"), .enable("false")) multiplexer_17 (
    .in0(multiplexer_16_out), .in1(LBR), .out(multiplexer_17_out), .sel(WB_lb));
  Register #(.width(32), .trigger("rising"), .Select("low")) register_1 (
    .D(mem_wb_1_wb_r2), .en(and_23_out), .Q(LedData), .clk(CLK));  // open: clr
  and and_23 (and_23_out, comparator_18_eq, mem_wb_1_ex_ecall);
  not not_9 (not_9_out, comparator_18_eq);
  Multiplexer #(.select(2), .width(8), .disabled("Z"), .enable("false")) multiplexer_18 (
    .in0(WB_Dre[7:0]), .in1(WB_Dre[15:8]), .in2(WB_Dre[23:16]), .in3(WB_Dre[31:24]),
    .out(multiplexer_18_out), .sel(WB_alu[1:0]));
  Multiplexer #(.select(1), .width(32), .disabled("Z"), .enable("false")) multiplexer_19 (
    .in0(multiplexer_17_out), .in1(adder_3_out), .out(RDin), .sel(or_12_out));
  or or_12 (or_12_out, mem_wb_1_ex_jal, mem_wb_1_ex_jalr);
  D_Flip_Flop #(.trigger("falling"), .Pre_Clr_Positions("ABOVE_BELOW"), .NegatePresetClear("false"), .enable("true"), .NewFFLayout("true")) d_ff_2 (
    .clk(CLK), .D(not_9_out), .Q(halt), .en(mem_wb_1_ex_ecall), .reset(Go));  // open: Qn, preset
  assign LBR = {{24{multiplexer_18_out[7]}}, multiplexer_18_out};  // Bit_Extender bit_extender_5

  // Other names for the same wires on the sheet: ID_IR (some bits) = func; EX_WriteReg_num[4:0] = EX_IR[11:7];
  //   op[4:0] = ID_IR[6:2]; Opcode[4:0] = IF_IR[6:2]; IF_IR[14:12] = Funct3; MEM_WriteReg_num[4:0] = MEM_IR[11:7];
  //   MEM_PC[31:0] = M_PC

  // Notes on the sheet:
  //   中断源
  //   时空图监测，可删除
  //   中断等待指示
  //   数码管输出
  //   生成开关中断信号
  //   中断控制逻辑
  //   中断控制信号逻辑生成
  //   中断优先级比较
  //   开中断
  //   关中断
  //   contents of rom_1 (hex, n*v repeats v):
  //   7d000113 100413 1f41993 41f9d993 433 c00913 800b13 140413 f47413 800293 100313 499993 89e9b3 1300533
  //   2200893 73 406282b3 fe0294e3 140413 f00f93 1f47433 1c41413 800293 100313 49d993 89e9b3 1300533
  //   2200893 73 406282b3 fe0294e3 1c45413 406b0b33 b0463 f95ff06f 2b3 fff2c293 1029293 fff2e293 500533
  //   2200893 73 f5dff06f 1112023 410113 a12023 410113 812023 410113 1312023 410113 1412023 410113 1512023
  //   410113 1612023 410113 40e073 100b13 300a13 100a93 1600433 441413 14469b3 1300533 2200893 73 fe0416e3
  //   415a0a33 fe0a10e3 40f073 ffc10113 12b03 ffc10113 12a83 ffc10113 12a03 ffc10113 12983 ffc10113 12403
  //   ffc10113 12503 ffc10113 12883 200073 1112023 410113 a12023 410113 812023 410113 1312023 410113
  //   1412023 410113 1512023 410113 1612023 410113 40e073 200b13 300a13 100a93 1600433 441413 14469b3
  //   1300533 2200893 73 fe0416e3 415a0a33 fe0a10e3 40f073 ffc10113 12b03 ffc10113 12a83 ffc10113 12a03
  //   ffc10113 12983 ffc10113 12403 ffc10113 12503 ffc10113 12883 200073 1112023 410113 a12023 410113
  //   812023 410113 1312023 410113 1412023 410113 1512023 410113 1612023 410113 40e073 300b13 300a13
  //   100a93 1600433 441413 14469b3 1300533 2200893 73 fe0416e3 415a0a33 fe0a10e3 40f073 ffc10113 12b03
  //   ffc10113 12a83 ffc10113 12a03 ffc10113 12983 ffc10113 12403 ffc10113 12503 ffc10113 12883 200073
  //   指令字
  //   I型指令
  //   控制位
  //   S型指令
  //   B型指令
  //   J型指令
  //   流水调试日志用
  //   暂停节拍，不能为0
  //   戳工具置1进入计数暂停模式，ctrl+k时钟自动运行到对应节拍暂停
  //   ctrl+k关闭时钟连续运行，将控制位置零，进入单步调试模式调试
  //   用这个时钟源需要去掉电路中的其他时钟源
  //   关中断
  //   开中断
  //   可计数暂停的时钟源
  //   中断使能信号
  //   中断寄存器保护
  //   为方便自动评测，需要输出流水线各段保存的PC值，注意是PC不是PC+4，另外ID段寄存器写入信息，Mem段内存写入信息也要输出
  //   中断地址输出逻辑
  //   中断清零信号产生
  //   rd
  //   单级中断测试信号模拟器
  //   重定向设置
endmodule

module \流水线_动态分支预测  (
  output RegWrite,
  output MemWrite,
  output [31:0] IF_PC,
  output [31:0] ID_PC,
  output [31:0] EX_PC,
  output [31:0] M_PC,
  output [31:0] WB_PC,
  output [31:0] RDin,
  output [31:0] MDin,
  output [31:0] LedData
);

  wire ALU_SRC, and_1_out, and_2_out, and_3_out, and_4_out, and_5_out, and_6_out, and_7_out, and_9_out,
       and_10_out, and_11_out, and_12_out, and_13_out, and_14_out, and_15_out, and_16_out, b_cranch, Beq,
       BGE, Bne, Branch, BranchTaken, CLK, clock_1_out, comparator_1_eq, comparator_1_lt, comparator_2_eq,
       comparator_3_eq, comparator_4_eq, comparator_5_eq, comparator_6_eq, comparator_7_eq, comparator_8_eq,
       comparator_9_eq, d_ff_1_q, DataHazzard, ecall, equal, ex_mem_1_ex_ecall, ex_mem_1_ex_jal,
       ex_mem_1_ex_jalr, ex_mem_1_ex_lb, ex_mem_1_ex_memtoreg, ex_mem_1_ex_uret, EX_MemToReg, EX_RegWrite,
       Go, great, halt, id_ex_1_ex_alusrcb, id_ex_1_ex_beq, id_ex_1_ex_bge, id_ex_1_ex_bne, id_ex_1_ex_ecall,
       id_ex_1_ex_jal, id_ex_1_ex_jalr, id_ex_1_ex_lb, id_ex_1_ex_memtoreg_2, id_ex_1_ex_uret, id_ex_1_pd_2,
       ID_MemToReg, ID_MemWrite, ID_RegWrite, IDt_MemToReg, IDt_RegWrite, if_id_1_pd_2, IR1, IR2, IR3, JAL,
       JALR, LB, lb_t, LoadUse, MEM_RegWrite, mem_wb_1_ex_ecall, mem_wb_1_ex_jal, mem_wb_1_ex_jalr,
       mem_wb_1_ex_memtoreg, nand_1_out, not_1_out, not_2_out, not_3_out, not_4_out, not_5_out, not_6_out,
       not_7_out, not_8_out, not_10_out, or_1_out, or_5_out, or_10_out, RST, RsUsed, RtUsed, tALU_SRC, URET,
       W1, W2, W3, WB_lb, wrong, \全相联cache_1_out_8 , \单周期硬布线控制器_1_s_type , \无条件分支 , \有条件分支 ;
  wire [0:0] or_4_out;
  wire [1:0] EX_R1_F, EX_R2_F, ID_R1_F, ID_R2_F, priority_encoder_1_out, priority_encoder_2_out;
  wire [3:0] ALU_OP, id_ex_1_ex_aluop;
  wire [4:0] func, rs, rt;
  wire [7:0] multiplexer_16_out;
  wire [11:0] bit_extender_3_out, multiplexer_8_out, multiplexer_9_out;
  wire [12:0] CNT_num;
  wire [15:0] \LoadUse次数 , \总周期数 , \插入气泡数 , \无条件分支数 , \有条件分支数 , \条件分支成功数 ;
  wire [31:0] adder_1_out, adder_3_out, adder_4_out, aluresult, bit_extender_1_out, bit_extender_2_out,
       bit_extender_4_out, branch_LPC, EX_IMM, EX_IR, ex_mem_1_mem_r1, ex_mem_1_mem_r2, EX_NRS, EX_NRT,
       EX_RS, EX_RT, ID_IR, IF_IR, L_PC, LBR, LPC, MEM_AluData, MEM_IR, mem_wb_1_wb_r1, mem_wb_1_wb_r2,
       multiplexer_10_out, multiplexer_11_out, multiplexer_14_out, multiplexer_15_out, P_PC, PC_4,
       ram_1_data, regifile_down_1_r1, regifile_down_1_r2, shifter_1_out, shifter_2_out, WB_alu, WB_Dre,
       WB_IR, \全相联cache_1_dataout ;

  Button \u_总复位  (.out(RST));
  Button _1 (.out(IR1));
  Button _2 (.out(IR2));
  Button _3 (.out(IR3));
  // Probe on \总周期数 
  // Probe on \总周期数 
  Priority_Encoder #(.select(2), .disabled("Z")) priority_encoder_1 (
    .in0(1'b1), .in1(id_ex_1_ex_jalr), .in2(id_ex_1_ex_jal), .in3(b_cranch), .out(priority_encoder_1_out));  // open: gs, en_out, en_in
  Multiplexer #(.select(2), .width(32), .disabled("Z"), .enable("false")) multiplexer_1 (
    .in0(IF_PC), .in1(aluresult), .in2(adder_3_out), .in3(adder_3_out), .out(branch_LPC),
    .sel(priority_encoder_1_out));
  Button \u_继续运行  (.out(Go));
  LED #(.active("true")) led_1 (.in(W1));
  LED #(.active("true")) led_2 (.in(W2));
  LED #(.active("true")) led_3 (.in(W3));
  Adder #(.width(32)) adder_1 (.a(EX_PC), .b(32'h4), .out(adder_1_out), .cin(1'b0));  // open: cout
  and and_1 (and_1_out, not_2_out, not_1_out);
  not not_1 (not_1_out, halt);
  not not_2 (not_2_out, LoadUse);
  Hex_Digit_Display hex_digit_display_1 (.value(LedData[31:28]));  // open: dp
  // Probe on IF_PC[19:0]
  // RiscV_Probe riscv_probe_1: pin names not known; wires that end beside it: IF_IR
  Priority_Encoder #(.select(2), .disabled("Z")) priority_encoder_2 (
    .in0(1'b1), .in1(id_ex_1_ex_jalr), .in2(id_ex_1_ex_jal), .in3(\无条件分支 ), .out(priority_encoder_2_out));  // open: gs, en_out, en_in
  Multiplexer #(.select(2), .width(32), .disabled("Z"), .enable("false")) multiplexer_2 (
    .in0(adder_1_out), .in1(aluresult), .in2(adder_3_out), .in3(adder_3_out), .out(LPC),
    .sel(priority_encoder_2_out));
  Counter #(.width(16), .max('hffff), .ongoal("wrap"), .trigger("rising"), .behavior("new")) counter_1 (
    .Q(\总周期数 ), .clk(and_2_out));  // open: load, D, count, carry, clr, preset, down
  and and_2 (and_2_out, ~halt, CLK);  // AND_Gate
  Hex_Digit_Display hex_digit_display_2 (.value(LedData[23:20]));  // open: dp
  Hex_Digit_Display hex_digit_display_3 (.value(LedData[27:24]));  // open: dp
  // Probe on ID_PC[19:0]
  // RiscV_Probe riscv_probe_2: pin names not known; wires that end beside it: {ID_IR[31], func[4], ID_IR[29:26], func[3], ID_IR[24:15], func[2:0], ID_IR[11:0]}
  \全相联cache  \u_全相联cache_1  (
    .IF_PC(IF_PC), .EX_PC(EX_PC), .BlockDataIn(branch_LPC), .BlkDataReady(Branch), .CLK(CLK),
    .jumpormot(BranchTaken), .DataOut(\全相联cache_1_dataout ), .out_8(\全相联cache_1_out_8 ));
  Hex_Digit_Display hex_digit_display_4 (.value(LedData[15:12]));  // open: dp
  Hex_Digit_Display hex_digit_display_5 (.value(LedData[19:16]));  // open: dp
  // Probe on IF_PC
  Register #(.width(32), .trigger("rising"), .Select("low")) PC (
    .D(L_PC), .en(and_1_out), .Q(IF_PC), .clk(CLK), .clr(RST));
  Counter #(.width(16), .max('hffff), .ongoal("wrap"), .trigger("rising"), .behavior("new")) counter_2 (
    .Q(\有条件分支数 ), .clk(and_3_out));  // open: load, D, count, carry, clr, preset, down
  and and_3 (and_3_out, \有条件分支 , CLK);
  Hex_Digit_Display hex_digit_display_6 (.value(LedData[11:8]));  // open: dp
  Hex_Digit_Display hex_digit_display_7 (.value(LedData[7:4]));  // open: dp
  // Probe on EX_PC[19:0]
  // RiscV_Probe riscv_probe_3: pin names not known; wires that end beside it: EX_IR
  not not_3 (not_3_out, LoadUse);
  and and_4 (and_4_out, not_3_out, not_4_out);
  not not_4 (not_4_out, halt);
  Multiplexer #(.select(1), .width(32), .disabled("Z"), .enable("false")) multiplexer_3 (
    .in0(PC_4), .in1(\全相联cache_1_dataout ), .out(P_PC), .sel(\全相联cache_1_out_8 ));
  Multiplexer #(.select(1), .width(32), .disabled("Z"), .enable("false")) multiplexer_4 (
    .in0(P_PC), .in1(LPC), .out(L_PC), .sel(wrong));
  Hex_Digit_Display hex_digit_display_8 (.value(LedData[3:0]));  // open: dp
  Adder #(.width(32)) adder_2 (.a(IF_PC), .b(32'h4), .out(PC_4));  // open: cin, cout
  Adder #(.width(32)) adder_3 (.a(EX_IMM), .b(EX_PC), .out(adder_3_out));  // open: cin, cout
  Counter #(.width(16), .max('hffff), .ongoal("wrap"), .trigger("rising"), .behavior("new")) counter_3 (
    .Q(\无条件分支数 ), .clk(and_5_out));  // open: load, D, count, carry, clr, preset, down
  and and_5 (and_5_out, \无条件分支 , CLK);
  // Probe on \总周期数 
  // Probe on M_PC[19:0]
  // RiscV_Probe riscv_probe_4: pin names not known; wires that end beside it: MEM_IR
  ROM #(.addrWidth(10), .dataWidth(32), .Select("high")) rom_1 (.addr(IF_PC[11:2]), .data(IF_IR));
  // Probe on \总周期数 
  // Probe on \无条件分支数 
  // Probe on \条件分支成功数 
  // Probe on \插入气泡数 
  // Probe on \LoadUse次数 
  or or_1 (or_1_out, wrong, RST);
  // RiscV_Probe riscv_probe_5: pin names not known; wires that end beside it: {ID_IR[31], func[4], ID_IR[29:26], func[3], ID_IR[24:15], func[2:0], ID_IR[11:0]}
  IF_ID if_id_1 (
    .CLK(CLK), .\使能端 (and_4_out), .\清零端 (or_1_out), .IF_IR(IF_IR), .IF_PC(IF_PC),
    .ID_IR({ID_IR[31], func[4], ID_IR[29:26], func[3], ID_IR[24:15], func[2:0], ID_IR[11:0]}), .ID_PC(ID_PC),
    .PD(\全相联cache_1_out_8 ), .PD_2(if_id_1_pd_2));
  and and_6 (and_6_out, BranchTaken, CLK);
  // Probe on IF_PC[11:0]
  // Probe on WB_PC[19:0]
  // RiscV_Probe riscv_probe_6: pin names not known; wires that end beside it: WB_IR
  not not_5 (not_5_out, halt);
  Counter #(.width(16), .max('hffff), .ongoal("wrap"), .trigger("rising"), .behavior("new")) counter_4 (
    .Q(\条件分支成功数 ), .clk(and_6_out));  // open: load, D, count, carry, clr, preset, down
  // Probe on EX_PC[11:0]
  // Probe on ID_PC[11:0]
  // Probe on M_PC[11:0]
  D_Flip_Flop #(.trigger("high"), .Pre_Clr_Positions("LEGACY"), .NegatePresetClear("false"), .enable("true"), .NewFFLayout("false")) d_ff_1 (.Q(d_ff_1_q));  // open: clk, D, Qn, preset, en, reset
  // Probe on 13'h322
  assign bit_extender_1_out = {{20{ID_IR[31]}}, {ID_IR[31], ID_IR[7], func[4], ID_IR[29:26], func[3], ID_IR[11:8]}};  // Bit_Extender bit_extender_1
  assign bit_extender_2_out = {{12{ID_IR[31]}}, {ID_IR[31], ID_IR[19:15], func[2:0], ID_IR[20], func[4], ID_IR[29:26], func[3], ID_IR[24:21]}};  // Bit_Extender bit_extender_2
  // Probe on WB_PC[11:0]
  Comparator #(.width(13), .mode("twosComplement")) comparator_1 (
    .a(CNT_num), .b(13'h322), .eq(comparator_1_eq), .lt(comparator_1_lt));  // open: gt
  Clock #(.highDuration(1), .lowDuration(1)) clock_1 (.out(clock_1_out));
  or or_2 (\有条件分支 , id_ex_1_ex_jal, id_ex_1_ex_jalr);
  assign bit_extender_3_out = {{4{ID_IR[27]}}, {ID_IR[27:26], func[3], ID_IR[24:20]}};  // Bit_Extender bit_extender_3
  nand nand_1 (nand_1_out, d_ff_1_q, comparator_1_eq);
  Counter #(.width(13), .max('h1fff), .ongoal("stay"), .trigger("rising"), .behavior("old")) counter_5 (
    .count(comparator_1_lt), .Q(CNT_num), .clk(clock_1_out));  // open: load, D, carry, clr, preset
  \单周期硬布线控制器  \u_单周期硬布线控制器_1  (
    .Funct(func), .OP(ID_IR[6:2]), .ALU_OP(ALU_OP), .MemToReg(IDt_MemToReg), .MemWrite(ID_MemWrite),
    .ALU_SRC(tALU_SRC), .RegWrite(IDt_RegWrite), .ecall(ecall), .S_type(\单周期硬布线控制器_1_s_type ), .Jalr(JALR),
    .Beq(Beq), .JAL(JAL), .Bne(Bne), .in_3(ID_IR[21]), .uret(URET), .BGE(BGE), .LB(LB));
  Multiplexer #(.select(1), .width(5), .disabled("Z"), .enable("false")) multiplexer_5 (
    .in0(ID_IR[19:15]), .in1(5'b10001), .out(rs), .sel(ecall));
  Multiplexer #(.select(1), .width(5), .disabled("Z"), .enable("false")) multiplexer_6 (
    .in0(ID_IR[24:20]), .in1(5'b01010), .out(rt), .sel(ecall));
  Shifter #(.width(32), .shift("ll")) shifter_1 (.in(bit_extender_1_out), .\dist (5'b00001), .out(shifter_1_out));
  Shifter #(.width(32), .shift("ll")) shifter_2 (.in(bit_extender_2_out), .\dist (5'b00001), .out(shifter_2_out));
  not not_6 (not_6_out, ID_IR[0]);
  and and_7 (and_7_out, LB, not_6_out);
  Multiplexer #(.select(1), .width(3), .disabled("Z"), .enable("false")) multiplexer_7 (
    .in0({IDt_RegWrite, tALU_SRC, IDt_MemToReg}), .in1(3'b000), .out({ID_RegWrite, ALU_SRC, ID_MemToReg}),
    .sel(and_7_out));
  and and_8 (lb_t, LB, ID_IR[0]);
  assign CLK = nand_1_out ? clock_1_out : 1'bz;  // Controlled_Buffer controlled_buffer_1
  or or_3 (BranchTaken, id_ex_1_ex_jalr, id_ex_1_ex_jal, \无条件分支 );
  Multiplexer #(.select(1), .width(12), .disabled("Z"), .enable("false")) multiplexer_8 (
    .in0({ID_IR[31], func[4], ID_IR[29:26], func[3], ID_IR[24:20]}), .in1(bit_extender_3_out),
    .out(multiplexer_8_out), .sel(lb_t));
  Multiplexer #(.select(1), .width(12), .disabled("Z"), .enable("false")) multiplexer_9 (
    .in0(multiplexer_8_out), .in1({ID_IR[31], func[4], ID_IR[29:26], func[3], ID_IR[11:7]}),
    .out(multiplexer_9_out), .sel(\单周期硬布线控制器_1_s_type ));
  Pull_Resistor #(.pull(1)) pull_resistor_1 (.node(CLK));
  or or_4 (or_4_out[0], Beq, Bne, BGE);
  assign bit_extender_4_out = {{20{multiplexer_9_out[11]}}, multiplexer_9_out};  // Bit_Extender bit_extender_4
  \used控制电路  \used控制电路_1  (
    .OP2(ID_IR[2]), .OP3(ID_IR[3]), .OP4(ID_IR[4]), .OP5(ID_IR[5]), .OP6(ID_IR[6]), .F12(func[0]),
    .F13(func[1]), .F14(func[2]), .F25(func[3]), .F30(func[4]), .RsUsed(RsUsed), .RtUesd(RtUsed));
  Multiplexer #(.select(2), .width(32), .disabled("Z"), .enable("false")) multiplexer_10 (
    .in0(bit_extender_4_out), .in1(shifter_1_out), .in2(shifter_2_out), .out(multiplexer_10_out),
    .sel({JAL, or_4_out[0]}));  // open: in3
  Regifile_down regifile_down_1 (
    .Din(RDin), .Clk(CLK), .R1(regifile_down_1_r1), .R2(regifile_down_1_r2), .WE(RegWrite),
    .W_num(WB_IR[11:7]), .R1_num(rs), .R2_num(rt));
  Comparator #(.width(5), .mode("twosComplement")) comparator_2 (
    .a(rs), .b(EX_IR[11:7]), .eq(comparator_2_eq));  // open: gt, lt
  Comparator #(.width(5), .mode("twosComplement")) comparator_3 (
    .a(rs), .b(MEM_IR[11:7]), .eq(comparator_3_eq));  // open: gt, lt
  Comparator #(.width(5), .mode("twosComplement")) comparator_4 (
    .a(rt), .b(EX_IR[11:7]), .eq(comparator_4_eq));  // open: gt, lt
  Comparator #(.width(5), .mode("twosComplement")) comparator_5 (
    .a(rt), .b(MEM_IR[11:7]), .eq(comparator_5_eq));  // open: gt, lt
  or or_5 (or_5_out, wrong, RST, LoadUse);
  ID_EX id_ex_1 (
    .CLK(CLK), .\使能端 (not_5_out), .\清零端 (or_5_out),
    .ID_IR({ID_IR[31], func[4], ID_IR[29:26], func[3], ID_IR[24:15], func[2:0], ID_IR[11:0]}), .EX_IR(EX_IR),
    .ID_PC(ID_PC), .EX_PC(EX_PC), .ID_R1(regifile_down_1_r1), .EX_R1(EX_RS), .ID_R2(regifile_down_1_r2),
    .EX_R2(EX_RT), .ID_MemToReg(ID_MemToReg), .EX_MemToReg(EX_MemToReg), .ID_MemWrite(ID_MemWrite),
    .EX_MemToReg_2(id_ex_1_ex_memtoreg_2), .ID_AluOP(ALU_OP), .EX_AluOP(id_ex_1_ex_aluop),
    .ID_AluSrcB(ALU_SRC), .EX_AluSrcB(id_ex_1_ex_alusrcb), .ID_RegWrite(ID_RegWrite),
    .EX_RegWrite(EX_RegWrite), .ID_ecall(ecall), .EX_ecall(id_ex_1_ex_ecall), .ID_JAL(JAL),
    .EX_JAL(id_ex_1_ex_jal), .ID_JALR(JALR), .EX_JALR(id_ex_1_ex_jalr), .ID_Beq(Beq),
    .EX_Beq(id_ex_1_ex_beq), .ID_Bne(Bne), .EX_Bne(id_ex_1_ex_bne), .ID_URET(URET),
    .EX_URET(id_ex_1_ex_uret), .ID_BGE(BGE), .EX_BGE(id_ex_1_ex_bge), .ID_IMM(multiplexer_10_out),
    .EX_IMM(EX_IMM), .ID_R1_F(ID_R1_F), .EX_R1_F(EX_R1_F), .ID_R2_F(ID_R2_F), .EX_R2_F(EX_R2_F),
    .ID_LB(lb_t), .EX_LB(id_ex_1_ex_lb), .PD(if_id_1_pd_2), .PD_2(id_ex_1_pd_2));
  Comparator #(.width(5), .mode("twosComplement")) comparator_6 (
    .a(rs), .b({5{1'b0}}), .eq(comparator_6_eq));  // open: gt, lt
  not not_7 (not_7_out, comparator_6_eq);
  not not_8 (not_8_out, comparator_7_eq);
  Comparator #(.width(5), .mode("twosComplement")) comparator_7 (
    .a(rt), .b({5{1'b0}}), .eq(comparator_7_eq));  // open: gt, lt
  and and_9 (and_9_out, RsUsed, EX_RegWrite, not_7_out, comparator_2_eq);
  and and_10 (and_10_out, RsUsed, MEM_RegWrite, not_7_out, comparator_3_eq);
  and and_11 (and_11_out, RtUsed, EX_RegWrite, not_8_out, comparator_4_eq);
  and and_12 (and_12_out, RtUsed, MEM_RegWrite, not_8_out, comparator_5_eq);
  Multiplexer #(.select(1), .width(32), .disabled("Z"), .enable("false")) multiplexer_11 (
    .in0(EX_NRT), .in1(EX_IMM), .out(multiplexer_11_out), .sel(id_ex_1_ex_alusrcb));
  Comparator #(.width(1), .mode("twosComplement")) comparator_8 (
    .a(id_ex_1_pd_2), .b(BranchTaken), .eq(comparator_8_eq));  // open: gt, lt
  and and_13 (and_13_out, id_ex_1_ex_beq, equal);
  not not_9 (wrong, comparator_8_eq);
  or or_6 (DataHazzard, and_9_out, and_10_out, and_11_out, and_12_out);
  or or_7 (b_cranch, id_ex_1_ex_beq, id_ex_1_ex_bne, id_ex_1_ex_bge);
  or or_8 (\无条件分支 , and_13_out, and_14_out, and_15_out);
  and and_14 (and_14_out, ~equal, id_ex_1_ex_bne);  // AND_Gate
  ALU alu_1 (
    .X(EX_NRS), .Y(multiplexer_11_out), .AluOP(id_ex_1_ex_aluop), .Equal(equal), .Result(aluresult),
    .out_4(great));  // open: Result_2, out_6
  and and_15 (and_15_out, great, id_ex_1_ex_bge);
  // Probe on EX_NRS
  or or_9 (Branch, id_ex_1_ex_jal, id_ex_1_ex_jalr, id_ex_1_ex_beq, id_ex_1_ex_bne, id_ex_1_ex_bge);
  // Probe on RDin
  EX_MEM ex_mem_1 (
    .CLK(CLK), .\使能端 (not_5_out), .\清零端 (RST), .EX_IR(EX_IR), .EX_PC(EX_PC), .EX_R1(EX_NRS),
    .ID_RegWrite(EX_RegWrite), .EX_R2(EX_NRT), .EX_ALU(aluresult), .ID_ecall(id_ex_1_ex_ecall),
    .EX_DATA(EX_NRT), .ID_URET(id_ex_1_ex_uret), .MEM_IR(MEM_IR), .MEM_PC(M_PC), .MEM_R1(ex_mem_1_mem_r1),
    .EX_RegWrite(MEM_RegWrite), .MEM_R2(ex_mem_1_mem_r2), .MEM_ALU(MEM_AluData),
    .EX_ecall(ex_mem_1_ex_ecall), .MEM_DATA(MDin), .EX_URET(ex_mem_1_ex_uret), .ID_MemToReg(EX_MemToReg),
    .EX_MemToReg(ex_mem_1_ex_memtoreg), .ID_MemWrite(id_ex_1_ex_memtoreg_2), .EX_MemWrite(MemWrite),
    .ID_JAL(id_ex_1_ex_jal), .EX_JAL(ex_mem_1_ex_jal), .ID_JALR(id_ex_1_ex_jalr), .EX_JALR(ex_mem_1_ex_jalr),
    .ID_LB(id_ex_1_ex_lb), .EX_LB(ex_mem_1_ex_lb));
  \used控制电路  \used控制电路_2  (
    .OP2(ID_IR[2]), .OP3(ID_IR[3]), .OP4(ID_IR[4]), .OP5(ID_IR[5]), .OP6(ID_IR[6]), .F12(func[0]),
    .F13(func[1]), .F14(func[2]), .F25(func[3]), .F30(func[4]), .RsUsed(RsUsed), .RtUesd(RtUsed));
  \LoadUse信号生成  \loaduse信号生成_1  (
    .R1Used(RsUsed), .EX_MemToReg(EX_MemToReg), .ID_R1(rs), .EX_RD(EX_IR[11:7]), .ID_R2(rt), .R2Used(RtUsed),
    .LoadUse(LoadUse));
  Multiplexer #(.select(2), .width(32), .disabled("Z"), .enable("false")) multiplexer_12 (
    .in0(EX_RS), .in1(RDin), .in2(MEM_AluData), .out(EX_NRS), .sel(EX_R1_F));  // open: in3
  Multiplexer #(.select(2), .width(32), .disabled("Z"), .enable("false")) multiplexer_13 (
    .in0(EX_RT), .in1(RDin), .in2(MEM_AluData), .out(EX_NRT), .sel(EX_R2_F));  // open: in3
  // Probe on ram_1_data
  RAM #(.addrWidth(10), .dataWidth(32), .bus("separate"), .Select("high")) ram_1 (
    .addr(MEM_AluData[11:2]), .din(MDin), .data(ram_1_data), .str(MemWrite), .clk(CLK), .ld(1'b1));  // open: sel, clr
  // Probe on MEM_AluData
  MEM_WB mem_wb_1 (
    .CLK(CLK), .\使能端 (not_5_out), .\清零端 (RST), .MEM_IR(MEM_IR), .ID_MemToReg(ex_mem_1_ex_memtoreg),
    .ID_RegWrite(MEM_RegWrite), .MEM_PC(M_PC), .ID_ecall(ex_mem_1_ex_ecall), .MEM_R1(ex_mem_1_mem_r1),
    .ID_URET(ex_mem_1_ex_uret), .MEM_R2(ex_mem_1_mem_r2), .WB_IR(WB_IR), .EX_MemToReg(mem_wb_1_ex_memtoreg),
    .EX_RegWrite(RegWrite), .WB_PC(WB_PC), .EX_ecall(mem_wb_1_ex_ecall), .WB_R1(mem_wb_1_wb_r1),
    .WB_R2(mem_wb_1_wb_r2), .MEM_DIN(ram_1_data), .WB_DIN(WB_Dre), .MEM_ALU(MEM_AluData), .WB_ALU(WB_alu),
    .ID_JAL(ex_mem_1_ex_jal), .EX_JAL(mem_wb_1_ex_jal), .ID_JALR(ex_mem_1_ex_jalr),
    .EX_JALR(mem_wb_1_ex_jalr), .ID_LB(ex_mem_1_ex_lb), .EX_LB(WB_lb));  // open: EX_URET
  \R1_F_R2_F信号生成  \r1_f_r2_f信号生成_1  (
    .R1Used(RsUsed), .ID_R1(rs), .EX_RegWrite(EX_RegWrite), .EX_RD(EX_IR[11:7]), .MEM_RegWrite(MEM_RegWrite),
    .MEM_RD(MEM_IR[11:7]), .R2Used(RtUsed), .ID_R2(rt), .R1_F(ID_R1_F), .R2_F(ID_R2_F));
  // Probe on WB_alu
  Multiplexer #(.select(1), .width(32), .disabled("Z"), .enable("false")) multiplexer_14 (
    .in0(WB_alu), .in1(WB_Dre), .out(multiplexer_14_out), .sel(mem_wb_1_ex_memtoreg));
  Adder #(.width(32)) adder_4 (.a(WB_PC), .b(32'h4), .out(adder_4_out));  // open: cin, cout
  Comparator #(.width(32), .mode("twosComplement")) comparator_9 (
    .a(mem_wb_1_wb_r1), .b(32'h22), .eq(comparator_9_eq));  // open: gt, lt
  Multiplexer #(.select(1), .width(32), .disabled("Z"), .enable("false")) multiplexer_15 (
    .in0(multiplexer_14_out), .in1(LBR), .out(multiplexer_15_out), .sel(WB_lb));
  Register #(.width(32), .trigger("rising"), .Select("low")) register_1 (
    .D(mem_wb_1_wb_r2), .en(and_16_out), .Q(LedData), .clk(CLK));  // open: clr
  and and_16 (and_16_out, comparator_9_eq, mem_wb_1_ex_ecall);
  not not_10 (not_10_out, comparator_9_eq);
  Multiplexer #(.select(2), .width(8), .disabled("Z"), .enable("false")) multiplexer_16 (
    .in0(WB_Dre[7:0]), .in1(WB_Dre[15:8]), .in2(WB_Dre[23:16]), .in3(WB_Dre[31:24]),
    .out(multiplexer_16_out), .sel(WB_alu[1:0]));
  Multiplexer #(.select(1), .width(32), .disabled("Z"), .enable("false")) multiplexer_17 (
    .in0(multiplexer_15_out), .in1(adder_4_out), .out(RDin), .sel(or_10_out));
  or or_10 (or_10_out, mem_wb_1_ex_jal, mem_wb_1_ex_jalr);
  D_Flip_Flop #(.trigger("falling"), .Pre_Clr_Positions("ABOVE_BELOW"), .NegatePresetClear("false"), .enable("true"), .NewFFLayout("true")) d_ff_2 (
    .clk(CLK), .D(not_10_out), .Q(halt), .en(mem_wb_1_ex_ecall), .reset(Go));  // open: Qn, preset
  assign LBR = {{24{multiplexer_16_out[7]}}, multiplexer_16_out};  // Bit_Extender bit_extender_5

  // Other names for the same wires on the sheet: ID_IR (some bits) = func; EX_WriteReg_num[4:0] = EX_IR[11:7];
  //   op[4:0] = ID_IR[6:2]; MEM_WriteReg_num[4:0] = MEM_IR[11:7]; MEM_PC[31:0] = M_PC

  // Notes on the sheet:
  //   中断源
  //   时空图监测，可删除
  //   中断等待指示
  //   数码管输出
  //   contents of rom_1 (hex, n*v repeats v):
  //   100493 100006f 100493 200913 300993 100006f 100493 200913 300993 100006f 100493 200913 300993
  //   100006f 100493 200913 300993 2c4000ef 100413 100493 1f49493 900533 2200893 73 24d493 48463 fedff06f
  //   900533 2200893 73 100493 249493 900533 2200893 73 48463 fedff06f 100493 1f49493 900533 2200893 73
  //   4034d493 900533 2200893 73 4044d493 900533 2200893 73 4044d493 900533 2200893 73 4044d493 900533
  //   2200893 73 4044d493 900533 2200893 73 4044d493 900533 2200893 73 4044d493 900533 2200893 73 4044d493
  //   900533 2200893 73 100413 1f41993 41f9d993 433 c00913 300b13 140413 f47413 800293 100313 499993
  //   89e9b3 1300533 2200893 73 406282b3 fe0294e3 140413 f00f93 1f47433 1c41413 800293 100313 49d993
  //   89e9b3 1300533 2200893 73 406282b3 fe0294e3 1c45413 406b0b33 b0463 f95ff06f 2b3 fff2c293 829293
  //   ff2e293 500533 2200893 73 fff00413 493 84a023 140413 448493 84a023 140413 448493 84a023 140413
  //   448493 84a023 140413 448493 84a023 140413 448493 84a023 140413 448493 84a023 140413 448493 84a023
  //   140413 448493 84a023 140413 448493 84a023 140413 448493 84a023 140413 448493 84a023 140413 448493
  //   84a023 140413 448493 84a023 140413 448493 84a023 140413 448493 84a023 140413 448493 140413 433
  //   3c00493 42983 4aa03 149a2b3 28663 134a023 1442023 ffc48493 fe9412e3 800533 2200893 73 440413 3c00493
  //   fc9416e3 3200893 73 f00493 900533 2200893 73 fff48493 fe04d8e3 a00893 73 a00893 73 413 140413 800533
  //   2200893 73 240413 800533 2200893 73 340413 800533 2200893 73 440413 800533 2200893 73 540413 800533
  //   2200893 73 640413 800533 2200893 73 740413 800533 2200893 73 840413 800533 2200893 2200893 73 8067
  //   指令字
  //   I型指令
  //   控制位
  //   S型指令
  //   B型指令
  //   J型指令
  //   流水调试日志用
  //   暂停节拍，不能为0
  //   戳工具置1进入计数暂停模式，ctrl+k时钟自动运行到对应节拍暂停
  //   ctrl+k关闭时钟连续运行，将控制位置零，进入单步调试模式调试
  //   用这个时钟源需要去掉电路中的其他时钟源
  //   可计数暂停的时钟源
  //   为方便自动评测，需要输出流水线各段保存的PC值，注意是PC不是PC+4，另外ID段寄存器写入信息，Mem段内存写入信息也要输出
  //   rd
  //   重定向设置
endmodule
// 单周期硬布线控制器
module \单周期硬布线控制器  (
  input  [4:0] OP,
  input  [4:0] Funct,
  input  in_3,
  output [3:0] ALU_OP,
  output uret,
  output MemToReg,
  output ecall,
  output MemWrite,
  output ALU_SRC,
  output RegWrite,
  output S_type,
  output Beq,
  output Bne,
  output Jalr,
  output JAL,
  output BGE,
  output LB
);

  wire \控制信号自动生成_1_ecall ;

  \运算控制器自动生成  \u_运算控制器自动生成_1  (
    .OP2(OP[0]), .OP3(OP[1]), .OP4(OP[2]), .OP5(OP[3]), .OP6(OP[4]), .F12(Funct[0]), .F13(Funct[1]),
    .F14(Funct[2]), .F25(Funct[3]), .F30(Funct[4]), .S0(ALU_OP[0]), .S1(ALU_OP[1]), .S2(ALU_OP[2]),
    .S3(ALU_OP[3]));
  \控制信号自动生成  \u_控制信号自动生成_1  (
    .OP2(OP[0]), .OP3(OP[1]), .OP4(OP[2]), .OP5(OP[3]), .MemToReg(MemToReg), .OP6(OP[4]), .F12(Funct[0]),
    .F13(Funct[1]), .F14(Funct[2]), .F25(Funct[3]), .F30(Funct[4]), .MemWrite(MemWrite), .ALU_SRC(ALU_SRC),
    .RegWrite(RegWrite), .ecall(\控制信号自动生成_1_ecall ), .S_Type(S_type), .BEQ(Beq), .BNE(Bne), .JALR(Jalr),
    .JAL(JAL), .bge(BGE), .lb(LB));
  and and_1 (uret, in_3, \控制信号自动生成_1_ecall );
  and and_2 (ecall, ~in_3, \控制信号自动生成_1_ecall );  // AND_Gate

  // Other names for the same wires on the sheet: IR21 = in_3; OP_CODE[4:0] = OP

  // Notes on the sheet:
  //   运算器控制器，根据指令生成运算器功能选择信号
  //   控制信号生成，产生数据通路需要的其他控制信号
endmodule

// ALU
module ALU (
  input  [31:0] X,
  input  [31:0] Y,
  input  [3:0] AluOP,
  output out_4,
  output Equal,
  output out_6,
  output [31:0] Result,
  output [31:0] Result_2
);

  wire [0:0] comparator_1_lt, comparator_2_lt;
  wire [31:0] adder_1_out, AND_out, divider_1_out, divider_1_rem, multiplier_1_cout, multiplier_1_out,
       NOR_out, OR_out, shifter_1_out, shifter_2_out, shifter_3_out, subtractor_1_out, XOR_out;

  assign AND_out = X & Y;  // AND_Gate AND, 32 bits wide
  assign OR_out = X | Y;  // OR_Gate OR, 32 bits wide
  Shifter #(.width(32), .shift("ll")) shifter_1 (.in(X), .\dist (Y[4:0]), .out(shifter_1_out));
  Shifter #(.width(32), .shift("ar")) shifter_2 (.in(X), .\dist (Y[4:0]), .out(shifter_2_out));
  Shifter #(.width(32), .shift("lr")) shifter_3 (.in(X), .\dist (Y[4:0]), .out(shifter_3_out));
  Multiplier #(.width(32)) multiplier_1 (.a(X), .b(Y), .out(multiplier_1_out), .cout(multiplier_1_cout));  // open: cin
  Divider #(.width(32)) divider_1 (.a(X), .b(Y), .out(divider_1_out), .rem(divider_1_rem));  // open: upper
  Adder #(.width(32)) adder_1 (.a(X), .b(Y), .out(adder_1_out));  // open: cin, cout
  Subtractor #(.width(32)) subtractor_1 (.a(X), .b(Y), .out(subtractor_1_out));  // open: bin, bout
  assign XOR_out = X ^ Y;  // XOR_Gate XOR, 32 bits wide
  assign NOR_out = ~(X | Y);  // NOR_Gate NOR, 32 bits wide
  Comparator #(.width(32), .mode("twosComplement")) comparator_1 (
    .a(X), .b(Y), .eq(Equal), .lt(comparator_1_lt[0]));  // open: gt
  Comparator #(.width(32), .mode("unsigned")) comparator_2 (.a(X), .b(Y), .lt(comparator_2_lt[0]));  // open: gt, eq
  Multiplexer #(.select(4), .width(32), .disabled("Z"), .enable("false")) multiplexer_1 (
    .in0(shifter_1_out), .in1(shifter_2_out), .in2(shifter_3_out), .in3(multiplier_1_out),
    .in4(divider_1_out), .in5(adder_1_out), .in6(subtractor_1_out), .in7(AND_out), .in8(OR_out),
    .in9(XOR_out), .in10(NOR_out), .in11({{31{1'b0}}, comparator_1_lt[0]}),
    .in12({{31{1'b0}}, comparator_2_lt[0]}), .in13({32{1'b0}}), .in14({32{1'b0}}), .in15({32{1'b0}}),
    .out(Result), .sel(AluOP));
  Multiplexer #(.select(4), .width(32), .disabled("Z"), .enable("false")) multiplexer_2 (
    .in0({32{1'b0}}), .in1({32{1'b0}}), .in2({32{1'b0}}), .in3(multiplier_1_cout), .in4(divider_1_rem),
    .in5({32{1'b0}}), .in6({32{1'b0}}), .in7({32{1'b0}}), .in8({32{1'b0}}), .in9({32{1'b0}}),
    .in10({32{1'b0}}), .in11({32{1'b0}}), .in12({32{1'b0}}), .in13({32{1'b0}}), .in14({32{1'b0}}),
    .in15({32{1'b0}}), .out(Result_2), .sel(AluOP));
  Multiplexer #(.select(4), .width(1), .disabled("Z"), .enable("false")) multiplexer_3 (
    .in0(1'b0), .in1(1'b0), .in2(1'b0), .in3(1'b0), .in4(1'b0), .in5(1'b0), .in6(1'b0), .in7(1'b0),
    .in8(1'b0), .in9(1'b0), .in10(1'b0), .in11(comparator_1_lt[0]), .in12(comparator_2_lt[0]), .in13(1'b0),
    .in14(1'b0), .in15(1'b0), .out(out_6), .sel(AluOP));
  not not_1 (out_4, out_6);

  // Other names for the same wires on the sheet: Result2[31:0] = Result_2; S[3:0] = AluOP; tunnel = out_6;
  //   tunnel_t = out_4

  // Notes on the sheet:
  //   不要改变此引脚区域内容，也不要改变ALU封装形式
  //   输入引脚
  //   输出引脚
endmodule

module Regifile (
  input  [31:0] Din,
  input  Clk,
  input  WE,
  input  [4:0] R1_num,
  input  [4:0] W_num,
  input  [4:0] R2_num,
  output [31:0] R1,
  output [31:0] R2
);

  // RegisterFile registerfile_1: pin names not known; wires that end beside it: Din, Clk, WE, W_num, R1_num, R2_num, R1, R2

  // Notes on the sheet:
  //   t0
  //   s0
  //   a0
  //   s2
  //   t3
endmodule

module Regifile_down (
  input  [31:0] Din,
  input  Clk,
  input  WE,
  input  [4:0] R1_num,
  input  [4:0] W_num,
  input  [4:0] R2_num,
  output [31:0] R1,
  output [31:0] R2
);

  // RegisterFile registerfile_1: pin names not known; wires that end beside it: Din, Clk, WE, W_num, R1_num, R2_num, R1, R2
endmodule

module \中断按键参考电路  (
  input  \同步清零信号 ,
  output \与中断屏蔽位与 
);

  wire \_1号中断_out , and_1_out, clock_1_out, d_ff_1_q, or_1_out, or_2_out;

  Clock #(.highDuration(1), .lowDuration(1)) clock_1 (.out(clock_1_out));
  Button \_1号中断  (.out(\_1号中断_out ));
  LED #(.active("true")) \_1号中断等待指示灯  (.in(or_1_out));
  or or_1 (or_1_out, \与中断屏蔽位与 , d_ff_1_q);
  D_Flip_Flop #(.trigger("rising"), .Pre_Clr_Positions("LEGACY"), .NegatePresetClear("false"), .enable("true"), .NewFFLayout("false")) d_ff_1 (
    .clk(\_1号中断_out ), .D(1'b1), .Q(d_ff_1_q), .reset(\与中断屏蔽位与 ));  // open: Qn, preset, en
  or or_2 (or_2_out, d_ff_1_q, \与中断屏蔽位与 );
  and and_1 (and_1_out, or_2_out, ~\同步清零信号 );  // AND_Gate
  D_Flip_Flop #(.trigger("rising"), .Pre_Clr_Positions("LEGACY"), .NegatePresetClear("false"), .enable("true"), .NewFFLayout("false")) IR1 (
    .clk(clock_1_out), .D(and_1_out), .Q(\与中断屏蔽位与 ));  // open: Qn, preset, en, reset

  // Notes on the sheet:
  //   中断信号采样参考电路
  //   Reset 
endmodule

module \封装正确性测试  (
);

  wire IR1, IR2, IR3, MemW, RegW;
  wire [31:0] EX_PC, ID_PC, IF_PC, IR, LED, MDin, MDinr, MEM_PC, PC, RDin, RDinr, WB_PC;

  \单周期RISC_V  \u_单周期risc_v_1  (
    .IR1(IR1), .IR2(IR2), .IR3(IR3), .RegWrite(RegW), .MemWrite(MemW), .PC(PC), .IR(IR), .RDin(RDin),
    .MDin(MDin), .LedData(LED));
  \气泡流水线  \u_气泡流水线_1  (
    .RegWrite(RegW), .MemWrite(MemW), .IF_PC(IF_PC), .ID_PC(ID_PC), .EX_PC(EX_PC), .M_PC(MEM_PC),
    .WB_PC(WB_PC), .RDin(RDinr), .MDin(MDinr), .LedData(LED));
  \单周期_单级中断  \u_单周期_单级中断_1  (
    .IR1(IR1), .IR2(IR2), .IR3(IR3), .RegWrite(RegW), .MemWrite(MemW), .PC(PC), .IR(IR), .RDin(RDin),
    .MDin(MDin), .LedData(LED));
  \理想流水线  \u_理想流水线_1  (
    .RegWrite(RegW), .MemWrite(MemW), .IF_PC(IF_PC), .ID_PC(ID_PC), .EX_PC(EX_PC), .M_PC(MEM_PC),
    .WB_PC(WB_PC), .RDin(RDinr), .MDin(MDinr), .LedData(LED));
  \重定向流水线  \u_重定向流水线_1  (
    .RegWrite(RegW), .MemWrite(MemW), .IF_PC(IF_PC), .ID_PC(ID_PC), .EX_PC(EX_PC), .M_PC(MEM_PC),
    .WB_PC(WB_PC), .RDin(RDinr), .MDin(MDinr), .LedData(LED));
  \单周期_多级中断  \u_单周期_多级中断_1  (
    .IR1(IR1), .IR2(IR2), .IR3(IR3), .RegWrite(RegW), .MemWrite(MemW), .PC(PC), .IR(IR), .RDin(RDin),
    .MDin(MDin), .LedData(LED));

  // Notes on the sheet:
  //   单周期封装测试
  //   气泡流水封装测试
  //   单周期+单级中断封装测试
  //   请检查上面封装有无位宽不匹配，引脚标签是否和连接的标签相对应，否则无法在educoder平台上正确测试
  //   理想流水封装测试
  //   重定向流水封装测试
  //   单周期+多级中断封装测试
endmodule

module IF_ID (
  input  CLK,
  input  \使能端 ,
  input  \清零端 ,
  input  [31:0] IF_IR,
  input  [31:0] IF_PC,
  input  PD,
  output [31:0] ID_IR,
  output [31:0] ID_PC,
  output PD_2
);

  wire multiplexer_3_out;
  wire [31:0] multiplexer_1_out, multiplexer_2_out;

  Multiplexer #(.select(1), .width(32), .disabled("Z"), .enable("false")) multiplexer_1 (
    .in0(IF_IR), .in1({32{1'b0}}), .out(multiplexer_1_out), .sel(\清零端 ));
  Multiplexer #(.select(1), .width(32), .disabled("Z"), .enable("false")) multiplexer_2 (
    .in0(IF_PC), .in1({32{1'b0}}), .out(multiplexer_2_out), .sel(\清零端 ));
  Multiplexer #(.select(1), .width(1), .disabled("Z"), .enable("false")) multiplexer_3 (
    .in0(PD), .in1(1'b0), .out(multiplexer_3_out), .sel(\清零端 ));
  Register #(.width(32), .trigger("rising"), .Select("low")) register_1 (
    .D(multiplexer_1_out), .en(\使能端 ), .Q(ID_IR), .clk(CLK));  // open: clr
  Register #(.width(32), .trigger("rising"), .Select("low")) register_2 (
    .D(multiplexer_2_out), .en(\使能端 ), .Q(ID_PC), .clk(CLK));  // open: clr
  Register #(.width(1), .trigger("rising"), .Select("low")) register_3 (
    .D(multiplexer_3_out), .en(\使能端 ), .Q(PD_2), .clk(CLK));  // open: clr
endmodule

module ID_EX (
  input  CLK,
  input  \使能端 ,
  input  \清零端 ,
  input  [31:0] ID_IR,
  input  ID_MemToReg,
  input  ID_MemWrite,
  input  [31:0] ID_PC,
  input  [3:0] ID_AluOP,
  input  [31:0] ID_R1,
  input  ID_AluSrcB,
  input  ID_RegWrite,
  input  [31:0] ID_R2,
  input  ID_LB,
  input  [31:0] ID_IMM,
  input  ID_ecall,
  input  ID_JAL,
  input  ID_JALR,
  input  ID_Beq,
  input  ID_Bne,
  input  ID_URET,
  input  ID_BGE,
  input  [1:0] ID_R1_F,
  input  [1:0] ID_R2_F,
  input  PD,
  output [31:0] EX_IR,
  output EX_MemToReg,
  output EX_MemToReg_2,
  output [31:0] EX_PC,
  output [3:0] EX_AluOP,
  output [31:0] EX_R1,
  output EX_AluSrcB,
  output EX_RegWrite,
  output [31:0] EX_R2,
  output EX_LB,
  output [31:0] EX_IMM,
  output EX_ecall,
  output EX_JAL,
  output EX_JALR,
  output EX_Beq,
  output EX_Bne,
  output EX_URET,
  output EX_BGE,
  output [1:0] EX_R1_F,
  output [1:0] EX_R2_F,
  output PD_2
);

  wire multiplexer_6_out, multiplexer_7_out, multiplexer_9_out, multiplexer_10_out, multiplexer_11_out,
       multiplexer_12_out, multiplexer_13_out, multiplexer_14_out, multiplexer_15_out, multiplexer_16_out,
       multiplexer_17_out, multiplexer_18_out, multiplexer_21_out;
  wire [1:0] multiplexer_19_out, multiplexer_20_out;
  wire [3:0] multiplexer_8_out;
  wire [31:0] multiplexer_1_out, multiplexer_2_out, multiplexer_3_out, multiplexer_4_out, multiplexer_5_out;

  Multiplexer #(.select(1), .width(32), .disabled("Z"), .enable("false")) multiplexer_1 (
    .in0(ID_IR), .in1({32{1'b0}}), .out(multiplexer_1_out), .sel(\清零端 ));
  Multiplexer #(.select(1), .width(32), .disabled("Z"), .enable("false")) multiplexer_2 (
    .in0(ID_PC), .in1({32{1'b0}}), .out(multiplexer_2_out), .sel(\清零端 ));
  Multiplexer #(.select(1), .width(32), .disabled("Z"), .enable("false")) multiplexer_3 (
    .in0(ID_R1), .in1({32{1'b0}}), .out(multiplexer_3_out), .sel(\清零端 ));
  Multiplexer #(.select(1), .width(32), .disabled("Z"), .enable("false")) multiplexer_4 (
    .in0(ID_R2), .in1({32{1'b0}}), .out(multiplexer_4_out), .sel(\清零端 ));
  Multiplexer #(.select(1), .width(32), .disabled("Z"), .enable("false")) multiplexer_5 (
    .in0(ID_IMM), .in1({32{1'b0}}), .out(multiplexer_5_out), .sel(\清零端 ));
  Register #(.width(32), .trigger("rising"), .Select("low")) register_1 (
    .D(multiplexer_1_out), .en(\使能端 ), .Q(EX_IR), .clk(CLK));  // open: clr
  Register #(.width(32), .trigger("rising"), .Select("low")) register_2 (
    .D(multiplexer_2_out), .en(\使能端 ), .Q(EX_PC), .clk(CLK));  // open: clr
  Register #(.width(32), .trigger("rising"), .Select("low")) register_3 (
    .D(multiplexer_3_out), .en(\使能端 ), .Q(EX_R1), .clk(CLK));  // open: clr
  Register #(.width(32), .trigger("rising"), .Select("low")) register_4 (
    .D(multiplexer_4_out), .en(\使能端 ), .Q(EX_R2), .clk(CLK));  // open: clr
  Register #(.width(32), .trigger("rising"), .Select("low")) register_5 (
    .D(multiplexer_5_out), .en(\使能端 ), .Q(EX_IMM), .clk(CLK));  // open: clr
  Multiplexer #(.select(1), .width(1), .disabled("Z"), .enable("false")) multiplexer_6 (
    .in0(ID_MemToReg), .in1(1'b0), .out(multiplexer_6_out), .sel(\清零端 ));
  Multiplexer #(.select(1), .width(1), .disabled("Z"), .enable("false")) multiplexer_7 (
    .in0(ID_MemWrite), .in1(1'b0), .out(multiplexer_7_out), .sel(\清零端 ));
  Multiplexer #(.select(1), .width(4), .disabled("Z"), .enable("false")) multiplexer_8 (
    .in0(ID_AluOP), .in1(4'b0000), .out(multiplexer_8_out), .sel(\清零端 ));
  Multiplexer #(.select(1), .width(1), .disabled("Z"), .enable("false")) multiplexer_9 (
    .in0(ID_AluSrcB), .in1(1'b0), .out(multiplexer_9_out), .sel(\清零端 ));
  Multiplexer #(.select(1), .width(1), .disabled("Z"), .enable("false")) multiplexer_10 (
    .in0(ID_RegWrite), .in1(1'b0), .out(multiplexer_10_out), .sel(\清零端 ));
  Multiplexer #(.select(1), .width(1), .disabled("Z"), .enable("false")) multiplexer_11 (
    .in0(ID_LB), .in1(1'b0), .out(multiplexer_11_out), .sel(\清零端 ));
  Multiplexer #(.select(1), .width(1), .disabled("Z"), .enable("false")) multiplexer_12 (
    .in0(ID_ecall), .in1(1'b0), .out(multiplexer_12_out), .sel(\清零端 ));
  Multiplexer #(.select(1), .width(1), .disabled("Z"), .enable("false")) multiplexer_13 (
    .in0(ID_JAL), .in1(1'b0), .out(multiplexer_13_out), .sel(\清零端 ));
  Multiplexer #(.select(1), .width(1), .disabled("Z"), .enable("false")) multiplexer_14 (
    .in0(ID_JALR), .in1(1'b0), .out(multiplexer_14_out), .sel(\清零端 ));
  Multiplexer #(.select(1), .width(1), .disabled("Z"), .enable("false")) multiplexer_15 (
    .in0(ID_Beq), .in1(1'b0), .out(multiplexer_15_out), .sel(\清零端 ));
  Multiplexer #(.select(1), .width(1), .disabled("Z"), .enable("false")) multiplexer_16 (
    .in0(ID_Bne), .in1(1'b0), .out(multiplexer_16_out), .sel(\清零端 ));
  Multiplexer #(.select(1), .width(1), .disabled("Z"), .enable("false")) multiplexer_17 (
    .in0(ID_URET), .in1(1'b0), .out(multiplexer_17_out), .sel(\清零端 ));
  Multiplexer #(.select(1), .width(1), .disabled("Z"), .enable("false")) multiplexer_18 (
    .in0(ID_BGE), .in1(1'b0), .out(multiplexer_18_out), .sel(\清零端 ));
  Multiplexer #(.select(1), .width(2), .disabled("Z"), .enable("false")) multiplexer_19 (
    .in0(ID_R1_F), .in1(2'b00), .out(multiplexer_19_out), .sel(\清零端 ));
  Multiplexer #(.select(1), .width(2), .disabled("Z"), .enable("false")) multiplexer_20 (
    .in0(ID_R2_F), .in1(2'b00), .out(multiplexer_20_out), .sel(\清零端 ));
  Multiplexer #(.select(1), .width(1), .disabled("Z"), .enable("false")) multiplexer_21 (
    .in0(PD), .in1(1'b0), .out(multiplexer_21_out), .sel(\清零端 ));
  Register #(.width(1), .trigger("rising"), .Select("low")) register_6 (
    .D(multiplexer_6_out), .en(\使能端 ), .Q(EX_MemToReg), .clk(CLK));  // open: clr
  Register #(.width(1), .trigger("rising"), .Select("low")) register_7 (
    .D(multiplexer_7_out), .en(\使能端 ), .Q(EX_MemToReg_2), .clk(CLK));  // open: clr
  Register #(.width(4), .trigger("rising"), .Select("low")) register_8 (
    .D(multiplexer_8_out), .en(\使能端 ), .Q(EX_AluOP), .clk(CLK));  // open: clr
  Register #(.width(1), .trigger("rising"), .Select("low")) register_9 (
    .D(multiplexer_9_out), .en(\使能端 ), .Q(EX_AluSrcB), .clk(CLK));  // open: clr
  Register #(.width(1), .trigger("rising"), .Select("low")) register_10 (
    .D(multiplexer_10_out), .en(\使能端 ), .Q(EX_RegWrite), .clk(CLK));  // open: clr
  Register #(.width(1), .trigger("rising"), .Select("low")) register_11 (
    .D(multiplexer_11_out), .en(\使能端 ), .Q(EX_LB), .clk(CLK));  // open: clr
  Register #(.width(1), .trigger("rising"), .Select("low")) register_12 (
    .D(multiplexer_12_out), .en(\使能端 ), .Q(EX_ecall), .clk(CLK));  // open: clr
  Register #(.width(1), .trigger("rising"), .Select("low")) register_13 (
    .D(multiplexer_13_out), .en(\使能端 ), .Q(EX_JAL), .clk(CLK));  // open: clr
  Register #(.width(1), .trigger("rising"), .Select("low")) register_14 (
    .D(multiplexer_14_out), .en(\使能端 ), .Q(EX_JALR), .clk(CLK));  // open: clr
  Register #(.width(1), .trigger("rising"), .Select("low")) register_15 (
    .D(multiplexer_15_out), .en(\使能端 ), .Q(EX_Beq), .clk(CLK));  // open: clr
  Register #(.width(1), .trigger("rising"), .Select("low")) register_16 (
    .D(multiplexer_16_out), .en(\使能端 ), .Q(EX_Bne), .clk(CLK));  // open: clr
  Register #(.width(1), .trigger("rising"), .Select("low")) register_17 (
    .D(multiplexer_17_out), .en(\使能端 ), .Q(EX_URET), .clk(CLK));  // open: clr
  Register #(.width(1), .trigger("rising"), .Select("low")) register_18 (
    .D(multiplexer_18_out), .en(\使能端 ), .Q(EX_BGE), .clk(CLK));  // open: clr
  Register #(.width(2), .trigger("rising"), .Select("low")) register_19 (
    .D(multiplexer_19_out), .en(\使能端 ), .Q(EX_R1_F), .clk(CLK));  // open: clr
  Register #(.width(2), .trigger("rising"), .Select("low")) register_20 (
    .D(multiplexer_20_out), .en(\使能端 ), .Q(EX_R2_F), .clk(CLK));  // open: clr
  Register #(.width(1), .trigger("rising"), .Select("low")) register_21 (
    .D(multiplexer_21_out), .en(\使能端 ), .Q(PD_2), .clk(CLK));  // open: clr
endmodule

module EX_MEM (
  input  CLK,
  input  \使能端 ,
  input  \清零端 ,
  input  [31:0] EX_IR,
  input  ID_MemToReg,
  input  ID_MemWrite,
  input  [31:0] EX_PC,
  input  ID_RegWrite,
  input  [31:0] EX_R1,
  input  ID_ecall,
  input  [31:0] EX_R2,
  input  ID_URET,
  input  ID_JAL,
  input  [31:0] EX_ALU,
  input  ID_JALR,
  input  [31:0] EX_DATA,
  input  ID_LB,
  output [31:0] MEM_IR,
  output EX_MemToReg,
  output EX_MemWrite,
  output [31:0] MEM_PC,
  output EX_RegWrite,
  output [31:0] MEM_R1,
  output EX_ecall,
  output [31:0] MEM_R2,
  output EX_URET,
  output EX_JAL,
  output [31:0] MEM_ALU,
  output EX_JALR,
  output [31:0] MEM_DATA,
  output EX_LB
);

  wire multiplexer_7_out, multiplexer_8_out, multiplexer_9_out, multiplexer_10_out, multiplexer_11_out,
       multiplexer_12_out, multiplexer_13_out, multiplexer_14_out;
  wire [31:0] multiplexer_1_out, multiplexer_2_out, multiplexer_3_out, multiplexer_4_out, multiplexer_5_out,
       multiplexer_6_out;

  Multiplexer #(.select(1), .width(32), .disabled("Z"), .enable("false")) multiplexer_1 (
    .in0(EX_IR), .in1({32{1'b0}}), .out(multiplexer_1_out), .sel(\清零端 ));
  Multiplexer #(.select(1), .width(32), .disabled("Z"), .enable("false")) multiplexer_2 (
    .in0(EX_PC), .in1({32{1'b0}}), .out(multiplexer_2_out), .sel(\清零端 ));
  Multiplexer #(.select(1), .width(32), .disabled("Z"), .enable("false")) multiplexer_3 (
    .in0(EX_R1), .in1({32{1'b0}}), .out(multiplexer_3_out), .sel(\清零端 ));
  Multiplexer #(.select(1), .width(32), .disabled("Z"), .enable("false")) multiplexer_4 (
    .in0(EX_R2), .in1({32{1'b0}}), .out(multiplexer_4_out), .sel(\清零端 ));
  Multiplexer #(.select(1), .width(32), .disabled("Z"), .enable("false")) multiplexer_5 (
    .in0(EX_ALU), .in1({32{1'b0}}), .out(multiplexer_5_out), .sel(\清零端 ));
  Multiplexer #(.select(1), .width(32), .disabled("Z"), .enable("false")) multiplexer_6 (
    .in0(EX_DATA), .in1({32{1'b0}}), .out(multiplexer_6_out), .sel(\清零端 ));
  Register #(.width(32), .trigger("rising"), .Select("low")) register_1 (
    .D(multiplexer_1_out), .en(\使能端 ), .Q(MEM_IR), .clk(CLK));  // open: clr
  Register #(.width(32), .trigger("rising"), .Select("low")) register_2 (
    .D(multiplexer_2_out), .en(\使能端 ), .Q(MEM_PC), .clk(CLK));  // open: clr
  Register #(.width(32), .trigger("rising"), .Select("low")) register_3 (
    .D(multiplexer_3_out), .en(\使能端 ), .Q(MEM_R1), .clk(CLK));  // open: clr
  Register #(.width(32), .trigger("rising"), .Select("low")) register_4 (
    .D(multiplexer_4_out), .en(\使能端 ), .Q(MEM_R2), .clk(CLK));  // open: clr
  Register #(.width(32), .trigger("rising"), .Select("low")) register_5 (
    .D(multiplexer_5_out), .en(\使能端 ), .Q(MEM_ALU), .clk(CLK));  // open: clr
  Register #(.width(32), .trigger("rising"), .Select("low")) register_6 (
    .D(multiplexer_6_out), .en(\使能端 ), .Q(MEM_DATA), .clk(CLK));  // open: clr
  Multiplexer #(.select(1), .width(1), .disabled("Z"), .enable("false")) multiplexer_7 (
    .in0(ID_MemToReg), .in1(1'b0), .out(multiplexer_7_out), .sel(\清零端 ));
  Multiplexer #(.select(1), .width(1), .disabled("Z"), .enable("false")) multiplexer_8 (
    .in0(ID_MemWrite), .in1(1'b0), .out(multiplexer_8_out), .sel(\清零端 ));
  Multiplexer #(.select(1), .width(1), .disabled("Z"), .enable("false")) multiplexer_9 (
    .in0(ID_RegWrite), .in1(1'b0), .out(multiplexer_9_out), .sel(\清零端 ));
  Multiplexer #(.select(1), .width(1), .disabled("Z"), .enable("false")) multiplexer_10 (
    .in0(ID_ecall), .in1(1'b0), .out(multiplexer_10_out), .sel(\清零端 ));
  Multiplexer #(.select(1), .width(1), .disabled("Z"), .enable("false")) multiplexer_11 (
    .in0(ID_URET), .in1(1'b0), .out(multiplexer_11_out), .sel(\清零端 ));
  Multiplexer #(.select(1), .width(1), .disabled("Z"), .enable("false")) multiplexer_12 (
    .in0(ID_JAL), .in1(1'b0), .out(multiplexer_12_out), .sel(\清零端 ));
  Multiplexer #(.select(1), .width(1), .disabled("Z"), .enable("false")) multiplexer_13 (
    .in0(ID_JALR), .in1(1'b0), .out(multiplexer_13_out), .sel(\清零端 ));
  Multiplexer #(.select(1), .width(1), .disabled("Z"), .enable("false")) multiplexer_14 (
    .in0(ID_LB), .in1(1'b0), .out(multiplexer_14_out), .sel(\清零端 ));
  Register #(.width(1), .trigger("rising"), .Select("low")) register_7 (
    .D(multiplexer_7_out), .en(\使能端 ), .Q(EX_MemToReg), .clk(CLK));  // open: clr
  Register #(.width(1), .trigger("rising"), .Select("low")) register_8 (
    .D(multiplexer_8_out), .en(\使能端 ), .Q(EX_MemWrite), .clk(CLK));  // open: clr
  Register #(.width(1), .trigger("rising"), .Select("low")) register_9 (
    .D(multiplexer_9_out), .en(\使能端 ), .Q(EX_RegWrite), .clk(CLK));  // open: clr
  Register #(.width(1), .trigger("rising"), .Select("low")) register_10 (
    .D(multiplexer_10_out), .en(\使能端 ), .Q(EX_ecall), .clk(CLK));  // open: clr
  Register #(.width(1), .trigger("rising"), .Select("low")) register_11 (
    .D(multiplexer_11_out), .en(\使能端 ), .Q(EX_URET), .clk(CLK));  // open: clr
  Register #(.width(1), .trigger("rising"), .Select("low")) register_12 (
    .D(multiplexer_12_out), .en(\使能端 ), .Q(EX_JAL), .clk(CLK));  // open: clr
  Register #(.width(1), .trigger("rising"), .Select("low")) register_13 (
    .D(multiplexer_13_out), .en(\使能端 ), .Q(EX_JALR), .clk(CLK));  // open: clr
  Register #(.width(1), .trigger("rising"), .Select("low")) register_14 (
    .D(multiplexer_14_out), .en(\使能端 ), .Q(EX_LB), .clk(CLK));  // open: clr
endmodule

module MEM_WB (
  input  CLK,
  input  \使能端 ,
  input  \清零端 ,
  input  [31:0] MEM_IR,
  input  ID_MemToReg,
  input  ID_RegWrite,
  input  [31:0] MEM_PC,
  input  ID_ecall,
  input  ID_URET,
  input  [31:0] MEM_R1,
  input  ID_JAL,
  input  [31:0] MEM_R2,
  input  ID_JALR,
  input  ID_LB,
  input  [31:0] MEM_DIN,
  input  [31:0] MEM_ALU,
  output [31:0] WB_IR,
  output EX_MemToReg,
  output EX_RegWrite,
  output [31:0] WB_PC,
  output EX_ecall,
  output EX_URET,
  output [31:0] WB_R1,
  output EX_JAL,
  output [31:0] WB_R2,
  output EX_JALR,
  output EX_LB,
  output [31:0] WB_DIN,
  output [31:0] WB_ALU
);

  wire multiplexer_7_out, multiplexer_8_out, multiplexer_9_out, multiplexer_10_out, multiplexer_11_out,
       multiplexer_12_out, multiplexer_13_out;
  wire [31:0] multiplexer_1_out, multiplexer_2_out, multiplexer_3_out, multiplexer_4_out, multiplexer_5_out,
       multiplexer_6_out;

  Multiplexer #(.select(1), .width(32), .disabled("Z"), .enable("false")) multiplexer_1 (
    .in0(MEM_IR), .in1({32{1'b0}}), .out(multiplexer_1_out), .sel(\清零端 ));
  Multiplexer #(.select(1), .width(32), .disabled("Z"), .enable("false")) multiplexer_2 (
    .in0(MEM_PC), .in1({32{1'b0}}), .out(multiplexer_2_out), .sel(\清零端 ));
  Multiplexer #(.select(1), .width(32), .disabled("Z"), .enable("false")) multiplexer_3 (
    .in0(MEM_R1), .in1({32{1'b0}}), .out(multiplexer_3_out), .sel(\清零端 ));
  Multiplexer #(.select(1), .width(32), .disabled("Z"), .enable("false")) multiplexer_4 (
    .in0(MEM_R2), .in1({32{1'b0}}), .out(multiplexer_4_out), .sel(\清零端 ));
  Multiplexer #(.select(1), .width(32), .disabled("Z"), .enable("false")) multiplexer_5 (
    .in0(MEM_DIN), .in1({32{1'b0}}), .out(multiplexer_5_out), .sel(\清零端 ));
  Multiplexer #(.select(1), .width(32), .disabled("Z"), .enable("false")) multiplexer_6 (
    .in0(MEM_ALU), .in1({32{1'b0}}), .out(multiplexer_6_out), .sel(\清零端 ));
  Register #(.width(32), .trigger("rising"), .Select("low")) register_1 (
    .D(multiplexer_1_out), .en(\使能端 ), .Q(WB_IR), .clk(CLK));  // open: clr
  Register #(.width(32), .trigger("rising"), .Select("low")) register_2 (
    .D(multiplexer_2_out), .en(\使能端 ), .Q(WB_PC), .clk(CLK));  // open: clr
  Register #(.width(32), .trigger("rising"), .Select("low")) register_3 (
    .D(multiplexer_3_out), .en(\使能端 ), .Q(WB_R1), .clk(CLK));  // open: clr
  Register #(.width(32), .trigger("rising"), .Select("low")) register_4 (
    .D(multiplexer_4_out), .en(\使能端 ), .Q(WB_R2), .clk(CLK));  // open: clr
  Register #(.width(32), .trigger("rising"), .Select("low")) register_5 (
    .D(multiplexer_5_out), .en(\使能端 ), .Q(WB_DIN), .clk(CLK));  // open: clr
  Register #(.width(32), .trigger("rising"), .Select("low")) register_6 (
    .D(multiplexer_6_out), .en(\使能端 ), .Q(WB_ALU), .clk(CLK));  // open: clr
  Multiplexer #(.select(1), .width(1), .disabled("Z"), .enable("false")) multiplexer_7 (
    .in0(ID_MemToReg), .in1(1'b0), .out(multiplexer_7_out), .sel(\清零端 ));
  Multiplexer #(.select(1), .width(1), .disabled("Z"), .enable("false")) multiplexer_8 (
    .in0(ID_RegWrite), .in1(1'b0), .out(multiplexer_8_out), .sel(\清零端 ));
  Multiplexer #(.select(1), .width(1), .disabled("Z"), .enable("false")) multiplexer_9 (
    .in0(ID_ecall), .in1(1'b0), .out(multiplexer_9_out), .sel(\清零端 ));
  Multiplexer #(.select(1), .width(1), .disabled("Z"), .enable("false")) multiplexer_10 (
    .in0(ID_URET), .in1(1'b0), .out(multiplexer_10_out), .sel(\清零端 ));
  Multiplexer #(.select(1), .width(1), .disabled("Z"), .enable("false")) multiplexer_11 (
    .in0(ID_JAL), .in1(1'b0), .out(multiplexer_11_out), .sel(\清零端 ));
  Multiplexer #(.select(1), .width(1), .disabled("Z"), .enable("false")) multiplexer_12 (
    .in0(ID_JALR), .in1(1'b0), .out(multiplexer_12_out), .sel(\清零端 ));
  Multiplexer #(.select(1), .width(1), .disabled("Z"), .enable("false")) multiplexer_13 (
    .in0(ID_LB), .in1(1'b0), .out(multiplexer_13_out), .sel(\清零端 ));
  Register #(.width(1), .trigger("rising"), .Select("low")) register_7 (
    .D(multiplexer_7_out), .en(\使能端 ), .Q(EX_MemToReg), .clk(CLK));  // open: clr
  Register #(.width(1), .trigger("rising"), .Select("low")) register_8 (
    .D(multiplexer_8_out), .en(\使能端 ), .Q(EX_RegWrite), .clk(CLK));  // open: clr
  Register #(.width(1), .trigger("rising"), .Select("low")) register_9 (
    .D(multiplexer_9_out), .en(\使能端 ), .Q(EX_ecall), .clk(CLK));  // open: clr
  Register #(.width(1), .trigger("rising"), .Select("low")) register_10 (
    .D(multiplexer_10_out), .en(\使能端 ), .Q(EX_URET), .clk(CLK));  // open: clr
  Register #(.width(1), .trigger("rising"), .Select("low")) register_11 (
    .D(multiplexer_11_out), .en(\使能端 ), .Q(EX_JAL), .clk(CLK));  // open: clr
  Register #(.width(1), .trigger("rising"), .Select("low")) register_12 (
    .D(multiplexer_12_out), .en(\使能端 ), .Q(EX_JALR), .clk(CLK));  // open: clr
  Register #(.width(1), .trigger("rising"), .Select("low")) register_13 (
    .D(multiplexer_13_out), .en(\使能端 ), .Q(EX_LB), .clk(CLK));  // open: clr
endmodule

module \LoadUse信号生成  (
  input  R1Used,
  input  EX_MemToReg,
  input  [4:0] ID_R1,
  input  [4:0] EX_RD,
  input  [4:0] ID_R2,
  input  R2Used,
  output LoadUse
);

  wire and_1_out, and_2_out, comparator_1_eq, comparator_2_eq, comparator_3_eq, comparator_4_eq;

  Comparator #(.width(5), .mode("twosComplement")) comparator_1 (
    .a(ID_R1), .b({5{1'b0}}), .eq(comparator_1_eq));  // open: gt, lt
  Comparator #(.width(5), .mode("twosComplement")) comparator_2 (
    .a(ID_R1), .b(EX_RD), .eq(comparator_2_eq));  // open: gt, lt
  Comparator #(.width(5), .mode("twosComplement")) comparator_3 (
    .a(EX_RD), .b(ID_R2), .eq(comparator_3_eq));  // open: gt, lt
  Comparator #(.width(5), .mode("twosComplement")) comparator_4 (
    .a({5{1'b0}}), .b(ID_R2), .eq(comparator_4_eq));  // open: gt, lt
  and and_1 (and_1_out, R1Used, EX_MemToReg, comparator_2_eq, ~comparator_1_eq);  // AND_Gate
  and and_2 (and_2_out, ~comparator_4_eq, comparator_3_eq, EX_MemToReg, R2Used);  // AND_Gate
  or or_1 (LoadUse, and_1_out, and_2_out);
endmodule

module \used控制电路  (
  input  OP2,
  input  OP3,
  input  OP4,
  input  OP5,
  input  OP6,
  input  F12,
  input  F13,
  input  F14,
  input  F25,
  input  F30,
  output RsUsed,
  output RtUesd
);

  wire and_1_out, and_2_out, and_3_out, and_4_out, and_5_out, and_6_out, and_7_out, and_8_out, and_9_out,
       and_10_out, and_11_out, and_12_out, and_13_out, and_14_out, and_15_out, and_16_out, and_17_out,
       and_18_out, and_19_out, and_20_out, and_21_out, and_22_out, and_23_out, and_24_out, and_25_out,
       and_26_out, and_27_out, and_28_out, and_29_out, and_30_out, and_31_out, and_32_out, and_33_out,
       and_34_out, and_35_out, and_36_out, not_1_out, not_2_out, not_3_out, not_4_out, not_5_out, not_6_out,
       not_7_out, not_8_out, not_9_out, not_10_out, not_11_out, not_12_out, not_13_out, not_14_out,
       not_15_out, not_16_out, not_17_out, not_18_out, not_19_out, not_20_out, not_21_out, not_22_out,
       not_23_out, not_24_out, not_25_out, not_26_out, not_27_out, not_28_out, not_29_out, not_30_out,
       not_31_out, not_32_out, not_33_out, not_34_out, not_35_out, not_36_out, not_37_out, not_38_out,
       not_39_out, not_40_out, not_41_out, not_42_out, not_43_out, not_44_out, not_45_out, not_46_out,
       not_47_out, not_48_out, not_49_out, not_50_out, not_51_out, not_52_out, not_53_out, not_54_out,
       not_55_out, not_56_out, not_57_out, not_58_out, not_59_out, not_60_out, not_61_out, not_62_out,
       not_63_out, not_64_out, not_65_out, not_66_out, not_67_out, not_68_out, not_69_out, not_70_out,
       not_71_out, not_72_out, not_73_out, not_74_out, not_75_out, not_76_out, not_77_out, not_78_out,
       not_79_out, not_80_out, not_81_out, not_82_out, not_83_out, not_84_out, not_85_out, not_86_out,
       not_87_out, not_88_out, not_89_out, not_90_out, not_91_out, not_92_out, not_93_out, not_94_out,
       not_95_out, not_96_out, not_97_out, not_98_out, not_99_out, not_100_out, not_101_out, not_102_out,
       not_103_out, not_104_out, not_105_out, not_106_out, not_107_out, not_108_out, not_109_out,
       not_110_out, not_111_out, not_112_out, not_113_out, not_114_out, not_115_out, not_116_out,
       not_117_out, not_118_out, not_119_out, not_120_out, not_121_out, not_122_out, not_123_out,
       not_124_out, not_125_out, not_126_out, not_127_out, not_128_out, not_129_out, not_130_out,
       not_131_out, not_132_out, not_133_out, not_134_out, not_135_out, not_136_out, not_137_out,
       not_138_out, not_139_out, not_140_out, not_141_out, not_142_out, not_143_out, not_144_out,
       not_145_out, not_146_out, not_147_out, not_148_out, not_149_out, not_150_out, not_151_out,
       not_152_out, not_153_out, not_154_out, not_155_out, not_156_out, not_157_out, not_158_out,
       not_159_out, not_160_out, not_161_out, not_162_out, not_163_out, not_164_out, not_165_out,
       not_166_out, not_167_out, not_168_out, not_169_out, not_170_out, not_171_out, not_172_out,
       not_173_out, not_174_out, not_175_out, not_176_out, not_177_out, not_178_out, not_179_out,
       not_180_out, not_181_out, not_182_out, not_183_out, not_184_out, not_185_out, not_186_out,
       not_187_out, not_188_out, not_189_out, not_190_out, not_191_out, not_192_out, not_193_out,
       not_194_out, not_195_out, not_196_out, not_197_out, not_198_out, not_199_out, not_200_out,
       not_201_out, not_202_out, not_203_out, not_204_out, not_205_out, not_206_out, not_207_out,
       not_208_out, not_209_out, not_210_out, not_211_out, not_212_out, not_213_out, not_214_out,
       not_215_out, not_216_out, not_217_out, not_218_out, not_219_out, not_220_out, not_221_out, not_222_out;

  not not_1 (not_1_out, F30);
  not not_2 (not_2_out, F25);
  not not_3 (not_3_out, F14);
  not not_4 (not_4_out, F13);
  not not_5 (not_5_out, F12);
  not not_6 (not_6_out, OP6);
  not not_7 (not_7_out, OP3);
  not not_8 (not_8_out, OP2);
  not not_9 (not_9_out, F25);
  not not_10 (not_10_out, F14);
  not not_11 (not_11_out, F13);
  not not_12 (not_12_out, F12);
  not not_13 (not_13_out, OP6);
  not not_14 (not_14_out, OP3);
  not not_15 (not_15_out, OP2);
  not not_16 (not_16_out, F30);
  not not_17 (not_17_out, F25);
  not not_18 (not_18_out, OP6);
  not not_19 (not_19_out, OP3);
  not not_20 (not_20_out, OP2);
  not not_21 (not_21_out, F30);
  not not_22 (not_22_out, F25);
  not not_23 (not_23_out, F12);
  not not_24 (not_24_out, OP6);
  not not_25 (not_25_out, OP3);
  not not_26 (not_26_out, OP2);
  not not_27 (not_27_out, F30);
  not not_28 (not_28_out, F25);
  not not_29 (not_29_out, F14);
  not not_30 (not_30_out, F12);
  not not_31 (not_31_out, OP6);
  not not_32 (not_32_out, OP3);
  not not_33 (not_33_out, OP2);
  not not_34 (not_34_out, F30);
  not not_35 (not_35_out, F25);
  not not_36 (not_36_out, F14);
  not not_37 (not_37_out, OP6);
  not not_38 (not_38_out, OP3);
  not not_39 (not_39_out, OP2);
  not not_40 (not_40_out, F14);
  not not_41 (not_41_out, F13);
  not not_42 (not_42_out, F12);
  not not_43 (not_43_out, OP6);
  not not_44 (not_44_out, OP5);
  not not_45 (not_45_out, OP3);
  not not_46 (not_46_out, OP2);
  not not_47 (not_47_out, OP6);
  not not_48 (not_48_out, OP5);
  not not_49 (not_49_out, OP3);
  not not_50 (not_50_out, OP2);
  not not_51 (not_51_out, F12);
  not not_52 (not_52_out, OP6);
  not not_53 (not_53_out, OP5);
  not not_54 (not_54_out, OP3);
  not not_55 (not_55_out, OP2);
  not not_56 (not_56_out, F13);
  not not_57 (not_57_out, F12);
  not not_58 (not_58_out, OP6);
  not not_59 (not_59_out, OP5);
  not not_60 (not_60_out, OP3);
  not not_61 (not_61_out, OP2);
  not not_62 (not_62_out, F14);
  not not_63 (not_63_out, F12);
  not not_64 (not_64_out, OP6);
  not not_65 (not_65_out, OP5);
  not not_66 (not_66_out, OP3);
  not not_67 (not_67_out, OP2);
  not not_68 (not_68_out, F30);
  not not_69 (not_69_out, F25);
  not not_70 (not_70_out, F14);
  not not_71 (not_71_out, F13);
  not not_72 (not_72_out, OP6);
  not not_73 (not_73_out, OP5);
  not not_74 (not_74_out, OP3);
  not not_75 (not_75_out, OP2);
  not not_76 (not_76_out, F30);
  not not_77 (not_77_out, F25);
  not not_78 (not_78_out, F13);
  not not_79 (not_79_out, OP6);
  not not_80 (not_80_out, OP5);
  not not_81 (not_81_out, OP3);
  not not_82 (not_82_out, OP2);
  not not_83 (not_83_out, F25);
  not not_84 (not_84_out, F13);
  not not_85 (not_85_out, OP6);
  not not_86 (not_86_out, OP5);
  not not_87 (not_87_out, OP3);
  not not_88 (not_88_out, OP2);
  not not_89 (not_89_out, F14);
  not not_90 (not_90_out, F12);
  not not_91 (not_91_out, OP6);
  not not_92 (not_92_out, OP5);
  not not_93 (not_93_out, OP4);
  not not_94 (not_94_out, OP3);
  not not_95 (not_95_out, OP2);
  not not_96 (not_96_out, F14);
  not not_97 (not_97_out, F12);
  not not_98 (not_98_out, OP6);
  not not_99 (not_99_out, OP4);
  not not_100 (not_100_out, OP3);
  not not_101 (not_101_out, OP2);
  not not_102 (not_102_out, F30);
  not not_103 (not_103_out, F25);
  not not_104 (not_104_out, F14);
  not not_105 (not_105_out, F13);
  not not_106 (not_106_out, F12);
  not not_107 (not_107_out, OP3);
  not not_108 (not_108_out, OP2);
  not not_109 (not_109_out, F14);
  not not_110 (not_110_out, F13);
  not not_111 (not_111_out, F12);
  not not_112 (not_112_out, OP4);
  not not_113 (not_113_out, OP3);
  not not_114 (not_114_out, OP2);
  not not_115 (not_115_out, F14);
  not not_116 (not_116_out, F13);
  not not_117 (not_117_out, OP4);
  not not_118 (not_118_out, OP3);
  not not_119 (not_119_out, OP2);
  not not_120 (not_120_out, F14);
  not not_121 (not_121_out, F13);
  not not_122 (not_122_out, F12);
  not not_123 (not_123_out, OP4);
  not not_124 (not_124_out, OP3);
  not not_125 (not_125_out, F30);
  not not_126 (not_126_out, F25);
  not not_127 (not_127_out, F13);
  not not_128 (not_128_out, F12);
  not not_129 (not_129_out, OP6);
  not not_130 (not_130_out, OP3);
  not not_131 (not_131_out, OP2);
  not not_132 (not_132_out, F14);
  not not_133 (not_133_out, OP6);
  not not_134 (not_134_out, OP5);
  not not_135 (not_135_out, OP3);
  not not_136 (not_136_out, OP2);
  not not_137 (not_137_out, F14);
  not not_138 (not_138_out, F13);
  not not_139 (not_139_out, F12);
  not not_140 (not_140_out, OP6);
  not not_141 (not_141_out, OP5);
  not not_142 (not_142_out, OP4);
  not not_143 (not_143_out, OP3);
  not not_144 (not_144_out, OP2);
  not not_145 (not_145_out, F13);
  not not_146 (not_146_out, OP4);
  not not_147 (not_147_out, OP3);
  not not_148 (not_148_out, OP2);
  not not_149 (not_149_out, F30);
  not not_150 (not_150_out, F25);
  not not_151 (not_151_out, F14);
  not not_152 (not_152_out, F13);
  not not_153 (not_153_out, F12);
  not not_154 (not_154_out, OP6);
  not not_155 (not_155_out, OP3);
  not not_156 (not_156_out, OP2);
  not not_157 (not_157_out, F25);
  not not_158 (not_158_out, F14);
  not not_159 (not_159_out, F13);
  not not_160 (not_160_out, F12);
  not not_161 (not_161_out, OP6);
  not not_162 (not_162_out, OP3);
  not not_163 (not_163_out, OP2);
  not not_164 (not_164_out, F30);
  not not_165 (not_165_out, F25);
  not not_166 (not_166_out, OP6);
  not not_167 (not_167_out, OP3);
  not not_168 (not_168_out, OP2);
  not not_169 (not_169_out, F30);
  not not_170 (not_170_out, F25);
  not not_171 (not_171_out, F12);
  not not_172 (not_172_out, OP6);
  not not_173 (not_173_out, OP3);
  not not_174 (not_174_out, OP2);
  not not_175 (not_175_out, F30);
  not not_176 (not_176_out, F25);
  not not_177 (not_177_out, F14);
  not not_178 (not_178_out, F12);
  not not_179 (not_179_out, OP6);
  not not_180 (not_180_out, OP3);
  not not_181 (not_181_out, OP2);
  not not_182 (not_182_out, F30);
  not not_183 (not_183_out, F25);
  not not_184 (not_184_out, F14);
  not not_185 (not_185_out, OP6);
  not not_186 (not_186_out, OP3);
  not not_187 (not_187_out, OP2);
  not not_188 (not_188_out, F14);
  not not_189 (not_189_out, F12);
  not not_190 (not_190_out, OP6);
  not not_191 (not_191_out, OP4);
  not not_192 (not_192_out, OP3);
  not not_193 (not_193_out, OP2);
  not not_194 (not_194_out, F30);
  not not_195 (not_195_out, F25);
  not not_196 (not_196_out, F14);
  not not_197 (not_197_out, F13);
  not not_198 (not_198_out, F12);
  not not_199 (not_199_out, OP3);
  not not_200 (not_200_out, OP2);
  not not_201 (not_201_out, F14);
  not not_202 (not_202_out, F13);
  not not_203 (not_203_out, F12);
  not not_204 (not_204_out, OP4);
  not not_205 (not_205_out, OP3);
  not not_206 (not_206_out, OP2);
  not not_207 (not_207_out, F14);
  not not_208 (not_208_out, F13);
  not not_209 (not_209_out, OP4);
  not not_210 (not_210_out, OP3);
  not not_211 (not_211_out, OP2);
  not not_212 (not_212_out, F30);
  not not_213 (not_213_out, F25);
  not not_214 (not_214_out, F13);
  not not_215 (not_215_out, F12);
  not not_216 (not_216_out, OP6);
  not not_217 (not_217_out, OP3);
  not not_218 (not_218_out, OP2);
  not not_219 (not_219_out, F13);
  not not_220 (not_220_out, OP4);
  not not_221 (not_221_out, OP3);
  not not_222 (not_222_out, OP2);
  and and_1 (and_1_out, not_1_out, not_2_out, not_3_out, not_4_out, not_5_out, not_6_out, OP5, OP4, not_7_out, not_8_out);
  and and_2 (and_2_out, F30, not_9_out, not_10_out, not_11_out, not_12_out, not_13_out, OP5, OP4, not_14_out, not_15_out);
  and and_3 (and_3_out, not_16_out, not_17_out, F14, F13, F12, not_18_out, OP5, OP4, not_19_out, not_20_out);
  and and_4 (and_4_out, not_21_out, not_22_out, F14, F13, not_23_out, not_24_out, OP5, OP4, not_25_out, not_26_out);
  and and_5 (and_5_out, not_27_out, not_28_out, not_29_out, F13, not_30_out, not_31_out, OP5, OP4, not_32_out, not_33_out);
  and and_6 (and_6_out, not_34_out, not_35_out, not_36_out, F13, F12, not_37_out, OP5, OP4, not_38_out, not_39_out);
  and and_7 (and_7_out, not_40_out, not_41_out, not_42_out, not_43_out, not_44_out, OP4, not_45_out, not_46_out);
  and and_8 (and_8_out, F14, F13, F12, not_47_out, not_48_out, OP4, not_49_out, not_50_out);
  and and_9 (and_9_out, F14, F13, not_51_out, not_52_out, not_53_out, OP4, not_54_out, not_55_out);
  and and_10 (and_10_out, F14, not_56_out, not_57_out, not_58_out, not_59_out, OP4, not_60_out, not_61_out);
  and and_11 (and_11_out, not_62_out, F13, not_63_out, not_64_out, not_65_out, OP4, not_66_out, not_67_out);
  and and_12 (and_12_out, not_68_out, not_69_out, not_70_out, not_71_out, F12, not_72_out, not_73_out, OP4, not_74_out, not_75_out);
  and and_13 (and_13_out, not_76_out, not_77_out, F14, not_78_out, F12, not_79_out, not_80_out, OP4, not_81_out, not_82_out);
  and and_14 (and_14_out, F30, not_83_out, F14, not_84_out, F12, not_85_out, not_86_out, OP4, not_87_out, not_88_out);
  and and_15 (and_15_out, not_89_out, F13, not_90_out, not_91_out, not_92_out, not_93_out, not_94_out, not_95_out);
  and and_16 (and_16_out, not_96_out, F13, not_97_out, not_98_out, OP5, not_99_out, not_100_out, not_101_out);
  and and_17 (and_17_out, not_102_out, not_103_out, not_104_out, not_105_out, not_106_out, OP6, OP5, OP4, not_107_out, not_108_out);
  and and_18 (and_18_out, not_109_out, not_110_out, not_111_out, OP6, OP5, not_112_out, not_113_out, not_114_out);
  and and_19 (and_19_out, not_115_out, not_116_out, F12, OP6, OP5, not_117_out, not_118_out, not_119_out);
  and and_20 (and_20_out, not_120_out, not_121_out, not_122_out, OP6, OP5, not_123_out, not_124_out, OP2);
  and and_21 (and_21_out, not_125_out, not_126_out, F14, not_127_out, not_128_out, not_129_out, OP5, OP4, not_130_out, not_131_out);
  and and_22 (and_22_out, not_132_out, F13, F12, not_133_out, not_134_out, OP4, not_135_out, not_136_out);
  and and_23 (and_23_out, not_137_out, not_138_out, not_139_out, not_140_out, not_141_out, not_142_out, not_143_out, not_144_out);
  and and_24 (and_24_out, F14, not_145_out, F12, OP6, OP5, not_146_out, not_147_out, not_148_out);
  and and_25 (and_25_out, not_149_out, not_150_out, not_151_out, not_152_out, not_153_out, not_154_out, OP5, OP4, not_155_out, not_156_out);
  and and_26 (and_26_out, F30, not_157_out, not_158_out, not_159_out, not_160_out, not_161_out, OP5, OP4, not_162_out, not_163_out);
  and and_27 (and_27_out, not_164_out, not_165_out, F14, F13, F12, not_166_out, OP5, OP4, not_167_out, not_168_out);
  and and_28 (and_28_out, not_169_out, not_170_out, F14, F13, not_171_out, not_172_out, OP5, OP4, not_173_out, not_174_out);
  and and_29 (and_29_out, not_175_out, not_176_out, not_177_out, F13, not_178_out, not_179_out, OP5, OP4, not_180_out, not_181_out);
  and and_30 (and_30_out, not_182_out, not_183_out, not_184_out, F13, F12, not_185_out, OP5, OP4, not_186_out, not_187_out);
  and and_31 (and_31_out, not_188_out, F13, not_189_out, not_190_out, OP5, not_191_out, not_192_out, not_193_out);
  and and_32 (and_32_out, not_194_out, not_195_out, not_196_out, not_197_out, not_198_out, OP6, OP5, OP4, not_199_out, not_200_out);
  and and_33 (and_33_out, not_201_out, not_202_out, not_203_out, OP6, OP5, not_204_out, not_205_out, not_206_out);
  and and_34 (and_34_out, not_207_out, not_208_out, F12, OP6, OP5, not_209_out, not_210_out, not_211_out);
  and and_35 (and_35_out, not_212_out, not_213_out, F14, not_214_out, not_215_out, not_216_out, OP5, OP4, not_217_out, not_218_out);
  and and_36 (and_36_out, F14, not_219_out, F12, OP6, OP5, not_220_out, not_221_out, not_222_out);
  or or_1 (RtUesd, and_25_out, and_26_out, and_27_out, and_28_out, and_29_out, and_30_out, and_31_out, and_32_out, and_33_out, and_34_out, and_35_out, and_36_out);
  or or_2 (RsUsed, and_1_out, and_2_out, and_3_out, and_4_out, and_5_out, and_6_out, and_7_out, and_8_out, and_9_out, and_10_out, and_11_out, and_12_out, and_13_out, and_14_out, and_15_out, and_16_out, and_17_out, and_18_out, and_19_out, and_20_out, and_21_out, and_22_out, and_23_out, and_24_out);
  \R1_F_R2_F信号生成  \r1_f_r2_f信号生成_1  ();  // open: R1Used, ID_R1, EX_RegWrite, EX_RD, MEM_RegWrite, MEM_RD, R2Used, ID_R2, R1_F, R2_F
endmodule

module \R1_F_R2_F信号生成  (
  input  R1Used,
  input  [4:0] ID_R1,
  input  EX_RegWrite,
  input  [4:0] EX_RD,
  input  MEM_RegWrite,
  input  [4:0] MEM_RD,
  input  R2Used,
  input  [4:0] ID_R2,
  output [1:0] R1_F,
  output [1:0] R2_F
);

  wire comparator_1_eq, comparator_2_eq, comparator_3_eq, comparator_4_eq, comparator_5_eq, comparator_6_eq,
       not_1_out, not_2_out;
  wire [1:0] and_1_out, and_3_out;

  not not_1 (not_1_out, comparator_1_eq);
  Comparator #(.width(5), .mode("twosComplement")) comparator_1 (
    .a(ID_R1), .b({5{1'b0}}), .eq(comparator_1_eq));  // open: gt, lt
  Comparator #(.width(5), .mode("twosComplement")) comparator_2 (
    .a(ID_R1), .b(EX_RD), .eq(comparator_2_eq));  // open: gt, lt
  Comparator #(.width(5), .mode("twosComplement")) comparator_3 (
    .a(ID_R1), .b(MEM_RD), .eq(comparator_3_eq));  // open: gt, lt
  Comparator #(.width(5), .mode("twosComplement")) comparator_4 (
    .a(ID_R2), .b({5{1'b0}}), .eq(comparator_4_eq));  // open: gt, lt
  not not_2 (not_2_out, comparator_4_eq);
  Comparator #(.width(5), .mode("twosComplement")) comparator_5 (
    .a(ID_R2), .b(EX_RD), .eq(comparator_5_eq));  // open: gt, lt
  Comparator #(.width(5), .mode("twosComplement")) comparator_6 (
    .a(ID_R2), .b(MEM_RD), .eq(comparator_6_eq));  // open: gt, lt
  and and_1 (and_1_out[0], R1Used, not_1_out, EX_RegWrite, comparator_2_eq);
  and and_2 (and_1_out[1], not_1_out, R1Used, MEM_RegWrite, comparator_3_eq);
  and and_3 (and_3_out[0], R2Used, not_2_out, EX_RegWrite, comparator_5_eq);
  and and_4 (and_3_out[1], not_2_out, R2Used, MEM_RegWrite, comparator_6_eq);
  Multiplexer #(.select(2), .width(2), .disabled("Z"), .enable("false")) multiplexer_1 (
    .in0(2'b00), .in1(2'b10), .in2(2'b01), .in3(2'b10), .out(R1_F), .sel(and_1_out));
  Multiplexer #(.select(2), .width(2), .disabled("Z"), .enable("false")) multiplexer_2 (
    .in0(2'b00), .in1(2'b10), .in2(2'b01), .in3(2'b10), .out(R2_F), .sel(and_3_out));
endmodule

module \中断控制器  (
  input  IRA,
  input  Clr1,
  input  IRB,
  input  Clr2,
  input  IRC,
  input  Clr3,
  input  CLK,
  input  RST,
  output [1:0] \中断号 ,
  output \中断请求 ,
  output W1,
  output W2,
  output W3
);

  wire and_1_out, and_2_out, and_3_out, not_1_out, not_2_out, not_3_out, or_4_out, or_5_out, or_6_out,
       or_7_out, or_8_out, or_9_out, register_1_q, register_2_q, register_3_q, register_4_q, register_5_q,
       register_6_q;

  or or_1 (W1, register_4_q, register_1_q);
  or or_2 (W2, register_5_q, register_2_q);
  or or_3 (W3, register_6_q, register_3_q);
  Register #(.width(1), .trigger("rising"), .Select("low")) register_1 (
    .D(1'b1), .Q(register_1_q), .clk(IRA), .clr(or_4_out));  // open: en
  or or_4 (or_4_out, register_4_q, RST);
  Register #(.width(1), .trigger("rising"), .Select("low")) register_2 (
    .D(1'b1), .Q(register_2_q), .clk(IRB), .clr(or_5_out));  // open: en
  or or_5 (or_5_out, register_5_q, RST);
  Register #(.width(1), .trigger("rising"), .Select("low")) register_3 (
    .D(1'b1), .Q(register_3_q), .clk(IRC), .clr(or_6_out));  // open: en
  or or_6 (or_6_out, register_6_q, RST);
  or or_7 (or_7_out, register_1_q, register_4_q);
  or or_8 (or_8_out, register_2_q, register_5_q);
  or or_9 (or_9_out, register_3_q, register_6_q);
  and and_1 (and_1_out, or_7_out, not_1_out);
  not not_1 (not_1_out, Clr1);
  and and_2 (and_2_out, or_8_out, not_2_out);
  not not_2 (not_2_out, Clr2);
  and and_3 (and_3_out, or_9_out, not_3_out);
  not not_3 (not_3_out, Clr3);
  Register #(.width(1), .trigger("rising"), .Select("low")) register_4 (
    .D(and_1_out), .Q(register_4_q), .clk(CLK), .clr(RST));  // open: en
  Register #(.width(1), .trigger("rising"), .Select("low")) register_5 (
    .D(and_2_out), .Q(register_5_q), .clk(CLK), .clr(RST));  // open: en
  Register #(.width(1), .trigger("rising"), .Select("low")) register_6 (
    .D(and_3_out), .Q(register_6_q), .clk(CLK), .clr(RST));  // open: en
  Priority_Encoder #(.select(2), .disabled("Z")) priority_encoder_1 (
    .in0(1'b1), .in1(register_4_q), .in2(register_5_q), .in3(register_6_q), .out(\中断号 ));  // open: gs, en_out, en_in
  or or_10 (\中断请求 , register_4_q, register_5_q, register_6_q);
endmodule

module \全相联cache  (
  input  [31:0] IF_PC,
  input  [31:0] EX_PC,
  input  [31:0] BlockDataIn,
  input  BlkDataReady,
  input  CLK,
  input  jumpormot,
  output [31:0] DataOut,
  output out_8
);

  wire and_1_out, and_2_out, and_3_out, and_4_out, and_5_out, and_6_out, and_7_out, and_8_out, and_9_out,
       and_26_out, and_27_out, and_28_out, and_29_out, and_30_out, and_31_out, and_32_out, and_33_out,
       and_34_out, and_35_out, and_36_out, and_37_out, and_38_out, and_39_out, and_40_out, and_41_out,
       comparator_1_eq, comparator_2_eq, comparator_3_eq, comparator_4_eq, comparator_5_eq, comparator_6_eq,
       comparator_7_eq, comparator_8_eq, comparator_9_eq, comparator_10_eq, comparator_11_eq,
       comparator_12_eq, comparator_13_eq, comparator_14_eq, comparator_15_eq, comparator_16_eq, full, Hit,
       L0, l0_t, L1, l1_t, L2, l2_t, L3, l3_t, L4, l4_t, L5, l5_t, L6, l6_t, L7, l7_t, Miss, not_1_out,
       not_2_out, not_3_out, not_4_out, not_5_out, not_6_out, not_7_out, not_8_out, or_1_out, or_2_out,
       or_3_out, or_4_out, or_5_out, or_6_out, or_7_out, or_8_out, v0, v1, v2, v3, v4, v5, v6, v7, writer0,
       writer1, writer2, writer3, writer4, writer5, writer6, writer7;
  wire [1:0] register_25_q, register_26_q, register_27_q, register_28_q, register_29_q, register_30_q,
       register_31_q, register_32_q, \状态转化_1_z0 , \状态转化_2_z0 , \状态转化_3_z0 , \状态转化_4_z0 , \状态转化_5_z0 ,
       \状态转化_6_z0 , \状态转化_7_z0 , \状态转化_8_z0 ;
  wire [2:0] \max3_三路比较_1_max_num , \max3_三路比较_2_max_num , \max3_三路比较_3_max_num , \max3_三路比较_4_max_num ,
       \max3_三路比较_5_max_num , \max3_三路比较_6_max_num , multiplexer_1_out, out, row;
  wire [15:0] c0, c1, c2, c3, c4, c5, c6, c7, \max3_三路比较_1_max , \max3_三路比较_2_max , \max3_三路比较_3_max ,
       \max3_三路比较_4_max , \max3_三路比较_5_max , \max3_三路比较_6_max ;
  wire [31:0] register_17_q, register_18_q, register_19_q, register_20_q, register_21_q, register_22_q,
       register_23_q, register_24_q, tag0, tag1, tag2, tag3, tag4, tag5, tag6, tag7;

  Register #(.width(1), .trigger("rising"), .Select("low")) register_1 (
    .D(1'b1), .en(writer0), .Q(v0), .clk(CLK));  // open: clr
  Register #(.width(1), .trigger("rising"), .Select("low")) register_2 (
    .D(1'b1), .en(writer1), .Q(v1), .clk(CLK));  // open: clr
  Register #(.width(1), .trigger("rising"), .Select("low")) register_3 (
    .D(1'b1), .en(writer2), .Q(v2), .clk(CLK));  // open: clr
  Register #(.width(1), .trigger("rising"), .Select("low")) register_4 (
    .D(1'b1), .en(writer3), .Q(v3), .clk(CLK));  // open: clr
  Register #(.width(1), .trigger("rising"), .Select("low")) register_5 (
    .D(1'b1), .en(writer4), .Q(v4), .clk(CLK));  // open: clr
  Register #(.width(1), .trigger("rising"), .Select("low")) register_6 (
    .D(1'b1), .en(writer5), .Q(v5), .clk(CLK));  // open: clr
  Register #(.width(1), .trigger("rising"), .Select("low")) register_7 (
    .D(1'b1), .en(writer6), .Q(v6), .clk(CLK));  // open: clr
  Register #(.width(1), .trigger("rising"), .Select("low")) register_8 (
    .D(1'b1), .en(writer7), .Q(v7), .clk(CLK));  // open: clr
  Register #(.width(32), .trigger("rising"), .Select("low")) register_9 (
    .D(EX_PC), .en(writer0), .Q(tag0), .clk(CLK));  // open: clr
  Register #(.width(32), .trigger("rising"), .Select("low")) register_10 (
    .D(EX_PC), .en(writer1), .Q(tag1), .clk(CLK));  // open: clr
  Register #(.width(32), .trigger("rising"), .Select("low")) register_11 (
    .D(EX_PC), .en(writer2), .Q(tag2), .clk(CLK));  // open: clr
  Register #(.width(32), .trigger("rising"), .Select("low")) register_12 (
    .D(EX_PC), .en(writer3), .Q(tag3), .clk(CLK));  // open: clr
  Register #(.width(32), .trigger("rising"), .Select("low")) register_13 (
    .D(EX_PC), .en(writer4), .Q(tag4), .clk(CLK));  // open: clr
  Register #(.width(32), .trigger("rising"), .Select("low")) register_14 (
    .D(EX_PC), .en(writer5), .Q(tag5), .clk(CLK));  // open: clr
  Register #(.width(32), .trigger("rising"), .Select("low")) register_15 (
    .D(EX_PC), .en(writer6), .Q(tag6), .clk(CLK));  // open: clr
  Register #(.width(32), .trigger("rising"), .Select("low")) register_16 (
    .D(EX_PC), .en(writer7), .Q(tag7), .clk(CLK));  // open: clr
  Counter #(.width(16), .max('hffff), .ongoal("wrap"), .trigger("rising"), .behavior("new")) counter_1 (
    .load(or_1_out), .D({16{1'b0}}), .Q(c0), .clk(CLK));  // open: count, carry, clr, preset, down
  or or_1 (or_1_out, L0, and_1_out);
  Counter #(.width(16), .max('hffff), .ongoal("wrap"), .trigger("rising"), .behavior("new")) counter_2 (
    .load(or_2_out), .D({16{1'b0}}), .Q(c1), .clk(CLK));  // open: count, carry, clr, preset, down
  or or_2 (or_2_out, L1, and_2_out);
  Counter #(.width(16), .max('hffff), .ongoal("wrap"), .trigger("rising"), .behavior("new")) counter_3 (
    .load(or_3_out), .D({16{1'b0}}), .Q(c2), .clk(CLK));  // open: count, carry, clr, preset, down
  or or_3 (or_3_out, L2, and_3_out);
  Counter #(.width(16), .max('hffff), .ongoal("wrap"), .trigger("rising"), .behavior("new")) counter_4 (
    .load(or_4_out), .D({16{1'b0}}), .Q(c3), .clk(CLK));  // open: count, carry, clr, preset, down
  or or_4 (or_4_out, L3, and_4_out);
  Counter #(.width(16), .max('hffff), .ongoal("wrap"), .trigger("rising"), .behavior("new")) counter_5 (
    .load(or_5_out), .D({16{1'b0}}), .Q(c4), .clk(CLK));  // open: count, carry, clr, preset, down
  or or_5 (or_5_out, L4, and_5_out);
  Counter #(.width(16), .max('hffff), .ongoal("wrap"), .trigger("rising"), .behavior("new")) counter_6 (
    .load(or_6_out), .D({16{1'b0}}), .Q(c5), .clk(CLK));  // open: count, carry, clr, preset, down
  or or_6 (or_6_out, L5, and_6_out);
  Counter #(.width(16), .max('hffff), .ongoal("wrap"), .trigger("rising"), .behavior("new")) counter_7 (
    .load(or_7_out), .D({16{1'b0}}), .Q(c6), .clk(CLK));  // open: count, carry, clr, preset, down
  or or_7 (or_7_out, L6, and_7_out);
  Counter #(.width(16), .max('hffff), .ongoal("wrap"), .trigger("rising"), .behavior("new")) counter_8 (
    .load(or_8_out), .D({16{1'b0}}), .Q(c7), .clk(CLK));  // open: count, carry, clr, preset, down
  or or_8 (or_8_out, L7, and_8_out);
  Register #(.width(32), .trigger("rising"), .Select("low")) register_17 (
    .D(BlockDataIn), .en(writer0), .Q(register_17_q), .clk(CLK));  // open: clr
  Register #(.width(32), .trigger("rising"), .Select("low")) register_18 (
    .D(BlockDataIn), .en(writer1), .Q(register_18_q), .clk(CLK));  // open: clr
  Register #(.width(32), .trigger("rising"), .Select("low")) register_19 (
    .D(BlockDataIn), .en(writer2), .Q(register_19_q), .clk(CLK));  // open: clr
  Register #(.width(32), .trigger("rising"), .Select("low")) register_20 (
    .D(BlockDataIn), .en(writer3), .Q(register_20_q), .clk(CLK));  // open: clr
  Register #(.width(32), .trigger("rising"), .Select("low")) register_21 (
    .D(BlockDataIn), .en(writer4), .Q(register_21_q), .clk(CLK));  // open: clr
  Register #(.width(32), .trigger("rising"), .Select("low")) register_22 (
    .D(BlockDataIn), .en(writer5), .Q(register_22_q), .clk(CLK));  // open: clr
  Register #(.width(32), .trigger("falling"), .Select("low")) register_23 (
    .D(BlockDataIn), .en(writer6), .Q(register_23_q), .clk(CLK));  // open: clr
  Register #(.width(32), .trigger("rising"), .Select("low")) register_24 (
    .D(BlockDataIn), .en(writer7), .Q(register_24_q), .clk(CLK));  // open: clr
  assign DataOut = L0 ? register_17_q : 32'bz;  // Controlled_Buffer controlled_buffer_1
  assign DataOut = L1 ? register_18_q : 32'bz;  // Controlled_Buffer controlled_buffer_2
  assign DataOut = L2 ? register_19_q : 32'bz;  // Controlled_Buffer controlled_buffer_3
  assign DataOut = L3 ? register_20_q : 32'bz;  // Controlled_Buffer controlled_buffer_4
  assign DataOut = L4 ? register_21_q : 32'bz;  // Controlled_Buffer controlled_buffer_5
  assign DataOut = L5 ? register_22_q : 32'bz;  // Controlled_Buffer controlled_buffer_6
  assign DataOut = L6 ? register_23_q : 32'bz;  // Controlled_Buffer controlled_buffer_7
  assign DataOut = L7 ? register_24_q : 32'bz;  // Controlled_Buffer controlled_buffer_8
  and and_1 (and_1_out, writer0, BlkDataReady);
  and and_2 (and_2_out, writer1, BlkDataReady);
  and and_3 (and_3_out, writer2, BlkDataReady);
  and and_4 (and_4_out, writer3, BlkDataReady);
  and and_5 (and_5_out, writer4, BlkDataReady);
  and and_6 (and_6_out, writer5, BlkDataReady);
  and and_7 (and_7_out, writer6, BlkDataReady);
  and and_8 (and_8_out, writer7, BlkDataReady);
  // Probe on out
  Multiplexer #(.select(1), .width(3), .disabled("Z"), .enable("false")) multiplexer_1 (
    .in0(row), .in1(out), .out(multiplexer_1_out), .sel(full));
  \Max3_三路比较  \max3_三路比较_1  (
    .Y(c1), .X(c0), .Y_num(3'b001), .X_num(3'b000), .MAX(\max3_三路比较_1_max ), .Max_num(\max3_三路比较_1_max_num ));
  \Max3_三路比较  \max3_三路比较_2  (
    .Y(c3), .X(c2), .Y_num(3'b011), .X_num(3'b010), .MAX(\max3_三路比较_2_max ), .Max_num(\max3_三路比较_2_max_num ));
  \Max3_三路比较  \max3_三路比较_3  (
    .Y(c5), .X(c4), .Y_num(3'b101), .X_num(3'b100), .MAX(\max3_三路比较_3_max ), .Max_num(\max3_三路比较_3_max_num ));
  \Max3_三路比较  \max3_三路比较_4  (
    .Y(c7), .X(c6), .Y_num(3'b111), .X_num(3'b110), .MAX(\max3_三路比较_4_max ), .Max_num(\max3_三路比较_4_max_num ));
  Demultiplexer #(.select(3), .width(1), .tristate("false"), .disabled("Z"), .enable("false")) demultiplexer_1 (
    .out0(writer0), .out1(writer1), .out2(writer2), .out3(writer3), .out4(writer4), .out5(writer5),
    .out6(writer6), .out7(writer7), .in(and_9_out), .sel(multiplexer_1_out));
  and and_9 (and_9_out, BlkDataReady, Miss);
  \Max3_三路比较  \max3_三路比较_5  (
    .Y(\max3_三路比较_2_max ), .X(\max3_三路比较_1_max ), .Y_num(\max3_三路比较_2_max_num ),
    .X_num(\max3_三路比较_1_max_num ), .MAX(\max3_三路比较_5_max ), .Max_num(\max3_三路比较_5_max_num ));
  \Max3_三路比较  \max3_三路比较_6  (
    .Y(\max3_三路比较_4_max ), .X(\max3_三路比较_3_max ), .Y_num(\max3_三路比较_4_max_num ),
    .X_num(\max3_三路比较_3_max_num ), .MAX(\max3_三路比较_6_max ), .Max_num(\max3_三路比较_6_max_num ));
  \Max3_三路比较  \max3_三路比较_7  (
    .Y(\max3_三路比较_6_max ), .X(\max3_三路比较_5_max ), .Y_num(\max3_三路比较_6_max_num ),
    .X_num(\max3_三路比较_5_max_num ), .Max_num(out));  // open: MAX
  Comparator #(.width(32), .mode("twosComplement")) comparator_1 (
    .a(EX_PC), .b(tag0), .eq(comparator_1_eq));  // open: gt, lt
  not not_1 (not_1_out, v0);
  and and_10 (l0_t, comparator_1_eq, v0);
  Comparator #(.width(32), .mode("twosComplement")) comparator_2 (
    .a(EX_PC), .b(tag1), .eq(comparator_2_eq));  // open: gt, lt
  not not_2 (not_2_out, v1);
  and and_11 (l1_t, comparator_2_eq, v1);
  Comparator #(.width(32), .mode("twosComplement")) comparator_3 (
    .a(EX_PC), .b(tag2), .eq(comparator_3_eq));  // open: gt, lt
  not not_3 (not_3_out, v2);
  and and_12 (l2_t, comparator_3_eq, v2);
  Comparator #(.width(32), .mode("twosComplement")) comparator_4 (
    .a(EX_PC), .b(tag3), .eq(comparator_4_eq));  // open: gt, lt
  not not_4 (not_4_out, v3);
  and and_13 (l3_t, comparator_4_eq, v3);
  Comparator #(.width(32), .mode("twosComplement")) comparator_5 (
    .a(EX_PC), .b(tag4), .eq(comparator_5_eq));  // open: gt, lt
  not not_5 (not_5_out, v4);
  and and_14 (l4_t, comparator_5_eq, v4);
  Comparator #(.width(32), .mode("twosComplement")) comparator_6 (
    .a(EX_PC), .b(tag5), .eq(comparator_6_eq));  // open: gt, lt
  not not_6 (not_6_out, v5);
  and and_15 (l5_t, comparator_6_eq, v5);
  Comparator #(.width(32), .mode("twosComplement")) comparator_7 (
    .a(EX_PC), .b(tag6), .eq(comparator_7_eq));  // open: gt, lt
  not not_7 (not_7_out, v6);
  and and_16 (l6_t, comparator_7_eq, v6);
  Comparator #(.width(32), .mode("twosComplement")) comparator_8 (
    .a(EX_PC), .b(tag7), .eq(comparator_8_eq));  // open: gt, lt
  not not_8 (not_8_out, v7);
  and and_17 (l7_t, comparator_8_eq, v7);
  Comparator #(.width(32), .mode("twosComplement")) comparator_9 (
    .a(IF_PC), .b(tag0), .eq(comparator_9_eq));  // open: gt, lt
  // NOT_Gate not_9 has open pins: in=v0, out=open
  and and_18 (L0, comparator_9_eq, v0);
  Comparator #(.width(32), .mode("twosComplement")) comparator_10 (
    .a(IF_PC), .b(tag1), .eq(comparator_10_eq));  // open: gt, lt
  // NOT_Gate not_10 has open pins: in=v1, out=open
  and and_19 (L1, comparator_10_eq, v1);
  Comparator #(.width(32), .mode("twosComplement")) comparator_11 (
    .a(IF_PC), .b(tag2), .eq(comparator_11_eq));  // open: gt, lt
  // NOT_Gate not_11 has open pins: in=v2, out=open
  and and_20 (L2, comparator_11_eq, v2);
  Comparator #(.width(32), .mode("twosComplement")) comparator_12 (
    .a(IF_PC), .b(tag3), .eq(comparator_12_eq));  // open: gt, lt
  // NOT_Gate not_12 has open pins: in=v3, out=open
  and and_21 (L3, comparator_12_eq, v3);
  Comparator #(.width(32), .mode("twosComplement")) comparator_13 (
    .a(IF_PC), .b(tag4), .eq(comparator_13_eq));  // open: gt, lt
  // NOT_Gate not_13 has open pins: in=v4, out=open
  and and_22 (L4, comparator_13_eq, v4);
  Comparator #(.width(32), .mode("twosComplement")) comparator_14 (
    .a(IF_PC), .b(tag5), .eq(comparator_14_eq));  // open: gt, lt
  // NOT_Gate not_14 has open pins: in=v5, out=open
  and and_23 (L5, comparator_14_eq, v5);
  Comparator #(.width(32), .mode("twosComplement")) comparator_15 (
    .a(IF_PC), .b(tag6), .eq(comparator_15_eq));  // open: gt, lt
  // NOT_Gate not_15 has open pins: in=v6, out=open
  and and_24 (L6, comparator_15_eq, v6);
  Comparator #(.width(32), .mode("twosComplement")) comparator_16 (
    .a(IF_PC), .b(tag7), .eq(comparator_16_eq));  // open: gt, lt
  // NOT_Gate not_16 has open pins: in=v7, out=open
  and and_25 (L7, comparator_16_eq, v7);
  or or_9 (Hit, l0_t, l1_t, l2_t, l3_t, l4_t, l5_t, l6_t, l7_t);
  not not_17 (Miss, Hit);
  // Probe on row
  Priority_Encoder #(.select(3), .disabled("Z")) priority_encoder_1 (
    .in0(not_1_out), .in1(not_2_out), .in2(not_3_out), .in3(not_4_out), .in4(not_5_out), .in5(not_6_out),
    .in6(not_7_out), .in7(not_8_out), .out(row), .en_out(full), .en_in(1'b1));  // open: gs
  \状态转化  \u_状态转化_1  (
    .Y1(register_25_q[1]), .Y0(register_25_q[0]), .\跳转 (jumpormot), .Z1(\状态转化_1_z0 [1]), .Z0(\状态转化_1_z0 [0]));
  \状态转化  \u_状态转化_2  (
    .Y1(register_26_q[1]), .Y0(register_26_q[0]), .\跳转 (jumpormot), .Z1(\状态转化_2_z0 [1]), .Z0(\状态转化_2_z0 [0]));
  \状态转化  \u_状态转化_3  (
    .Y1(register_27_q[1]), .Y0(register_27_q[0]), .\跳转 (jumpormot), .Z1(\状态转化_3_z0 [1]), .Z0(\状态转化_3_z0 [0]));
  \状态转化  \u_状态转化_4  (
    .Y1(register_28_q[1]), .Y0(register_28_q[0]), .\跳转 (jumpormot), .Z1(\状态转化_4_z0 [1]), .Z0(\状态转化_4_z0 [0]));
  \状态转化  \u_状态转化_5  (
    .Y1(register_29_q[1]), .Y0(register_29_q[0]), .\跳转 (jumpormot), .Z1(\状态转化_5_z0 [1]), .Z0(\状态转化_5_z0 [0]));
  \状态转化  \u_状态转化_6  (
    .Y1(register_30_q[1]), .Y0(register_30_q[0]), .\跳转 (jumpormot), .Z1(\状态转化_6_z0 [1]), .Z0(\状态转化_6_z0 [0]));
  \状态转化  \u_状态转化_7  (
    .Y1(register_31_q[1]), .Y0(register_31_q[0]), .\跳转 (jumpormot), .Z1(\状态转化_7_z0 [1]), .Z0(\状态转化_7_z0 [0]));
  \状态转化  \u_状态转化_8  (
    .Y1(register_32_q[1]), .Y0(register_32_q[0]), .\跳转 (jumpormot), .Z1(\状态转化_8_z0 [1]), .Z0(\状态转化_8_z0 [0]));
  and and_26 (and_26_out, BlkDataReady, l0_t);
  and and_27 (and_27_out, BlkDataReady, l1_t);
  and and_28 (and_28_out, BlkDataReady, l2_t);
  and and_29 (and_29_out, BlkDataReady, l3_t);
  and and_30 (and_30_out, BlkDataReady, l4_t);
  and and_31 (and_31_out, BlkDataReady, l5_t);
  and and_32 (and_32_out, BlkDataReady, l6_t);
  and and_33 (and_33_out, BlkDataReady, l7_t);
  Register #(.width(2), .trigger("falling"), .Select("low")) register_25 (
    .D(\状态转化_1_z0 ), .en(and_26_out), .Q(register_25_q), .clk(CLK));  // open: clr
  Register #(.width(2), .trigger("falling"), .Select("low")) register_26 (
    .D(\状态转化_2_z0 ), .en(and_27_out), .Q(register_26_q), .clk(CLK));  // open: clr
  Register #(.width(2), .trigger("falling"), .Select("low")) register_27 (
    .D(\状态转化_3_z0 ), .en(and_28_out), .Q(register_27_q), .clk(CLK));  // open: clr
  Register #(.width(2), .trigger("falling"), .Select("low")) register_28 (
    .D(\状态转化_4_z0 ), .en(and_29_out), .Q(register_28_q), .clk(CLK));  // open: clr
  Register #(.width(2), .trigger("falling"), .Select("low")) register_29 (
    .D(\状态转化_5_z0 ), .en(and_30_out), .Q(register_29_q), .clk(CLK));  // open: clr
  Register #(.width(2), .trigger("falling"), .Select("low")) register_30 (
    .D(\状态转化_6_z0 ), .en(and_31_out), .Q(register_30_q), .clk(CLK));  // open: clr
  Register #(.width(2), .trigger("falling"), .Select("low")) register_31 (
    .D(\状态转化_7_z0 ), .en(and_32_out), .Q(register_31_q), .clk(CLK));  // open: clr
  Register #(.width(2), .trigger("falling"), .Select("low")) register_32 (
    .D(\状态转化_8_z0 ), .en(and_33_out), .Q(register_32_q), .clk(CLK));  // open: clr
  and and_34 (and_34_out, register_25_q[1], L0);
  and and_35 (and_35_out, register_26_q[1], L1);
  and and_36 (and_36_out, register_27_q[1], L2);
  and and_37 (and_37_out, register_28_q[1], L3);
  and and_38 (and_38_out, register_29_q[1], L4);
  and and_39 (and_39_out, register_30_q[1], L5);
  and and_40 (and_40_out, register_31_q[1], L6);
  and and_41 (and_41_out, register_32_q[1], L7);
  or or_10 (out_8, and_34_out, and_35_out, and_36_out, and_37_out, and_38_out, and_39_out, and_40_out, and_41_out);

  // Other names for the same wires on the sheet: Blk[31:0] = BlockDataIn; BlkReady = BlkDataReady; jump = out_8;
  //   SlotData[31:0] = DataOut

  // Notes on the sheet:
  //   输入引脚区
  //   请勿增改引脚，请勿修改子电路封装
  //   电路功能：利用上面给定的隧道构建8行的Cache，cache映射方式自选
  //   请在下方利用上方输入输出引脚的隧道信号构建电路，ctrl+d复制选择部件
  //   输出引脚区
  //   分支指令地址写入
  //   查找指令
endmodule

module \Max3_三路比较  (
  input  [15:0] Y,
  input  [15:0] X,
  input  [2:0] Y_num,
  input  [2:0] X_num,
  output [15:0] MAX,
  output [2:0] Max_num
);

  wire comparator_1_eq, comparator_1_gt, or_1_out;

  Multiplexer #(.select(1), .width(16), .disabled("Z"), .enable("false")) multiplexer_1 (
    .in0(Y), .in1(X), .out(MAX), .sel(or_1_out));
  Comparator #(.width(16), .mode("unsigned")) comparator_1 (
    .a(X), .b(Y), .gt(comparator_1_gt), .eq(comparator_1_eq));  // open: lt
  or or_1 (or_1_out, comparator_1_gt, comparator_1_eq);
  Multiplexer #(.select(1), .width(3), .disabled("Z"), .enable("false")) multiplexer_2 (
    .in0(Y_num), .in1(X_num), .out(Max_num), .sel(or_1_out));

  // Notes on the sheet:
  //   输出两个输入中的较大值，并输出较大值的3位编号
endmodule

module \状态转化  (
  input  Y1,
  input  Y0,
  input  \跳转 ,
  output Z1,
  output Z0
);

  wire and_1_out, and_2_out, and_3_out, and_4_out, not_1_out, not_2_out, not_3_out, not_4_out, not_5_out;

  not not_1 (not_1_out, Y0);
  not not_2 (not_2_out, Y1);
  not not_3 (not_3_out, Y0);
  not not_4 (not_4_out, Y0);
  not not_5 (not_5_out, \跳转 );
  and and_1 (and_1_out, Y0, \跳转 );
  and and_2 (and_2_out, Y1, not_1_out);
  and and_3 (and_3_out, not_2_out, not_3_out, \跳转 );
  and and_4 (and_4_out, Y1, not_4_out, not_5_out);
  or or_1 (Z1, and_1_out, and_2_out);
  or or_2 (Z0, and_3_out, and_4_out);
endmodule
