// Logisim project cpu21-riscv.circ as structural Verilog: 22 circuits, main circuit ◇单周期RISC-V
module \单周期RISC_V  (
  input  IR1,
  input  IR2,
  input  IR3,
  output RegWrite,
  output MemWrite,
  output [31:0] PC,
  output [31:0] IR,
  output [31:0] RDin,
  output [31:0] MDin,
  output [31:0] LedData
);

  wire and_1_out, and_2_out, and_3_out, and_4_out, Beq, Blt, Bne, CLK, clock_1_out, comparator_1_eq,
       comparator_2_eq, comparator_2_lt, d_ff_1_q, ecall, equal, Go, halt, IR1_t, IR2_t, IR3_t, IRA, IRB,
       IRC, Jal, Jalr, less, Lhu, MemToReg, nand_1_out, not_1_out, not_2_out, not_3_out, not_4_out,
       not_5_out, or_2_out, or_6_out, priority_encoder_1_p5, S_Type, W1, W2, W3, \单周期硬布线控制器_1_alu_src ;
  wire [1:0] priority_encoder_1_p3;
  wire [3:0] \单周期硬布线控制器_1_alu_op ;
  wire [4:0] multiplexer_2_out, multiplexer_3_out;
  wire [11:0] multiplexer_4_out;
  wire [12:0] CNT_num;
  wire [15:0] multiplexer_6_out, \总周期数 ;
  wire [31:0] adder_2_out, adder_3_out, ALU_ans, bit_extender_1_out, bit_extender_2_out, bit_extender_3_out,
       bit_extender_4_out, multiplexer_1_out, multiplexer_5_out, multiplexer_7_out, multiplexer_8_out, PC_4,
       ram_1_data, regifile_1_r1, shifter_1_out, shifter_2_out;

  Button \u_继续运行  (.out(Go));
  Button _1 (.out(IRA));
  Button _2 (.out(IRB));
  Button _3 (.out(IRC));
  LED led_1 (.in(W1));
  LED led_2 (.in(W2));
  LED led_3 (.in(W3));
  and and_1 (and_1_out, Beq, equal);
  // Priority_Encoder #(.select(2)) priority_encoder_1: pin names not known; wires that end beside it: 1'b1, Jalr, priority_encoder_1_p3, Jal, priority_encoder_1_p5, 1'b1
  Multiplexer #(.select(2), .width(32), .enable("false")) multiplexer_1 (
    .in0(PC_4), .in1(ALU_ans), .in2(adder_3_out), .in3(adder_2_out), .out(multiplexer_1_out),
    .sel(priority_encoder_1_p3));
  Hex_Digit_Display hex_digit_display_1 (.value(LedData[31:28]));  // open: dp
  not not_1 (not_1_out, equal);
  and and_2 (and_2_out, not_1_out, Bne);
  or or_1 (priority_encoder_1_p5, and_1_out, and_2_out, and_3_out);
  or or_2 (or_2_out, not_2_out, Go);
  not not_2 (not_2_out, halt);
  Hex_Digit_Display hex_digit_display_2 (.value(LedData[23:20]));  // open: dp
  Hex_Digit_Display hex_digit_display_3 (.value(LedData[27:24]));  // open: dp
  and and_3 (and_3_out, Blt, less);
  Register #(.width(32)) u_PC (.D(multiplexer_1_out), .en(or_2_out), .Q(PC), .clk(CLK), .clr(1'b0));
  Hex_Digit_Display hex_digit_display_4 (.value(LedData[15:12]));  // open: dp
  Hex_Digit_Display hex_digit_display_5 (.value(LedData[19:16]));  // open: dp
  Adder #(.width(32)) adder_1 (.a(PC), .b(32'h4), .out(PC_4), .cin(1'b0));  // open: cout
  Hex_Digit_Display hex_digit_display_6 (.value(LedData[11:8]));  // open: dp
  Hex_Digit_Display hex_digit_display_7 (.value(LedData[7:4]));  // open: dp
  // Probe on \总周期数 
  // RiscV_Probe riscv_probe_1: pin names not known; wires that end beside it: IR
  ROM #(.addrWidth(10), .dataWidth(32)) rom_1 (.addr(PC[11:2]), .data(IR));  // open: sel
  Hex_Digit_Display hex_digit_display_8 (.value(LedData[3:0]));  // open: dp
  \单周期硬布线控制器  \u_单周期硬布线控制器_1  (
    .Funct({IR[30], IR[25], IR[14:12]}), .OP(IR[6:2]), .ALU_OP(\单周期硬布线控制器_1_alu_op ), .MemToReg(MemToReg),
    .MemWrite(MemWrite), .ALU_SRC(\单周期硬布线控制器_1_alu_src ), .RegWrite(RegWrite), .ecall(ecall),
    .S_type(S_Type), .Jalr(Jalr), .Beq(Beq), .JAL(Jal), .Bne(Bne), .in_3(IR[21]), .LHU(Lhu), .BLT(Blt));  // open: uret
  Multiplexer #(.width(5), .enable("false")) multiplexer_2 (
    .in0(IR[19:15]), .in1(5'b10001), .out(multiplexer_2_out), .sel(ecall));
  Multiplexer #(.width(5), .enable("false")) multiplexer_3 (
    .in0(IR[24:20]), .in1(5'b01010), .out(multiplexer_3_out), .sel(ecall));
  Multiplexer #(.width(12), .enable("false")) multiplexer_4 (
    .in0(IR[31:20]), .in1({IR[31:25], IR[11:7]}), .out(multiplexer_4_out), .sel(S_Type));
  or or_3 (IR1_t, IR1, IRA);
  assign bit_extender_1_out = {{20{multiplexer_4_out[11]}}, multiplexer_4_out};  // Bit_Extender bit_extender_1
  assign bit_extender_2_out = {{20{IR[31]}}, {IR[31], IR[7], IR[30:25], IR[11:8]}};  // Bit_Extender bit_extender_2
  assign bit_extender_3_out = {{12{IR[31]}}, {IR[31], IR[19:12], IR[20], IR[30:21]}};  // Bit_Extender bit_extender_3
  or or_4 (IR2_t, IR2, IRB);
  Shifter #(.width(32)) shifter_1 (.in(bit_extender_2_out), .\dist (5'b00001), .out(shifter_1_out));
  Shifter #(.width(32)) shifter_2 (.in(bit_extender_3_out), .\dist (5'b00001), .out(shifter_2_out));
  Regifile regifile_1 (
    .Din(RDin), .Clk(CLK), .R1(regifile_1_r1), .R2(MDin), .WE(RegWrite), .W_num(IR[11:7]),
    .R1_num(multiplexer_2_out), .R2_num(multiplexer_3_out));
  Adder #(.width(32)) adder_2 (.a(shifter_1_out), .b(PC), .out(adder_2_out), .cin(1'b0));  // open: cout
  Adder #(.width(32)) adder_3 (.a(shifter_2_out), .b(PC), .out(adder_3_out), .cin(1'b0));  // open: cout
  or or_5 (IR3_t, IR3, IRC);
  Multiplexer #(.width(32), .enable("false")) multiplexer_5 (
    .in0(MDin), .in1(bit_extender_1_out), .out(multiplexer_5_out), .sel(\单周期硬布线控制器_1_alu_src ));
  Register #(.width(32)) register_1 (.D(MDin), .en(and_4_out), .Q(LedData), .clk(CLK), .clr(1'b0));
  ALU alu_1 (
    .X(regifile_1_r1), .Y(multiplexer_5_out), .AluOP(\单周期硬布线控制器_1_alu_op ), .Equal(equal), .Result(ALU_ans),
    .out_6(less));  // open: Result_2, out_4
  Comparator #(.width(32)) comparator_1 (.a(regifile_1_r1), .b(32'h22), .eq(comparator_1_eq));  // open: gt, lt
  not not_3 (not_3_out, comparator_1_eq);
  and and_4 (and_4_out, ecall, comparator_1_eq);
  and and_5 (halt, ecall, not_3_out);
  not not_4 (not_4_out, MemWrite);
  RAM #(.addrWidth(10), .dataWidth(32), .bus("separate")) ram_1 (
    .addr(ALU_ans[11:2]), .din(MDin), .data(ram_1_data), .str(MemWrite), .clk(CLK), .ld(not_4_out));  // open: sel, clr
  not not_5 (not_5_out, halt);
  Counter #(.width(16), .max('hffff)) counter_1 (
    .count(not_5_out), .Q(\总周期数 ), .clk(CLK));  // open: load, D, carry, clr
  Multiplexer #(.width(16), .enable("false")) multiplexer_6 (
    .in0(ram_1_data[15:0]), .in1(ram_1_data[31:16]), .out(multiplexer_6_out), .sel(ALU_ans[1]));
  assign bit_extender_4_out = {{16{1'b0}}, multiplexer_6_out};  // Bit_Extender bit_extender_4
  D_Flip_Flop #(.trigger("high")) d_ff_1 (.Q(d_ff_1_q));  // open: clk, D, Qn, preset, en, reset
  // Probe on 13'hc
  Multiplexer #(.width(32), .enable("false")) multiplexer_7 (
    .in0(ram_1_data), .in1(bit_extender_4_out), .out(multiplexer_7_out), .sel(Lhu));
  or or_6 (or_6_out, Jal, Jalr);
  Comparator #(.width(13)) comparator_2 (
    .a(CNT_num), .b(13'hc), .eq(comparator_2_eq), .lt(comparator_2_lt));  // open: gt
  Clock clock_1 (.out(clock_1_out));
  Multiplexer #(.width(32), .enable("false")) multiplexer_8 (
    .in0(ALU_ans), .in1(multiplexer_7_out), .out(multiplexer_8_out), .sel(MemToReg));
  Multiplexer #(.width(32), .enable("false")) multiplexer_9 (
    .in0(multiplexer_8_out), .in1(PC_4), .out(RDin), .sel(or_6_out));
  Counter #(.width(13), .max('h1fff), .ongoal("stay")) counter_2 (
    .count(comparator_2_lt), .Q(CNT_num), .clk(clock_1_out));  // open: load, D, carry, clr
  nand nand_1 (nand_1_out, d_ff_1_q, comparator_2_eq);
  assign CLK = nand_1_out ? clock_1_out : 1'bz;  // Controlled_Buffer controlled_buffer_1
  Pull_Resistor #(.pull(1)) pull_resistor_1 (.node(CLK));

  // Notes on the sheet:
  //   中断源
  //   中断等待指示
  //   数码管输出应该用寄存器锁存，否则显示数据只能一闪而过
  //   数码管输出
  //   指令存储器
  //   指令探针
  //   contents of rom_1 (hex, n*v repeats v):
  //   100493 100006f 100493 200913 300993 100006f 100493 200913 300993 100006f 100493 200913 300993
  //   100006f 100493 200913 300993 3bc000ef 100413 100493 1f49493 900533 2200893 73 24d493 48463 fedff06f
  //   900533 2200893 73 100493 249493 900533 2200893 73 48463 fedff06f 100493 1f49493 900533 2200893 73
  //   4034d493 900533 2200893 73 4044d493 900533 2200893 73 4044d493 900533 2200893 73 4044d493 900533
  //   2200893 73 4044d493 900533 2200893 73 4044d493 900533 2200893 73 4044d493 900533 2200893 73 4044d493
  //   900533 2200893 73 100413 1f41993 41f9d993 433 c00913 300b13 140413 f47413 800293 100313 499993
  //   89e9b3 1300533 2200893 73 406282b3 fe0294e3 140413 f00f93 1f47433 1c41413 800293 100313 49d993
  //   89e9b3 1300533 2200893 73 406282b3 fe0294e3 1c45413 406b0b33 b0463 f95ff06f 2b3 fff2c293 829293
  //   ff2e293 500533 2200893 73 fff00413 493 84a023 140413 448493 84a023 140413 448493 84a023 140413
  //   448493 84a023 140413 448493 84a023 140413 448493 84a023 140413 448493 84a023 140413 448493 84a023
  //   140413 448493 84a023 140413 448493 84a023 140413 448493 84a023 140413 448493 84a023 140413 448493
  //   84a023 140413 448493 84a023 140413 448493 84a023 140413 448493 84a023 140413 448493 140413 433
  //   3c00493 42983 4aa03 149a2b3 28663 134a023 1442023 ffc48493 fe9412e3 800533 2200893 73 440413 3c00493
  //   fc9416e3 a00893 73 100293 300313 800493 849493 7648493 1449493 900533 2200893 73 800e13 4054d4b3
  //   4064d4b3 900533 2200893 73 fffe0e13 fe0e14e3 a00893 73 fff00293 313 1900413 841413 9700493 940533
  //   2200893 73 5484b3 494b313 fe0306e3 a00893 73 313 1000e13 8400493 849493 8348493 400913 891913 490913
  //   849493 8248493 849493 8148493 891913 490913 891913 490913 932023 12484b3 430313 fffe0e13 fe0e18e3
  //   2000e13 313 35483 900533 2200893 73 230313 fffe0e13 fe0e14e3 a00893 73 ff100493 900533 2200893 73
  //   148493 fe04c8e3 a00893 73 413 140413 800533 2200893 73 240413 800533 2200893 73 340413 800533
  //   2200893 73 440413 800533 2200893 73 540413 800533 2200893 73 640413 800533 2200893 73 740413 800533
  //   2200893 73 840413 800533 2200893 2200893 73 8067
  //   指令字
  //   I指令
  //   S指令
  //   B指令
  //   J指令
  //   Beq
  //   Bne
  //   MemToReg
  //   MemWrite
  //   AluOP
  //   AluSrcB
  //   RegWrite
  //   为方便自动评测，需要输出PC，IR，寄存器堆写如数据RDin
  //   RAM写使能MemWrite、RAM写入数据MDin等信号
  //   数据存储器
  //   控制位
  //   暂停节拍，不能为0
  //   戳工具置1进入计数暂停模式，ctrl+k时钟自动运行到对应节拍暂停
  //   ctrl+k关闭时钟连续运行，将控制位置零，进入单步调试模式调试
  //   用这个时钟源需要去掉电路中的其他时钟源
  //   可计数暂停的时钟源
endmodule

// 单周期硬布线控制器
module \单周期硬布线控制器  (
  input  [4:0] OP,
  input  [4:0] Funct,
  input  in_3,
  output [3:0] ALU_OP,
  output uret,
  output MemToReg,
  output ecall,
  output MemWrite,
  output ALU_SRC,
  output RegWrite,
  output S_type,
  output Beq,
  output Bne,
  output Jalr,
  output JAL,
  output LHU,
  output BLT
);

  wire \控制信号自动生成_1_ecall ;

  \运算控制器自动生成  \u_运算控制器自动生成_1  (
    .OP2(OP[0]), .OP3(OP[1]), .OP4(OP[2]), .OP5(OP[3]), .OP6(OP[4]), .F12(Funct[0]), .F13(Funct[1]),
    .F14(Funct[2]), .F25(Funct[3]), .F30(Funct[4]), .S0(ALU_OP[0]), .S1(ALU_OP[1]), .S2(ALU_OP[2]),
    .S3(ALU_OP[3]));
  \控制信号自动生成  \u_控制信号自动生成_1  (
    .OP2(OP[0]), .OP3(OP[1]), .OP4(OP[2]), .OP5(OP[3]), .MemToReg(MemToReg), .OP6(OP[4]), .F12(Funct[0]),
    .F13(Funct[1]), .F14(Funct[2]), .F25(Funct[3]), .F30(Funct[4]), .MemWrite(MemWrite), .ALU_SRC(ALU_SRC),
    .RegWrite(RegWrite), .ecall(\控制信号自动生成_1_ecall ), .S_Type(S_type), .BEQ(Beq), .BNE(Bne), .JALR(Jalr),
    .JAL(JAL), .LHU(LHU), .BLT(BLT));
  and and_1 (uret, in_3, \控制信号自动生成_1_ecall );
  and and_2 (ecall, ~in_3, \控制信号自动生成_1_ecall );  // AND_Gate

  // Other names for the same wires on the sheet: IR21 = in_3; OP_CODE[4:0] = OP

  // Notes on the sheet:
  //   运算器控制器，根据指令生成运算器功能选择信号
  //   控制信号生成，产生数据通路需要的其他控制信号
endmodule

// 运算器控制器
module \运算控制器自动生成  (
  input  OP2,
  input  OP3,
  input  OP4,
  input  OP5,
  input  OP6,
  input  F12,
  input  F13,
  input  F14,
  input  F25,
  input  F30,
  output S0,
  output S1,
  output S2,
  output S3
);

  wire and_1_out, and_2_out, and_3_out, and_4_out, and_5_out, and_6_out, and_7_out, and_8_out, and_9_out,
       and_10_out, and_11_out, and_12_out, and_13_out, and_14_out, and_15_out, and_16_out, and_17_out,
       and_18_out, and_19_out, and_20_out, and_21_out, and_22_out, and_23_out, and_24_out, and_25_out,
       and_26_out, and_27_out, and_28_out, and_29_out, and_30_out, and_31_out, and_32_out, and_33_out,
       and_34_out, and_35_out, and_36_out, and_37_out, and_38_out, and_39_out, and_40_out, and_41_out,
       and_42_out, and_43_out, and_44_out, and_45_out, and_46_out, and_47_out, and_48_out, not_1_out,
       not_2_out, not_3_out, not_4_out, not_5_out, not_6_out, not_7_out, not_8_out, not_9_out, not_10_out,
       not_11_out, not_12_out, not_13_out, not_14_out, not_15_out, not_16_out, not_17_out, not_18_out,
       not_19_out, not_20_out, not_21_out, not_22_out, not_23_out, not_24_out, not_25_out, not_26_out,
       not_27_out, not_28_out, not_29_out, not_30_out, not_31_out, not_32_out, not_33_out, not_34_out,
       not_35_out, not_36_out, not_37_out, not_38_out, not_39_out, not_40_out, not_41_out, not_42_out,
       not_43_out, not_44_out, not_45_out, not_46_out, not_47_out, not_48_out, not_49_out, not_50_out,
       not_51_out, not_52_out, not_53_out, not_54_out, not_55_out, not_56_out, not_57_out, not_58_out,
       not_59_out, not_60_out, not_61_out, not_62_out, not_63_out, not_64_out, not_65_out, not_66_out,
       not_67_out, not_68_out, not_69_out, not_70_out, not_71_out, not_72_out, not_73_out, not_74_out,
       not_75_out, not_76_out, not_77_out, not_78_out, not_79_out, not_80_out, not_81_out, not_82_out,
       not_83_out, not_84_out, not_85_out, not_86_out, not_87_out, not_88_out, not_89_out, not_90_out,
       not_91_out, not_92_out, not_93_out, not_94_out, not_95_out, not_96_out, not_97_out, not_98_out,
       not_99_out, not_100_out, not_101_out, not_102_out, not_103_out, not_104_out, not_105_out, not_106_out,
       not_107_out, not_108_out, not_109_out, not_110_out, not_111_out, not_112_out, not_113_out,
       not_114_out, not_115_out, not_116_out, not_117_out, not_118_out, not_119_out, not_120_out,
       not_121_out, not_122_out, not_123_out, not_124_out, not_125_out, not_126_out, not_127_out,
       not_128_out, not_129_out, not_130_out, not_131_out, not_132_out, not_133_out, not_134_out,
       not_135_out, not_136_out, not_137_out, not_138_out, not_139_out, not_140_out, not_141_out,
       not_142_out, not_143_out, not_144_out, not_145_out, not_146_out, not_147_out, not_148_out,
       not_149_out, not_150_out, not_151_out, not_152_out, not_153_out, not_154_out, not_155_out,
       not_156_out, not_157_out, not_158_out, not_159_out, not_160_out, not_161_out, not_162_out,
       not_163_out, not_164_out, not_165_out, not_166_out, not_167_out, not_168_out, not_169_out,
       not_170_out, not_171_out, not_172_out, not_173_out, not_174_out, not_175_out, not_176_out,
       not_177_out, not_178_out, not_179_out, not_180_out, not_181_out, not_182_out, not_183_out,
       not_184_out, not_185_out, not_186_out, not_187_out, not_188_out, not_189_out, not_190_out,
       not_191_out, not_192_out, not_193_out, not_194_out, not_195_out, not_196_out, not_197_out,
       not_198_out, not_199_out, not_200_out, not_201_out, not_202_out, not_203_out, not_204_out,
       not_205_out, not_206_out, not_207_out, not_208_out, not_209_out, not_210_out, not_211_out,
       not_212_out, not_213_out, not_214_out, not_215_out, not_216_out, not_217_out, not_218_out,
       not_219_out, not_220_out, not_221_out, not_222_out, not_223_out, not_224_out, not_225_out,
       not_226_out, not_227_out, not_228_out, not_229_out, not_230_out, not_231_out, not_232_out,
       not_233_out, not_234_out, not_235_out, not_236_out, not_237_out, not_238_out, not_239_out,
       not_240_out, not_241_out, not_242_out, not_243_out, not_244_out, not_245_out, not_246_out,
       not_247_out, not_248_out, not_249_out, not_250_out, not_251_out, not_252_out, not_253_out,
       not_254_out, not_255_out, not_256_out, not_257_out, not_258_out, not_259_out, not_260_out,
       not_261_out, not_262_out, not_263_out, not_264_out, not_265_out, not_266_out, not_267_out;

  not not_1 (not_1_out, F30);
  not not_2 (not_2_out, F25);
  not not_3 (not_3_out, F14);
  not not_4 (not_4_out, F13);
  not not_5 (not_5_out, F12);
  not not_6 (not_6_out, OP6);
  not not_7 (not_7_out, OP3);
  not not_8 (not_8_out, OP2);
  not not_9 (not_9_out, F30);
  not not_10 (not_10_out, F25);
  not not_11 (not_11_out, OP6);
  not not_12 (not_12_out, OP3);
  not not_13 (not_13_out, OP2);
  not not_14 (not_14_out, F30);
  not not_15 (not_15_out, F25);
  not not_16 (not_16_out, F14);
  not not_17 (not_17_out, F12);
  not not_18 (not_18_out, OP6);
  not not_19 (not_19_out, OP3);
  not not_20 (not_20_out, OP2);
  not not_21 (not_21_out, F14);
  not not_22 (not_22_out, F13);
  not not_23 (not_23_out, F12);
  not not_24 (not_24_out, OP6);
  not not_25 (not_25_out, OP5);
  not not_26 (not_26_out, OP3);
  not not_27 (not_27_out, OP2);
  not not_28 (not_28_out, OP6);
  not not_29 (not_29_out, OP5);
  not not_30 (not_30_out, OP3);
  not not_31 (not_31_out, OP2);
  not not_32 (not_32_out, F13);
  not not_33 (not_33_out, F12);
  not not_34 (not_34_out, OP6);
  not not_35 (not_35_out, OP5);
  not not_36 (not_36_out, OP3);
  not not_37 (not_37_out, OP2);
  not not_38 (not_38_out, F14);
  not not_39 (not_39_out, F12);
  not not_40 (not_40_out, OP6);
  not not_41 (not_41_out, OP5);
  not not_42 (not_42_out, OP3);
  not not_43 (not_43_out, OP2);
  not not_44 (not_44_out, F25);
  not not_45 (not_45_out, F13);
  not not_46 (not_46_out, OP6);
  not not_47 (not_47_out, OP5);
  not not_48 (not_48_out, OP3);
  not not_49 (not_49_out, OP2);
  not not_50 (not_50_out, F14);
  not not_51 (not_51_out, F12);
  not not_52 (not_52_out, OP6);
  not not_53 (not_53_out, OP5);
  not not_54 (not_54_out, OP4);
  not not_55 (not_55_out, OP3);
  not not_56 (not_56_out, OP2);
  not not_57 (not_57_out, F14);
  not not_58 (not_58_out, F12);
  not not_59 (not_59_out, OP6);
  not not_60 (not_60_out, OP4);
  not not_61 (not_61_out, OP3);
  not not_62 (not_62_out, OP2);
  not not_63 (not_63_out, OP3);
  not not_64 (not_64_out, OP2);
  not not_65 (not_65_out, F25);
  not not_66 (not_66_out, F13);
  not not_67 (not_67_out, OP6);
  not not_68 (not_68_out, OP3);
  not not_69 (not_69_out, OP2);
  not not_70 (not_70_out, F13);
  not not_71 (not_71_out, OP6);
  not not_72 (not_72_out, OP5);
  not not_73 (not_73_out, OP4);
  not not_74 (not_74_out, OP3);
  not not_75 (not_75_out, OP2);
  not not_76 (not_76_out, F13);
  not not_77 (not_77_out, F12);
  not not_78 (not_78_out, OP4);
  not not_79 (not_79_out, OP3);
  not not_80 (not_80_out, OP2);
  not not_81 (not_81_out, F25);
  not not_82 (not_82_out, F14);
  not not_83 (not_83_out, F13);
  not not_84 (not_84_out, F12);
  not not_85 (not_85_out, OP6);
  not not_86 (not_86_out, OP3);
  not not_87 (not_87_out, OP2);
  not not_88 (not_88_out, F30);
  not not_89 (not_89_out, F25);
  not not_90 (not_90_out, OP6);
  not not_91 (not_91_out, OP3);
  not not_92 (not_92_out, OP2);
  not not_93 (not_93_out, F30);
  not not_94 (not_94_out, F25);
  not not_95 (not_95_out, F14);
  not not_96 (not_96_out, F12);
  not not_97 (not_97_out, OP6);
  not not_98 (not_98_out, OP3);
  not not_99 (not_99_out, OP2);
  not not_100 (not_100_out, OP6);
  not not_101 (not_101_out, OP5);
  not not_102 (not_102_out, OP3);
  not not_103 (not_103_out, OP2);
  not not_104 (not_104_out, F14);
  not not_105 (not_105_out, F12);
  not not_106 (not_106_out, OP6);
  not not_107 (not_107_out, OP5);
  not not_108 (not_108_out, OP3);
  not not_109 (not_109_out, OP2);
  not not_110 (not_110_out, F30);
  not not_111 (not_111_out, F25);
  not not_112 (not_112_out, F13);
  not not_113 (not_113_out, OP6);
  not not_114 (not_114_out, OP5);
  not not_115 (not_115_out, OP3);
  not not_116 (not_116_out, OP2);
  not not_117 (not_117_out, F14);
  not not_118 (not_118_out, F13);
  not not_119 (not_119_out, F12);
  not not_120 (not_120_out, OP4);
  not not_121 (not_121_out, OP3);
  not not_122 (not_122_out, OP2);
  not not_123 (not_123_out, F14);
  not not_124 (not_124_out, F13);
  not not_125 (not_125_out, OP4);
  not not_126 (not_126_out, OP3);
  not not_127 (not_127_out, OP2);
  not not_128 (not_128_out, F14);
  not not_129 (not_129_out, F13);
  not not_130 (not_130_out, F12);
  not not_131 (not_131_out, OP4);
  not not_132 (not_132_out, OP3);
  not not_133 (not_133_out, OP3);
  not not_134 (not_134_out, OP2);
  not not_135 (not_135_out, F13);
  not not_136 (not_136_out, F12);
  not not_137 (not_137_out, OP4);
  not not_138 (not_138_out, OP3);
  not not_139 (not_139_out, OP2);
  not not_140 (not_140_out, F30);
  not not_141 (not_141_out, F25);
  not not_142 (not_142_out, F14);
  not not_143 (not_143_out, F13);
  not not_144 (not_144_out, F12);
  not not_145 (not_145_out, OP6);
  not not_146 (not_146_out, OP3);
  not not_147 (not_147_out, OP2);
  not not_148 (not_148_out, F25);
  not not_149 (not_149_out, F14);
  not not_150 (not_150_out, F13);
  not not_151 (not_151_out, F12);
  not not_152 (not_152_out, OP6);
  not not_153 (not_153_out, OP3);
  not not_154 (not_154_out, OP2);
  not not_155 (not_155_out, F30);
  not not_156 (not_156_out, F25);
  not not_157 (not_157_out, OP6);
  not not_158 (not_158_out, OP3);
  not not_159 (not_159_out, OP2);
  not not_160 (not_160_out, F30);
  not not_161 (not_161_out, F25);
  not not_162 (not_162_out, F14);
  not not_163 (not_163_out, OP6);
  not not_164 (not_164_out, OP3);
  not not_165 (not_165_out, OP2);
  not not_166 (not_166_out, F14);
  not not_167 (not_167_out, F13);
  not not_168 (not_168_out, F12);
  not not_169 (not_169_out, OP6);
  not not_170 (not_170_out, OP5);
  not not_171 (not_171_out, OP3);
  not not_172 (not_172_out, OP2);
  not not_173 (not_173_out, OP6);
  not not_174 (not_174_out, OP5);
  not not_175 (not_175_out, OP3);
  not not_176 (not_176_out, OP2);
  not not_177 (not_177_out, F14);
  not not_178 (not_178_out, F12);
  not not_179 (not_179_out, OP6);
  not not_180 (not_180_out, OP5);
  not not_181 (not_181_out, OP4);
  not not_182 (not_182_out, OP3);
  not not_183 (not_183_out, OP2);
  not not_184 (not_184_out, F14);
  not not_185 (not_185_out, F12);
  not not_186 (not_186_out, OP6);
  not not_187 (not_187_out, OP4);
  not not_188 (not_188_out, OP3);
  not not_189 (not_189_out, OP2);
  not not_190 (not_190_out, F14);
  not not_191 (not_191_out, F13);
  not not_192 (not_192_out, F12);
  not not_193 (not_193_out, OP4);
  not not_194 (not_194_out, OP3);
  not not_195 (not_195_out, OP2);
  not not_196 (not_196_out, F14);
  not not_197 (not_197_out, F13);
  not not_198 (not_198_out, OP4);
  not not_199 (not_199_out, OP3);
  not not_200 (not_200_out, OP2);
  not not_201 (not_201_out, F14);
  not not_202 (not_202_out, F13);
  not not_203 (not_203_out, F12);
  not not_204 (not_204_out, OP4);
  not not_205 (not_205_out, OP3);
  not not_206 (not_206_out, OP3);
  not not_207 (not_207_out, OP2);
  not not_208 (not_208_out, F14);
  not not_209 (not_209_out, OP6);
  not not_210 (not_210_out, OP5);
  not not_211 (not_211_out, OP3);
  not not_212 (not_212_out, OP2);
  not not_213 (not_213_out, F13);
  not not_214 (not_214_out, OP6);
  not not_215 (not_215_out, OP5);
  not not_216 (not_216_out, OP4);
  not not_217 (not_217_out, OP3);
  not not_218 (not_218_out, OP2);
  not not_219 (not_219_out, F30);
  not not_220 (not_220_out, F25);
  not not_221 (not_221_out, F12);
  not not_222 (not_222_out, OP6);
  not not_223 (not_223_out, OP3);
  not not_224 (not_224_out, OP2);
  not not_225 (not_225_out, F30);
  not not_226 (not_226_out, F25);
  not not_227 (not_227_out, F14);
  not not_228 (not_228_out, F12);
  not not_229 (not_229_out, OP6);
  not not_230 (not_230_out, OP3);
  not not_231 (not_231_out, OP2);
  not not_232 (not_232_out, F30);
  not not_233 (not_233_out, F25);
  not not_234 (not_234_out, F14);
  not not_235 (not_235_out, OP6);
  not not_236 (not_236_out, OP3);
  not not_237 (not_237_out, OP2);
  not not_238 (not_238_out, F12);
  not not_239 (not_239_out, OP6);
  not not_240 (not_240_out, OP5);
  not not_241 (not_241_out, OP3);
  not not_242 (not_242_out, OP2);
  not not_243 (not_243_out, F13);
  not not_244 (not_244_out, F12);
  not not_245 (not_245_out, OP6);
  not not_246 (not_246_out, OP5);
  not not_247 (not_247_out, OP3);
  not not_248 (not_248_out, OP2);
  not not_249 (not_249_out, F14);
  not not_250 (not_250_out, F12);
  not not_251 (not_251_out, OP6);
  not not_252 (not_252_out, OP5);
  not not_253 (not_253_out, OP3);
  not not_254 (not_254_out, OP2);
  not not_255 (not_255_out, F12);
  not not_256 (not_256_out, OP3);
  not not_257 (not_257_out, OP2);
  not not_258 (not_258_out, F14);
  not not_259 (not_259_out, OP6);
  not not_260 (not_260_out, OP5);
  not not_261 (not_261_out, OP3);
  not not_262 (not_262_out, OP2);
  not not_263 (not_263_out, F13);
  not not_264 (not_264_out, F12);
  not not_265 (not_265_out, OP4);
  not not_266 (not_266_out, OP3);
  not not_267 (not_267_out, OP2);
  and and_1 (and_1_out, not_1_out, not_2_out, not_3_out, not_4_out, not_5_out, not_6_out, OP5, OP4, not_7_out, not_8_out);
  and and_2 (and_2_out, not_9_out, not_10_out, F14, F13, F12, not_11_out, OP5, OP4, not_12_out, not_13_out);
  and and_3 (and_3_out, not_14_out, not_15_out, not_16_out, F13, not_17_out, not_18_out, OP5, OP4, not_19_out, not_20_out);
  and and_4 (and_4_out, not_21_out, not_22_out, not_23_out, not_24_out, not_25_out, OP4, not_26_out, not_27_out);
  and and_5 (and_5_out, F14, F13, F12, not_28_out, not_29_out, OP4, not_30_out, not_31_out);
  and and_6 (and_6_out, F14, not_32_out, not_33_out, not_34_out, not_35_out, OP4, not_36_out, not_37_out);
  and and_7 (and_7_out, not_38_out, F13, not_39_out, not_40_out, not_41_out, OP4, not_42_out, not_43_out);
  and and_8 (and_8_out, F30, not_44_out, F14, not_45_out, F12, not_46_out, not_47_out, OP4, not_48_out, not_49_out);
  and and_9 (and_9_out, not_50_out, F13, not_51_out, not_52_out, not_53_out, not_54_out, not_55_out, not_56_out);
  and and_10 (and_10_out, not_57_out, F13, not_58_out, not_59_out, OP5, not_60_out, not_61_out, not_62_out);
  and and_11 (and_11_out, F14, F13, F12, OP6, OP5, OP4, not_63_out, not_64_out);
  and and_12 (and_12_out, F30, not_65_out, F14, not_66_out, F12, not_67_out, OP5, OP4, not_68_out, not_69_out);
  and and_13 (and_13_out, F14, not_70_out, F12, not_71_out, not_72_out, not_73_out, not_74_out, not_75_out);
  and and_14 (and_14_out, F14, not_76_out, not_77_out, OP6, OP5, not_78_out, not_79_out, not_80_out);
  and and_15 (and_15_out, F30, not_81_out, not_82_out, not_83_out, not_84_out, not_85_out, OP5, OP4, not_86_out, not_87_out);
  and and_16 (and_16_out, not_88_out, not_89_out, F14, F13, F12, not_90_out, OP5, OP4, not_91_out, not_92_out);
  and and_17 (and_17_out, not_93_out, not_94_out, not_95_out, F13, not_96_out, not_97_out, OP5, OP4, not_98_out, not_99_out);
  and and_18 (and_18_out, F14, F13, F12, not_100_out, not_101_out, OP4, not_102_out, not_103_out);
  and and_19 (and_19_out, not_104_out, F13, not_105_out, not_106_out, not_107_out, OP4, not_108_out, not_109_out);
  and and_20 (and_20_out, not_110_out, not_111_out, F14, not_112_out, F12, not_113_out, not_114_out, OP4, not_115_out, not_116_out);
  and and_21 (and_21_out, not_117_out, not_118_out, not_119_out, OP6, OP5, not_120_out, not_121_out, not_122_out);
  and and_22 (and_22_out, not_123_out, not_124_out, F12, OP6, OP5, not_125_out, not_126_out, not_127_out);
  and and_23 (and_23_out, not_128_out, not_129_out, not_130_out, OP6, OP5, not_131_out, not_132_out, OP2);
  and and_24 (and_24_out, F14, F13, F12, OP6, OP5, OP4, not_133_out, not_134_out);
  and and_25 (and_25_out, F14, not_135_out, not_136_out, OP6, OP5, not_137_out, not_138_out, not_139_out);
  and and_26 (and_26_out, not_140_out, not_141_out, not_142_out, not_143_out, not_144_out, not_145_out, OP5, OP4, not_146_out, not_147_out);
  and and_27 (and_27_out, F30, not_148_out, not_149_out, not_150_out, not_151_out, not_152_out, OP5, OP4, not_153_out, not_154_out);
  and and_28 (and_28_out, not_155_out, not_156_out, F14, F13, F12, not_157_out, OP5, OP4, not_158_out, not_159_out);
  and and_29 (and_29_out, not_160_out, not_161_out, not_162_out, F13, F12, not_163_out, OP5, OP4, not_164_out, not_165_out);
  and and_30 (and_30_out, not_166_out, not_167_out, not_168_out, not_169_out, not_170_out, OP4, not_171_out, not_172_out);
  and and_31 (and_31_out, F14, F13, F12, not_173_out, not_174_out, OP4, not_175_out, not_176_out);
  and and_32 (and_32_out, not_177_out, F13, not_178_out, not_179_out, not_180_out, not_181_out, not_182_out, not_183_out);
  and and_33 (and_33_out, not_184_out, F13, not_185_out, not_186_out, OP5, not_187_out, not_188_out, not_189_out);
  and and_34 (and_34_out, not_190_out, not_191_out, not_192_out, OP6, OP5, not_193_out, not_194_out, not_195_out);
  and and_35 (and_35_out, not_196_out, not_197_out, F12, OP6, OP5, not_198_out, not_199_out, not_200_out);
  and and_36 (and_36_out, not_201_out, not_202_out, not_203_out, OP6, OP5, not_204_out, not_205_out, OP2);
  and and_37 (and_37_out, F14, F13, F12, OP6, OP5, OP4, not_206_out, not_207_out);
  and and_38 (and_38_out, not_208_out, F13, F12, not_209_out, not_210_out, OP4, not_211_out, not_212_out);
  and and_39 (and_39_out, F14, not_213_out, F12, not_214_out, not_215_out, not_216_out, not_217_out, not_218_out);
  and and_40 (and_40_out, not_219_out, not_220_out, F14, F13, not_221_out, not_222_out, OP5, OP4, not_223_out, not_224_out);
  and and_41 (and_41_out, not_225_out, not_226_out, not_227_out, F13, not_228_out, not_229_out, OP5, OP4, not_230_out, not_231_out);
  and and_42 (and_42_out, not_232_out, not_233_out, not_234_out, F13, F12, not_235_out, OP5, OP4, not_236_out, not_237_out);
  and and_43 (and_43_out, F14, F13, not_238_out, not_239_out, not_240_out, OP4, not_241_out, not_242_out);
  and and_44 (and_44_out, F14, not_243_out, not_244_out, not_245_out, not_246_out, OP4, not_247_out, not_248_out);
  and and_45 (and_45_out, not_249_out, F13, not_250_out, not_251_out, not_252_out, OP4, not_253_out, not_254_out);
  and and_46 (and_46_out, F14, F13, not_255_out, OP6, OP5, OP4, not_256_out, not_257_out);
  and and_47 (and_47_out, not_258_out, F13, F12, not_259_out, not_260_out, OP4, not_261_out, not_262_out);
  and and_48 (and_48_out, F14, not_263_out, not_264_out, OP6, OP5, not_265_out, not_266_out, not_267_out);
  or or_1 (S0, and_1_out, and_2_out, and_3_out, and_4_out, and_5_out, and_6_out, and_7_out, and_8_out, and_9_out, and_10_out, and_11_out, and_12_out, and_13_out, and_14_out);
  or or_2 (S1, and_15_out, and_16_out, and_17_out, and_18_out, and_19_out, and_20_out, and_21_out, and_22_out, and_23_out, and_24_out, and_25_out);
  or or_3 (S2, and_26_out, and_27_out, and_28_out, and_29_out, and_30_out, and_31_out, and_32_out, and_33_out, and_34_out, and_35_out, and_36_out, and_37_out, and_38_out, and_39_out);
  or or_4 (S3, and_40_out, and_41_out, and_42_out, and_43_out, and_44_out, and_45_out, and_46_out, and_47_out, and_48_out);
endmodule

// 控制信号生成
module \控制信号自动生成  (
  input  OP2,
  input  OP3,
  input  OP4,
  input  OP5,
  input  OP6,
  input  F12,
  input  F13,
  input  F14,
  input  F25,
  input  F30,
  output MemToReg,
  output MemWrite,
  output ALU_SRC,
  output RegWrite,
  output ecall,
  output S_Type,
  output BEQ,
  output BNE,
  output JALR,
  output JAL,
  output LHU,
  output BLT
);

  wire and_1_out, and_2_out, and_4_out, and_5_out, and_6_out, and_7_out, and_8_out, and_9_out, and_10_out,
       and_11_out, and_12_out, and_13_out, and_14_out, and_15_out, and_16_out, and_17_out, and_18_out,
       and_19_out, and_20_out, and_21_out, and_22_out, and_23_out, and_24_out, and_25_out, and_26_out,
       and_27_out, and_28_out, and_29_out, and_30_out, and_31_out, and_32_out, and_33_out, and_34_out,
       and_35_out, and_36_out, not_1_out, not_2_out, not_3_out, not_4_out, not_5_out, not_6_out, not_7_out,
       not_8_out, not_9_out, not_10_out, not_11_out, not_12_out, not_13_out, not_14_out, not_15_out,
       not_16_out, not_17_out, not_18_out, not_19_out, not_20_out, not_21_out, not_22_out, not_23_out,
       not_24_out, not_25_out, not_26_out, not_27_out, not_28_out, not_29_out, not_30_out, not_31_out,
       not_32_out, not_33_out, not_34_out, not_35_out, not_36_out, not_37_out, not_38_out, not_39_out,
       not_40_out, not_41_out, not_42_out, not_43_out, not_44_out, not_45_out, not_46_out, not_47_out,
       not_48_out, not_49_out, not_50_out, not_51_out, not_52_out, not_53_out, not_54_out, not_55_out,
       not_56_out, not_57_out, not_58_out, not_59_out, not_60_out, not_61_out, not_62_out, not_63_out,
       not_64_out, not_65_out, not_66_out, not_67_out, not_68_out, not_69_out, not_70_out, not_71_out,
       not_72_out, not_73_out, not_74_out, not_75_out, not_76_out, not_77_out, not_78_out, not_79_out,
       not_80_out, not_81_out, not_82_out, not_83_out, not_84_out, not_85_out, not_86_out, not_87_out,
       not_88_out, not_89_out, not_90_out, not_91_out, not_92_out, not_93_out, not_94_out, not_95_out,
       not_96_out, not_97_out, not_98_out, not_99_out, not_100_out, not_101_out, not_102_out, not_103_out,
       not_104_out, not_105_out, not_106_out, not_107_out, not_108_out, not_109_out, not_110_out,
       not_111_out, not_112_out, not_113_out, not_114_out, not_115_out, not_116_out, not_117_out,
       not_118_out, not_119_out, not_120_out, not_121_out, not_122_out, not_123_out, not_124_out,
       not_125_out, not_126_out, not_127_out, not_128_out, not_129_out, not_130_out, not_131_out,
       not_132_out, not_133_out, not_134_out, not_135_out, not_136_out, not_137_out, not_138_out,
       not_139_out, not_140_out, not_141_out, not_142_out, not_143_out, not_144_out, not_145_out,
       not_146_out, not_147_out, not_148_out, not_149_out, not_150_out, not_151_out, not_152_out,
       not_153_out, not_154_out, not_155_out, not_156_out, not_157_out, not_158_out, not_159_out,
       not_160_out, not_161_out, not_162_out, not_163_out, not_164_out, not_165_out, not_166_out,
       not_167_out, not_168_out, not_169_out, not_170_out, not_171_out, not_172_out, not_173_out,
       not_174_out, not_175_out, not_176_out, not_177_out, not_178_out, not_179_out, not_180_out,
       not_181_out, not_182_out, not_183_out, not_184_out, not_185_out, not_186_out, not_187_out,
       not_188_out, not_189_out, not_190_out, not_191_out, not_192_out, not_193_out, not_194_out,
       not_195_out, not_196_out, not_197_out, not_198_out, not_199_out, not_200_out, not_201_out,
       not_202_out, not_203_out, not_204_out, not_205_out, not_206_out, not_207_out, not_208_out,
       not_209_out, not_210_out, not_211_out, not_212_out, not_213_out, not_214_out, not_215_out,
       not_216_out, not_217_out, not_218_out, not_219_out, not_220_out, not_221_out, not_222_out,
       not_223_out, not_224_out, not_225_out, not_226_out, not_227_out, not_228_out, not_229_out,
       not_230_out, not_231_out, not_232_out, not_233_out, not_234_out, not_235_out, not_236_out,
       not_237_out, not_238_out, not_239_out, not_240_out, not_241_out, not_242_out, not_243_out,
       not_244_out, not_245_out, not_246_out, not_247_out, not_248_out, not_249_out, not_250_out,
       not_251_out, not_252_out, not_253_out, not_254_out, not_255_out;

  not not_1 (not_1_out, F14);
  not not_2 (not_2_out, F12);
  not not_3 (not_3_out, OP6);
  not not_4 (not_4_out, OP5);
  not not_5 (not_5_out, OP4);
  not not_6 (not_6_out, OP3);
  not not_7 (not_7_out, OP2);
  not not_8 (not_8_out, F13);
  not not_9 (not_9_out, OP6);
  not not_10 (not_10_out, OP5);
  not not_11 (not_11_out, OP4);
  not not_12 (not_12_out, OP3);
  not not_13 (not_13_out, OP2);
  not not_14 (not_14_out, F14);
  not not_15 (not_15_out, F12);
  not not_16 (not_16_out, OP6);
  not not_17 (not_17_out, OP4);
  not not_18 (not_18_out, OP3);
  not not_19 (not_19_out, OP2);
  not not_20 (not_20_out, F14);
  not not_21 (not_21_out, F13);
  not not_22 (not_22_out, F12);
  not not_23 (not_23_out, OP6);
  not not_24 (not_24_out, OP5);
  not not_25 (not_25_out, OP3);
  not not_26 (not_26_out, OP2);
  not not_27 (not_27_out, OP6);
  not not_28 (not_28_out, OP5);
  not not_29 (not_29_out, OP3);
  not not_30 (not_30_out, OP2);
  not not_31 (not_31_out, F12);
  not not_32 (not_32_out, OP6);
  not not_33 (not_33_out, OP5);
  not not_34 (not_34_out, OP3);
  not not_35 (not_35_out, OP2);
  not not_36 (not_36_out, F13);
  not not_37 (not_37_out, F12);
  not not_38 (not_38_out, OP6);
  not not_39 (not_39_out, OP5);
  not not_40 (not_40_out, OP3);
  not not_41 (not_41_out, OP2);
  not not_42 (not_42_out, F14);
  not not_43 (not_43_out, F12);
  not not_44 (not_44_out, OP6);
  not not_45 (not_45_out, OP5);
  not not_46 (not_46_out, OP3);
  not not_47 (not_47_out, OP2);
  not not_48 (not_48_out, F30);
  not not_49 (not_49_out, F25);
  not not_50 (not_50_out, F14);
  not not_51 (not_51_out, F13);
  not not_52 (not_52_out, OP6);
  not not_53 (not_53_out, OP5);
  not not_54 (not_54_out, OP3);
  not not_55 (not_55_out, OP2);
  not not_56 (not_56_out, F30);
  not not_57 (not_57_out, F25);
  not not_58 (not_58_out, F13);
  not not_59 (not_59_out, OP6);
  not not_60 (not_60_out, OP5);
  not not_61 (not_61_out, OP3);
  not not_62 (not_62_out, OP2);
  not not_63 (not_63_out, F25);
  not not_64 (not_64_out, F13);
  not not_65 (not_65_out, OP6);
  not not_66 (not_66_out, OP5);
  not not_67 (not_67_out, OP3);
  not not_68 (not_68_out, OP2);
  not not_69 (not_69_out, F14);
  not not_70 (not_70_out, F12);
  not not_71 (not_71_out, OP6);
  not not_72 (not_72_out, OP5);
  not not_73 (not_73_out, OP4);
  not not_74 (not_74_out, OP3);
  not not_75 (not_75_out, OP2);
  not not_76 (not_76_out, F14);
  not not_77 (not_77_out, F12);
  not not_78 (not_78_out, OP6);
  not not_79 (not_79_out, OP4);
  not not_80 (not_80_out, OP3);
  not not_81 (not_81_out, OP2);
  not not_82 (not_82_out, F14);
  not not_83 (not_83_out, F13);
  not not_84 (not_84_out, F12);
  not not_85 (not_85_out, OP4);
  not not_86 (not_86_out, OP3);
  not not_87 (not_87_out, F14);
  not not_88 (not_88_out, OP6);
  not not_89 (not_89_out, OP5);
  not not_90 (not_90_out, OP3);
  not not_91 (not_91_out, OP2);
  not not_92 (not_92_out, F13);
  not not_93 (not_93_out, OP6);
  not not_94 (not_94_out, OP5);
  not not_95 (not_95_out, OP4);
  not not_96 (not_96_out, OP3);
  not not_97 (not_97_out, OP2);
  not not_98 (not_98_out, F30);
  not not_99 (not_99_out, F25);
  not not_100 (not_100_out, F14);
  not not_101 (not_101_out, F13);
  not not_102 (not_102_out, F12);
  not not_103 (not_103_out, OP6);
  not not_104 (not_104_out, OP3);
  not not_105 (not_105_out, OP2);
  not not_106 (not_106_out, F25);
  not not_107 (not_107_out, F14);
  not not_108 (not_108_out, F13);
  not not_109 (not_109_out, F12);
  not not_110 (not_110_out, OP6);
  not not_111 (not_111_out, OP3);
  not not_112 (not_112_out, OP2);
  not not_113 (not_113_out, F30);
  not not_114 (not_114_out, F25);
  not not_115 (not_115_out, OP6);
  not not_116 (not_116_out, OP3);
  not not_117 (not_117_out, OP2);
  not not_118 (not_118_out, F30);
  not not_119 (not_119_out, F25);
  not not_120 (not_120_out, F12);
  not not_121 (not_121_out, OP6);
  not not_122 (not_122_out, OP3);
  not not_123 (not_123_out, OP2);
  not not_124 (not_124_out, F30);
  not not_125 (not_125_out, F25);
  not not_126 (not_126_out, F14);
  not not_127 (not_127_out, F12);
  not not_128 (not_128_out, OP6);
  not not_129 (not_129_out, OP3);
  not not_130 (not_130_out, OP2);
  not not_131 (not_131_out, F30);
  not not_132 (not_132_out, F25);
  not not_133 (not_133_out, F14);
  not not_134 (not_134_out, OP6);
  not not_135 (not_135_out, OP3);
  not not_136 (not_136_out, OP2);
  not not_137 (not_137_out, F14);
  not not_138 (not_138_out, F13);
  not not_139 (not_139_out, F12);
  not not_140 (not_140_out, OP6);
  not not_141 (not_141_out, OP5);
  not not_142 (not_142_out, OP3);
  not not_143 (not_143_out, OP2);
  not not_144 (not_144_out, OP6);
  not not_145 (not_145_out, OP5);
  not not_146 (not_146_out, OP3);
  not not_147 (not_147_out, OP2);
  not not_148 (not_148_out, F12);
  not not_149 (not_149_out, OP6);
  not not_150 (not_150_out, OP5);
  not not_151 (not_151_out, OP3);
  not not_152 (not_152_out, OP2);
  not not_153 (not_153_out, F13);
  not not_154 (not_154_out, F12);
  not not_155 (not_155_out, OP6);
  not not_156 (not_156_out, OP5);
  not not_157 (not_157_out, OP3);
  not not_158 (not_158_out, OP2);
  not not_159 (not_159_out, F14);
  not not_160 (not_160_out, F12);
  not not_161 (not_161_out, OP6);
  not not_162 (not_162_out, OP5);
  not not_163 (not_163_out, OP3);
  not not_164 (not_164_out, OP2);
  not not_165 (not_165_out, F30);
  not not_166 (not_166_out, F25);
  not not_167 (not_167_out, F14);
  not not_168 (not_168_out, F13);
  not not_169 (not_169_out, OP6);
  not not_170 (not_170_out, OP5);
  not not_171 (not_171_out, OP3);
  not not_172 (not_172_out, OP2);
  not not_173 (not_173_out, F30);
  not not_174 (not_174_out, F25);
  not not_175 (not_175_out, F13);
  not not_176 (not_176_out, OP6);
  not not_177 (not_177_out, OP5);
  not not_178 (not_178_out, OP3);
  not not_179 (not_179_out, OP2);
  not not_180 (not_180_out, F25);
  not not_181 (not_181_out, F13);
  not not_182 (not_182_out, OP6);
  not not_183 (not_183_out, OP5);
  not not_184 (not_184_out, OP3);
  not not_185 (not_185_out, OP2);
  not not_186 (not_186_out, F14);
  not not_187 (not_187_out, F12);
  not not_188 (not_188_out, OP6);
  not not_189 (not_189_out, OP5);
  not not_190 (not_190_out, OP4);
  not not_191 (not_191_out, OP3);
  not not_192 (not_192_out, OP2);
  not not_193 (not_193_out, OP4);
  not not_194 (not_194_out, F14);
  not not_195 (not_195_out, F13);
  not not_196 (not_196_out, F12);
  not not_197 (not_197_out, OP4);
  not not_198 (not_198_out, OP3);
  not not_199 (not_199_out, F25);
  not not_200 (not_200_out, F13);
  not not_201 (not_201_out, OP6);
  not not_202 (not_202_out, OP3);
  not not_203 (not_203_out, OP2);
  not not_204 (not_204_out, F14);
  not not_205 (not_205_out, OP6);
  not not_206 (not_206_out, OP5);
  not not_207 (not_207_out, OP3);
  not not_208 (not_208_out, OP2);
  not not_209 (not_209_out, F13);
  not not_210 (not_210_out, OP6);
  not not_211 (not_211_out, OP5);
  not not_212 (not_212_out, OP4);
  not not_213 (not_213_out, OP3);
  not not_214 (not_214_out, OP2);
  not not_215 (not_215_out, F30);
  not not_216 (not_216_out, F25);
  not not_217 (not_217_out, F14);
  not not_218 (not_218_out, F13);
  not not_219 (not_219_out, F12);
  not not_220 (not_220_out, OP3);
  not not_221 (not_221_out, OP2);
  not not_222 (not_222_out, F14);
  not not_223 (not_223_out, F12);
  not not_224 (not_224_out, OP6);
  not not_225 (not_225_out, OP4);
  not not_226 (not_226_out, OP3);
  not not_227 (not_227_out, OP2);
  not not_228 (not_228_out, F14);
  not not_229 (not_229_out, F13);
  not not_230 (not_230_out, F12);
  not not_231 (not_231_out, OP4);
  not not_232 (not_232_out, OP3);
  not not_233 (not_233_out, OP2);
  not not_234 (not_234_out, F14);
  not not_235 (not_235_out, F13);
  not not_236 (not_236_out, OP4);
  not not_237 (not_237_out, OP3);
  not not_238 (not_238_out, OP2);
  not not_239 (not_239_out, F14);
  not not_240 (not_240_out, F13);
  not not_241 (not_241_out, F12);
  not not_242 (not_242_out, OP4);
  not not_243 (not_243_out, OP3);
  not not_244 (not_244_out, OP4);
  not not_245 (not_245_out, F13);
  not not_246 (not_246_out, OP6);
  not not_247 (not_247_out, OP5);
  not not_248 (not_248_out, OP4);
  not not_249 (not_249_out, OP3);
  not not_250 (not_250_out, OP2);
  not not_251 (not_251_out, F13);
  not not_252 (not_252_out, F12);
  not not_253 (not_253_out, OP4);
  not not_254 (not_254_out, OP3);
  not not_255 (not_255_out, OP2);
  and and_1 (and_1_out, not_1_out, F13, not_2_out, not_3_out, not_4_out, not_5_out, not_6_out, not_7_out);
  and and_2 (and_2_out, F14, not_8_out, F12, not_9_out, not_10_out, not_11_out, not_12_out, not_13_out);
  and and_3 (MemWrite, not_14_out, F13, not_15_out, not_16_out, OP5, not_17_out, not_18_out, not_19_out);
  and and_4 (and_4_out, not_20_out, not_21_out, not_22_out, not_23_out, not_24_out, OP4, not_25_out, not_26_out);
  and and_5 (and_5_out, F14, F13, F12, not_27_out, not_28_out, OP4, not_29_out, not_30_out);
  and and_6 (and_6_out, F14, F13, not_31_out, not_32_out, not_33_out, OP4, not_34_out, not_35_out);
  and and_7 (and_7_out, F14, not_36_out, not_37_out, not_38_out, not_39_out, OP4, not_40_out, not_41_out);
  and and_8 (and_8_out, not_42_out, F13, not_43_out, not_44_out, not_45_out, OP4, not_46_out, not_47_out);
  and and_9 (and_9_out, not_48_out, not_49_out, not_50_out, not_51_out, F12, not_52_out, not_53_out, OP4, not_54_out, not_55_out);
  and and_10 (and_10_out, not_56_out, not_57_out, F14, not_58_out, F12, not_59_out, not_60_out, OP4, not_61_out, not_62_out);
  and and_11 (and_11_out, F30, not_63_out, F14, not_64_out, F12, not_65_out, not_66_out, OP4, not_67_out, not_68_out);
  and and_12 (and_12_out, not_69_out, F13, not_70_out, not_71_out, not_72_out, not_73_out, not_74_out, not_75_out);
  and and_13 (and_13_out, not_76_out, F13, not_77_out, not_78_out, OP5, not_79_out, not_80_out, not_81_out);
  and and_14 (and_14_out, not_82_out, not_83_out, not_84_out, OP6, OP5, not_85_out, not_86_out, OP2);
  and and_15 (and_15_out, not_87_out, F13, F12, not_88_out, not_89_out, OP4, not_90_out, not_91_out);
  and and_16 (and_16_out, F14, not_92_out, F12, not_93_out, not_94_out, not_95_out, not_96_out, not_97_out);
  and and_17 (and_17_out, not_98_out, not_99_out, not_100_out, not_101_out, not_102_out, not_103_out, OP5, OP4, not_104_out, not_105_out);
  and and_18 (and_18_out, F30, not_106_out, not_107_out, not_108_out, not_109_out, not_110_out, OP5, OP4, not_111_out, not_112_out);
  and and_19 (and_19_out, not_113_out, not_114_out, F14, F13, F12, not_115_out, OP5, OP4, not_116_out, not_117_out);
  and and_20 (and_20_out, not_118_out, not_119_out, F14, F13, not_120_out, not_121_out, OP5, OP4, not_122_out, not_123_out);
  and and_21 (and_21_out, not_124_out, not_125_out, not_126_out, F13, not_127_out, not_128_out, OP5, OP4, not_129_out, not_130_out);
  and and_22 (and_22_out, not_131_out, not_132_out, not_133_out, F13, F12, not_134_out, OP5, OP4, not_135_out, not_136_out);
  and and_23 (and_23_out, not_137_out, not_138_out, not_139_out, not_140_out, not_141_out, OP4, not_142_out, not_143_out);
  and and_24 (and_24_out, F14, F13, F12, not_144_out, not_145_out, OP4, not_146_out, not_147_out);
  and and_25 (and_25_out, F14, F13, not_148_out, not_149_out, not_150_out, OP4, not_151_out, not_152_out);
  and and_26 (and_26_out, F14, not_153_out, not_154_out, not_155_out, not_156_out, OP4, not_157_out, not_158_out);
  and and_27 (and_27_out, not_159_out, F13, not_160_out, not_161_out, not_162_out, OP4, not_163_out, not_164_out);
  and and_28 (and_28_out, not_165_out, not_166_out, not_167_out, not_168_out, F12, not_169_out, not_170_out, OP4, not_171_out, not_172_out);
  and and_29 (and_29_out, not_173_out, not_174_out, F14, not_175_out, F12, not_176_out, not_177_out, OP4, not_178_out, not_179_out);
  and and_30 (and_30_out, F30, not_180_out, F14, not_181_out, F12, not_182_out, not_183_out, OP4, not_184_out, not_185_out);
  and and_31 (and_31_out, not_186_out, F13, not_187_out, not_188_out, not_189_out, not_190_out, not_191_out, not_192_out);
  and and_32 (and_32_out, OP6, OP5, not_193_out, OP3, OP2);
  and and_33 (and_33_out, not_194_out, not_195_out, not_196_out, OP6, OP5, not_197_out, not_198_out, OP2);
  and and_34 (and_34_out, F30, not_199_out, F14, not_200_out, F12, not_201_out, OP5, OP4, not_202_out, not_203_out);
  and and_35 (and_35_out, not_204_out, F13, F12, not_205_out, not_206_out, OP4, not_207_out, not_208_out);
  and and_36 (and_36_out, F14, not_209_out, F12, not_210_out, not_211_out, not_212_out, not_213_out, not_214_out);
  and and_37 (ecall, not_215_out, not_216_out, not_217_out, not_218_out, not_219_out, OP6, OP5, OP4, not_220_out, not_221_out);
  and and_38 (S_Type, not_222_out, F13, not_223_out, not_224_out, OP5, not_225_out, not_226_out, not_227_out);
  and and_39 (BEQ, not_228_out, not_229_out, not_230_out, OP6, OP5, not_231_out, not_232_out, not_233_out);
  and and_40 (BNE, not_234_out, not_235_out, F12, OP6, OP5, not_236_out, not_237_out, not_238_out);
  and and_41 (JALR, not_239_out, not_240_out, not_241_out, OP6, OP5, not_242_out, not_243_out, OP2);
  and and_42 (JAL, OP6, OP5, not_244_out, OP3, OP2);
  and and_43 (LHU, F14, not_245_out, F12, not_246_out, not_247_out, not_248_out, not_249_out, not_250_out);
  and and_44 (BLT, F14, not_251_out, not_252_out, OP6, OP5, not_253_out, not_254_out, not_255_out);
  or or_1 (MemToReg, and_1_out, and_2_out);
  or or_2 (ALU_SRC, and_4_out, and_5_out, and_6_out, and_7_out, and_8_out, and_9_out, and_10_out, and_11_out, and_12_out, and_13_out, and_14_out, and_15_out, and_16_out);
  or or_3 (RegWrite, and_17_out, and_18_out, and_19_out, and_20_out, and_21_out, and_22_out, and_23_out, and_24_out, and_25_out, and_26_out, and_27_out, and_28_out, and_29_out, and_30_out, and_31_out, and_32_out, and_33_out, and_34_out, and_35_out, and_36_out);
endmodule

// ALU
module ALU (
  input  [31:0] X,
  input  [31:0] Y,
  input  [3:0] AluOP,
  output out_4,
  output Equal,
  output out_6,
  output [31:0] Result,
  output [31:0] Result_2
);

  wire [0:0] comparator_1_lt, comparator_2_lt;
  wire [31:0] adder_1_out, AND_out, divider_1_out, divider_1_rem, multiplier_1_cout, multiplier_1_out,
       NOR_out, OR_out, shifter_1_out, shifter_2_out, shifter_3_out, subtractor_1_out, XOR_out;

  assign AND_out = X & Y;  // AND_Gate AND, 32 bits wide
  assign OR_out = X | Y;  // OR_Gate OR, 32 bits wide
  Shifter #(.width(32)) shifter_1 (.in(X), .\dist (Y[4:0]), .out(shifter_1_out));
  Shifter #(.width(32), .shift("ar")) shifter_2 (.in(X), .\dist (Y[4:0]), .out(shifter_2_out));
  Shifter #(.width(32), .shift("lr")) shifter_3 (.in(X), .\dist (Y[4:0]), .out(shifter_3_out));
  Multiplier #(.width(32)) multiplier_1 (.a(X), .b(Y), .out(multiplier_1_out), .cout(multiplier_1_cout));  // open: cin
  Divider #(.width(32)) divider_1 (.a(X), .b(Y), .out(divider_1_out), .rem(divider_1_rem));  // open: upper
  Adder #(.width(32)) adder_1 (.a(X), .b(Y), .out(adder_1_out));  // open: cin, cout
  Subtractor #(.width(32)) subtractor_1 (.a(X), .b(Y), .out(subtractor_1_out));  // open: bin, bout
  assign XOR_out = X ^ Y;  // XOR_Gate XOR, 32 bits wide
  assign NOR_out = ~(X | Y);  // NOR_Gate NOR, 32 bits wide
  Comparator #(.width(32)) comparator_1 (.a(X), .b(Y), .eq(Equal), .lt(comparator_1_lt[0]));  // open: gt
  Comparator #(.width(32), .mode("unsigned")) comparator_2 (.a(X), .b(Y), .lt(comparator_2_lt[0]));  // open: gt, eq
  Multiplexer #(.select(4), .width(32), .enable("false")) multiplexer_1 (
    .in0(shifter_1_out), .in1(shifter_2_out), .in2(shifter_3_out), .in3(multiplier_1_out),
    .in4(divider_1_out), .in5(adder_1_out), .in6(subtractor_1_out), .in7(AND_out), .in8(OR_out),
    .in9(XOR_out), .in10(NOR_out), .in11({{31{1'b0}}, comparator_1_lt[0]}),
    .in12({{31{1'b0}}, comparator_2_lt[0]}), .in13({32{1'b0}}), .in14({32{1'b0}}), .in15({32{1'b0}}),
    .out(Result), .sel(AluOP));
  Multiplexer #(.select(4), .width(32), .enable("false")) multiplexer_2 (
    .in0({32{1'b0}}), .in1({32{1'b0}}), .in2({32{1'b0}}), .in3(multiplier_1_cout), .in4(divider_1_rem),
    .in5({32{1'b0}}), .in6({32{1'b0}}), .in7({32{1'b0}}), .in8({32{1'b0}}), .in9({32{1'b0}}),
    .in10({32{1'b0}}), .in11({32{1'b0}}), .in12({32{1'b0}}), .in13({32{1'b0}}), .in14({32{1'b0}}),
    .in15({32{1'b0}}), .out(Result_2), .sel(AluOP));
  Multiplexer #(.select(4), .enable("false")) multiplexer_3 (
    .in0(1'b0), .in1(1'b0), .in2(1'b0), .in3(1'b0), .in4(1'b0), .in5(1'b0), .in6(1'b0), .in7(1'b0),
    .in8(1'b0), .in9(1'b0), .in10(1'b0), .in11(comparator_1_lt[0]), .in12(comparator_2_lt[0]), .in13(1'b0),
    .in14(1'b0), .in15(1'b0), .out(out_6), .sel(AluOP));
  not not_1 (out_4, out_6);

  // Other names for the same wires on the sheet: Result2[31:0] = Result_2; S[3:0] = AluOP; tunnel = out_6;
  //   tunnel_t = out_4

  // Notes on the sheet:
  //   不要改变此引脚区域内容，也不要改变ALU封装形式
  //   输入引脚
  //   输出引脚
endmodule

module Regifile (
  input  [31:0] Din,
  input  Clk,
  input  WE,
  input  [4:0] R1_num,
  input  [4:0] W_num,
  input  [4:0] R2_num,
  output [31:0] R1,
  output [31:0] R2
);

  // RegisterFile registerfile_1: pin names not known; wires that end beside it: Din, Clk, WE, W_num, R1_num, R2_num, R1, R2
endmodule

module \理想流水线  (
  output RegWrite,
  output MemWrite,
  output [31:0] IF_PC,
  output [31:0] ID_PC,
  output [31:0] EX_PC,
  output [31:0] M_PC,
  output [31:0] WB_PC,
  output [31:0] RDin,
  output [31:0] MDin,
  output [31:0] LedData
);

  wire alu_1_equal, alu_1_out_6, and_2_out, and_3_out, and_4_out, and_5_out, and_6_out, and_7_out, bJump,
       Blt, CLK, clock_1_out, comparator_1_eq, comparator_1_lt, comparator_2_eq, d_ff_1_q, Ecall, en, Equal,
       EX_Beq, EX_Blt, EX_Bne, ex_mem_1_mem_ecall, ex_mem_1_mem_equal, ex_mem_1_mem_jal, ex_mem_1_mem_jalr,
       ex_mem_1_mem_lhu, ex_mem_1_mem_memtoreg, ex_mem_1_mem_regwrite, Go, halt, id_ex_1_ex_alusrcb,
       id_ex_1_ex_ecall, id_ex_1_ex_jal, id_ex_1_ex_jalr, id_ex_1_ex_lhu, id_ex_1_ex_memtoreg,
       id_ex_1_ex_memwrite, id_ex_1_ex_regwrite, IR1, IR2, IR3, Jal, Jalr, Jump, Lhu, mem_wb_1_wb_jal,
       mem_wb_1_wb_jalr, nand_1_out, not_1_out, not_2_out, not_3_out, not_4_out, or_2_out, or_5_out, RST,
       S_Type, W1, W2, W3, \单周期硬布线控制器_1_alu_src , \单周期硬布线控制器_1_beq , \单周期硬布线控制器_1_bne , \单周期硬布线控制器_1_ecall ,
       \单周期硬布线控制器_1_memtoreg , \单周期硬布线控制器_1_memwrite , \单周期硬布线控制器_1_regwrite ;
  wire [3:0] id_ex_1_ex_aluop, \单周期硬布线控制器_1_alu_op ;
  wire [4:0] ex_mem_1_mem_rd, id_ex_1_ex_rd, multiplexer_3_out, multiplexer_4_out, WB_rd;
  wire [11:0] multiplexer_5_out;
  wire [12:0] CNT_num;
  wire [15:0] \LoadUse次数 , multiplexer_8_out, \总周期数 , \插入气泡数 , \无条件分支数 , \条件分支成功数 ;
  wire [31:0] adder_1_out, adder_3_out, adder_4_out, alu_1_result, bAddr, bit_extender_1_out,
       bit_extender_2_out, bit_extender_3_out, bit_extender_4_out, EX_IR, ex_mem_1_mem_calc,
       id_ex_1_ex_imm_b, id_ex_1_ex_imm_i, id_ex_1_ex_imm_j, ID_IR, IF_IR, jAddr, MEM_IR,
       mem_wb_1_wb_calc_mout, multiplexer_1_out, multiplexer_2_out, multiplexer_6_out, multiplexer_9_out,
       multiplexer_10_out, ram_1_data, regifile_1_r1, regifile_1_r2, RegR1, RegR2, shifter_1_out,
       shifter_2_out, WB_IR;

  Button \u_总复位  (.out(RST));
  Button _1 (.out(IR1));
  Button _2 (.out(IR2));
  Button _3 (.out(IR3));
  // Probe on \总周期数 
  // Probe on \总周期数 
  Button \u_继续运行  (.out(Go));
  LED led_1 (.in(W1));
  LED led_2 (.in(W2));
  LED led_3 (.in(W3));
  Register #(.width(32)) PC (.D(multiplexer_2_out), .en(en), .Q(IF_PC), .clk(CLK), .clr(RST));
  Hex_Digit_Display hex_digit_display_1 (.value(LedData[31:28]));  // open: dp
  // Probe on IF_PC[19:0]
  // RiscV_Probe riscv_probe_1: pin names not known; wires that end beside it: IF_IR
  or or_1 (en, not_1_out, Go);
  not not_1 (not_1_out, halt);
  Hex_Digit_Display hex_digit_display_2 (.value(LedData[23:20]));  // open: dp
  Hex_Digit_Display hex_digit_display_3 (.value(LedData[27:24]));  // open: dp
  // Probe on ID_PC[19:0]
  // RiscV_Probe riscv_probe_2: pin names not known; wires that end beside it: ID_IR
  Adder #(.width(32)) adder_1 (.a(IF_PC), .b(32'h4), .out(adder_1_out));  // open: cin, cout
  Hex_Digit_Display hex_digit_display_4 (.value(LedData[15:12]));  // open: dp
  Hex_Digit_Display hex_digit_display_5 (.value(LedData[19:16]));  // open: dp
  ROM #(.addrWidth(10), .dataWidth(32)) rom_1 (.addr(IF_PC[11:2]), .data(IF_IR));  // open: sel
  or or_2 (or_2_out, bJump, Jump);
  Multiplexer #(.width(32), .enable("false")) multiplexer_1 (
    .in0(bAddr), .in1(jAddr), .out(multiplexer_1_out), .sel(Jump));
  Hex_Digit_Display hex_digit_display_6 (.value(LedData[11:8]));  // open: dp
  Hex_Digit_Display hex_digit_display_7 (.value(LedData[7:4]));  // open: dp
  // Probe on EX_PC[19:0]
  // RiscV_Probe riscv_probe_3: pin names not known; wires that end beside it: EX_IR
  Multiplexer #(.width(32), .enable("false")) multiplexer_2 (
    .in0(adder_1_out), .in1(multiplexer_1_out), .out(multiplexer_2_out), .sel(or_2_out));
  not not_2 (not_2_out, Equal);
  Hex_Digit_Display hex_digit_display_8 (.value(LedData[3:0]));  // open: dp
  IF_ID if_id_1 (.IF_PC(IF_PC), .IF_IR(IF_IR), .clk(CLK), .en(en), .ID_PC(ID_PC), .ID_IR(ID_IR), .rst(RST));
  and and_1 (halt, Ecall, not_2_out);
  and and_2 (and_2_out, Ecall, Equal);
  // Probe on \总周期数 
  // Probe on M_PC[19:0]
  // RiscV_Probe riscv_probe_4: pin names not known; wires that end beside it: MEM_IR
  Multiplexer #(.width(5), .enable("false")) multiplexer_3 (
    .in0(ID_IR[19:15]), .in1(5'b10001), .out(multiplexer_3_out), .sel(\单周期硬布线控制器_1_ecall ));
  Multiplexer #(.width(5), .enable("false")) multiplexer_4 (
    .in0(ID_IR[24:20]), .in1(5'b01010), .out(multiplexer_4_out), .sel(\单周期硬布线控制器_1_ecall ));
  Register #(.width(32)) register_1 (.D(RegR2), .en(and_2_out), .Q(LedData), .clk(CLK), .clr(1'b0));
  // Probe on \总周期数 
  // Probe on \无条件分支数 
  // Probe on \条件分支成功数 
  // Probe on \插入气泡数 
  // Probe on \LoadUse次数 
  \单周期硬布线控制器  \u_单周期硬布线控制器_1  (
    .Funct({ID_IR[30], ID_IR[25], ID_IR[14:12]}), .OP(ID_IR[6:2]), .ALU_OP(\单周期硬布线控制器_1_alu_op ),
    .MemToReg(\单周期硬布线控制器_1_memtoreg ), .MemWrite(\单周期硬布线控制器_1_memwrite ), .ALU_SRC(\单周期硬布线控制器_1_alu_src ),
    .RegWrite(\单周期硬布线控制器_1_regwrite ), .ecall(\单周期硬布线控制器_1_ecall ), .S_type(S_Type), .Jalr(Jalr),
    .Beq(\单周期硬布线控制器_1_beq ), .JAL(Jal), .Bne(\单周期硬布线控制器_1_bne ), .in_3(ID_IR[21]), .LHU(Lhu), .BLT(Blt));  // open: uret
  Multiplexer #(.width(12), .enable("false")) multiplexer_5 (
    .in0(ID_IR[31:20]), .in1({ID_IR[31:25], ID_IR[11:7]}), .out(multiplexer_5_out), .sel(S_Type));
  assign bit_extender_1_out = {{20{ID_IR[31]}}, {ID_IR[31], ID_IR[7], ID_IR[30:25], ID_IR[11:8]}};  // Bit_Extender bit_extender_1
  assign bit_extender_2_out = {{12{ID_IR[31]}}, {ID_IR[31], ID_IR[19:12], ID_IR[20], ID_IR[30:21]}};  // Bit_Extender bit_extender_2
  // Probe on IF_PC[11:0]
  // Probe on WB_PC[19:0]
  // RiscV_Probe riscv_probe_5: pin names not known; wires that end beside it: WB_IR
  assign bit_extender_3_out = {{20{multiplexer_5_out[11]}}, multiplexer_5_out};  // Bit_Extender bit_extender_3
  Shifter #(.width(32)) shifter_1 (.in(bit_extender_1_out), .\dist (5'b00001), .out(shifter_1_out));
  Shifter #(.width(32)) shifter_2 (.in(bit_extender_2_out), .\dist (5'b00001), .out(shifter_2_out));
  // Probe on ID_PC[11:0]
  // Probe on EX_PC[11:0]
  Regifile regifile_1 (
    .Din(RDin), .Clk(CLK), .R1(regifile_1_r1), .R2(regifile_1_r2), .WE(RegWrite), .W_num(WB_rd),
    .R1_num(multiplexer_3_out), .R2_num(multiplexer_4_out));
  // Probe on M_PC[11:0]
  D_Flip_Flop #(.trigger("high")) d_ff_1 (.Q(d_ff_1_q));  // open: clk, D, Qn, preset, en, reset
  // Probe on 13'hc
  Counter #(.width(16), .max('hffff)) counter_1 (.count(en), .Q(\总周期数 ), .clk(CLK));  // open: load, D, carry, clr
  // Probe on WB_PC[11:0]
  Comparator #(.width(13)) comparator_1 (
    .a(CNT_num), .b(13'hc), .eq(comparator_1_eq), .lt(comparator_1_lt));  // open: gt
  Clock clock_1 (.out(clock_1_out));
  ID_EX id_ex_1 (
    .ID_PC(ID_PC), .ID_IR(ID_IR), .ID_Beq(\单周期硬布线控制器_1_beq ), .ID_Bne(\单周期硬布线控制器_1_bne ), .ID_Blt(Blt),
    .ID_MemToReg(\单周期硬布线控制器_1_memtoreg ), .ID_MemWrite(\单周期硬布线控制器_1_memwrite ),
    .ID_AluOP(\单周期硬布线控制器_1_alu_op ), .ID_AluSrcB(\单周期硬布线控制器_1_alu_src ),
    .ID_RegWrite(\单周期硬布线控制器_1_regwrite ), .ID_Jal(Jal), .ID_Jalr(Jalr), .ID_rd(ID_IR[11:7]),
    .ID_Ecall(\单周期硬布线控制器_1_ecall ), .ID_Lhu(Lhu), .ID_R1(regifile_1_r1), .ID_R2(regifile_1_r2),
    .ID_imm_I(bit_extender_3_out), .ID_imm_B(shifter_1_out), .ID_imm_J(shifter_2_out), .clk(CLK), .en(en),
    .EX_PC(EX_PC), .EX_IR(EX_IR), .EX_Beq(EX_Beq), .EX_Bne(EX_Bne), .EX_Blt(EX_Blt),
    .EX_MemToReg(id_ex_1_ex_memtoreg), .EX_MemWrite(id_ex_1_ex_memwrite), .EX_AluOP(id_ex_1_ex_aluop),
    .EX_AluSrcB(id_ex_1_ex_alusrcb), .EX_RegWrite(id_ex_1_ex_regwrite), .EX_Jal(id_ex_1_ex_jal),
    .EX_Jalr(id_ex_1_ex_jalr), .EX_rd(id_ex_1_ex_rd), .EX_Ecall(id_ex_1_ex_ecall), .EX_Lhu(id_ex_1_ex_lhu),
    .EX_A(RegR1), .EX_B(RegR2), .EX_imm_I(id_ex_1_ex_imm_i), .EX_imm_B(id_ex_1_ex_imm_b),
    .EX_imm_J(id_ex_1_ex_imm_j), .rst(RST));
  Adder #(.width(32)) adder_2 (.a(id_ex_1_ex_imm_b), .b(EX_PC), .out(bAddr));  // open: cin, cout
  and and_3 (and_3_out, en, Jump);
  nand nand_1 (nand_1_out, d_ff_1_q, comparator_1_eq);
  Counter #(.width(13), .max('h1fff), .ongoal("stay")) counter_2 (
    .count(comparator_1_lt), .Q(CNT_num), .clk(clock_1_out));  // open: load, D, carry, clr
  Multiplexer #(.width(32), .enable("false")) multiplexer_6 (
    .in0(RegR2), .in1(id_ex_1_ex_imm_i), .out(multiplexer_6_out), .sel(id_ex_1_ex_alusrcb));
  and and_4 (and_4_out, EX_Beq, alu_1_equal);
  Counter #(.width(16), .max('hffff)) counter_3 (
    .count(and_3_out), .Q(\无条件分支数 ), .clk(CLK));  // open: load, D, carry, clr
  assign CLK = nand_1_out ? clock_1_out : 1'bz;  // Controlled_Buffer controlled_buffer_1
  ALU alu_1 (
    .X(RegR1), .Y(multiplexer_6_out), .AluOP(id_ex_1_ex_aluop), .Equal(alu_1_equal), .Result(alu_1_result),
    .out_6(alu_1_out_6));  // open: Result_2, out_4
  not not_3 (not_3_out, alu_1_equal);
  and and_5 (and_5_out, EX_Bne, not_3_out);
  or or_3 (bJump, and_4_out, and_5_out, and_6_out);
  Pull_Resistor #(.pull(1)) pull_resistor_1 (.node(CLK));
  or or_4 (Jump, id_ex_1_ex_jal, id_ex_1_ex_jalr);
  and and_6 (and_6_out, EX_Blt, alu_1_out_6);
  and and_7 (and_7_out, en, bJump);
  Adder #(.width(32)) adder_3 (.a(EX_PC), .b(id_ex_1_ex_imm_j), .out(adder_3_out));  // open: cin, cout
  Counter #(.width(16), .max('hffff)) counter_4 (
    .count(and_7_out), .Q(\条件分支成功数 ), .clk(CLK));  // open: load, D, carry, clr
  Comparator #(.width(32)) comparator_2 (.a(RegR1), .b(32'h22), .eq(comparator_2_eq));  // open: gt, lt
  Multiplexer #(.width(32), .enable("false")) multiplexer_7 (
    .in0(alu_1_result), .in1(adder_3_out), .out(jAddr), .sel(id_ex_1_ex_jal));
  EX_MEM ex_mem_1 (
    .EX_PC(EX_PC), .EX_IR(EX_IR), .EX_MemToReg(id_ex_1_ex_memtoreg), .EX_MemWrite(id_ex_1_ex_memwrite),
    .EX_RegWrite(id_ex_1_ex_regwrite), .EX_Jal(id_ex_1_ex_jal), .EX_Jalr(id_ex_1_ex_jalr), .EX_MDin(RegR2),
    .EX_Calc(alu_1_result), .EX_rd(id_ex_1_ex_rd), .EX_Ecall(id_ex_1_ex_ecall), .EX_Equal(comparator_2_eq),
    .EX_Lhu(id_ex_1_ex_lhu), .clk(CLK), .en(en), .MEM_PC(M_PC), .MEM_IR(MEM_IR),
    .MEM_MemToReg(ex_mem_1_mem_memtoreg), .MEM_MemWrite(MemWrite), .MEM_RegWrite(ex_mem_1_mem_regwrite),
    .MEM_Jal(ex_mem_1_mem_jal), .MEM_Jalr(ex_mem_1_mem_jalr), .MEM_MDin(MDin), .MEM_Calc(ex_mem_1_mem_calc),
    .MEM_rd(ex_mem_1_mem_rd), .MEM_Ecall(ex_mem_1_mem_ecall), .MEM_Equal(ex_mem_1_mem_equal),
    .MEM_Lhu(ex_mem_1_mem_lhu), .rst(RST));
  not not_4 (not_4_out, MemWrite);
  RAM #(.addrWidth(10), .dataWidth(32), .bus("separate")) ram_1 (
    .addr(ex_mem_1_mem_calc[11:2]), .din(MDin), .data(ram_1_data), .str(MemWrite), .clk(CLK), .ld(not_4_out));  // open: sel, clr
  Multiplexer #(.width(16), .enable("false")) multiplexer_8 (
    .in0(ram_1_data[15:0]), .in1(ram_1_data[31:16]), .out(multiplexer_8_out), .sel(ex_mem_1_mem_calc[1]));
  Multiplexer #(.width(32), .enable("false")) multiplexer_9 (
    .in0(ram_1_data), .in1(bit_extender_4_out), .out(multiplexer_9_out), .sel(ex_mem_1_mem_lhu));
  assign bit_extender_4_out = {{16{1'b0}}, multiplexer_8_out};  // Bit_Extender bit_extender_4
  Multiplexer #(.width(32), .enable("false")) multiplexer_10 (
    .in0(ex_mem_1_mem_calc), .in1(multiplexer_9_out), .out(multiplexer_10_out), .sel(ex_mem_1_mem_memtoreg));
  MEM_WB mem_wb_1 (
    .MEM_PC(M_PC), .MEM_IR(MEM_IR), .MEM_RegWrite(ex_mem_1_mem_regwrite), .MEM_Jal(ex_mem_1_mem_jal),
    .MEM_Jalr(ex_mem_1_mem_jalr), .MEM_Calc_Mout(multiplexer_10_out), .MEM_rd(ex_mem_1_mem_rd),
    .MEM_Ecall(ex_mem_1_mem_ecall), .MEM_Equal(ex_mem_1_mem_equal), .clk(CLK), .en(en), .WB_PC(WB_PC),
    .WB_IR(WB_IR), .WB_RegWrite(RegWrite), .WB_Jal(mem_wb_1_wb_jal), .WB_Jalr(mem_wb_1_wb_jalr),
    .WB_Calc_Mout(mem_wb_1_wb_calc_mout), .WB_rd(WB_rd), .WB_Ecall(Ecall), .WB_Equal(Equal), .rst(RST));
  or or_5 (or_5_out, mem_wb_1_wb_jal, mem_wb_1_wb_jalr);
  Adder #(.width(32)) adder_4 (.a(WB_PC), .b(32'h4), .out(adder_4_out));  // open: cin, cout
  Multiplexer #(.width(32), .enable("false")) multiplexer_11 (
    .in0(mem_wb_1_wb_calc_mout), .in1(adder_4_out), .out(RDin), .sel(or_5_out));

  // Other names for the same wires on the sheet: rd[4:0] = ID_IR[11:7]; MEM_PC[31:0] = M_PC

  // Notes on the sheet:
  //   中断源
  //   时空图监测，可删除
  //   中断等待指示
  //   指令存储器
  //   数码管输出
  //   contents of rom_1 (hex, n*v repeats v):
  //   413 493 913 993 46413 14e493 296913 39e993 842023 942223 1242423 1342623 a00893 493 913 993 73
  //   I指令
  //   S指令
  //   B指令
  //   J指令
  //   LED显示
  //   控制位
  //   计数
  //   流水调试日志用
  //   暂停节拍，不能为0
  //   戳工具置1进入计数暂停模式，ctrl+k时钟自动运行到对应节拍暂停
  //   ctrl+k关闭时钟连续运行，将控制位置零，进入单步调试模式调试
  //   用这个时钟源需要去掉电路中的其他时钟源
  //   可计数暂停的时钟源
  //   为方便自动评测，需要输出流水线各段保存的PC值，注意是PC不是PC+4，另外ID段寄存器写入信息，Mem段内存写入信息也要输出
endmodule

module \气泡流水线  (
  output RegWrite,
  output MemWrite,
  output [31:0] IF_PC,
  output [31:0] ID_PC,
  output [31:0] EX_PC,
  output [31:0] M_PC,
  output [31:0] WB_PC,
  output [31:0] RDin,
  output [31:0] MDin,
  output [31:0] LedData
);

  wire and_1_out, and_3_out, and_4_out, and_5_out, and_6_out, Blt, CLK, clock_1_out, comparator_1_eq,
       comparator_1_lt, comparator_2_eq, d_ff_1_q, equal, Go, halt, IR1, IR2, IR3, Jal, Jalr, less, Lhu,
       multiplexer_2_out, nand_1_out, not_1_out, not_2_out, not_3_out, not_4_out, not_5_out, not_6_out,
       or_1_out, or_2_out, or_3_out, or_4_out, or_5_out, priority_encoder_1_p4, priority_encoder_1_p5, RST,
       S_Type, W1, W2, W3, \单周期硬布线控制器_1_alu_src , \单周期硬布线控制器_1_beq , \单周期硬布线控制器_1_bne , \单周期硬布线控制器_1_ecall ,
       \单周期硬布线控制器_1_memtoreg , \单周期硬布线控制器_1_memwrite , \单周期硬布线控制器_1_regwrite , \流水线寄存器_1_valid_2 ,
       \流水线寄存器_2_alusrcb_2 , \流水线寄存器_2_beq_2 , \流水线寄存器_2_blt_2 , \流水线寄存器_2_bne_2 , \流水线寄存器_2_ecall_2 ,
       \流水线寄存器_2_lhu_2 , \流水线寄存器_2_memtoreg_2 , \流水线寄存器_2_memwrite_2 , \流水线寄存器_2_regwrite_2 ,
       \流水线寄存器_2_valid_2 , \流水线寄存器_3_halt_3 , \流水线寄存器_3_jal_2 , \流水线寄存器_3_jalr_2 , \流水线寄存器_3_lhu_2 ,
       \流水线寄存器_3_memtoreg_2 , \流水线寄存器_3_regwrite_2 , \流水线寄存器_3_valid_2 , \流水线寄存器_4_halt_3 , \清空 ,
       \源寄存器使用情况_1_r1_used , \源寄存器使用情况_1_r2_used , \阻塞 ;
  wire [1:0] priority_encoder_1_p3, priority_encoder_2_out;
  wire [3:0] \单周期硬布线控制器_1_alu_op , \流水线寄存器_2_aluop_2 ;
  wire [4:0] multiplexer_3_out, multiplexer_4_out, \流水线寄存器_2_rd_2 , \流水线寄存器_3_rd_2 , \流水线寄存器_4_rd_2 ;
  wire [9:0] \流水线寄存器_3_alu_ans_2_2 ;
  wire [11:0] multiplexer_5_out;
  wire [12:0] CNT_num;
  wire [15:0] \LoadUse次数 , multiplexer_7_out, \总周期数 , \插入气泡数 , \无条件分支数 , \条件分支成功数 ;
  wire [31:0] adder_1_out, and_2_out, b_Addr, bit_extender_1_out, bit_extender_2_out, bit_extender_3_out,
       bit_extender_4_out, EX_IR, ID_IR, IF_IR, jal_Addr, jalr_Addr, MEM_IR, multiplexer_1_out,
       multiplexer_6_out, multiplexer_8_out, multiplexer_9_out, ram_1_data, regifile_1_r1, regifile_1_r2,
       shifter_1_out, shifter_2_out, WB_IR, \流水线寄存器_1_pc_4_2 , \流水线寄存器_2_imm_b_2 , \流水线寄存器_2_imm_j_2 ,
       \流水线寄存器_2_imm_si_2 , \流水线寄存器_2_pc_4_2 , \流水线寄存器_2_r1_2 , \流水线寄存器_2_r2_2 , \流水线寄存器_3_alu_ans_2 ,
       \流水线寄存器_3_pc_4_2 ;

  Button \u_总复位  (.out(RST));
  Button _1 (.out(IR1));
  Button _2 (.out(IR2));
  Button _3 (.out(IR3));
  // Probe on \总周期数 
  // Probe on \总周期数 
  Button \u_继续运行  (.out(Go));
  LED led_1 (.in(W1));
  LED led_2 (.in(W2));
  LED led_3 (.in(W3));
  and and_1 (and_1_out, \流水线寄存器_2_beq_2 , equal);
  assign and_2_out = jalr_Addr & 32'hfffffffe;  // AND_Gate and_2, 32 bits wide
  Hex_Digit_Display hex_digit_display_1 (.value(LedData[31:28]));  // open: dp
  // Probe on IF_PC[19:0]
  // RiscV_Probe riscv_probe_1: pin names not known; wires that end beside it: IF_IR
  not not_1 (not_1_out, equal);
  and and_3 (and_3_out, not_1_out, \流水线寄存器_2_bne_2 );
  or or_1 (or_1_out, and_1_out, and_3_out, and_4_out);
  // Priority_Encoder #(.select(2)) priority_encoder_1: pin names not known; wires that end beside it: 1'b1, or_1_out, priority_encoder_1_p3, priority_encoder_1_p4, priority_encoder_1_p5
  Multiplexer #(.select(2), .width(32), .enable("false")) multiplexer_1 (
    .in0(adder_1_out), .in1(b_Addr), .in2(jal_Addr), .in3(and_2_out), .out(multiplexer_1_out),
    .sel(priority_encoder_1_p3));
  not not_2 (not_2_out, or_2_out);
  or or_2 (or_2_out, halt, \阻塞 );
  Hex_Digit_Display hex_digit_display_2 (.value(LedData[23:20]));  // open: dp
  Hex_Digit_Display hex_digit_display_3 (.value(LedData[27:24]));  // open: dp
  // Probe on ID_PC[19:0]
  // RiscV_Probe riscv_probe_2: pin names not known; wires that end beside it: ID_IR
  and and_4 (and_4_out, \流水线寄存器_2_blt_2 , less);
  Register #(.width(32)) PC (.D(multiplexer_1_out), .en(not_2_out), .Q(IF_PC), .clk(CLK), .clr(RST));
  Hex_Digit_Display hex_digit_display_4 (.value(LedData[19:16]));  // open: dp
  Hex_Digit_Display hex_digit_display_5 (.value(LedData[15:12]));  // open: dp
  Hex_Digit_Display hex_digit_display_6 (.value(LedData[7:4]));  // open: dp
  Hex_Digit_Display hex_digit_display_7 (.value(LedData[11:8]));  // open: dp
  // Probe on EX_PC[19:0]
  // RiscV_Probe riscv_probe_3: pin names not known; wires that end beside it: EX_IR
  Multiplexer #(.enable("false")) multiplexer_2 (.in0(1'b1), .in1(1'b0), .out(multiplexer_2_out), .sel(halt));
  Adder #(.width(32)) adder_1 (.a(IF_PC), .b(32'h4), .out(adder_1_out));  // open: cin, cout
  Hex_Digit_Display hex_digit_display_8 (.value(LedData[3:0]));  // open: dp
  ROM #(.addrWidth(10), .dataWidth(32)) rom_1 (.addr(IF_PC[11:2]), .data(IF_IR));  // open: sel
  // Probe on \总周期数 
  // Probe on M_PC[19:0]
  // RiscV_Probe riscv_probe_4: pin names not known; wires that end beside it: MEM_IR
  \流水线寄存器  \u_流水线寄存器_1  (
    .valid(multiplexer_2_out), .PC(IF_PC), .PC_4(adder_1_out), .valid_2(\流水线寄存器_1_valid_2 ), .PC_2(ID_PC),
    .PC_4_2(\流水线寄存器_1_pc_4_2 ), .IR_2(ID_IR), .reset(1'b0), .refresh(\清空 ), .halt_2(\阻塞 ), .clk(CLK),
    .IR(IF_IR));  // open: Jal, Jalr, Lhu, Beq, Bne, Blt, MemToReg, MemWrite, AluSrcB, RegWrite, ecall, halt, AluOP, rd, R1, R2, imm_si, imm_b, imm_j, Jal_2, Jalr_2, Lhu_2, Beq_2, Bne_2, Blt_2, MemToReg_2, MemWrite_2, AluSrcB_2, RegWrite_2, ecall_2, halt_3, AluOP_2, rd_2, R1_2, R2_2, imm_si_2, imm_b_2, imm_j_2, Alu_ans_2, Alu_ans, RDin, RDin_2
  // Probe on \总周期数 
  // Probe on \无条件分支数 
  // Probe on \条件分支成功数 
  // Probe on \插入气泡数 
  // Probe on \LoadUse次数 
  or or_3 (or_3_out, \清空 , \阻塞 );
  \源寄存器使用情况  \u_源寄存器使用情况_1  (
    .OP(ID_IR[6:2]), .Funct({ID_IR[30], ID_IR[25], ID_IR[14:12]}), .r1_used(\源寄存器使用情况_1_r1_used ),
    .r2_used(\源寄存器使用情况_1_r2_used ));
  // Probe on IF_PC[11:0]
  // Probe on WB_PC[19:0]
  // RiscV_Probe riscv_probe_5: pin names not known; wires that end beside it: WB_IR
  \单周期硬布线控制器  \u_单周期硬布线控制器_1  (
    .Funct({ID_IR[30], ID_IR[25], ID_IR[14:12]}), .OP(ID_IR[6:2]), .ALU_OP(\单周期硬布线控制器_1_alu_op ),
    .MemToReg(\单周期硬布线控制器_1_memtoreg ), .MemWrite(\单周期硬布线控制器_1_memwrite ), .ALU_SRC(\单周期硬布线控制器_1_alu_src ),
    .RegWrite(\单周期硬布线控制器_1_regwrite ), .ecall(\单周期硬布线控制器_1_ecall ), .S_type(S_Type), .Jalr(Jalr),
    .Beq(\单周期硬布线控制器_1_beq ), .JAL(Jal), .Bne(\单周期硬布线控制器_1_bne ), .in_3(ID_IR[21]), .LHU(Lhu), .BLT(Blt));  // open: uret
  Multiplexer #(.width(5), .enable("false")) multiplexer_3 (
    .in0(ID_IR[19:15]), .in1(5'b10001), .out(multiplexer_3_out), .sel(\单周期硬布线控制器_1_ecall ));
  Multiplexer #(.width(5), .enable("false")) multiplexer_4 (
    .in0(ID_IR[24:20]), .in1(5'b01010), .out(multiplexer_4_out), .sel(\单周期硬布线控制器_1_ecall ));
  Multiplexer #(.width(12), .enable("false")) multiplexer_5 (
    .in0(ID_IR[31:20]), .in1({ID_IR[31:25], ID_IR[11:7]}), .out(multiplexer_5_out), .sel(S_Type));
  // Probe on ID_PC[11:0]
  // Probe on EX_PC[11:0]
  assign bit_extender_1_out = {{20{ID_IR[31]}}, {ID_IR[31], ID_IR[7], ID_IR[30:25], ID_IR[11:8]}};  // Bit_Extender bit_extender_1
  assign bit_extender_2_out = {{12{ID_IR[31]}}, {ID_IR[31], ID_IR[19:12], ID_IR[20], ID_IR[30:21]}};  // Bit_Extender bit_extender_2
  // Probe on M_PC[11:0]
  D_Flip_Flop #(.trigger("high")) d_ff_1 (.Q(d_ff_1_q));  // open: clk, D, Qn, preset, en, reset
  // Probe on 13'hc
  \相关处理逻辑_气泡  \u_相关处理逻辑_气泡_1  (
    .rs1(multiplexer_3_out), .rs1_used(\源寄存器使用情况_1_r1_used ), .EX_RegWrite(\流水线寄存器_2_regwrite_2 ),
    .EX_rd(\流水线寄存器_2_rd_2 ), .rs2(multiplexer_4_out), .rs2_used(\源寄存器使用情况_1_r2_used ),
    .MEM_RegWrite(\流水线寄存器_3_regwrite_2 ), .MEM_rd(\流水线寄存器_3_rd_2 ), .\阻塞 (\阻塞 ), .BranchTaken(or_4_out),
    .\清空 (\清空 ));
  not not_3 (not_3_out, CLK);
  assign bit_extender_3_out = {{20{multiplexer_5_out[11]}}, multiplexer_5_out};  // Bit_Extender bit_extender_3
  Shifter #(.width(32)) shifter_1 (.in(bit_extender_1_out), .\dist (5'b00001), .out(shifter_1_out));
  Shifter #(.width(32)) shifter_2 (.in(bit_extender_2_out), .\dist (5'b00001), .out(shifter_2_out));
  // Probe on WB_PC[11:0]
  Comparator #(.width(13)) comparator_1 (
    .a(CNT_num), .b(13'hc), .eq(comparator_1_eq), .lt(comparator_1_lt));  // open: gt
  Clock clock_1 (.out(clock_1_out));
  or or_4 (or_4_out, priority_encoder_1_p3[0], priority_encoder_1_p3[1]);
  not not_4 (not_4_out, \流水线寄存器_1_valid_2 );
  Regifile regifile_1 (
    .Din(RDin), .Clk(not_3_out), .R1(regifile_1_r1), .R2(regifile_1_r2), .WE(RegWrite),
    .W_num(\流水线寄存器_4_rd_2 ), .R1_num(multiplexer_3_out), .R2_num(multiplexer_4_out));
  nand nand_1 (nand_1_out, d_ff_1_q, comparator_1_eq);
  Counter #(.width(13), .max('h1fff), .ongoal("stay")) counter_1 (
    .count(comparator_1_lt), .Q(CNT_num), .clk(clock_1_out));  // open: load, D, carry, clr
  \流水线寄存器  \u_流水线寄存器_2  (
    .Jal(Jal), .Jalr(Jalr), .Lhu(Lhu), .Beq(\单周期硬布线控制器_1_beq ), .Bne(\单周期硬布线控制器_1_bne ), .Blt(Blt),
    .MemToReg(\单周期硬布线控制器_1_memtoreg ), .MemWrite(\单周期硬布线控制器_1_memwrite ), .AluSrcB(\单周期硬布线控制器_1_alu_src ),
    .RegWrite(\单周期硬布线控制器_1_regwrite ), .ecall(\单周期硬布线控制器_1_ecall ), .AluOP(\单周期硬布线控制器_1_alu_op ),
    .rd(ID_IR[11:7]), .valid(\流水线寄存器_1_valid_2 ), .R1(regifile_1_r1), .R2(regifile_1_r2), .PC(ID_PC),
    .PC_4(\流水线寄存器_1_pc_4_2 ), .imm_si(bit_extender_3_out), .imm_b(shifter_1_out), .imm_j(shifter_2_out),
    .Jal_2(priority_encoder_1_p4), .Jalr_2(priority_encoder_1_p5), .Lhu_2(\流水线寄存器_2_lhu_2 ),
    .Beq_2(\流水线寄存器_2_beq_2 ), .Bne_2(\流水线寄存器_2_bne_2 ), .Blt_2(\流水线寄存器_2_blt_2 ),
    .MemToReg_2(\流水线寄存器_2_memtoreg_2 ), .MemWrite_2(\流水线寄存器_2_memwrite_2 ), .AluSrcB_2(\流水线寄存器_2_alusrcb_2 ),
    .RegWrite_2(\流水线寄存器_2_regwrite_2 ), .ecall_2(\流水线寄存器_2_ecall_2 ), .AluOP_2(\流水线寄存器_2_aluop_2 ),
    .rd_2(\流水线寄存器_2_rd_2 ), .valid_2(\流水线寄存器_2_valid_2 ), .R1_2(\流水线寄存器_2_r1_2 ), .R2_2(\流水线寄存器_2_r2_2 ),
    .PC_2(EX_PC), .PC_4_2(\流水线寄存器_2_pc_4_2 ), .imm_si_2(\流水线寄存器_2_imm_si_2 ), .imm_b_2(\流水线寄存器_2_imm_b_2 ),
    .imm_j_2(\流水线寄存器_2_imm_j_2 ), .IR_2(EX_IR), .reset(not_4_out), .refresh(or_3_out), .halt_2(halt),
    .clk(CLK), .IR(ID_IR));  // open: halt, halt_3, Alu_ans_2, Alu_ans, RDin, RDin_2
  assign CLK = nand_1_out ? clock_1_out : 1'bz;  // Controlled_Buffer controlled_buffer_1
  Multiplexer #(.width(32), .enable("false")) multiplexer_6 (
    .in0(\流水线寄存器_2_r2_2 ), .in1(\流水线寄存器_2_imm_si_2 ), .out(multiplexer_6_out), .sel(\流水线寄存器_2_alusrcb_2 ));
  Adder #(.width(32)) adder_2 (.a(\流水线寄存器_2_imm_b_2 ), .b(EX_PC), .out(b_Addr));  // open: cin, cout
  Adder #(.width(32)) adder_3 (.a(\流水线寄存器_2_imm_j_2 ), .b(EX_PC), .out(jal_Addr));  // open: cin, cout
  Pull_Resistor #(.pull(1)) pull_resistor_1 (.node(CLK));
  ALU alu_1 (
    .X(\流水线寄存器_2_r1_2 ), .Y(multiplexer_6_out), .AluOP(\流水线寄存器_2_aluop_2 ), .Equal(equal),
    .Result(jalr_Addr), .out_6(less));  // open: Result_2, out_4
  Register #(.width(32)) register_1 (.D(\流水线寄存器_2_r2_2 ), .en(and_5_out), .Q(LedData), .clk(CLK));  // open: clr
  Comparator #(.width(32)) comparator_2 (.a(\流水线寄存器_2_r1_2 ), .b(32'h22), .eq(comparator_2_eq));  // open: gt, lt
  and and_5 (and_5_out, \流水线寄存器_2_ecall_2 , comparator_2_eq);
  not not_5 (not_5_out, \流水线寄存器_2_valid_2 );
  and and_6 (and_6_out, \流水线寄存器_2_ecall_2 , ~comparator_2_eq);  // AND_Gate
  \流水线寄存器  \u_流水线寄存器_3  (
    .Jal(priority_encoder_1_p4), .Jalr(priority_encoder_1_p5), .Lhu(\流水线寄存器_2_lhu_2 ),
    .MemToReg(\流水线寄存器_2_memtoreg_2 ), .MemWrite(\流水线寄存器_2_memwrite_2 ), .RegWrite(\流水线寄存器_2_regwrite_2 ),
    .halt(and_6_out), .rd(\流水线寄存器_2_rd_2 ), .valid(\流水线寄存器_2_valid_2 ), .PC(EX_PC), .PC_4(\流水线寄存器_2_pc_4_2 ),
    .Jal_2(\流水线寄存器_3_jal_2 ), .Jalr_2(\流水线寄存器_3_jalr_2 ), .Lhu_2(\流水线寄存器_3_lhu_2 ),
    .MemToReg_2(\流水线寄存器_3_memtoreg_2 ), .MemWrite_2(MemWrite), .RegWrite_2(\流水线寄存器_3_regwrite_2 ),
    .halt_3(\流水线寄存器_3_halt_3 ), .rd_2(\流水线寄存器_3_rd_2 ), .valid_2(\流水线寄存器_3_valid_2 ), .R2_2(MDin),
    .PC_2(M_PC), .PC_4_2(\流水线寄存器_3_pc_4_2 ), .IR_2(MEM_IR), .reset(not_5_out), .refresh(1'b0), .halt_2(halt),
    .clk(CLK), .Alu_ans_2({\流水线寄存器_3_alu_ans_2 [31:12], \流水线寄存器_3_alu_ans_2_2 , \流水线寄存器_3_alu_ans_2 [1:0]}),
    .IR(EX_IR), .Alu_ans(jalr_Addr));  // open: Beq, Bne, Blt, AluSrcB, ecall, AluOP, R1, R2, imm_si, imm_b, imm_j, Beq_2, Bne_2, Blt_2, AluSrcB_2, ecall_2, AluOP_2, R1_2, imm_si_2, imm_b_2, imm_j_2, RDin, RDin_2
  or or_5 (or_5_out, \流水线寄存器_3_jal_2 , \流水线寄存器_3_jalr_2 );
  RAM #(.addrWidth(10), .dataWidth(32), .bus("separate")) ram_1 (
    .addr(\流水线寄存器_3_alu_ans_2_2 ), .din(MDin), .data(ram_1_data), .str(MemWrite), .sel(1'b1),
    .ld(\流水线寄存器_3_memtoreg_2 ), .clr(1'b0));  // open: clk
  Priority_Encoder #(.select(2)) priority_encoder_2 (
    .in0(1'b1), .in1(or_5_out), .in2(\流水线寄存器_3_memtoreg_2 ), .in3(1'b0), .out(priority_encoder_2_out));  // open: gs, en_out, en_in
  Multiplexer #(.width(16), .enable("false")) multiplexer_7 (
    .in0(ram_1_data[15:0]), .in1(ram_1_data[31:16]), .out(multiplexer_7_out), .sel(\流水线寄存器_3_alu_ans_2 [1]));
  assign bit_extender_4_out = {{16{1'b0}}, multiplexer_7_out};  // Bit_Extender bit_extender_4
  Multiplexer #(.width(32), .enable("false")) multiplexer_8 (
    .in0(ram_1_data), .in1(bit_extender_4_out), .out(multiplexer_8_out), .sel(\流水线寄存器_3_lhu_2 ));
  not not_6 (not_6_out, \流水线寄存器_3_valid_2 );
  Multiplexer #(.select(2), .width(32), .enable("false")) multiplexer_9 (
    .in0({\流水线寄存器_3_alu_ans_2 [31:12], \流水线寄存器_3_alu_ans_2_2 , \流水线寄存器_3_alu_ans_2 [1:0]}),
    .in1(\流水线寄存器_3_pc_4_2 ), .in2(multiplexer_8_out), .out(multiplexer_9_out), .sel(priority_encoder_2_out));  // open: in3
  \流水线寄存器  \u_流水线寄存器_4  (
    .RegWrite(\流水线寄存器_3_regwrite_2 ), .halt(\流水线寄存器_3_halt_3 ), .rd(\流水线寄存器_3_rd_2 ),
    .valid(\流水线寄存器_3_valid_2 ), .PC(M_PC), .PC_4(\流水线寄存器_3_pc_4_2 ), .RegWrite_2(RegWrite),
    .halt_3(\流水线寄存器_4_halt_3 ), .rd_2(\流水线寄存器_4_rd_2 ), .PC_2(WB_PC), .IR_2(WB_IR), .reset(not_6_out),
    .refresh(1'b0), .halt_2(halt), .clk(CLK), .IR(MEM_IR), .RDin(multiplexer_9_out), .RDin_2(RDin));  // open: Jal, Jalr, Lhu, Beq, Bne, Blt, MemToReg, MemWrite, AluSrcB, ecall, AluOP, R1, R2, imm_si, imm_b, imm_j, Jal_2, Jalr_2, Lhu_2, Beq_2, Bne_2, Blt_2, MemToReg_2, MemWrite_2, AluSrcB_2, ecall_2, AluOP_2, valid_2, R1_2, R2_2, PC_4_2, imm_si_2, imm_b_2, imm_j_2, Alu_ans_2, Alu_ans
  and and_7 (halt, ~Go, \流水线寄存器_4_halt_3 );  // AND_Gate

  // Other names for the same wires on the sheet: rd[4:0] = ID_IR[11:7]; MEM_PC[31:0] = M_PC

  // Notes on the sheet:
  //   中断源
  //   时空图监测，可删除
  //   中断等待指示
  //   数码管输出
  //   指令存储器
  //   contents of rom_1 (hex, n*v repeats v):
  //   413 493 913 993 46413 14e493 296913 39e993 842023 942223 1242423 1342623 a00893 493 913 993 73
  //   I指令
  //   S指令
  //   B指令
  //   J指令
  //   控制位
  //   流水调试日志用
  //   暂停节拍，不能为0
  //   戳工具置1进入计数暂停模式，ctrl+k时钟自动运行到对应节拍暂停
  //   ctrl+k关闭时钟连续运行，将控制位置零，进入单步调试模式调试
  //   可计数暂停的时钟源
  //   为方便自动评测，需要输出流水线各段保存的PC值，注意是PC不是PC+4，另外ID段寄存器写入信息，Mem段内存写入信息也要输出
endmodule

module \重定向流水线  (
  output RegWrite,
  output MemWrite,
  output [31:0] IF_PC,
  output [31:0] ID_PC,
  output [31:0] EX_PC,
  output [31:0] M_PC,
  output [31:0] WB_PC,
  output [31:0] RDin,
  output [31:0] MDin,
  output [31:0] LedData
);

  wire and_1_out, and_3_out, and_4_out, and_5_out, and_6_out, Blt, CLK, clock_1_out, comparator_1_eq,
       comparator_1_lt, comparator_2_eq, d_ff_1_q, equal, Go, halt, IR1, IR2, IR3, Jal, Jalr, less, Lhu,
       LoadUse, multiplexer_2_out, nand_1_out, not_1_out, not_2_out, not_3_out, not_4_out, not_5_out,
       not_6_out, or_1_out, or_2_out, or_3_out, or_4_out, priority_encoder_1_p4, priority_encoder_1_p5, RST,
       S_Type, W1, W2, W3, \单周期硬布线控制器_1_alu_src , \单周期硬布线控制器_1_beq , \单周期硬布线控制器_1_bne , \单周期硬布线控制器_1_ecall ,
       \单周期硬布线控制器_1_memtoreg , \单周期硬布线控制器_1_memwrite , \单周期硬布线控制器_1_regwrite , \流水线寄存器_1_valid_2 ,
       \流水线寄存器_2_alusrcb_2 , \流水线寄存器_2_beq_2 , \流水线寄存器_2_blt_2 , \流水线寄存器_2_bne_2 , \流水线寄存器_2_ecall_2 ,
       \流水线寄存器_2_lhu_2 , \流水线寄存器_2_memtoreg_2 , \流水线寄存器_2_memwrite_2 , \流水线寄存器_2_regwrite_2 ,
       \流水线寄存器_2_valid_2 , \流水线寄存器_3_halt_3 , \流水线寄存器_3_jal_2 , \流水线寄存器_3_jalr_2 , \流水线寄存器_3_lhu_2 ,
       \流水线寄存器_3_memtoreg_2 , \流水线寄存器_3_regwrite_2 , \流水线寄存器_3_valid_2 , \流水线寄存器_4_halt_3 ,
       \源寄存器使用情况_1_r1_used , \源寄存器使用情况_1_r2_used ;
  wire [1:0] forward_1_rs1_forward_2, forward_1_rs2_forward_2, priority_encoder_1_p3, priority_encoder_2_out,
       \相关处理逻辑_重定向_1_rs1_forward , \相关处理逻辑_重定向_1_rs2_forward ;
  wire [3:0] \单周期硬布线控制器_1_alu_op , \流水线寄存器_2_aluop_2 ;
  wire [4:0] multiplexer_3_out, multiplexer_4_out, \流水线寄存器_2_rd_2 , \流水线寄存器_3_rd_2 , \流水线寄存器_4_rd_2 ;
  wire [9:0] \流水线寄存器_3_alu_ans_2_2 ;
  wire [11:0] multiplexer_5_out;
  wire [12:0] CNT_num;
  wire [15:0] \LoadUse次数 , multiplexer_9_out, \总周期数 , \插入气泡数 , \无条件分支数 , \条件分支成功数 ;
  wire [31:0] adder_1_out, and_2_out, b_Addr, bit_extender_1_out, bit_extender_2_out, bit_extender_3_out,
       bit_extender_4_out, EX_IR, ID_IR, IF_IR, jal_Addr, jalr_Addr, MEM_IR, multiplexer_1_out,
       multiplexer_6_out, multiplexer_10_out, multiplexer_11_out, r1, r1_, r2, r2_, ram_1_data,
       regifile_1_r1, regifile_1_r2, shifter_1_out, shifter_2_out, WB_IR, \流水线寄存器_1_pc_4_2 ,
       \流水线寄存器_2_imm_b_2 , \流水线寄存器_2_imm_j_2 , \流水线寄存器_2_imm_si_2 , \流水线寄存器_2_pc_4_2 , \流水线寄存器_3_alu_ans_2 ,
       \流水线寄存器_3_pc_4_2 ;

  Button \u_总复位  (.out(RST));
  Button _1 (.out(IR1));
  Button _2 (.out(IR2));
  Button _3 (.out(IR3));
  // Probe on \总周期数 
  // Probe on \总周期数 
  Button \u_继续运行  (.out(Go));
  LED led_1 (.in(W1));
  LED led_2 (.in(W2));
  LED led_3 (.in(W3));
  and and_1 (and_1_out, \流水线寄存器_2_beq_2 , equal);
  assign and_2_out = jalr_Addr & 32'hfffffffe;  // AND_Gate and_2, 32 bits wide
  Hex_Digit_Display hex_digit_display_1 (.value(LedData[31:28]));  // open: dp
  // Probe on IF_PC[19:0]
  // RiscV_Probe riscv_probe_1: pin names not known; wires that end beside it: IF_IR
  not not_1 (not_1_out, equal);
  and and_3 (and_3_out, not_1_out, \流水线寄存器_2_bne_2 );
  or or_1 (or_1_out, and_1_out, and_3_out, and_4_out);
  // Priority_Encoder #(.select(2)) priority_encoder_1: pin names not known; wires that end beside it: 1'b1, or_1_out, priority_encoder_1_p3, priority_encoder_1_p4, priority_encoder_1_p5
  Multiplexer #(.select(2), .width(32), .enable("false")) multiplexer_1 (
    .in0(adder_1_out), .in1(b_Addr), .in2(jal_Addr), .in3(and_2_out), .out(multiplexer_1_out),
    .sel(priority_encoder_1_p3));
  not not_2 (not_2_out, or_2_out);
  or or_2 (or_2_out, halt, LoadUse);
  Hex_Digit_Display hex_digit_display_2 (.value(LedData[27:24]));  // open: dp
  Hex_Digit_Display hex_digit_display_3 (.value(LedData[23:20]));  // open: dp
  // Probe on ID_PC[19:0]
  // RiscV_Probe riscv_probe_2: pin names not known; wires that end beside it: ID_IR
  or or_3 (or_3_out, priority_encoder_1_p3[0], priority_encoder_1_p3[1]);
  and and_4 (and_4_out, \流水线寄存器_2_blt_2 , less);
  Register #(.width(32)) PC (.D(multiplexer_1_out), .en(not_2_out), .Q(IF_PC), .clk(CLK), .clr(RST));
  Hex_Digit_Display hex_digit_display_4 (.value(LedData[15:12]));  // open: dp
  Hex_Digit_Display hex_digit_display_5 (.value(LedData[19:16]));  // open: dp
  Hex_Digit_Display hex_digit_display_6 (.value(LedData[7:4]));  // open: dp
  Hex_Digit_Display hex_digit_display_7 (.value(LedData[11:8]));  // open: dp
  // Probe on EX_PC[19:0]
  // RiscV_Probe riscv_probe_3: pin names not known; wires that end beside it: EX_IR
  Multiplexer #(.enable("false")) multiplexer_2 (.in0(1'b1), .in1(1'b0), .out(multiplexer_2_out), .sel(halt));
  Adder #(.width(32)) adder_1 (.a(IF_PC), .b(32'h4), .out(adder_1_out));  // open: cin, cout
  Hex_Digit_Display hex_digit_display_8 (.value(LedData[3:0]));  // open: dp
  ROM #(.addrWidth(10), .dataWidth(32)) rom_1 (.addr(IF_PC[11:2]), .data(IF_IR));  // open: sel
  // Probe on \总周期数 
  // Probe on M_PC[19:0]
  // RiscV_Probe riscv_probe_4: pin names not known; wires that end beside it: MEM_IR
  \流水线寄存器  \u_流水线寄存器_1  (
    .valid(multiplexer_2_out), .PC(IF_PC), .PC_4(adder_1_out), .valid_2(\流水线寄存器_1_valid_2 ), .PC_2(ID_PC),
    .PC_4_2(\流水线寄存器_1_pc_4_2 ), .IR_2(ID_IR), .reset(1'b0), .refresh(or_3_out), .halt_2(LoadUse), .clk(CLK),
    .IR(IF_IR));  // open: Jal, Jalr, Lhu, Beq, Bne, Blt, MemToReg, MemWrite, AluSrcB, RegWrite, ecall, halt, AluOP, rd, R1, R2, imm_si, imm_b, imm_j, Jal_2, Jalr_2, Lhu_2, Beq_2, Bne_2, Blt_2, MemToReg_2, MemWrite_2, AluSrcB_2, RegWrite_2, ecall_2, halt_3, AluOP_2, rd_2, R1_2, R2_2, imm_si_2, imm_b_2, imm_j_2, Alu_ans_2, Alu_ans, RDin, RDin_2
  // Probe on \总周期数 
  // Probe on \无条件分支数 
  // Probe on \条件分支成功数 
  // Probe on \插入气泡数 
  // Probe on \LoadUse次数 
  \源寄存器使用情况  \u_源寄存器使用情况_1  (
    .OP(ID_IR[6:2]), .Funct({ID_IR[30], ID_IR[25], ID_IR[14:12]}), .r1_used(\源寄存器使用情况_1_r1_used ),
    .r2_used(\源寄存器使用情况_1_r2_used ));
  // Probe on IF_PC[11:0]
  // Probe on WB_PC[19:0]
  // RiscV_Probe riscv_probe_5: pin names not known; wires that end beside it: WB_IR
  \单周期硬布线控制器  \u_单周期硬布线控制器_1  (
    .Funct({ID_IR[30], ID_IR[25], ID_IR[14:12]}), .OP(ID_IR[6:2]), .ALU_OP(\单周期硬布线控制器_1_alu_op ),
    .MemToReg(\单周期硬布线控制器_1_memtoreg ), .MemWrite(\单周期硬布线控制器_1_memwrite ), .ALU_SRC(\单周期硬布线控制器_1_alu_src ),
    .RegWrite(\单周期硬布线控制器_1_regwrite ), .ecall(\单周期硬布线控制器_1_ecall ), .S_type(S_Type), .Jalr(Jalr),
    .Beq(\单周期硬布线控制器_1_beq ), .JAL(Jal), .Bne(\单周期硬布线控制器_1_bne ), .in_3(ID_IR[21]), .LHU(Lhu), .BLT(Blt));  // open: uret
  Multiplexer #(.width(5), .enable("false")) multiplexer_3 (
    .in0(ID_IR[19:15]), .in1(5'b10001), .out(multiplexer_3_out), .sel(\单周期硬布线控制器_1_ecall ));
  Multiplexer #(.width(5), .enable("false")) multiplexer_4 (
    .in0(ID_IR[24:20]), .in1(5'b01010), .out(multiplexer_4_out), .sel(\单周期硬布线控制器_1_ecall ));
  Multiplexer #(.width(12), .enable("false")) multiplexer_5 (
    .in0(ID_IR[31:20]), .in1({ID_IR[31:25], ID_IR[11:7]}), .out(multiplexer_5_out), .sel(S_Type));
  // Probe on ID_PC[11:0]
  // Probe on EX_PC[11:0]
  \相关处理逻辑_重定向  \u_相关处理逻辑_重定向_1  (
    .rs1(multiplexer_3_out), .rs1_used(\源寄存器使用情况_1_r1_used ), .rs2(multiplexer_4_out),
    .rs2_used(\源寄存器使用情况_1_r2_used ), .EX_RegWrite(\流水线寄存器_2_regwrite_2 ), .EX_rd(\流水线寄存器_2_rd_2 ),
    .EX_MemToReg(\流水线寄存器_2_memtoreg_2 ), .MEM_RegWrite(\流水线寄存器_3_regwrite_2 ), .MEM_rd(\流水线寄存器_3_rd_2 ),
    .rs1_forward(\相关处理逻辑_重定向_1_rs1_forward ), .LoadUse(LoadUse), .rs2_forward(\相关处理逻辑_重定向_1_rs2_forward ));
  assign bit_extender_1_out = {{20{ID_IR[31]}}, {ID_IR[31], ID_IR[7], ID_IR[30:25], ID_IR[11:8]}};  // Bit_Extender bit_extender_1
  assign bit_extender_2_out = {{12{ID_IR[31]}}, {ID_IR[31], ID_IR[19:12], ID_IR[20], ID_IR[30:21]}};  // Bit_Extender bit_extender_2
  // Probe on M_PC[11:0]
  D_Flip_Flop #(.trigger("high")) d_ff_1 (.Q(d_ff_1_q));  // open: clk, D, Qn, preset, en, reset
  // Probe on 13'hc
  forward forward_1 (
    .rs1_forward(\相关处理逻辑_重定向_1_rs1_forward ), .rs2_forward(\相关处理逻辑_重定向_1_rs2_forward ),
    .rs1_forward_2(forward_1_rs1_forward_2), .rs2_forward_2(forward_1_rs2_forward_2), .LoadUse(LoadUse),
    .clk(CLK));
  not not_3 (not_3_out, CLK);
  assign bit_extender_3_out = {{20{multiplexer_5_out[11]}}, multiplexer_5_out};  // Bit_Extender bit_extender_3
  Shifter #(.width(32)) shifter_1 (.in(bit_extender_1_out), .\dist (5'b00001), .out(shifter_1_out));
  Shifter #(.width(32)) shifter_2 (.in(bit_extender_2_out), .\dist (5'b00001), .out(shifter_2_out));
  // Probe on WB_PC[11:0]
  Comparator #(.width(13)) comparator_1 (
    .a(CNT_num), .b(13'hc), .eq(comparator_1_eq), .lt(comparator_1_lt));  // open: gt
  Clock clock_1 (.out(clock_1_out));
  not not_4 (not_4_out, \流水线寄存器_1_valid_2 );
  Regifile regifile_1 (
    .Din(RDin), .Clk(not_3_out), .R1(regifile_1_r1), .R2(regifile_1_r2), .WE(RegWrite),
    .W_num(\流水线寄存器_4_rd_2 ), .R1_num(multiplexer_3_out), .R2_num(multiplexer_4_out));
  nand nand_1 (nand_1_out, d_ff_1_q, comparator_1_eq);
  Counter #(.width(13), .max('h1fff), .ongoal("stay")) counter_1 (
    .count(comparator_1_lt), .Q(CNT_num), .clk(clock_1_out));  // open: load, D, carry, clr
  \流水线寄存器  \u_流水线寄存器_2  (
    .Jal(Jal), .Jalr(Jalr), .Lhu(Lhu), .Beq(\单周期硬布线控制器_1_beq ), .Bne(\单周期硬布线控制器_1_bne ), .Blt(Blt),
    .MemToReg(\单周期硬布线控制器_1_memtoreg ), .MemWrite(\单周期硬布线控制器_1_memwrite ), .AluSrcB(\单周期硬布线控制器_1_alu_src ),
    .RegWrite(\单周期硬布线控制器_1_regwrite ), .ecall(\单周期硬布线控制器_1_ecall ), .AluOP(\单周期硬布线控制器_1_alu_op ),
    .rd(ID_IR[11:7]), .valid(\流水线寄存器_1_valid_2 ), .R1(regifile_1_r1), .R2(regifile_1_r2), .PC(ID_PC),
    .PC_4(\流水线寄存器_1_pc_4_2 ), .imm_si(bit_extender_3_out), .imm_b(shifter_1_out), .imm_j(shifter_2_out),
    .Jal_2(priority_encoder_1_p4), .Jalr_2(priority_encoder_1_p5), .Lhu_2(\流水线寄存器_2_lhu_2 ),
    .Beq_2(\流水线寄存器_2_beq_2 ), .Bne_2(\流水线寄存器_2_bne_2 ), .Blt_2(\流水线寄存器_2_blt_2 ),
    .MemToReg_2(\流水线寄存器_2_memtoreg_2 ), .MemWrite_2(\流水线寄存器_2_memwrite_2 ), .AluSrcB_2(\流水线寄存器_2_alusrcb_2 ),
    .RegWrite_2(\流水线寄存器_2_regwrite_2 ), .ecall_2(\流水线寄存器_2_ecall_2 ), .AluOP_2(\流水线寄存器_2_aluop_2 ),
    .rd_2(\流水线寄存器_2_rd_2 ), .valid_2(\流水线寄存器_2_valid_2 ), .R1_2(r1), .R2_2(r2), .PC_2(EX_PC),
    .PC_4_2(\流水线寄存器_2_pc_4_2 ), .imm_si_2(\流水线寄存器_2_imm_si_2 ), .imm_b_2(\流水线寄存器_2_imm_b_2 ),
    .imm_j_2(\流水线寄存器_2_imm_j_2 ), .IR_2(EX_IR), .reset(not_4_out), .refresh(or_3_out), .halt_2(halt),
    .clk(CLK), .IR(ID_IR));  // open: halt, halt_3, Alu_ans_2, Alu_ans, RDin, RDin_2
  assign CLK = nand_1_out ? clock_1_out : 1'bz;  // Controlled_Buffer controlled_buffer_1
  Multiplexer #(.width(32), .enable("false")) multiplexer_6 (
    .in0(r2_), .in1(\流水线寄存器_2_imm_si_2 ), .out(multiplexer_6_out), .sel(\流水线寄存器_2_alusrcb_2 ));
  Adder #(.width(32)) adder_2 (.a(\流水线寄存器_2_imm_b_2 ), .b(EX_PC), .out(b_Addr));  // open: cin, cout
  Adder #(.width(32)) adder_3 (.a(\流水线寄存器_2_imm_j_2 ), .b(EX_PC), .out(jal_Addr));  // open: cin, cout
  Pull_Resistor #(.pull(1)) pull_resistor_1 (.node(CLK));
  ALU alu_1 (
    .X(r1_), .Y(multiplexer_6_out), .AluOP(\流水线寄存器_2_aluop_2 ), .Equal(equal), .Result(jalr_Addr),
    .out_6(less));  // open: Result_2, out_4
  Register #(.width(32)) register_1 (.D(r2_), .en(and_5_out), .Q(LedData), .clk(CLK));  // open: clr
  Comparator #(.width(32)) comparator_2 (.a(r1_), .b(32'h22), .eq(comparator_2_eq));  // open: gt, lt
  and and_5 (and_5_out, \流水线寄存器_2_ecall_2 , comparator_2_eq);
  not not_5 (not_5_out, \流水线寄存器_2_valid_2 );
  and and_6 (and_6_out, \流水线寄存器_2_ecall_2 , ~comparator_2_eq);  // AND_Gate
  \流水线寄存器  \u_流水线寄存器_3  (
    .Jal(priority_encoder_1_p4), .Jalr(priority_encoder_1_p5), .Lhu(\流水线寄存器_2_lhu_2 ),
    .MemToReg(\流水线寄存器_2_memtoreg_2 ), .MemWrite(\流水线寄存器_2_memwrite_2 ), .RegWrite(\流水线寄存器_2_regwrite_2 ),
    .halt(and_6_out), .rd(\流水线寄存器_2_rd_2 ), .valid(\流水线寄存器_2_valid_2 ), .R2(r2_), .PC(EX_PC),
    .PC_4(\流水线寄存器_2_pc_4_2 ), .Jal_2(\流水线寄存器_3_jal_2 ), .Jalr_2(\流水线寄存器_3_jalr_2 ), .Lhu_2(\流水线寄存器_3_lhu_2 ),
    .MemToReg_2(\流水线寄存器_3_memtoreg_2 ), .MemWrite_2(MemWrite), .RegWrite_2(\流水线寄存器_3_regwrite_2 ),
    .halt_3(\流水线寄存器_3_halt_3 ), .rd_2(\流水线寄存器_3_rd_2 ), .valid_2(\流水线寄存器_3_valid_2 ), .R2_2(MDin),
    .PC_2(M_PC), .PC_4_2(\流水线寄存器_3_pc_4_2 ), .IR_2(MEM_IR), .reset(not_5_out), .refresh(1'b0), .halt_2(halt),
    .clk(CLK), .Alu_ans_2({\流水线寄存器_3_alu_ans_2 [31:12], \流水线寄存器_3_alu_ans_2_2 , \流水线寄存器_3_alu_ans_2 [1:0]}),
    .IR(EX_IR), .Alu_ans(jalr_Addr));  // open: Beq, Bne, Blt, AluSrcB, ecall, AluOP, R1, imm_si, imm_b, imm_j, Beq_2, Bne_2, Blt_2, AluSrcB_2, ecall_2, AluOP_2, R1_2, imm_si_2, imm_b_2, imm_j_2, RDin, RDin_2
  or or_4 (or_4_out, \流水线寄存器_3_jal_2 , \流水线寄存器_3_jalr_2 );
  RAM #(.addrWidth(10), .dataWidth(32), .bus("separate")) ram_1 (
    .addr(\流水线寄存器_3_alu_ans_2_2 ), .din(MDin), .data(ram_1_data), .str(MemWrite), .sel(1'b1),
    .ld(\流水线寄存器_3_memtoreg_2 ), .clr(1'b0));  // open: clk
  Multiplexer #(.select(2), .width(32), .enable("false")) multiplexer_7 (
    .in0(r1), .in1(RDin),
    .in2({\流水线寄存器_3_alu_ans_2 [31:12], \流水线寄存器_3_alu_ans_2_2 , \流水线寄存器_3_alu_ans_2 [1:0]}), .out(r1_),
    .sel(forward_1_rs1_forward_2));  // open: in3
  Multiplexer #(.select(2), .width(32), .enable("false")) multiplexer_8 (
    .in0(r2), .in1(RDin),
    .in2({\流水线寄存器_3_alu_ans_2 [31:12], \流水线寄存器_3_alu_ans_2_2 , \流水线寄存器_3_alu_ans_2 [1:0]}), .out(r2_),
    .sel(forward_1_rs2_forward_2));  // open: in3
  Priority_Encoder #(.select(2)) priority_encoder_2 (
    .in0(1'b1), .in1(or_4_out), .in2(\流水线寄存器_3_memtoreg_2 ), .in3(1'b0), .out(priority_encoder_2_out));  // open: gs, en_out, en_in
  Multiplexer #(.width(16), .enable("false")) multiplexer_9 (
    .in0(ram_1_data[15:0]), .in1(ram_1_data[31:16]), .out(multiplexer_9_out), .sel(\流水线寄存器_3_alu_ans_2 [1]));
  assign bit_extender_4_out = {{16{1'b0}}, multiplexer_9_out};  // Bit_Extender bit_extender_4
  Multiplexer #(.width(32), .enable("false")) multiplexer_10 (
    .in0(ram_1_data), .in1(bit_extender_4_out), .out(multiplexer_10_out), .sel(\流水线寄存器_3_lhu_2 ));
  not not_6 (not_6_out, \流水线寄存器_3_valid_2 );
  Multiplexer #(.select(2), .width(32), .enable("false")) multiplexer_11 (
    .in0({\流水线寄存器_3_alu_ans_2 [31:12], \流水线寄存器_3_alu_ans_2_2 , \流水线寄存器_3_alu_ans_2 [1:0]}),
    .in1(\流水线寄存器_3_pc_4_2 ), .in2(multiplexer_10_out), .out(multiplexer_11_out), .sel(priority_encoder_2_out));  // open: in3
  \流水线寄存器  \u_流水线寄存器_4  (
    .RegWrite(\流水线寄存器_3_regwrite_2 ), .halt(\流水线寄存器_3_halt_3 ), .rd(\流水线寄存器_3_rd_2 ),
    .valid(\流水线寄存器_3_valid_2 ), .PC(M_PC), .PC_4(\流水线寄存器_3_pc_4_2 ), .RegWrite_2(RegWrite),
    .halt_3(\流水线寄存器_4_halt_3 ), .rd_2(\流水线寄存器_4_rd_2 ), .PC_2(WB_PC), .IR_2(WB_IR), .reset(not_6_out),
    .refresh(1'b0), .halt_2(halt), .clk(CLK), .IR(MEM_IR), .RDin(multiplexer_11_out), .RDin_2(RDin));  // open: Jal, Jalr, Lhu, Beq, Bne, Blt, MemToReg, MemWrite, AluSrcB, ecall, AluOP, R1, R2, imm_si, imm_b, imm_j, Jal_2, Jalr_2, Lhu_2, Beq_2, Bne_2, Blt_2, MemToReg_2, MemWrite_2, AluSrcB_2, ecall_2, AluOP_2, valid_2, R1_2, R2_2, PC_4_2, imm_si_2, imm_b_2, imm_j_2, Alu_ans_2, Alu_ans
  and and_7 (halt, ~Go, \流水线寄存器_4_halt_3 );  // AND_Gate

  // Other names for the same wires on the sheet: rd[4:0] = ID_IR[11:7]; MEM_PC[31:0] = M_PC

  // Notes on the sheet:
  //   中断源
  //   时空图监测，可删除
  //   中断等待指示
  //   数码管输出
  //   指令存储器
  //   contents of rom_1 (hex, n*v repeats v):
  //   100493 100006f 100493 200913 300993 100006f 100493 200913 300993 100006f 100493 200913 300993
  //   100006f 100493 200913 300993 29c000ef 100413 100493 1f49493 900533 2200893 73 24d493 48463 fedff06f
  //   900533 2200893 73 100493 249493 900533 2200893 73 48463 fedff06f 100493 1f49493 900533 2200893 73
  //   4034d493 900533 2200893 73 4044d493 900533 2200893 73 4044d493 900533 2200893 73 4044d493 900533
  //   2200893 73 4044d493 900533 2200893 73 4044d493 900533 2200893 73 4044d493 900533 2200893 73 4044d493
  //   900533 2200893 73 100413 1f41993 41f9d993 433 c00913 300b13 140413 f47413 800293 100313 499993
  //   89e9b3 1300533 2200893 73 406282b3 fe0294e3 140413 f00f93 1f47433 1c41413 800293 100313 49d993
  //   89e9b3 1300533 2200893 73 406282b3 fe0294e3 1c45413 406b0b33 b0463 f95ff06f 2b3 fff2c293 829293
  //   ff2e293 500533 2200893 73 fff00413 493 84a023 140413 448493 84a023 140413 448493 84a023 140413
  //   448493 84a023 140413 448493 84a023 140413 448493 84a023 140413 448493 84a023 140413 448493 84a023
  //   140413 448493 84a023 140413 448493 84a023 140413 448493 84a023 140413 448493 84a023 140413 448493
  //   84a023 140413 448493 84a023 140413 448493 84a023 140413 448493 84a023 140413 448493 140413 433
  //   3c00493 42983 4aa03 149a2b3 28663 134a023 1442023 ffc48493 fe9412e3 800533 2200893 73 440413 3c00493
  //   fc9416e3 a00893 73 413 140413 800533 2200893 73 240413 800533 2200893 73 340413 800533 2200893 73
  //   440413 800533 2200893 73 540413 800533 2200893 73 640413 800533 2200893 73 740413 800533 2200893 73
  //   840413 800533 2200893 2200893 73 8067
  //   I指令
  //   S指令
  //   B指令
  //   J指令
  //   控制位
  //   流水调试日志用
  //   暂停节拍，不能为0
  //   戳工具置1进入计数暂停模式，ctrl+k时钟自动运行到对应节拍暂停
  //   ctrl+k关闭时钟连续运行，将控制位置零，进入单步调试模式调试
  //   可计数暂停的时钟源
  //   为方便自动评测，需要输出流水线各段保存的PC值，注意是PC不是PC+4，另外ID段寄存器写入信息，Mem段内存写入信息也要输出
endmodule

module \中断按键参考电路  (
  input  \同步清零信号 ,
  output \与中断屏蔽位与 
);

  wire \_1号中断_out , and_1_out, clock_1_out, d_ff_1_q, or_1_out, or_2_out;

  Clock clock_1 (.out(clock_1_out));
  Button \_1号中断  (.out(\_1号中断_out ));
  LED \_1号中断等待指示灯  (.in(or_1_out));
  or or_1 (or_1_out, \与中断屏蔽位与 , d_ff_1_q);
  D_Flip_Flop d_ff_1 (.clk(\_1号中断_out ), .D(1'b1), .Q(d_ff_1_q), .reset(\与中断屏蔽位与 ));  // open: Qn, preset, en
  or or_2 (or_2_out, d_ff_1_q, \与中断屏蔽位与 );
  and and_1 (and_1_out, or_2_out, ~\同步清零信号 );  // AND_Gate
  D_Flip_Flop IR1 (.clk(clock_1_out), .D(and_1_out), .Q(\与中断屏蔽位与 ));  // open: Qn, preset, en, reset

  // Notes on the sheet:
  //   中断信号采样参考电路
  //   Reset 
endmodule
module \单周期_单级中断  (
  input  IR1,
  input  IR2,
  input  IR3,
  output RegWrite,
  output MemWrite,
  output [31:0] PC,
  output [31:0] IR,
  output [31:0] RDin,
  output [31:0] MDin,
  output [31:0] LedData
);

  wire and_1_out, and_2_out, and_3_out, and_5_out, and_6_out, and_7_out, and_8_out, and_10_out, Beq, Blt,
       Bne, CLK, clock_1_out, clock_2_out, clock_3_out, clock_4_out, comparator_1_eq, comparator_2_eq,
       comparator_3_eq, comparator_4_eq, comparator_5_eq, comparator_5_lt, comparator_6_eq, d_ff_1_q,
       d_ff_2_q, d_ff_3_q, d_ff_4_q, demultiplexer_1_out0, demultiplexer_1_out1, demultiplexer_1_out2, ecall,
       equal, Go, halt, intr, IR1_2_q, IR1_q, IR1_t, IR2_q, IR2_t, IR3_t, IRA, IRB, IRC, Jal, Jalr, less,
       Lhu, MemToReg, nand_1_out, not_1_out, not_2_out, not_3_out, not_4_out, not_5_out, or_4_out, or_5_out,
       or_6_out, or_7_out, or_8_out, or_9_out, or_14_out, priority_encoder_2_p5, register_5_q, S_Type, stop,
       URET, W1, W2, W3, \关中断 , \单周期硬布线控制器_1_alu_src ;
  wire [1:0] priority_encoder_1_out, priority_encoder_2_p3, priority_encoder_3_p3, register_2_q;
  wire [3:0] \单周期硬布线控制器_1_alu_op ;
  wire [4:0] multiplexer_4_out, multiplexer_5_out;
  wire [11:0] multiplexer_6_out;
  wire [12:0] CNT_num;
  wire [15:0] multiplexer_8_out, \总周期数 ;
  wire [31:0] B_Addr, bit_extender_1_out, bit_extender_2_out, bit_extender_3_out, bit_extender_4_out,
       Jal_Addr, Jalr_Addr, multiplexer_1_out, multiplexer_2_out, multiplexer_3_out, multiplexer_7_out,
       multiplexer_9_out, multiplexer_10_out, PC_4, ram_1_data, regifile_1_r1, register_3_q, shifter_1_out,
       shifter_2_out;

  Button \u_继续运行  (.out(Go));
  Button _1 (.out(IRA));
  Button _2 (.out(IRB));
  Button _3 (.out(IRC));
  Clock clock_1 (.out(clock_1_out));
  Clock clock_2 (.out(clock_2_out));
  Clock clock_3 (.out(clock_3_out));
  LED led_1 (.in(W1));
  LED led_2 (.in(W2));
  LED led_3 (.in(W3));
  D_Flip_Flop d_ff_1 (.clk(IRA), .D(1'b1), .Q(d_ff_1_q), .reset(IR1_q));  // open: Qn, preset, en
  or or_1 (W1, IR1_q, d_ff_1_q);
  D_Flip_Flop d_ff_2 (.clk(IRB), .D(1'b1), .Q(d_ff_2_q), .reset(IR2_q));  // open: Qn, preset, en
  or or_2 (W2, IR2_q, d_ff_2_q);
  D_Flip_Flop d_ff_3 (.clk(IRC), .D(1'b1), .Q(d_ff_3_q), .reset(IR1_2_q));  // open: Qn, preset, en
  or or_3 (W3, IR1_2_q, d_ff_3_q);
  Hex_Digit_Display hex_digit_display_1 (.value(LedData[31:28]));  // open: dp
  Comparator #(.width(16)) comparator_1 (.a(16'h23b), .b(\总周期数 ), .eq(comparator_1_eq));  // open: gt, lt
  Comparator #(.width(16)) comparator_2 (.a(\总周期数 ), .b(16'h1), .eq(comparator_2_eq));  // open: gt, lt
  Comparator #(.width(16)) comparator_3 (.a(\总周期数 ), .b(16'h4), .eq(comparator_3_eq));  // open: gt, lt
  Comparator #(.width(16)) comparator_4 (.a(\总周期数 ), .b(16'h7), .eq(comparator_4_eq));  // open: gt, lt
  or or_4 (or_4_out, d_ff_1_q, IR1_q);
  or or_5 (or_5_out, d_ff_2_q, IR2_q);
  or or_6 (or_6_out, d_ff_3_q, IR1_2_q);
  Hex_Digit_Display hex_digit_display_2 (.value(LedData[23:20]));  // open: dp
  Hex_Digit_Display hex_digit_display_3 (.value(LedData[27:24]));  // open: dp
  or or_7 (or_7_out, comparator_1_eq, comparator_2_eq);
  assign IRA = or_7_out ? ~CLK : 1'bz;  // Controlled_Inverter controlled_inverter_1
  assign IRB = comparator_3_eq ? ~CLK : 1'bz;  // Controlled_Inverter controlled_inverter_2
  assign IRC = comparator_4_eq ? ~CLK : 1'bz;  // Controlled_Inverter controlled_inverter_3
  and and_1 (and_1_out, or_4_out, ~demultiplexer_1_out0);  // AND_Gate
  and and_2 (and_2_out, or_5_out, ~demultiplexer_1_out1);  // AND_Gate
  and and_3 (and_3_out, or_6_out, ~demultiplexer_1_out2);  // AND_Gate
  Hex_Digit_Display hex_digit_display_4 (.value(LedData[19:16]));  // open: dp
  Hex_Digit_Display hex_digit_display_5 (.value(LedData[15:12]));  // open: dp
  Pull_Resistor pull_resistor_1 (.node(IRA));
  Pull_Resistor pull_resistor_2 (.node(IRB));
  Pull_Resistor pull_resistor_3 (.node(IRC));
  D_Flip_Flop u_IR1 (.clk(clock_1_out), .D(and_1_out), .Q(IR1_q));  // open: Qn, preset, en, reset
  D_Flip_Flop u_IR2 (.clk(clock_2_out), .D(and_2_out), .Q(IR2_q));  // open: Qn, preset, en, reset
  D_Flip_Flop IR1_2 (.clk(clock_3_out), .D(and_3_out), .Q(IR1_2_q));  // open: Qn, preset, en, reset
  Hex_Digit_Display hex_digit_display_6 (.value(LedData[7:4]));  // open: dp
  Hex_Digit_Display hex_digit_display_7 (.value(LedData[11:8]));  // open: dp
  // Probe on \总周期数 
  Hex_Digit_Display hex_digit_display_8 (.value(LedData[3:0]));  // open: dp
  Counter #(.width(16), .max('hffff)) counter_1 (
    .count(not_1_out), .Q(\总周期数 ), .clk(CLK));  // open: load, D, carry, clr
  not not_1 (not_1_out, halt);
  or or_8 (or_8_out, URET, ~or_9_out);  // OR_Gate
  or or_9 (or_9_out, IR1_q, IR2_q, IR1_2_q);
  Priority_Encoder #(.select(2)) priority_encoder_1 (
    .in0(IR1_q), .in1(IR2_q), .in2(IR1_2_q), .in3(1'b0), .out(priority_encoder_1_out));  // open: gs, en_out, en_in
  Register #(.width(1)) register_1 (.D(or_8_out), .Q(\关中断 ), .clk(CLK));  // open: en, clr
  Multiplexer #(.select(2), .width(32), .enable("false")) multiplexer_1 (
    .in0(32'h30ac), .in1(32'h3150), .in2(32'h31f4), .out(multiplexer_1_out), .sel(priority_encoder_1_out));  // open: in3
  or or_10 (IR1_t, IR1, IRA);
  and and_4 (intr, \关中断 , or_9_out);
  Register #(.width(2)) register_2 (.D(priority_encoder_1_out), .Q(register_2_q));  // open: en, clk, clr
  or or_11 (IR2_t, IR2, IRB);
  Demultiplexer #(.select(2), .enable("false")) demultiplexer_1 (
    .out0(demultiplexer_1_out0), .out1(demultiplexer_1_out1), .out2(demultiplexer_1_out2), .in(URET),
    .sel(register_2_q));  // open: out3
  or or_12 (IR3_t, IR3, IRC);
  and and_5 (and_5_out, Beq, equal);
  // Priority_Encoder #(.select(2)) priority_encoder_2: pin names not known; wires that end beside it: 1'b1, Jalr, priority_encoder_2_p3, Jal, priority_encoder_2_p5, 1'b1
  Multiplexer #(.select(2), .width(32), .enable("false")) multiplexer_2 (
    .in0(PC_4), .in1(Jalr_Addr), .in2(Jal_Addr), .in3(B_Addr), .out(multiplexer_2_out),
    .sel(priority_encoder_2_p3));
  not not_2 (not_2_out, equal);
  and and_6 (and_6_out, not_2_out, Bne);
  or or_13 (priority_encoder_2_p5, and_5_out, and_6_out, and_7_out);
  Register #(.width(32)) register_3 (.D(multiplexer_2_out), .en(intr), .Q(register_3_q), .clk(CLK));  // open: clr
  and and_7 (and_7_out, Blt, less);
  // Priority_Encoder #(.select(2)) priority_encoder_3: pin names not known; wires that end beside it: 1'b1, intr, priority_encoder_3_p3, URET
  Multiplexer #(.select(2), .width(32), .enable("false")) multiplexer_3 (
    .in0(multiplexer_2_out), .in1(multiplexer_1_out), .in2(register_3_q), .out(multiplexer_3_out),
    .sel(priority_encoder_3_p3));  // open: in3
  Register #(.width(32)) u_PC (.D(multiplexer_3_out), .en(not_3_out), .Q(PC), .clk(CLK), .clr(1'b0));
  not not_3 (not_3_out, halt);
  D_Flip_Flop #(.trigger("high")) d_ff_4 (.Q(d_ff_4_q));  // open: clk, D, Qn, preset, en, reset
  // Probe on 13'hc
  // RiscV_Probe riscv_probe_1: pin names not known; wires that end beside it: IR
  Adder #(.width(32)) adder_1 (.a(PC), .b(32'h4), .out(PC_4), .cin(1'b0));  // open: cout
  Comparator #(.width(13)) comparator_5 (
    .a(CNT_num), .b(13'hc), .eq(comparator_5_eq), .lt(comparator_5_lt));  // open: gt
  Clock clock_4 (.out(clock_4_out));
  ROM #(.addrWidth(10), .dataWidth(32)) rom_1 (.addr(PC[11:2]), .data(IR));  // open: sel
  Counter #(.width(13), .max('h1fff), .ongoal("stay")) counter_2 (
    .count(comparator_5_lt), .Q(CNT_num), .clk(clock_4_out));  // open: load, D, carry, clr
  nand nand_1 (nand_1_out, d_ff_4_q, comparator_5_eq);
  \单周期硬布线控制器  \u_单周期硬布线控制器_1  (
    .Funct({IR[30], IR[25], IR[14:12]}), .OP(IR[6:2]), .ALU_OP(\单周期硬布线控制器_1_alu_op ), .MemToReg(MemToReg),
    .MemWrite(MemWrite), .ALU_SRC(\单周期硬布线控制器_1_alu_src ), .RegWrite(RegWrite), .ecall(ecall),
    .S_type(S_Type), .Jalr(Jalr), .Beq(Beq), .JAL(Jal), .Bne(Bne), .in_3(IR[21]), .uret(URET), .LHU(Lhu),
    .BLT(Blt));
  Multiplexer #(.width(5), .enable("false")) multiplexer_4 (
    .in0(IR[19:15]), .in1(5'b10001), .out(multiplexer_4_out), .sel(ecall));
  Multiplexer #(.width(5), .enable("false")) multiplexer_5 (
    .in0(IR[24:20]), .in1(5'b01010), .out(multiplexer_5_out), .sel(ecall));
  Multiplexer #(.width(12), .enable("false")) multiplexer_6 (
    .in0(IR[31:20]), .in1({IR[31:25], IR[11:7]}), .out(multiplexer_6_out), .sel(S_Type));
  assign bit_extender_1_out = {{20{IR[31]}}, {IR[31], IR[7], IR[30:25], IR[11:8]}};  // Bit_Extender bit_extender_1
  assign bit_extender_2_out = {{12{IR[31]}}, {IR[31], IR[19:12], IR[20], IR[30:21]}};  // Bit_Extender bit_extender_2
  assign CLK = nand_1_out ? clock_4_out : 1'bz;  // Controlled_Buffer controlled_buffer_1
  Pull_Resistor #(.pull(1)) pull_resistor_4 (.node(CLK));
  assign bit_extender_3_out = {{20{multiplexer_6_out[11]}}, multiplexer_6_out};  // Bit_Extender bit_extender_3
  Shifter #(.width(32)) shifter_1 (.in(bit_extender_1_out), .\dist (5'b00001), .out(shifter_1_out));
  Shifter #(.width(32)) shifter_2 (.in(bit_extender_2_out), .\dist (5'b00001), .out(shifter_2_out));
  Regifile regifile_1 (
    .Din(RDin), .Clk(CLK), .R1(regifile_1_r1), .R2(MDin), .WE(RegWrite), .W_num(IR[11:7]),
    .R1_num(multiplexer_4_out), .R2_num(multiplexer_5_out));
  Adder #(.width(32)) adder_2 (.a(shifter_1_out), .b(PC), .out(B_Addr), .cin(1'b0));  // open: cout
  Adder #(.width(32)) adder_3 (.a(shifter_2_out), .b(PC), .out(Jal_Addr), .cin(1'b0));  // open: cout
  Multiplexer #(.width(32), .enable("false")) multiplexer_7 (
    .in0(MDin), .in1(bit_extender_3_out), .out(multiplexer_7_out), .sel(\单周期硬布线控制器_1_alu_src ));
  Comparator #(.width(32)) comparator_6 (.a(regifile_1_r1), .b(32'h22), .eq(comparator_6_eq));  // open: gt, lt
  Register #(.width(32)) register_4 (.D(MDin), .en(and_8_out), .Q(LedData), .clk(CLK), .clr(1'b0));
  ALU alu_1 (
    .X(regifile_1_r1), .Y(multiplexer_7_out), .AluOP(\单周期硬布线控制器_1_alu_op ), .Equal(equal),
    .Result(Jalr_Addr), .out_6(less));  // open: Result_2, out_4
  not not_4 (not_4_out, comparator_6_eq);
  and and_8 (and_8_out, ecall, comparator_6_eq);
  and and_9 (stop, ecall, not_4_out);
  not not_5 (not_5_out, MemWrite);
  RAM #(.addrWidth(10), .dataWidth(32), .bus("separate")) ram_1 (
    .addr(Jalr_Addr[11:2]), .din(MDin), .data(ram_1_data), .str(MemWrite), .clk(CLK), .ld(not_5_out));  // open: sel, clr
  Register #(.width(1)) register_5 (.D(Go), .Q(register_5_q), .clk(stop));  // open: en, clr
  Multiplexer #(.width(16), .enable("false")) multiplexer_8 (
    .in0(ram_1_data[15:0]), .in1(ram_1_data[31:16]), .out(multiplexer_8_out), .sel(Jalr_Addr[1]));
  and and_10 (and_10_out, ~register_5_q, stop);  // AND_Gate
  assign bit_extender_4_out = {{16{1'b0}}, multiplexer_8_out};  // Bit_Extender bit_extender_4
  Register #(.width(1)) register_6 (.D(and_10_out), .Q(halt), .clk(CLK));  // open: en, clr
  Multiplexer #(.width(32), .enable("false")) multiplexer_9 (
    .in0(ram_1_data), .in1(bit_extender_4_out), .out(multiplexer_9_out), .sel(Lhu));
  Multiplexer #(.width(32), .enable("false")) multiplexer_10 (
    .in0(Jalr_Addr), .in1(multiplexer_9_out), .out(multiplexer_10_out), .sel(MemToReg));
  or or_14 (or_14_out, Jal, Jalr);
  Multiplexer #(.width(32), .enable("false")) multiplexer_11 (
    .in0(multiplexer_10_out), .in1(PC_4), .out(RDin), .sel(or_14_out));

  // Notes on the sheet:
  //   中断源
  //   中断等待指示
  //   总复位信号应将除ROM以外所有存储组件全部清零
  //   单级中断测试信号模拟器
  //   数码管输出
  //   数码管输出应该用寄存器锁存，否则显示数据只能一闪而过
  //   为方便自动评测，需要输出PC，IR，寄存器堆写如数据RDin
  //   RAM写使能MemWrite、RAM写入数据MDin等信号
  //   控制位
  //   暂停节拍，不能为0
  //   指令探针
  //   指令存储器
  //   戳工具置1进入计数暂停模式，ctrl+k时钟自动运行到对应节拍暂停
  //   ctrl+k关闭时钟连续运行，将控制位置零，进入单步调试模式调试
  //   指令字
  //   contents of rom_1 (hex, n*v repeats v):
  //   7d000113 100413 1f41993 41f9d993 433 c00913 800b13 140413 f47413 800293 100313 499993 89e9b3 1300533
  //   2200893 73 406282b3 fe0294e3 140413 f00f93 1f47433 1c41413 800293 100313 49d993 89e9b3 1300533
  //   2200893 73 406282b3 fe0294e3 1c45413 406b0b33 b0463 f95ff06f 2b3 fff2c293 1029293 fff2e293 500533
  //   2200893 73 f5dff06f 1112023 410113 a12023 410113 812023 410113 1312023 410113 1412023 410113 1512023
  //   410113 1612023 410113 100b13 300a13 100a93 1600433 441413 14469b3 1300533 2200893 73 fe0416e3
  //   415a0a33 fe0a10e3 ffc10113 12b03 ffc10113 12a83 ffc10113 12a03 ffc10113 12983 ffc10113 12403
  //   ffc10113 12503 ffc10113 12883 200073 1112023 410113 a12023 410113 812023 410113 1312023 410113
  //   1412023 410113 1512023 410113 1612023 410113 200b13 300a13 100a93 1600433 441413 14469b3 1300533
  //   2200893 73 fe0416e3 415a0a33 fe0a10e3 ffc10113 12b03 ffc10113 12a83 ffc10113 12a03 ffc10113 12983
  //   ffc10113 12403 ffc10113 12503 ffc10113 12883 200073 1112023 410113 a12023 410113 812023 410113
  //   1312023 410113 1412023 410113 1512023 410113 1612023 410113 300b13 300a13 100a93 1600433 441413
  //   14469b3 1300533 2200893 73 fe0416e3 415a0a33 fe0a10e3 ffc10113 12b03 ffc10113 12a83 ffc10113 12a03
  //   ffc10113 12983 ffc10113 12403 ffc10113 12503 ffc10113 12883 200073
  //   I指令
  //   S指令
  //   B指令
  //   J指令
  //   Beq
  //   Bne
  //   MemToReg
  //   MemWrite
  //   AluOP
  //   AluSrcB
  //   RegWrite
  //   可计数暂停的时钟源
  //   数据存储器
endmodule

module \单周期_多级中断  (
  input  IR1,
  input  IR2,
  input  IR3,
  output RegWrite,
  output MemWrite,
  output [31:0] PC,
  output [31:0] IR,
  output [31:0] RDin,
  output [31:0] MDin,
  output [31:0] LedData
);

  wire and_1_out, and_2_out, and_3_out, and_4_out, and_5_out, and_6_out, and_9_out, and_10_out, and_11_out,
       and_12_out, and_14_out, and_15_out, and_16_out, and_18_out, Beq, Blt, Bne, CLK, clock_1_out,
       comparator_1_eq, comparator_2_eq, comparator_3_eq, comparator_4_eq, comparator_5_eq, comparator_6_eq,
       comparator_7_eq, comparator_8_eq, comparator_9_eq, comparator_10_lt, comparator_11_eq,
       comparator_13_eq, comparator_13_lt, csrr, csrrci, csrrsi, d_ff_1_q, d_ff_2_q, d_ff_3_q, d_ff_4_q,
       decoder_1_out1, decoder_1_out2, decoder_1_out3, decoder_2_out1, decoder_2_out2, decoder_2_out3,
       demultiplexer_1_out0, demultiplexer_1_out1, demultiplexer_1_out2, demultiplexer_1_out3, ecall, equal,
       Go, halt, ie, in, intr, intrrequest, IR1_q, IR1_t, IR2_q, IR2_t, IR3_q, IR3_t, IRA, IRB, IRC, Jal,
       Jalr, less, Lhu, MemToReg, nand_1_out, not_1_out, not_2_out, not_3_out, not_4_out, not_5_out,
       not_6_out, or_1_out, or_2_out, or_7_out, or_8_out, or_9_out, or_14_out, or_15_out, or_16_out,
       or_17_out, or_18_out, priority_encoder_1_p5, register_6_q, S_Type, stop, URET, W1, W2, W3,
       \单周期硬布线控制器_1_alu_src ;
  wire [1:0] adder_4_out, count, cur_itrnum, irnum, multiplexer_10_out, priority_encoder_1_p3, Qnum,
       register_1_q, register_2_q, register_3_q;
  wire [3:0] \单周期硬布线控制器_1_alu_op ;
  wire [4:0] multiplexer_5_out, multiplexer_6_out;
  wire [11:0] multiplexer_7_out;
  wire [12:0] CNT_num;
  wire [15:0] counter_2_q, multiplexer_11_out, \总周期数 ;
  wire [31:0] B_Addr, bit_extender_1_out, bit_extender_2_out, bit_extender_3_out, bit_extender_4_out,
       intr_pc, Jal_Addr, Jalr_Addr, multiplexer_2_out, multiplexer_3_out, multiplexer_9_out,
       multiplexer_13_out, multiplexer_14_out, now_pc, PC_4, ram_1_data, regifile_1_r1, register_8_q,
       register_9_q, register_10_q, return_pc, shifter_1_out, shifter_2_out;

  Button \u_继续运行  (.out(Go));
  Button _1 (.out(IRA));
  Button _2 (.out(IRB));
  Button _3 (.out(IRC));
  LED led_1 (.in(W1));
  LED led_2 (.in(W2));
  LED led_3 (.in(W3));
  Hex_Digit_Display hex_digit_display_1 (.value(LedData[31:28]));  // open: dp
  Comparator #(.width(16)) comparator_1 (.a(\总周期数 ), .b(16'h7), .eq(comparator_1_eq));  // open: gt, lt
  Comparator #(.width(16)) comparator_2 (.a(\总周期数 ), .b(16'h241), .eq(comparator_2_eq));  // open: gt, lt
  // Priority_Encoder #(.select(2)) priority_encoder_1: pin names not known; wires that end beside it: 1'b1, Jalr, priority_encoder_1_p3, Jal, priority_encoder_1_p5, 1'b1
  Hex_Digit_Display hex_digit_display_2 (.value(LedData[23:20]));  // open: dp
  Hex_Digit_Display hex_digit_display_3 (.value(LedData[27:24]));  // open: dp
  Comparator #(.width(16)) comparator_3 (.a(16'h258), .b(\总周期数 ), .eq(comparator_3_eq));  // open: gt, lt
  or or_1 (or_1_out, comparator_3_eq, comparator_4_eq);
  Comparator #(.width(16)) comparator_4 (.a(\总周期数 ), .b(16'h1), .eq(comparator_4_eq));  // open: gt, lt
  Comparator #(.width(16)) comparator_5 (.a(\总周期数 ), .b(16'h4), .eq(comparator_5_eq));  // open: gt, lt
  or or_2 (or_2_out, comparator_1_eq, comparator_2_eq);
  or or_3 (W1, IR1_q, d_ff_1_q);
  or or_4 (W2, IR2_q, d_ff_2_q);
  or or_5 (W3, IR3_q, d_ff_3_q);
  not not_1 (not_1_out, equal);
  and and_1 (and_1_out, not_1_out, Bne);
  and and_2 (and_2_out, Beq, equal);
  or or_6 (priority_encoder_1_p5, and_2_out, and_1_out, and_3_out);
  Multiplexer #(.select(2), .width(32), .enable("false")) multiplexer_1 (
    .in0(PC_4), .in1(Jalr_Addr), .in2(Jal_Addr), .in3(B_Addr), .out(now_pc), .sel(priority_encoder_1_p3));
  Hex_Digit_Display hex_digit_display_4 (.value(LedData[15:12]));  // open: dp
  Hex_Digit_Display hex_digit_display_5 (.value(LedData[19:16]));  // open: dp
  Pull_Resistor pull_resistor_1 (.node(IRA));
  assign IRA = or_1_out ? ~CLK : 1'bz;  // Controlled_Inverter controlled_inverter_1
  Pull_Resistor pull_resistor_2 (.node(IRB));
  assign IRB = comparator_5_eq ? ~CLK : 1'bz;  // Controlled_Inverter controlled_inverter_2
  Pull_Resistor pull_resistor_3 (.node(IRC));
  assign IRC = or_2_out ? ~CLK : 1'bz;  // Controlled_Inverter controlled_inverter_3
  D_Flip_Flop d_ff_1 (.clk(IRA), .D(1'b1), .Q(d_ff_1_q), .reset(IR1_q));  // open: Qn, preset, en
  D_Flip_Flop d_ff_2 (.clk(IRB), .D(1'b1), .Q(d_ff_2_q), .reset(IR2_q));  // open: Qn, preset, en
  D_Flip_Flop d_ff_3 (.clk(IRC), .D(1'b1), .Q(d_ff_3_q), .reset(IR3_q));  // open: Qn, preset, en
  and and_3 (and_3_out, Blt, less);
  Multiplexer #(.width(32), .enable("false")) multiplexer_2 (
    .in0(now_pc), .in1(return_pc), .out(multiplexer_2_out), .sel(URET));
  Hex_Digit_Display hex_digit_display_6 (.value(LedData[7:4]));  // open: dp
  Hex_Digit_Display hex_digit_display_7 (.value(LedData[11:8]));  // open: dp
  // Probe on \总周期数 
  not not_2 (not_2_out, halt);
  or or_7 (or_7_out, d_ff_1_q, IR1_q);
  and and_4 (and_4_out, or_7_out, ~demultiplexer_1_out1);  // AND_Gate
  or or_8 (or_8_out, d_ff_2_q, IR2_q);
  and and_5 (and_5_out, or_8_out, ~demultiplexer_1_out2);  // AND_Gate
  or or_9 (or_9_out, d_ff_3_q, IR3_q);
  and and_6 (and_6_out, or_9_out, ~demultiplexer_1_out3);  // AND_Gate
  Hex_Digit_Display hex_digit_display_8 (.value(LedData[3:0]));  // open: dp
  Counter #(.width(16), .max('hffff)) counter_1 (
    .count(not_2_out), .Q(\总周期数 ), .clk(CLK));  // open: load, D, carry, clr
  D_Flip_Flop u_IR1 (.clk(CLK), .D(and_4_out), .Q(IR1_q));  // open: Qn, preset, en, reset
  D_Flip_Flop u_IR2 (.clk(CLK), .D(and_5_out), .Q(IR2_q));  // open: Qn, preset, en, reset
  D_Flip_Flop u_IR3 (.clk(CLK), .D(and_6_out), .Q(IR3_q));  // open: Qn, preset, en, reset
  Multiplexer #(.width(32), .enable("false")) multiplexer_3 (
    .in0(multiplexer_2_out), .in1(intr_pc), .out(multiplexer_3_out), .sel(intr));
  not not_3 (not_3_out, halt);
  or or_10 (IR1_t, IR1, IRA);
  Comparator #(.width(5)) comparator_6 (.a(5'b11100), .b(IR[6:2]), .eq(comparator_6_eq));  // open: gt, lt
  Comparator #(.width(5)) comparator_7 (.a(IR[6:2]), .b(5'b11100), .eq(comparator_7_eq));  // open: gt, lt
  Priority_Encoder #(.select(2)) priority_encoder_2 (
    .in0(1'b1), .in1(IR1_q), .in2(IR2_q), .in3(IR3_q), .out(irnum), .gs(intrrequest));  // open: en_out, en_in
  Register #(.width(32)) u_PC (.D(multiplexer_3_out), .en(not_3_out), .Q(PC), .clk(CLK), .clr(1'b0));
  or or_11 (IR2_t, IR2, IRB);
  Comparator #(.width(3)) comparator_8 (.a(3'b110), .b(IR[14:12]), .eq(comparator_8_eq));  // open: gt, lt
  Comparator #(.width(3)) comparator_9 (.a(IR[14:12]), .b(3'b111), .eq(comparator_9_eq));  // open: gt, lt
  Demultiplexer #(.select(2), .enable("false")) demultiplexer_1 (
    .out0(demultiplexer_1_out0), .out1(demultiplexer_1_out1), .out2(demultiplexer_1_out2),
    .out3(demultiplexer_1_out3), .in(URET), .sel(irnum));
  and and_7 (csrrsi, comparator_6_eq, comparator_8_eq);
  and and_8 (csrrci, comparator_9_eq, comparator_7_eq);
  // RiscV_Probe riscv_probe_1: pin names not known; wires that end beside it: IR
  Adder #(.width(32)) adder_1 (.a(PC), .b(32'h4), .out(PC_4), .cin(1'b0));  // open: cout
  or or_12 (IR3_t, IR3, IRC);
  or or_13 (csrr, csrrsi, csrrci);
  Multiplexer #(.select(2), .width(32), .enable("false")) multiplexer_4 (
    .in0(now_pc), .in1(32'h30ac), .in2(32'h3158), .in3(32'h3204), .out(intr_pc), .sel(irnum));
  Decoder #(.select(2), .enable("false")) decoder_1 (
    .out1(decoder_1_out1), .out2(decoder_1_out2), .out3(decoder_1_out3), .sel(Qnum));  // open: out0
  ROM #(.addrWidth(10), .dataWidth(32)) rom_1 (.addr(PC[11:2]), .data(IR));  // open: sel
  Multiplexer #(.width(5), .enable("false")) multiplexer_5 (
    .in0(IR[19:15]), .in1(5'b10001), .out(multiplexer_5_out), .sel(ecall));
  Multiplexer #(.width(5), .enable("false")) multiplexer_6 (
    .in0(IR[24:20]), .in1(5'b01010), .out(multiplexer_6_out), .sel(ecall));
  and and_9 (and_9_out, decoder_1_out1, intr);
  and and_10 (and_10_out, decoder_1_out2, intr);
  and and_11 (and_11_out, decoder_1_out3, intr);
  \单周期硬布线控制器  \u_单周期硬布线控制器_1  (
    .Funct({IR[30], IR[25], IR[14:12]}), .OP(IR[6:2]), .ALU_OP(\单周期硬布线控制器_1_alu_op ), .MemToReg(MemToReg),
    .MemWrite(MemWrite), .ALU_SRC(\单周期硬布线控制器_1_alu_src ), .RegWrite(RegWrite), .ecall(ecall),
    .S_type(S_Type), .Jalr(Jalr), .Beq(Beq), .JAL(Jal), .Bne(Bne), .in_3(IR[21]), .uret(URET), .LHU(Lhu),
    .BLT(Blt));
  Multiplexer #(.width(12), .enable("false")) multiplexer_7 (
    .in0(IR[31:20]), .in1({IR[31:25], IR[11:7]}), .out(multiplexer_7_out), .sel(S_Type));
  assign bit_extender_1_out = {{20{IR[31]}}, {IR[31], IR[7], IR[30:25], IR[11:8]}};  // Bit_Extender bit_extender_1
  assign bit_extender_2_out = {{12{IR[31]}}, {IR[31], IR[19:12], IR[20], IR[30:21]}};  // Bit_Extender bit_extender_2
  or or_14 (or_14_out, csrrsi, csrrci);
  Counter #(.width(16), .max('hffff)) counter_2 (.Q(counter_2_q), .clk(CLK));  // open: load, D, count, carry, clr
  // Probe on irnum
  Register #(.width(2)) register_1 (.D(irnum), .en(and_9_out), .Q(register_1_q), .clk(CLK));  // open: clr
  Register #(.width(2)) register_2 (.D(irnum), .en(and_10_out), .Q(register_2_q), .clk(CLK));  // open: clr
  assign bit_extender_3_out = {{20{multiplexer_7_out[11]}}, multiplexer_7_out};  // Bit_Extender bit_extender_3
  Shifter #(.width(32)) shifter_1 (.in(bit_extender_1_out), .\dist (5'b00001), .out(shifter_1_out));
  Shifter #(.width(32)) shifter_2 (.in(bit_extender_2_out), .\dist (5'b00001), .out(shifter_2_out));
  or or_15 (or_15_out, intr, csrrci);
  or or_16 (or_16_out, or_14_out, comparator_10_lt, intr, URET);
  Comparator #(.width(16), .mode("unsigned")) comparator_10 (
    .a(counter_2_q), .b(16'h2), .lt(comparator_10_lt));  // open: gt, eq
  // Probe on count
  Register #(.width(2)) register_3 (.D(irnum), .en(and_11_out), .Q(register_3_q), .clk(CLK));  // open: clr
  Regifile regifile_1 (
    .Din(RDin), .Clk(CLK), .R1(regifile_1_r1), .R2(MDin), .WE(RegWrite), .W_num(IR[11:7]),
    .R1_num(multiplexer_5_out), .R2_num(multiplexer_6_out));
  Adder #(.width(32)) adder_2 (.a(shifter_1_out), .b(PC), .out(B_Addr), .cin(1'b0));  // open: cout
  Adder #(.width(32)) adder_3 (.a(shifter_2_out), .b(PC), .out(Jal_Addr), .cin(1'b0));  // open: cout
  Register #(.width(1)) register_4 (.D(not_4_out), .en(or_16_out), .Q(ie), .clk(CLK));  // open: clr
  not not_4 (not_4_out, or_15_out);
  Multiplexer #(.select(2), .width(2), .enable("false")) multiplexer_8 (
    .in0(2'b00), .in1(register_1_q), .in2(register_2_q), .in3(register_3_q), .out(cur_itrnum), .sel(count));
  Multiplexer #(.width(32), .enable("false")) multiplexer_9 (
    .in0(MDin), .in1(bit_extender_3_out), .out(multiplexer_9_out), .sel(\单周期硬布线控制器_1_alu_src ));
  // Probe on cur_itrnum
  // Probe on irnum
  ALU alu_1 (
    .X(regifile_1_r1), .Y(multiplexer_9_out), .AluOP(\单周期硬布线控制器_1_alu_op ), .Equal(equal),
    .Result(Jalr_Addr), .out_6(less));  // open: Result_2, out_4
  Comparator #(.width(32)) comparator_11 (.a(regifile_1_r1), .b(32'h22), .eq(comparator_11_eq));  // open: gt, lt
  and and_12 (and_12_out, ecall, comparator_11_eq);
  Register #(.width(32)) register_5 (.D(MDin), .en(and_12_out), .Q(LedData), .clk(CLK), .clr(1'b0));
  D_Flip_Flop #(.trigger("high")) d_ff_4 (.Q(d_ff_4_q));  // open: clk, D, Qn, preset, en, reset
  // Probe on 13'hc
  Comparator #(.width(2), .mode("unsigned")) comparator_12 (.a(cur_itrnum), .b(irnum), .lt(in));  // open: gt, eq
  not not_5 (not_5_out, comparator_11_eq);
  Comparator #(.width(13)) comparator_13 (
    .a(CNT_num), .b(13'hc), .eq(comparator_13_eq), .lt(comparator_13_lt));  // open: gt
  Clock clock_1 (.out(clock_1_out));
  Decoder #(.select(2), .enable("false")) decoder_2 (
    .out1(decoder_2_out1), .out2(decoder_2_out2), .out3(decoder_2_out3), .sel(irnum));  // open: out0
  and and_13 (stop, ecall, not_5_out);
  Counter #(.width(13), .max('h1fff), .ongoal("stay")) counter_3 (
    .count(comparator_13_lt), .Q(CNT_num), .clk(clock_1_out));  // open: load, D, carry, clr
  Multiplexer #(.width(2), .enable("false")) multiplexer_10 (
    .in0(2'b11), .in1(2'b01), .out(multiplexer_10_out), .sel(intr));
  not not_6 (not_6_out, MemWrite);
  nand nand_1 (nand_1_out, d_ff_4_q, comparator_13_eq);
  and and_14 (and_14_out, decoder_2_out1, intr);
  and and_15 (and_15_out, decoder_2_out2, intr);
  and and_16 (and_16_out, decoder_2_out3, intr);
  Adder #(.width(2)) adder_4 (.a(count), .b(multiplexer_10_out), .out(adder_4_out));  // open: cin, cout
  or or_17 (or_17_out, intr, URET);
  RAM #(.addrWidth(10), .dataWidth(32), .bus("separate")) ram_1 (
    .addr(Jalr_Addr[11:2]), .din(MDin), .data(ram_1_data), .str(MemWrite), .clk(CLK), .ld(not_6_out));  // open: sel, clr
  Register #(.width(1)) register_6 (.D(Go), .Q(register_6_q), .clk(stop));  // open: en, clr
  assign CLK = nand_1_out ? clock_1_out : 1'bz;  // Controlled_Buffer controlled_buffer_1
  Pull_Resistor #(.pull(1)) pull_resistor_4 (.node(CLK));
  and and_17 (intr, ie, intrrequest, in);
  Register #(.width(2)) register_7 (.D(adder_4_out), .en(or_17_out), .Q(count), .clk(CLK));  // open: clr
  Multiplexer #(.width(16), .enable("false")) multiplexer_11 (
    .in0(ram_1_data[15:0]), .in1(ram_1_data[31:16]), .out(multiplexer_11_out), .sel(Jalr_Addr[1]));
  and and_18 (and_18_out, ~register_6_q, stop);  // AND_Gate
  Register #(.width(32)) register_8 (.D(now_pc), .en(and_14_out), .Q(register_8_q), .clk(CLK));  // open: clr
  Register #(.width(32)) register_9 (.D(now_pc), .en(and_15_out), .Q(register_9_q), .clk(CLK));  // open: clr
  Register #(.width(32)) register_10 (.D(now_pc), .en(and_16_out), .Q(register_10_q), .clk(CLK));  // open: clr
  // Probe on count
  assign bit_extender_4_out = {{16{1'b0}}, multiplexer_11_out};  // Bit_Extender bit_extender_4
  Register #(.width(1)) register_11 (.D(and_18_out), .Q(halt), .clk(CLK));  // open: en, clr
  Multiplexer #(.select(2), .width(32), .enable("false")) multiplexer_12 (
    .in1(register_8_q), .in2(register_9_q), .in3(register_10_q), .out(return_pc), .sel(cur_itrnum));  // open: in0
  Adder #(.width(2)) adder_5 (.a(count), .b(2'b01), .out(Qnum));  // open: cin, cout
  Multiplexer #(.width(32), .enable("false")) multiplexer_13 (
    .in0(ram_1_data), .in1(bit_extender_4_out), .out(multiplexer_13_out), .sel(Lhu));
  Multiplexer #(.width(32), .enable("false")) multiplexer_14 (
    .in0(Jalr_Addr), .in1(multiplexer_13_out), .out(multiplexer_14_out), .sel(MemToReg));
  or or_18 (or_18_out, Jal, Jalr);
  Multiplexer #(.width(32), .enable("false")) multiplexer_15 (
    .in0(multiplexer_14_out), .in1(PC_4), .out(RDin), .sel(or_18_out));
  // also tied to GND on the sheet: demultiplexer_1_out0

  // Other names for the same wires on the sheet: fun3[2:0] = IR[14:12]; opcode[4:0] = IR[6:2]

  // Notes on the sheet:
  //   中断源
  //   中断等待指示
  //   总复位信号应将除ROM以外所有存储组件全部清零
  //   多级中断测试信号模拟器
  //   数码管输出
  //   数码管输出应该用寄存器锁存，否则显示数据只能一闪而过
  //   Reset 
  //   Reset 
  //   Reset 
  //   指令探针
  //   指令存储器
  //   指令字
  //   contents of rom_1 (hex, n*v repeats v):
  //   7d000113 100413 1f41993 41f9d993 433 c00913 800b13 140413 f47413 800293 100313 499993 89e9b3 1300533
  //   2200893 73 406282b3 fe0294e3 140413 f00f93 1f47433 1c41413 800293 100313 49d993 89e9b3 1300533
  //   2200893 73 406282b3 fe0294e3 1c45413 406b0b33 b0463 f95ff06f 2b3 fff2c293 1029293 fff2e293 500533
  //   2200893 73 f5dff06f 1112023 410113 a12023 410113 812023 410113 1312023 410113 1412023 410113 1512023
  //   410113 1612023 410113 40e073 100b13 300a13 100a93 1600433 441413 14469b3 1300533 2200893 73 fe0416e3
  //   415a0a33 fe0a10e3 40f073 ffc10113 12b03 ffc10113 12a83 ffc10113 12a03 ffc10113 12983 ffc10113 12403
  //   ffc10113 12503 ffc10113 12883 200073 1112023 410113 a12023 410113 812023 410113 1312023 410113
  //   1412023 410113 1512023 410113 1612023 410113 40e073 200b13 300a13 100a93 1600433 441413 14469b3
  //   1300533 2200893 73 fe0416e3 415a0a33 fe0a10e3 40f073 ffc10113 12b03 ffc10113 12a83 ffc10113 12a03
  //   ffc10113 12983 ffc10113 12403 ffc10113 12503 ffc10113 12883 200073 1112023 410113 a12023 410113
  //   812023 410113 1312023 410113 1412023 410113 1512023 410113 1612023 410113 40e073 300b13 300a13
  //   100a93 1600433 441413 14469b3 1300533 2200893 73 fe0416e3 415a0a33 fe0a10e3 40f073 ffc10113 12b03
  //   ffc10113 12a83 ffc10113 12a03 ffc10113 12983 ffc10113 12403 ffc10113 12503 ffc10113 12883 200073
  //   I指令
  //   S指令
  //   B指令
  //   J指令
  //   Beq
  //   Bne
  //   MemToReg
  //   MemWrite
  //   AluOP
  //   AluSrcB
  //   RegWrite
  //   为方便自动评测，需要输出PC，IR，寄存器堆写如数据RDin
  //   RAM写使能MemWrite、RAM写入数据MDin等信号
  //   设置关中断
  //   控制位
  //   暂停节拍，不能为0
  //   戳工具置1进入计数暂停模式，ctrl+k时钟自动运行到对应节拍暂停
  //   ctrl+k关闭时钟连续运行，将控制位置零，进入单步调试模式调试
  //   数据存储器
  //   可计数暂停的时钟源
  //   因为我们最多只有三个中断，我们只要分别保存对应的epc即可
  //   in表示我们堆栈里面还有没有处理完的堆栈
  //   当前存储中断的的存储器编号
  //   这个表示下一位有空的存储器编号
  //   处理完中断返回的地址
endmodule

module \封装正确性测试  (
);

  wire IR1, IR2, IR3, MemW, RegW;
  wire [31:0] EX_PC, ID_PC, IF_PC, IR, LED, MDin, MDinr, MEM_PC, PC, RDin, RDinr, WB_PC;

  \单周期RISC_V  \u_单周期risc_v_1  (
    .IR1(IR1), .IR2(IR2), .IR3(IR3), .RegWrite(RegW), .MemWrite(MemW), .PC(PC), .IR(IR), .RDin(RDin),
    .MDin(MDin), .LedData(LED));
  \气泡流水线  \u_气泡流水线_1  (
    .RegWrite(RegW), .MemWrite(MemW), .IF_PC(IF_PC), .ID_PC(ID_PC), .EX_PC(EX_PC), .M_PC(MEM_PC),
    .WB_PC(WB_PC), .RDin(RDinr), .MDin(MDinr), .LedData(LED));
  \单周期_单级中断  \u_单周期_单级中断_1  (
    .IR1(IR1), .IR2(IR2), .IR3(IR3), .RegWrite(RegW), .MemWrite(MemW), .PC(PC), .IR(IR), .RDin(RDin),
    .MDin(MDin), .LedData(LED));
  \理想流水线  \u_理想流水线_1  (
    .RegWrite(RegW), .MemWrite(MemW), .IF_PC(IF_PC), .ID_PC(ID_PC), .EX_PC(EX_PC), .M_PC(MEM_PC),
    .WB_PC(WB_PC), .RDin(RDinr), .MDin(MDinr), .LedData(LED));
  \重定向流水线  \u_重定向流水线_1  (
    .RegWrite(RegW), .MemWrite(MemW), .IF_PC(IF_PC), .ID_PC(ID_PC), .EX_PC(EX_PC), .M_PC(MEM_PC),
    .WB_PC(WB_PC), .RDin(RDinr), .MDin(MDinr), .LedData(LED));
  \单周期_多级中断  \u_单周期_多级中断_1  (
    .IR1(IR1), .IR2(IR2), .IR3(IR3), .RegWrite(RegW), .MemWrite(MemW), .PC(PC), .IR(IR), .RDin(RDin),
    .MDin(MDin), .LedData(LED));

  // Notes on the sheet:
  //   单周期封装测试
  //   气泡流水封装测试
  //   单周期+单级中断封装测试
  //   请检查上面封装有无位宽不匹配，引脚标签是否和连接的标签相对应，否则无法在educoder平台上正确测试
  //   理想流水封装测试
  //   重定向流水封装测试
  //   单周期+多级中断封装测试
endmodule

module IF_ID (
  input  [31:0] IF_PC,
  input  [31:0] IF_IR,
  input  clk,
  input  rst,
  input  en,
  output [31:0] ID_PC,
  output [31:0] ID_IR
);

  Register #(.width(32)) PC (.D(IF_PC), .en(en), .Q(ID_PC), .clk(clk), .clr(rst));
  Register #(.width(32)) IR (.D(IF_IR), .en(en), .Q(ID_IR), .clk(clk), .clr(rst));
endmodule

module ID_EX (
  input  [31:0] ID_PC,
  input  [31:0] ID_IR,
  input  ID_Beq,
  input  ID_Bne,
  input  ID_Blt,
  input  ID_MemToReg,
  input  ID_MemWrite,
  input  [3:0] ID_AluOP,
  input  ID_AluSrcB,
  input  ID_RegWrite,
  input  ID_Jal,
  input  ID_Jalr,
  input  [4:0] ID_rd,
  input  ID_Ecall,
  input  ID_Lhu,
  input  [31:0] ID_R1,
  input  [31:0] ID_R2,
  input  [31:0] ID_imm_I,
  input  [31:0] ID_imm_B,
  input  [31:0] ID_imm_J,
  input  clk,
  input  rst,
  input  en,
  output [31:0] EX_PC,
  output [31:0] EX_IR,
  output EX_Beq,
  output EX_Bne,
  output EX_Blt,
  output EX_MemToReg,
  output EX_MemWrite,
  output [3:0] EX_AluOP,
  output EX_AluSrcB,
  output EX_RegWrite,
  output EX_Jal,
  output EX_Jalr,
  output [4:0] EX_rd,
  output EX_Ecall,
  output EX_Lhu,
  output [31:0] EX_A,
  output [31:0] EX_B,
  output [31:0] EX_imm_I,
  output [31:0] EX_imm_B,
  output [31:0] EX_imm_J
);

  Register #(.width(32)) register_1 (.D(ID_PC), .en(en), .Q(EX_PC), .clk(clk), .clr(rst));
  Register #(.width(32)) register_2 (.D(ID_IR), .en(en), .Q(EX_IR), .clk(clk), .clr(rst));
  Register #(.width(1)) register_3 (.D(ID_Beq), .en(en), .Q(EX_Beq), .clk(clk), .clr(rst));
  Register #(.width(1)) register_4 (.D(ID_Bne), .en(en), .Q(EX_Bne), .clk(clk), .clr(rst));
  Register #(.width(1)) register_5 (.D(ID_Blt), .en(en), .Q(EX_Blt), .clk(clk), .clr(rst));
  Register #(.width(1)) register_6 (.D(ID_MemToReg), .en(en), .Q(EX_MemToReg), .clk(clk), .clr(rst));
  Register #(.width(1)) register_7 (.D(ID_MemWrite), .en(en), .Q(EX_MemWrite), .clk(clk), .clr(rst));
  Register #(.width(4)) register_8 (.D(ID_AluOP), .en(en), .Q(EX_AluOP), .clk(clk), .clr(rst));
  Register #(.width(1)) register_9 (.D(ID_AluSrcB), .en(en), .Q(EX_AluSrcB), .clk(clk), .clr(rst));
  Register #(.width(1)) register_10 (.D(ID_RegWrite), .en(en), .Q(EX_RegWrite), .clk(clk), .clr(rst));
  Register #(.width(1)) register_11 (.D(ID_Jal), .en(en), .Q(EX_Jal), .clk(clk), .clr(rst));
  Register #(.width(1)) register_12 (.D(ID_Jalr), .en(en), .Q(EX_Jalr), .clk(clk), .clr(rst));
  Register #(.width(5)) register_13 (.D(ID_rd), .en(en), .Q(EX_rd), .clk(clk), .clr(rst));
  Register #(.width(1)) register_14 (.D(ID_Ecall), .en(en), .Q(EX_Ecall), .clk(clk), .clr(rst));
  Register #(.width(1)) register_15 (.D(ID_Lhu), .en(en), .Q(EX_Lhu), .clk(clk), .clr(rst));
  Register #(.width(32)) register_16 (.D(ID_R1), .en(en), .Q(EX_A), .clk(clk), .clr(rst));
  Register #(.width(32)) register_17 (.D(ID_R2), .en(en), .Q(EX_B), .clk(clk), .clr(rst));
  Register #(.width(32)) register_18 (.D(ID_imm_I), .en(en), .Q(EX_imm_I), .clk(clk), .clr(rst));
  Register #(.width(32)) register_19 (.D(ID_imm_B), .en(en), .Q(EX_imm_B), .clk(clk), .clr(rst));
  Register #(.width(32)) register_20 (.D(ID_imm_J), .en(en), .Q(EX_imm_J), .clk(clk), .clr(rst));
endmodule

module EX_MEM (
  input  [31:0] EX_PC,
  input  [31:0] EX_IR,
  input  EX_MemToReg,
  input  EX_MemWrite,
  input  EX_RegWrite,
  input  EX_Jal,
  input  EX_Jalr,
  input  [31:0] EX_MDin,
  input  [31:0] EX_Calc,
  input  [4:0] EX_rd,
  input  EX_Ecall,
  input  EX_Equal,
  input  EX_Lhu,
  input  clk,
  input  rst,
  input  en,
  output [31:0] MEM_PC,
  output [31:0] MEM_IR,
  output MEM_MemToReg,
  output MEM_MemWrite,
  output MEM_RegWrite,
  output MEM_Jal,
  output MEM_Jalr,
  output [31:0] MEM_MDin,
  output [31:0] MEM_Calc,
  output [4:0] MEM_rd,
  output MEM_Ecall,
  output MEM_Equal,
  output MEM_Lhu
);

  Register #(.width(32)) register_1 (.D(EX_PC), .en(en), .Q(MEM_PC), .clk(clk), .clr(rst));
  Register #(.width(32)) register_2 (.D(EX_IR), .en(en), .Q(MEM_IR), .clk(clk), .clr(rst));
  Register #(.width(1)) register_3 (.D(EX_MemToReg), .en(en), .Q(MEM_MemToReg), .clk(clk), .clr(rst));
  Register #(.width(1)) register_4 (.D(EX_MemWrite), .en(en), .Q(MEM_MemWrite), .clk(clk), .clr(rst));
  Register #(.width(1)) register_5 (.D(EX_RegWrite), .en(en), .Q(MEM_RegWrite), .clk(clk), .clr(rst));
  Register #(.width(1)) register_6 (.D(EX_Jal), .en(en), .Q(MEM_Jal), .clk(clk), .clr(rst));
  Register #(.width(1)) register_7 (.D(EX_Jalr), .en(en), .Q(MEM_Jalr), .clk(clk), .clr(rst));
  Register #(.width(32)) register_8 (.D(EX_MDin), .en(en), .Q(MEM_MDin), .clk(clk), .clr(rst));
  Register #(.width(32)) register_9 (.D(EX_Calc), .en(en), .Q(MEM_Calc), .clk(clk), .clr(rst));
  Register #(.width(5)) register_10 (.D(EX_rd), .en(en), .Q(MEM_rd), .clk(clk), .clr(rst));
  Register #(.width(1)) register_11 (.D(EX_Ecall), .en(en), .Q(MEM_Ecall), .clk(clk), .clr(rst));
  Register #(.width(1)) register_12 (.D(EX_Equal), .en(en), .Q(MEM_Equal), .clk(clk), .clr(rst));
  Register #(.width(1)) register_13 (.D(EX_Lhu), .en(en), .Q(MEM_Lhu), .clk(clk), .clr(rst));
endmodule

module MEM_WB (
  input  [31:0] MEM_PC,
  input  [31:0] MEM_IR,
  input  MEM_RegWrite,
  input  MEM_Jal,
  input  MEM_Jalr,
  input  [31:0] MEM_Calc_Mout,
  input  [4:0] MEM_rd,
  input  MEM_Ecall,
  input  MEM_Equal,
  input  clk,
  input  rst,
  input  en,
  output [31:0] WB_PC,
  output [31:0] WB_IR,
  output WB_RegWrite,
  output WB_Jal,
  output WB_Jalr,
  output [31:0] WB_Calc_Mout,
  output [4:0] WB_rd,
  output WB_Ecall,
  output WB_Equal
);

  Register #(.width(32)) register_1 (.D(MEM_PC), .en(en), .Q(WB_PC), .clk(clk), .clr(rst));
  Register #(.width(32)) register_2 (.D(MEM_IR), .en(en), .Q(WB_IR), .clk(clk), .clr(rst));
  Register #(.width(1)) register_3 (.D(MEM_RegWrite), .en(en), .Q(WB_RegWrite), .clk(clk), .clr(rst));
  Register #(.width(1)) register_4 (.D(MEM_Jal), .en(en), .Q(WB_Jal), .clk(clk), .clr(rst));
  Register #(.width(1)) register_5 (.D(MEM_Jalr), .en(en), .Q(WB_Jalr), .clk(clk), .clr(rst));
  Register #(.width(32)) register_6 (.D(MEM_Calc_Mout), .en(en), .Q(WB_Calc_Mout), .clk(clk), .clr(rst));
  Register #(.width(5)) register_7 (.D(MEM_rd), .en(en), .Q(WB_rd), .clk(clk), .clr(rst));
  Register #(.width(1)) register_8 (.D(MEM_Ecall), .en(en), .Q(WB_Ecall), .clk(clk), .clr(rst));
  Register #(.width(1)) register_9 (.D(MEM_Equal), .en(en), .Q(WB_Equal), .clk(clk), .clr(rst));
endmodule

module \源寄存器使用情况  (
  input  [4:0] OP,
  input  [4:0] Funct,
  output r1_used,
  output r2_used
);

  wire and_1_out, and_2_out, and_3_out, and_4_out, and_5_out, and_6_out, and_7_out, and_8_out, and_9_out,
       and_10_out, and_11_out, and_12_out, and_13_out, and_14_out, and_15_out, and_16_out, and_17_out,
       and_18_out, and_19_out, and_20_out, and_21_out, and_22_out, and_23_out, and_24_out, and_25_out,
       and_26_out, and_27_out, and_28_out, and_29_out, and_30_out, and_31_out, and_32_out, and_33_out,
       and_34_out, not_1_out, not_2_out, not_3_out, not_4_out, not_5_out, not_6_out, not_7_out, not_8_out,
       not_9_out, not_10_out, not_11_out, not_12_out, not_13_out, not_14_out, not_15_out, not_16_out,
       not_17_out, not_18_out, not_19_out, not_20_out, not_21_out, not_22_out, not_23_out, not_24_out,
       not_25_out, not_26_out, not_27_out, not_28_out, not_29_out, not_30_out, not_31_out, not_32_out,
       not_33_out, not_34_out, not_35_out, not_36_out, not_37_out, not_38_out, not_39_out, not_40_out,
       not_41_out, not_42_out, not_43_out, not_44_out, not_45_out, not_46_out, not_47_out, not_48_out,
       not_49_out, not_50_out, not_51_out, not_52_out, not_53_out, not_54_out, not_55_out, not_56_out,
       not_57_out, not_58_out, not_59_out, not_60_out, not_61_out, not_62_out, not_63_out, not_64_out,
       not_65_out, not_66_out, not_67_out, not_68_out, not_69_out, not_70_out, not_71_out, not_72_out,
       not_73_out, not_74_out, not_75_out, not_76_out, not_77_out, not_78_out, not_79_out, not_80_out,
       not_81_out, not_82_out, not_83_out, not_84_out, not_85_out, not_86_out, not_87_out, not_88_out,
       not_89_out, not_90_out, not_91_out, not_92_out, not_93_out, not_94_out, not_95_out, not_96_out,
       not_97_out, not_98_out, not_99_out, not_100_out, not_101_out, not_102_out, not_103_out, not_104_out,
       not_105_out, not_106_out, not_107_out, not_108_out, not_109_out, not_110_out, not_111_out,
       not_112_out, not_113_out, not_114_out, not_115_out, not_116_out, not_117_out, not_118_out,
       not_119_out, not_120_out, not_121_out, not_122_out, not_123_out, not_124_out, not_125_out,
       not_126_out, not_127_out, not_128_out, not_129_out, not_130_out, not_131_out, not_132_out,
       not_133_out, not_134_out, not_135_out, not_136_out, not_137_out, not_138_out, not_139_out,
       not_140_out, not_141_out, not_142_out, not_143_out, not_144_out, not_145_out, not_146_out,
       not_147_out, not_148_out, not_149_out, not_150_out, not_151_out, not_152_out, not_153_out,
       not_154_out, not_155_out, not_156_out, not_157_out, not_158_out, not_159_out, not_160_out,
       not_161_out, not_162_out, not_163_out, not_164_out, not_165_out, not_166_out, not_167_out,
       not_168_out, not_169_out, not_170_out, not_171_out, not_172_out, not_173_out, not_174_out,
       not_175_out, not_176_out, not_177_out, not_178_out, not_179_out, not_180_out, not_181_out,
       not_182_out, not_183_out, not_184_out, not_185_out, not_186_out, not_187_out, not_188_out,
       not_189_out, not_190_out, not_191_out, not_192_out, not_193_out, not_194_out, not_195_out,
       not_196_out, not_197_out, not_198_out, not_199_out, not_200_out, not_201_out, not_202_out,
       not_203_out, not_204_out;

  not not_1 (not_1_out, Funct[4]);
  not not_2 (not_2_out, Funct[3]);
  not not_3 (not_3_out, Funct[2]);
  not not_4 (not_4_out, Funct[1]);
  not not_5 (not_5_out, Funct[0]);
  not not_6 (not_6_out, OP[4]);
  not not_7 (not_7_out, OP[1]);
  not not_8 (not_8_out, OP[0]);
  not not_9 (not_9_out, Funct[3]);
  not not_10 (not_10_out, Funct[2]);
  not not_11 (not_11_out, Funct[1]);
  not not_12 (not_12_out, Funct[0]);
  not not_13 (not_13_out, OP[4]);
  not not_14 (not_14_out, OP[1]);
  not not_15 (not_15_out, OP[0]);
  not not_16 (not_16_out, Funct[4]);
  not not_17 (not_17_out, Funct[3]);
  not not_18 (not_18_out, OP[4]);
  not not_19 (not_19_out, OP[1]);
  not not_20 (not_20_out, OP[0]);
  not not_21 (not_21_out, Funct[4]);
  not not_22 (not_22_out, Funct[3]);
  not not_23 (not_23_out, Funct[0]);
  not not_24 (not_24_out, OP[4]);
  not not_25 (not_25_out, OP[1]);
  not not_26 (not_26_out, OP[0]);
  not not_27 (not_27_out, Funct[4]);
  not not_28 (not_28_out, Funct[3]);
  not not_29 (not_29_out, Funct[2]);
  not not_30 (not_30_out, Funct[0]);
  not not_31 (not_31_out, OP[4]);
  not not_32 (not_32_out, OP[1]);
  not not_33 (not_33_out, OP[0]);
  not not_34 (not_34_out, Funct[4]);
  not not_35 (not_35_out, Funct[3]);
  not not_36 (not_36_out, Funct[2]);
  not not_37 (not_37_out, OP[4]);
  not not_38 (not_38_out, OP[1]);
  not not_39 (not_39_out, OP[0]);
  not not_40 (not_40_out, Funct[2]);
  not not_41 (not_41_out, Funct[1]);
  not not_42 (not_42_out, Funct[0]);
  not not_43 (not_43_out, OP[4]);
  not not_44 (not_44_out, OP[3]);
  not not_45 (not_45_out, OP[1]);
  not not_46 (not_46_out, OP[0]);
  not not_47 (not_47_out, OP[4]);
  not not_48 (not_48_out, OP[3]);
  not not_49 (not_49_out, OP[1]);
  not not_50 (not_50_out, OP[0]);
  not not_51 (not_51_out, Funct[0]);
  not not_52 (not_52_out, OP[4]);
  not not_53 (not_53_out, OP[3]);
  not not_54 (not_54_out, OP[1]);
  not not_55 (not_55_out, OP[0]);
  not not_56 (not_56_out, Funct[1]);
  not not_57 (not_57_out, Funct[0]);
  not not_58 (not_58_out, OP[4]);
  not not_59 (not_59_out, OP[3]);
  not not_60 (not_60_out, OP[1]);
  not not_61 (not_61_out, OP[0]);
  not not_62 (not_62_out, Funct[2]);
  not not_63 (not_63_out, Funct[0]);
  not not_64 (not_64_out, OP[4]);
  not not_65 (not_65_out, OP[3]);
  not not_66 (not_66_out, OP[1]);
  not not_67 (not_67_out, OP[0]);
  not not_68 (not_68_out, Funct[4]);
  not not_69 (not_69_out, Funct[3]);
  not not_70 (not_70_out, Funct[2]);
  not not_71 (not_71_out, Funct[1]);
  not not_72 (not_72_out, OP[4]);
  not not_73 (not_73_out, OP[3]);
  not not_74 (not_74_out, OP[1]);
  not not_75 (not_75_out, OP[0]);
  not not_76 (not_76_out, Funct[4]);
  not not_77 (not_77_out, Funct[3]);
  not not_78 (not_78_out, Funct[1]);
  not not_79 (not_79_out, OP[4]);
  not not_80 (not_80_out, OP[3]);
  not not_81 (not_81_out, OP[1]);
  not not_82 (not_82_out, OP[0]);
  not not_83 (not_83_out, Funct[3]);
  not not_84 (not_84_out, Funct[1]);
  not not_85 (not_85_out, OP[4]);
  not not_86 (not_86_out, OP[3]);
  not not_87 (not_87_out, OP[1]);
  not not_88 (not_88_out, OP[0]);
  not not_89 (not_89_out, Funct[2]);
  not not_90 (not_90_out, Funct[0]);
  not not_91 (not_91_out, OP[4]);
  not not_92 (not_92_out, OP[3]);
  not not_93 (not_93_out, OP[2]);
  not not_94 (not_94_out, OP[1]);
  not not_95 (not_95_out, OP[0]);
  not not_96 (not_96_out, Funct[2]);
  not not_97 (not_97_out, Funct[0]);
  not not_98 (not_98_out, OP[4]);
  not not_99 (not_99_out, OP[2]);
  not not_100 (not_100_out, OP[1]);
  not not_101 (not_101_out, OP[0]);
  not not_102 (not_102_out, Funct[2]);
  not not_103 (not_103_out, Funct[1]);
  not not_104 (not_104_out, Funct[0]);
  not not_105 (not_105_out, OP[2]);
  not not_106 (not_106_out, OP[1]);
  not not_107 (not_107_out, OP[0]);
  not not_108 (not_108_out, Funct[2]);
  not not_109 (not_109_out, Funct[1]);
  not not_110 (not_110_out, OP[2]);
  not not_111 (not_111_out, OP[1]);
  not not_112 (not_112_out, OP[0]);
  not not_113 (not_113_out, Funct[2]);
  not not_114 (not_114_out, Funct[1]);
  not not_115 (not_115_out, Funct[0]);
  not not_116 (not_116_out, OP[2]);
  not not_117 (not_117_out, OP[1]);
  not not_118 (not_118_out, Funct[3]);
  not not_119 (not_119_out, Funct[1]);
  not not_120 (not_120_out, OP[4]);
  not not_121 (not_121_out, OP[1]);
  not not_122 (not_122_out, OP[0]);
  not not_123 (not_123_out, Funct[2]);
  not not_124 (not_124_out, OP[4]);
  not not_125 (not_125_out, OP[3]);
  not not_126 (not_126_out, OP[1]);
  not not_127 (not_127_out, OP[0]);
  not not_128 (not_128_out, Funct[1]);
  not not_129 (not_129_out, OP[4]);
  not not_130 (not_130_out, OP[3]);
  not not_131 (not_131_out, OP[2]);
  not not_132 (not_132_out, OP[1]);
  not not_133 (not_133_out, OP[0]);
  not not_134 (not_134_out, Funct[1]);
  not not_135 (not_135_out, Funct[0]);
  not not_136 (not_136_out, OP[2]);
  not not_137 (not_137_out, OP[1]);
  not not_138 (not_138_out, OP[0]);
  not not_139 (not_139_out, Funct[4]);
  not not_140 (not_140_out, Funct[3]);
  not not_141 (not_141_out, Funct[2]);
  not not_142 (not_142_out, Funct[1]);
  not not_143 (not_143_out, Funct[0]);
  not not_144 (not_144_out, OP[4]);
  not not_145 (not_145_out, OP[1]);
  not not_146 (not_146_out, OP[0]);
  not not_147 (not_147_out, Funct[3]);
  not not_148 (not_148_out, Funct[2]);
  not not_149 (not_149_out, Funct[1]);
  not not_150 (not_150_out, Funct[0]);
  not not_151 (not_151_out, OP[4]);
  not not_152 (not_152_out, OP[1]);
  not not_153 (not_153_out, OP[0]);
  not not_154 (not_154_out, Funct[4]);
  not not_155 (not_155_out, Funct[3]);
  not not_156 (not_156_out, OP[4]);
  not not_157 (not_157_out, OP[1]);
  not not_158 (not_158_out, OP[0]);
  not not_159 (not_159_out, Funct[4]);
  not not_160 (not_160_out, Funct[3]);
  not not_161 (not_161_out, Funct[0]);
  not not_162 (not_162_out, OP[4]);
  not not_163 (not_163_out, OP[1]);
  not not_164 (not_164_out, OP[0]);
  not not_165 (not_165_out, Funct[4]);
  not not_166 (not_166_out, Funct[3]);
  not not_167 (not_167_out, Funct[2]);
  not not_168 (not_168_out, Funct[0]);
  not not_169 (not_169_out, OP[4]);
  not not_170 (not_170_out, OP[1]);
  not not_171 (not_171_out, OP[0]);
  not not_172 (not_172_out, Funct[4]);
  not not_173 (not_173_out, Funct[3]);
  not not_174 (not_174_out, Funct[2]);
  not not_175 (not_175_out, OP[4]);
  not not_176 (not_176_out, OP[1]);
  not not_177 (not_177_out, OP[0]);
  not not_178 (not_178_out, Funct[2]);
  not not_179 (not_179_out, Funct[0]);
  not not_180 (not_180_out, OP[4]);
  not not_181 (not_181_out, OP[2]);
  not not_182 (not_182_out, OP[1]);
  not not_183 (not_183_out, OP[0]);
  not not_184 (not_184_out, Funct[2]);
  not not_185 (not_185_out, Funct[1]);
  not not_186 (not_186_out, Funct[0]);
  not not_187 (not_187_out, OP[2]);
  not not_188 (not_188_out, OP[1]);
  not not_189 (not_189_out, OP[0]);
  not not_190 (not_190_out, Funct[2]);
  not not_191 (not_191_out, Funct[1]);
  not not_192 (not_192_out, OP[2]);
  not not_193 (not_193_out, OP[1]);
  not not_194 (not_194_out, OP[0]);
  not not_195 (not_195_out, Funct[3]);
  not not_196 (not_196_out, Funct[1]);
  not not_197 (not_197_out, OP[4]);
  not not_198 (not_198_out, OP[1]);
  not not_199 (not_199_out, OP[0]);
  not not_200 (not_200_out, Funct[1]);
  not not_201 (not_201_out, Funct[0]);
  not not_202 (not_202_out, OP[2]);
  not not_203 (not_203_out, OP[1]);
  not not_204 (not_204_out, OP[0]);
  and and_1 (and_1_out, not_1_out, not_2_out, not_3_out, not_4_out, not_5_out, not_6_out, OP[3], OP[2], not_7_out, not_8_out);
  and and_2 (and_2_out, Funct[4], not_9_out, not_10_out, not_11_out, not_12_out, not_13_out, OP[3], OP[2], not_14_out, not_15_out);
  and and_3 (and_3_out, not_16_out, not_17_out, Funct[2], Funct[1], Funct[0], not_18_out, OP[3], OP[2], not_19_out, not_20_out);
  and and_4 (and_4_out, not_21_out, not_22_out, Funct[2], Funct[1], not_23_out, not_24_out, OP[3], OP[2], not_25_out, not_26_out);
  and and_5 (and_5_out, not_27_out, not_28_out, not_29_out, Funct[1], not_30_out, not_31_out, OP[3], OP[2], not_32_out, not_33_out);
  and and_6 (and_6_out, not_34_out, not_35_out, not_36_out, Funct[1], Funct[0], not_37_out, OP[3], OP[2], not_38_out, not_39_out);
  and and_7 (and_7_out, not_40_out, not_41_out, not_42_out, not_43_out, not_44_out, OP[2], not_45_out, not_46_out);
  and and_8 (and_8_out, Funct[2], Funct[1], Funct[0], not_47_out, not_48_out, OP[2], not_49_out, not_50_out);
  and and_9 (and_9_out, Funct[2], Funct[1], not_51_out, not_52_out, not_53_out, OP[2], not_54_out, not_55_out);
  and and_10 (and_10_out, Funct[2], not_56_out, not_57_out, not_58_out, not_59_out, OP[2], not_60_out, not_61_out);
  and and_11 (and_11_out, not_62_out, Funct[1], not_63_out, not_64_out, not_65_out, OP[2], not_66_out, not_67_out);
  and and_12 (and_12_out, not_68_out, not_69_out, not_70_out, not_71_out, Funct[0], not_72_out, not_73_out, OP[2], not_74_out, not_75_out);
  and and_13 (and_13_out, not_76_out, not_77_out, Funct[2], not_78_out, Funct[0], not_79_out, not_80_out, OP[2], not_81_out, not_82_out);
  and and_14 (and_14_out, Funct[4], not_83_out, Funct[2], not_84_out, Funct[0], not_85_out, not_86_out, OP[2], not_87_out, not_88_out);
  and and_15 (and_15_out, not_89_out, Funct[1], not_90_out, not_91_out, not_92_out, not_93_out, not_94_out, not_95_out);
  and and_16 (and_16_out, not_96_out, Funct[1], not_97_out, not_98_out, OP[3], not_99_out, not_100_out, not_101_out);
  and and_17 (and_17_out, not_102_out, not_103_out, not_104_out, OP[4], OP[3], not_105_out, not_106_out, not_107_out);
  and and_18 (and_18_out, not_108_out, not_109_out, Funct[0], OP[4], OP[3], not_110_out, not_111_out, not_112_out);
  and and_19 (and_19_out, not_113_out, not_114_out, not_115_out, OP[4], OP[3], not_116_out, not_117_out, OP[0]);
  and and_20 (and_20_out, Funct[4], not_118_out, Funct[2], not_119_out, Funct[0], not_120_out, OP[3], OP[2], not_121_out, not_122_out);
  and and_21 (and_21_out, not_123_out, Funct[1], Funct[0], not_124_out, not_125_out, OP[2], not_126_out, not_127_out);
  and and_22 (and_22_out, Funct[2], not_128_out, Funct[0], not_129_out, not_130_out, not_131_out, not_132_out, not_133_out);
  and and_23 (and_23_out, Funct[2], not_134_out, not_135_out, OP[4], OP[3], not_136_out, not_137_out, not_138_out);
  and and_24 (and_24_out, not_139_out, not_140_out, not_141_out, not_142_out, not_143_out, not_144_out, OP[3], OP[2], not_145_out, not_146_out);
  and and_25 (and_25_out, Funct[4], not_147_out, not_148_out, not_149_out, not_150_out, not_151_out, OP[3], OP[2], not_152_out, not_153_out);
  and and_26 (and_26_out, not_154_out, not_155_out, Funct[2], Funct[1], Funct[0], not_156_out, OP[3], OP[2], not_157_out, not_158_out);
  and and_27 (and_27_out, not_159_out, not_160_out, Funct[2], Funct[1], not_161_out, not_162_out, OP[3], OP[2], not_163_out, not_164_out);
  and and_28 (and_28_out, not_165_out, not_166_out, not_167_out, Funct[1], not_168_out, not_169_out, OP[3], OP[2], not_170_out, not_171_out);
  and and_29 (and_29_out, not_172_out, not_173_out, not_174_out, Funct[1], Funct[0], not_175_out, OP[3], OP[2], not_176_out, not_177_out);
  and and_30 (and_30_out, not_178_out, Funct[1], not_179_out, not_180_out, OP[3], not_181_out, not_182_out, not_183_out);
  and and_31 (and_31_out, not_184_out, not_185_out, not_186_out, OP[4], OP[3], not_187_out, not_188_out, not_189_out);
  and and_32 (and_32_out, not_190_out, not_191_out, Funct[0], OP[4], OP[3], not_192_out, not_193_out, not_194_out);
  and and_33 (and_33_out, Funct[4], not_195_out, Funct[2], not_196_out, Funct[0], not_197_out, OP[3], OP[2], not_198_out, not_199_out);
  and and_34 (and_34_out, Funct[2], not_200_out, not_201_out, OP[4], OP[3], not_202_out, not_203_out, not_204_out);
  or or_1 (r1_used, and_1_out, and_2_out, and_3_out, and_4_out, and_5_out, and_6_out, and_7_out, and_8_out, and_9_out, and_10_out, and_11_out, and_12_out, and_13_out, and_14_out, and_15_out, and_16_out, and_17_out, and_18_out, and_19_out, and_20_out, and_21_out, and_22_out, and_23_out);
  or or_2 (r2_used, and_24_out, and_25_out, and_26_out, and_27_out, and_28_out, and_29_out, and_30_out, and_31_out, and_32_out, and_33_out, and_34_out);
endmodule

module \相关处理逻辑_气泡  (
  input  [4:0] rs1,
  input  rs1_used,
  input  EX_RegWrite,
  input  [4:0] EX_rd,
  input  [4:0] rs2,
  input  rs2_used,
  input  MEM_RegWrite,
  input  [4:0] MEM_rd,
  input  BranchTaken,
  output \阻塞 ,
  output \清空 
);

  wire and_1_out, and_2_out, and_3_out, and_4_out, comparator_1_eq, comparator_2_eq, comparator_3_eq,
       comparator_4_eq, comparator_5_eq, comparator_6_eq, comparator_7_eq, comparator_8_eq, not_1_out,
       not_2_out, not_3_out, not_4_out;

  Comparator #(.width(5)) comparator_1 (.a({5{1'b0}}), .b(rs1), .eq(comparator_1_eq));  // open: gt, lt
  Comparator #(.width(5)) comparator_2 (.a(rs1), .b(EX_rd), .eq(comparator_2_eq));  // open: gt, lt
  Comparator #(.width(5)) comparator_3 (.a({5{1'b0}}), .b(rs2), .eq(comparator_3_eq));  // open: gt, lt
  Comparator #(.width(5)) comparator_4 (.a(rs2), .b(EX_rd), .eq(comparator_4_eq));  // open: gt, lt
  Comparator #(.width(5)) comparator_5 (.a({5{1'b0}}), .b(rs1), .eq(comparator_5_eq));  // open: gt, lt
  Comparator #(.width(5)) comparator_6 (.a(rs1), .b(MEM_rd), .eq(comparator_6_eq));  // open: gt, lt
  Comparator #(.width(5)) comparator_7 (.a({5{1'b0}}), .b(rs2), .eq(comparator_7_eq));  // open: gt, lt
  Comparator #(.width(5)) comparator_8 (.a(rs2), .b(MEM_rd), .eq(comparator_8_eq));  // open: gt, lt
  not not_1 (not_1_out, comparator_1_eq);
  not not_2 (not_2_out, comparator_3_eq);
  not not_3 (not_3_out, comparator_5_eq);
  not not_4 (not_4_out, comparator_7_eq);
  and and_1 (and_1_out, rs1_used, not_1_out, comparator_2_eq, EX_RegWrite);
  and and_2 (and_2_out, rs2_used, not_2_out, comparator_4_eq, EX_RegWrite);
  and and_3 (and_3_out, rs1_used, not_3_out, comparator_6_eq, MEM_RegWrite);
  and and_4 (and_4_out, rs2_used, not_4_out, comparator_8_eq, MEM_RegWrite);
  or or_1 (\阻塞 , and_1_out, and_2_out, and_3_out, and_4_out);

  assign \清空  = BranchTaken;
endmodule

module \流水线寄存器  (
  input  Jal,
  input  Jalr,
  input  Lhu,
  input  Beq,
  input  Bne,
  input  Blt,
  input  MemToReg,
  input  MemWrite,
  input  AluSrcB,
  input  RegWrite,
  input  ecall,
  input  halt,
  input  [3:0] AluOP,
  input  [4:0] rd,
  input  valid,
  input  [31:0] R1,
  input  [31:0] R2,
  input  [31:0] PC,
  input  [31:0] PC_4,
  input  [31:0] imm_si,
  input  [31:0] imm_b,
  input  [31:0] imm_j,
  input  [31:0] Alu_ans,
  input  [31:0] RDin,
  input  [31:0] IR,
  input  reset,
  input  refresh,
  input  halt_2,
  input  clk,
  output Jal_2,
  output Jalr_2,
  output Lhu_2,
  output Beq_2,
  output Bne_2,
  output Blt_2,
  output MemToReg_2,
  output MemWrite_2,
  output AluSrcB_2,
  output RegWrite_2,
  output ecall_2,
  output halt_3,
  output [3:0] AluOP_2,
  output [4:0] rd_2,
  output valid_2,
  output [31:0] R1_2,
  output [31:0] R2_2,
  output [31:0] PC_2,
  output [31:0] PC_4_2,
  output [31:0] imm_si_2,
  output [31:0] imm_b_2,
  output [31:0] imm_j_2,
  output [31:0] Alu_ans_2,
  output [31:0] RDin_2,
  output [31:0] IR_2
);

  wire multiplexer_1_out, multiplexer_2_out, multiplexer_3_out, multiplexer_4_out, multiplexer_5_out,
       multiplexer_6_out, multiplexer_7_out, multiplexer_8_out, multiplexer_9_out, multiplexer_10_out,
       multiplexer_11_out, multiplexer_12_out, multiplexer_15_out, not_1_out, or_1_out;
  wire [3:0] multiplexer_13_out;
  wire [4:0] multiplexer_14_out;
  wire [31:0] multiplexer_16_out, multiplexer_17_out, multiplexer_18_out, multiplexer_19_out,
       multiplexer_20_out, multiplexer_21_out, multiplexer_22_out, multiplexer_23_out, multiplexer_24_out,
       multiplexer_25_out;

  Multiplexer #(.enable("false")) multiplexer_1 (.in0(Jal), .in1(1'b0), .out(multiplexer_1_out), .sel(or_1_out));
  Multiplexer #(.enable("false")) multiplexer_2 (.in0(Jalr), .in1(1'b0), .out(multiplexer_2_out), .sel(or_1_out));
  Multiplexer #(.enable("false")) multiplexer_3 (.in0(Lhu), .in1(1'b0), .out(multiplexer_3_out), .sel(or_1_out));
  Multiplexer #(.enable("false")) multiplexer_4 (.in0(Beq), .in1(1'b0), .out(multiplexer_4_out), .sel(or_1_out));
  Multiplexer #(.enable("false")) multiplexer_5 (.in0(Bne), .in1(1'b0), .out(multiplexer_5_out), .sel(or_1_out));
  Multiplexer #(.enable("false")) multiplexer_6 (.in0(Blt), .in1(1'b0), .out(multiplexer_6_out), .sel(or_1_out));
  Multiplexer #(.enable("false")) multiplexer_7 (.in0(MemToReg), .in1(1'b0), .out(multiplexer_7_out), .sel(or_1_out));
  Multiplexer #(.enable("false")) multiplexer_8 (.in0(MemWrite), .in1(1'b0), .out(multiplexer_8_out), .sel(or_1_out));
  Multiplexer #(.enable("false")) multiplexer_9 (.in0(AluSrcB), .in1(1'b0), .out(multiplexer_9_out), .sel(or_1_out));
  Multiplexer #(.enable("false")) multiplexer_10 (.in0(RegWrite), .in1(1'b0), .out(multiplexer_10_out), .sel(or_1_out));
  Multiplexer #(.enable("false")) multiplexer_11 (.in0(ecall), .in1(1'b0), .out(multiplexer_11_out), .sel(or_1_out));
  Multiplexer #(.enable("false")) multiplexer_12 (.in0(halt), .in1(1'b0), .out(multiplexer_12_out), .sel(or_1_out));
  Multiplexer #(.width(4), .enable("false")) multiplexer_13 (
    .in0(AluOP), .in1(4'b0000), .out(multiplexer_13_out), .sel(or_1_out));
  Multiplexer #(.width(5), .enable("false")) multiplexer_14 (
    .in0(rd), .in1({5{1'b0}}), .out(multiplexer_14_out), .sel(or_1_out));
  Multiplexer #(.enable("false")) multiplexer_15 (.in0(valid), .in1(1'b0), .out(multiplexer_15_out), .sel(or_1_out));
  Multiplexer #(.width(32), .enable("false")) multiplexer_16 (
    .in0(R1), .in1({32{1'b0}}), .out(multiplexer_16_out), .sel(or_1_out));
  Multiplexer #(.width(32), .enable("false")) multiplexer_17 (
    .in0(R2), .in1({32{1'b0}}), .out(multiplexer_17_out), .sel(or_1_out));
  Multiplexer #(.width(32), .enable("false")) multiplexer_18 (
    .in0(PC), .in1({32{1'b0}}), .out(multiplexer_18_out), .sel(or_1_out));
  Multiplexer #(.width(32), .enable("false")) multiplexer_19 (
    .in0(PC_4), .in1({32{1'b0}}), .out(multiplexer_19_out), .sel(or_1_out));
  Multiplexer #(.width(32), .enable("false")) multiplexer_20 (
    .in0(imm_si), .in1({32{1'b0}}), .out(multiplexer_20_out), .sel(or_1_out));
  Multiplexer #(.width(32), .enable("false")) multiplexer_21 (
    .in0(imm_b), .in1({32{1'b0}}), .out(multiplexer_21_out), .sel(or_1_out));
  Multiplexer #(.width(32), .enable("false")) multiplexer_22 (
    .in0(imm_j), .in1({32{1'b0}}), .out(multiplexer_22_out), .sel(or_1_out));
  Multiplexer #(.width(32), .enable("false")) multiplexer_23 (
    .in0(Alu_ans), .in1({32{1'b0}}), .out(multiplexer_23_out), .sel(or_1_out));
  Multiplexer #(.width(32), .enable("false")) multiplexer_24 (
    .in0(RDin), .in1({32{1'b0}}), .out(multiplexer_24_out), .sel(or_1_out));
  Multiplexer #(.width(32), .enable("false")) multiplexer_25 (
    .in0(IR), .in1({32{1'b0}}), .out(multiplexer_25_out), .sel(or_1_out));
  or or_1 (or_1_out, reset, refresh);
  not not_1 (not_1_out, halt_2);
  Register #(.width(1)) register_1 (.D(multiplexer_1_out), .en(not_1_out), .Q(Jal_2), .clk(clk));  // open: clr
  Register #(.width(1)) register_2 (.D(multiplexer_2_out), .en(not_1_out), .Q(Jalr_2), .clk(clk));  // open: clr
  Register #(.width(1)) register_3 (.D(multiplexer_3_out), .en(not_1_out), .Q(Lhu_2), .clk(clk));  // open: clr
  Register #(.width(1)) register_4 (.D(multiplexer_4_out), .en(not_1_out), .Q(Beq_2), .clk(clk));  // open: clr
  Register #(.width(1)) register_5 (.D(multiplexer_5_out), .en(not_1_out), .Q(Bne_2), .clk(clk));  // open: clr
  Register #(.width(1)) register_6 (.D(multiplexer_6_out), .en(not_1_out), .Q(Blt_2), .clk(clk));  // open: clr
  Register #(.width(1)) register_7 (.D(multiplexer_7_out), .en(not_1_out), .Q(MemToReg_2), .clk(clk));  // open: clr
  Register #(.width(1)) register_8 (.D(multiplexer_8_out), .en(not_1_out), .Q(MemWrite_2), .clk(clk));  // open: clr
  Register #(.width(1)) register_9 (.D(multiplexer_9_out), .en(not_1_out), .Q(AluSrcB_2), .clk(clk));  // open: clr
  Register #(.width(1)) register_10 (.D(multiplexer_10_out), .en(not_1_out), .Q(RegWrite_2), .clk(clk));  // open: clr
  Register #(.width(1)) register_11 (.D(multiplexer_11_out), .en(not_1_out), .Q(ecall_2), .clk(clk));  // open: clr
  Register #(.width(1)) register_12 (.D(multiplexer_12_out), .en(not_1_out), .Q(halt_3), .clk(clk));  // open: clr
  Register #(.width(4)) register_13 (.D(multiplexer_13_out), .en(not_1_out), .Q(AluOP_2), .clk(clk));  // open: clr
  Register #(.width(5)) register_14 (.D(multiplexer_14_out), .en(not_1_out), .Q(rd_2), .clk(clk));  // open: clr
  Register #(.width(1)) register_15 (.D(multiplexer_15_out), .en(not_1_out), .Q(valid_2), .clk(clk));  // open: clr
  Register #(.width(32)) register_16 (.D(multiplexer_16_out), .en(not_1_out), .Q(R1_2), .clk(clk));  // open: clr
  Register #(.width(32)) register_17 (.D(multiplexer_17_out), .en(not_1_out), .Q(R2_2), .clk(clk));  // open: clr
  Register #(.width(32)) register_18 (.D(multiplexer_18_out), .en(not_1_out), .Q(PC_2), .clk(clk));  // open: clr
  Register #(.width(32)) register_19 (.D(multiplexer_19_out), .en(not_1_out), .Q(PC_4_2), .clk(clk));  // open: clr
  Register #(.width(32)) register_20 (.D(multiplexer_20_out), .en(not_1_out), .Q(imm_si_2), .clk(clk));  // open: clr
  Register #(.width(32)) register_21 (.D(multiplexer_21_out), .en(not_1_out), .Q(imm_b_2), .clk(clk));  // open: clr
  Register #(.width(32)) register_22 (.D(multiplexer_22_out), .en(not_1_out), .Q(imm_j_2), .clk(clk));  // open: clr
  Register #(.width(32)) register_23 (.D(multiplexer_23_out), .en(not_1_out), .Q(Alu_ans_2), .clk(clk));  // open: clr
  Register #(.width(32)) register_24 (.D(multiplexer_24_out), .en(not_1_out), .Q(RDin_2), .clk(clk));  // open: clr
  Register #(.width(32)) register_25 (.D(multiplexer_25_out), .en(not_1_out), .Q(IR_2), .clk(clk));  // open: clr
endmodule

module \相关处理逻辑_重定向  (
  input  [4:0] rs1,
  input  rs1_used,
  input  [4:0] rs2,
  input  rs2_used,
  input  EX_RegWrite,
  input  [4:0] EX_rd,
  input  EX_MemToReg,
  input  MEM_RegWrite,
  input  [4:0] MEM_rd,
  output [1:0] rs1_forward,
  output LoadUse,
  output [1:0] rs2_forward
);

  wire and_1_out, and_2_out, and_3_out, and_4_out, and_5_out, and_6_out, comparator_1_eq, comparator_2_eq,
       comparator_3_eq, comparator_4_eq, comparator_5_eq, comparator_6_eq, comparator_7_eq, comparator_8_eq,
       comparator_9_eq, comparator_10_eq, comparator_11_eq, comparator_12_eq, not_1_out, not_2_out,
       not_3_out, not_4_out, not_5_out, not_6_out;

  Comparator #(.width(5)) comparator_1 (.a({5{1'b0}}), .b(rs1), .eq(comparator_1_eq));  // open: gt, lt
  Comparator #(.width(5)) comparator_2 (.a(rs1), .b(EX_rd), .eq(comparator_2_eq));  // open: gt, lt
  Comparator #(.width(5)) comparator_3 (.a({5{1'b0}}), .b(rs2), .eq(comparator_3_eq));  // open: gt, lt
  Comparator #(.width(5)) comparator_4 (.a(rs2), .b(EX_rd), .eq(comparator_4_eq));  // open: gt, lt
  not not_1 (not_1_out, comparator_1_eq);
  not not_2 (not_2_out, comparator_3_eq);
  and and_1 (and_1_out, rs1_used, not_1_out, comparator_2_eq, EX_MemToReg);
  and and_2 (and_2_out, rs2_used, not_2_out, comparator_4_eq, EX_MemToReg);
  or or_1 (LoadUse, and_1_out, and_2_out);
  not not_3 (not_3_out, comparator_5_eq);
  Comparator #(.width(5)) comparator_5 (.a({5{1'b0}}), .b(rs1), .eq(comparator_5_eq));  // open: gt, lt
  Comparator #(.width(5)) comparator_6 (.a(rs1), .b(MEM_rd), .eq(comparator_6_eq));  // open: gt, lt
  Comparator #(.width(5)) comparator_7 (.a({5{1'b0}}), .b(rs1), .eq(comparator_7_eq));  // open: gt, lt
  not not_4 (not_4_out, comparator_7_eq);
  Comparator #(.width(5)) comparator_8 (.a(rs1), .b(EX_rd), .eq(comparator_8_eq));  // open: gt, lt
  Comparator #(.width(5)) comparator_9 (.a({5{1'b0}}), .b(rs2), .eq(comparator_9_eq));  // open: gt, lt
  not not_5 (not_5_out, comparator_9_eq);
  Comparator #(.width(5)) comparator_10 (.a(rs2), .b(MEM_rd), .eq(comparator_10_eq));  // open: gt, lt
  not not_6 (not_6_out, comparator_11_eq);
  Comparator #(.width(5)) comparator_11 (.a({5{1'b0}}), .b(rs2), .eq(comparator_11_eq));  // open: gt, lt
  Comparator #(.width(5)) comparator_12 (.a(rs2), .b(EX_rd), .eq(comparator_12_eq));  // open: gt, lt
  and and_3 (and_3_out, rs1_used, not_3_out, comparator_6_eq, MEM_RegWrite);
  and and_4 (and_4_out, rs1_used, not_4_out, comparator_8_eq, EX_RegWrite);
  and and_5 (and_5_out, rs2_used, not_5_out, comparator_10_eq, MEM_RegWrite);
  and and_6 (and_6_out, rs2_used, not_6_out, comparator_12_eq, EX_RegWrite);
  Priority_Encoder #(.select(2)) priority_encoder_1 (
    .in0(1'b1), .in1(and_3_out), .in2(and_4_out), .in3(1'b0), .out(rs1_forward));  // open: gs, en_out, en_in
  Priority_Encoder #(.select(2)) priority_encoder_2 (
    .in0(1'b1), .in1(and_5_out), .in2(and_6_out), .in3(1'b0), .out(rs2_forward));  // open: gs, en_out, en_in
endmodule

module forward (
  input  [1:0] rs1_forward,
  input  [1:0] rs2_forward,
  input  LoadUse,
  input  clk,
  output [1:0] rs1_forward_2,
  output [1:0] rs2_forward_2
);

  wire [1:0] multiplexer_1_out, multiplexer_2_out;

  Multiplexer #(.width(2), .enable("false")) multiplexer_1 (
    .in0(rs1_forward), .in1(2'b00), .out(multiplexer_1_out), .sel(LoadUse));
  Multiplexer #(.width(2), .enable("false")) multiplexer_2 (
    .in0(rs2_forward), .in1(2'b00), .out(multiplexer_2_out), .sel(LoadUse));
  Register #(.width(2)) register_1 (.D(multiplexer_1_out), .Q(rs1_forward_2), .clk(clk));  // open: en, clr
  Register #(.width(2)) register_2 (.D(multiplexer_2_out), .Q(rs2_forward_2), .clk(clk));  // open: en, clr
endmodule
